// Digital circuit CPU.dig as structural Verilog
module CPU (
  input  ALU_Invert,
  input  ALU_Increment,
  input  [3:0] REG_Select,
  input  Pulse,
  input  BRA_Unconditional,
  input  ALU_Propagate,
  input  ALU_CarryOut,
  input  ALU_ResultOut,
  input  ALU_OrOut,
  input  BRA_Greater,
  input  BRA_Less,
  input  BRA_Equal,
  input  BRA_NotEqual,
  input  ALU_UseCarry,
  input  MEM_Store,
  input  MEM_Load,
  input  REG_WriteALU,
  input  REG_WriteMDR,
  input  MDR_WriteReg,
  input  MDR_WriteMem,
  input  ADR_Direct,
  input  [15:0] ImmediateValue,
  input  ADR_Immediate,
  input  D_CLK_PC,
  input  D_CLK_Flags,
  input  D_CLK_RegBufferFirst,
  input  D_CLK_RegBufferSecond,
  input  D_CLK_Write,
  input  D_CLK_CIRFirst,
  input  D_CLK_CIRSecond,
  input  D_CLK_SRAM,
  input  D_CLK_MDR,
  input  D_ALU_Increment,
  input  D_RPC_MemAdder,
  input  D_RPC_Registers
);

  wire alu_1_p9, alu_1_p10, alu_1_p11, alu_1_p12, alu_1_p14, clock_1_clock_1, clock_1_clock_2,
       clock_1_clock_3, clock_1_clock_4, clock_1_clock_5, clock_1_clock_6, clock_1_clock_7, clock_1_clock_8,
       flags_1_carry_out, flags_1_equal_out, flags_1_less_out, flags_1_notequal_out;
  wire [7:0] buffer_1_r1_out, buffer_1_r2_out, buffer_2_r1_out, buffer_2_r2_out, eeprom_1_data_out,
       mdr_1_data_out, registers_1_p4, registers_1_p6, sram_1_data_out;
  wire [11:0] rpc_1_p1, rpc_1_p5;
  wire [15:0] rpc_1_p4;

  Clock clock_1 (
    .Pulse(Pulse), .Clock_1(clock_1_clock_1), .Clock_2(clock_1_clock_2), .Clock_3(clock_1_clock_3),
    .Clock_4(clock_1_clock_4), .Clock_5(clock_1_clock_5), .Clock_6(clock_1_clock_6),
    .Clock_7(clock_1_clock_7), .Clock_8(clock_1_clock_8));
  // RPC rpc_1: pin names not known; wires that end beside it: rpc_1_p1, D_RPC_Registers, D_RPC_MemAdder, rpc_1_p4, rpc_1_p5, D_CLK_PC
  MemoryAdder memoryadder_1 (.Data_in(rpc_1_p5), .Data_out(rpc_1_p1));
  EEPROM eeprom_1 (.Address_in(rpc_1_p5), .Data_out(eeprom_1_data_out));
  Buffer buffer_1 (
    .R1_out(buffer_1_r1_out), .R2_out(buffer_1_r2_out), .Data_in(eeprom_1_data_out),
    .Clk_R1_write(D_CLK_CIRFirst), .Clk_R2_write(D_CLK_CIRSecond));
  SRAM sram_1 (
    .Address_in(rpc_1_p4), .Store(MEM_Store), .Clk_write(D_CLK_SRAM), .Load(MEM_Load),
    .Data_out(sram_1_data_out), .Data_in(mdr_1_data_out));
  MDR mdr_1 (
    .Data_mem(sram_1_data_out), .Clk_write(D_CLK_MDR), .Data_out(mdr_1_data_out), .Data_reg(registers_1_p4),
    .Write_mem(MDR_WriteMem), .Write_reg(MDR_WriteReg));
  // Registers registers_1: pin names not known; wires that end beside it: REG_WriteMDR, REG_WriteALU, mdr_1_data_out, registers_1_p4, D_CLK_Write, registers_1_p6, REG_Select
  Buffer buffer_2 (
    .R1_out(buffer_2_r1_out), .R2_out(buffer_2_r2_out), .Data_in(registers_1_p6),
    .Clk_R1_write(D_CLK_RegBufferFirst), .Clk_R2_write(D_CLK_RegBufferSecond));
  Addressor addressor_1 (
    .Data_direct1(buffer_2_r1_out), .Data_imm(ImmediateValue), .Data_out(rpc_1_p4),
    .Enable_direct(ADR_Direct), .Enable_imm(ADR_Immediate), .Data_direct2(buffer_2_r2_out));
  // ALU alu_1: pin names not known; wires that end beside it: buffer_2_r1_out, buffer_2_r2_out, ALU_Invert, D_ALU_Increment, ALU_Propagate, ALU_CarryOut, ALU_ResultOut, ALU_OrOut, alu_1_p9, alu_1_p10, alu_1_p11, alu_1_p12, registers_1_p4, alu_1_p14
  Flags flags_1 (
    .Less_out(flags_1_less_out), .Less_in(alu_1_p10), .Greater_in(alu_1_p9), .Equal_in(alu_1_p11),
    .Greater_out(alu_1_p14), .Equal_out(flags_1_equal_out), .Carry_out(flags_1_carry_out),
    .Clock(D_CLK_Flags), .NotEqual_out(flags_1_notequal_out), .NotEqual_in(alu_1_p12));  // open: Carry_in
  FlagUnit flagunit_1 (
    .ALU_usecarry(ALU_UseCarry), .ALU_increment(ALU_Increment), .BRA_unconditional(BRA_Less),
    .BRA_less(BRA_Unconditional), .BRA_greater(BRA_Greater), .BRA_equal(BRA_Equal),
    .BRA_notequal(BRA_NotEqual), .Clock_1(clock_1_clock_2), .Clock_2(clock_1_clock_4),
    .Clock_5(clock_1_clock_5), .Greater(flags_1_less_out), .Less(alu_1_p14), .Equal(flags_1_equal_out),
    .Carry(flags_1_notequal_out), .ALU_Increment_2(flags_1_carry_out));  // open: PC_Write, PC_Registers, PC_MemAdder

  // Notes on the sheet:
  //   TICK 1
  //   -> First byte of instruction fetched
  //   -> Program counter incremented
  //   TICK 2
  //   -> Second byte of instruction fetched
  //   -> Program counter incremented
  //   TICK 3
  //   -> First register fetched
  //   TICK 4
  //   -> Second register fetched
  //   TICK 5
  //   -> Flag register written to
  //   -> Output register written to
  //   -> Program counter written to
  //   TICK 6
  //   -> Memory written to
  //   conitrol unit
endmodule
