// Digital circuit EEPROM.dig as structural Verilog
module EEPROM (
  input  [15:0] Address_in,
  output [7:0] Data_out
);

  EEPROM #(.AddrBits(13), .Bits(8)) eeprom_1 (.A(Address_in[12:0]), .CS(1'b1), .WE(1'b0), .OE(1'b1), .D(Data_out));

  // Notes on the sheet:
  //   Address_in: pin 4
  //   Data_out: pin 6
  //   Data_out will always be the byte stored at Address_in
  //   contents of eeprom_1 (hex, n*v repeats v):
  //   e9,131*0,97,5547*0,51
endmodule
