// Digital circuit CPU.dig as structural Verilog
module CPU (
  input  Pulse,
  input  [3:0] Tick,
  output [7:0] Test_out
);

  wire alu_1_carry, alu_1_equal, alu_1_greater, alu_1_less, alu_1_notequal, clock_1_clock_1, clock_1_clock_2,
       clock_1_clock_3, clock_1_clock_4, clock_1_clock_5, clock_1_clock_6, clock_1_clock_7, clock_1_clock_8,
       controlunit_1_d_alu_increment, controlunit_1_d_wrt_cirfirst, controlunit_1_d_wrt_cirsecond,
       controlunit_1_d_wrt_flags, controlunit_1_d_wrt_mdr, controlunit_1_d_wrt_regbufferfirst,
       controlunit_1_d_wrt_regbuffersecond, controlunit_1_d_wrt_regoutput, controlunit_1_d_wrt_sram,
       controlunit_1_s_adr_direct, controlunit_1_s_adr_immediate, controlunit_1_s_alu_carryout,
       controlunit_1_s_alu_invert, controlunit_1_s_alu_orout, controlunit_1_s_alu_propagate,
       controlunit_1_s_alu_resultout, controlunit_1_s_ctl_halt, controlunit_1_s_mdr_writealu,
       controlunit_1_s_mdr_writemem, controlunit_1_s_mem_store, controlunit_1_s_reg_writealu,
       controlunit_1_s_reg_writemdr, controlunit_1_s_reg_writeval, flags_1_carry_out, flags_1_equal_out,
       flags_1_greater_out, flags_1_less_out, flags_1_notequal_out, rpc_1_p2, rpc_1_p3, rpc_1_p6;
  wire [3:0] controlunit_1_select;
  wire [7:0] alu_1_data_out, buffer_1_r1_out, buffer_1_r2_out, buffer_2_r1_out, buffer_2_r2_out,
       eeprom_1_data_out, mdr_1_data_out, register_file_1_data_out, sram_1_data_out;
  wire [11:0] controlunit_1_value, rpc_1_p1, rpc_1_p5;
  wire [15:0] rpc_1_p4;

  // RPC rpc_1: pin names not known; wires that end beside it: rpc_1_p1, rpc_1_p2, rpc_1_p3, rpc_1_p4, rpc_1_p5, rpc_1_p6
  EEPROM eeprom_1 (.Address_in(rpc_1_p5), .Data_out(eeprom_1_data_out));
  MemoryAdder memoryadder_1 (.Data_in(rpc_1_p5), .Data_out(rpc_1_p1));
  // Probe on rpc_1_p5
  // Probe on eeprom_1_data_out
  Buffer buffer_1 (
    .R1_out(buffer_1_r1_out), .R2_out(buffer_1_r2_out), .Data_in(eeprom_1_data_out),
    .Clk_R1_write(controlunit_1_d_wrt_cirfirst), .Clk_R2_write(controlunit_1_d_wrt_cirsecond));
  Clock clock_1 (
    .Halt(controlunit_1_s_ctl_halt), .Pulse(Pulse), .Clock_1(clock_1_clock_1), .Clock_2(clock_1_clock_2),
    .Clock_3(clock_1_clock_3), .Clock_4(clock_1_clock_4), .Clock_5(clock_1_clock_5),
    .Clock_6(clock_1_clock_6), .Clock_7(clock_1_clock_7), .Clock_8(clock_1_clock_8));
  // Probe on buffer_1_r2_out
  // Probe on buffer_1_r1_out
  ControlUnit controlunit_1 (
    .FirstByte(buffer_1_r1_out), .SecondByte(buffer_1_r2_out), .Clock_1(clock_1_clock_1),
    .Clock_2(clock_1_clock_2), .Clock_3(clock_1_clock_3), .Clock_4(clock_1_clock_4),
    .Clock_5(clock_1_clock_5), .Clock_6(clock_1_clock_6), .Clock_7(clock_1_clock_7),
    .Clock_8(clock_1_clock_8), .S_CTL_Halt(controlunit_1_s_ctl_halt),
    .S_ADR_Direct(controlunit_1_s_adr_direct), .S_ADR_Immediate(controlunit_1_s_adr_immediate),
    .S_ALU_OrOut(controlunit_1_s_alu_orout), .S_ALU_ResultOut(controlunit_1_s_alu_resultout),
    .S_ALU_Propagate(controlunit_1_s_alu_propagate), .S_ALU_Invert(controlunit_1_s_alu_invert),
    .S_ALU_CarryOut(controlunit_1_s_alu_carryout), .S_MDR_WriteMEM(controlunit_1_s_mdr_writemem),
    .S_MDR_WriteALU(controlunit_1_s_mdr_writealu), .S_MEM_Store(controlunit_1_s_mem_store),
    .S_REG_WriteVAL(controlunit_1_s_reg_writeval), .S_REG_WriteMDR(controlunit_1_s_reg_writemdr),
    .S_REG_WriteALU(controlunit_1_s_reg_writealu), .D_WRT_MDR(controlunit_1_d_wrt_mdr),
    .D_WRT_SRAM(controlunit_1_d_wrt_sram), .D_WRT_RegOutput(controlunit_1_d_wrt_regoutput),
    .D_WRT_RegBufferFirst(controlunit_1_d_wrt_regbufferfirst),
    .D_WRT_RegBufferSecond(controlunit_1_d_wrt_regbuffersecond), .D_WRT_Flags(controlunit_1_d_wrt_flags),
    .D_WRT_RPC(rpc_1_p6), .D_WRT_CIRSecond(controlunit_1_d_wrt_cirsecond),
    .D_WRT_CIRFirst(controlunit_1_d_wrt_cirfirst), .D_RPC_Registers(rpc_1_p2), .D_RPC_MemAdder(rpc_1_p3),
    .D_ALU_Increment(controlunit_1_d_alu_increment), .Select(controlunit_1_select),
    .Value(controlunit_1_value), .F_NotEqual(flags_1_notequal_out), .F_Equal(flags_1_equal_out),
    .F_Less(flags_1_less_out), .F_Greater(flags_1_greater_out), .Carry(flags_1_carry_out));
  SRAM sram_1 (
    .Address_in(rpc_1_p4), .Store(controlunit_1_s_mem_store), .Clk_write(controlunit_1_d_wrt_sram),
    .Data_out(sram_1_data_out), .Data_in(mdr_1_data_out));
  MDR mdr_1 (
    .Data_mem(sram_1_data_out), .Clk_write(controlunit_1_d_wrt_mdr), .Data_out(mdr_1_data_out),
    .Data_reg(alu_1_data_out), .Write_mem(controlunit_1_s_mdr_writemem),
    .Write_reg(controlunit_1_s_mdr_writealu));
  // Probe on sram_1_data_out
  // Probe on mdr_1_data_out
  // Probe on rpc_1_p4
  Register_File register_file_1 (
    .Select(controlunit_1_select), .Clk_write(controlunit_1_d_wrt_regoutput), .Data_alu(alu_1_data_out),
    .Data_out(register_file_1_data_out), .Data_mdr(mdr_1_data_out), .Write_mdr(controlunit_1_s_reg_writemdr),
    .Write_alu(controlunit_1_s_reg_writealu), .Test_out(Test_out), .Data_val(controlunit_1_value),
    .Write_val(controlunit_1_s_reg_writeval));
  // Probe on controlunit_1_select
  Buffer buffer_2 (
    .R1_out(buffer_2_r1_out), .R2_out(buffer_2_r2_out), .Data_in(register_file_1_data_out),
    .Clk_R1_write(controlunit_1_d_wrt_regbufferfirst), .Clk_R2_write(controlunit_1_d_wrt_regbuffersecond));
  // Probe on buffer_2_r2_out
  // Probe on buffer_2_r1_out
  // Addressor addressor_1: pin names not known; wires that end beside it: buffer_2_r1_out, buffer_2_r2_out, controlunit_1_value, controlunit_1_s_adr_direct, controlunit_1_s_adr_immediate, rpc_1_p4
  // Probe on alu_1_data_out
  ALU alu_1 (
    .Data_2_in(buffer_2_r1_out), .Data_1_in(buffer_2_r2_out), .Data_out(alu_1_data_out), .Carry(alu_1_carry),
    .Invert(controlunit_1_s_alu_invert), .Increment(controlunit_1_d_alu_increment), .Equal(alu_1_equal),
    .Greater(alu_1_greater), .Less(alu_1_less), .Out_carry(controlunit_1_s_alu_carryout),
    .Propagate(controlunit_1_s_alu_propagate), .Out_or(controlunit_1_s_alu_orout),
    .Out_result(controlunit_1_s_alu_resultout), .NotEqual(alu_1_notequal));
  Flags flags_1 (
    .Less_out(flags_1_less_out), .Less_in(alu_1_less), .Greater_in(alu_1_greater), .Equal_in(alu_1_equal),
    .Carry_in(alu_1_carry), .Greater_out(flags_1_greater_out), .Equal_out(flags_1_equal_out),
    .Carry_out(flags_1_carry_out), .Clock(controlunit_1_d_wrt_flags), .NotEqual_out(flags_1_notequal_out),
    .NotEqual_in(alu_1_notequal));
endmodule

/* Test case ADD:
Tick Pulse Test_out
# SET 3 r1
memory ProgramMemory(0)=240;
memory ProgramMemory(1)=49;
# SET 45 r6
memory ProgramMemory(2)=242;
memory ProgramMemory(3)=214;
# ADD r1 r6
memory ProgramMemory(4)=8;
memory ProgramMemory(5)=97;
# SET -8 r1
memory ProgramMemory(6)=255;
memory ProgramMemory(7)=129;
# ADD r1 r6
memory ProgramMemory(8)=8;
memory ProgramMemory(9)=97;
# SET 3 r1
1 1 X
1 0 X
2 1 X
2 0 X
3 1 X
3 0 X
4 1 X
4 0 X
5 1 X
5 0 X
6 1 X
6 0 X
7 1 X
7 0 X
8 1 X
8 0 X
# SET 45 r6
1 1 X
1 0 X
2 1 X
2 0 X
3 1 X
3 0 X
4 1 X
4 0 X
5 1 X
5 0 X
6 1 X
6 0 X
7 1 X
7 0 X
8 1 X
8 0 X
# ADD r1 r6
1 1 X
1 0 X
2 1 X
2 0 X
3 1 X
3 0 X
4 1 X
4 0 X
5 1 X
5 0 X
6 1 X
6 0 X
7 1 X
7 0 X
8 1 X
8 0 (48)
# SET -8 r1
1 1 X
1 0 X
2 1 X
2 0 X
3 1 X
3 0 X
4 1 X
4 0 X
5 1 X
5 0 X
6 1 X
6 0 X
7 1 X
7 0 X
8 1 X
8 0 X
# ADD r1 r6
1 1 X
1 0 X
2 1 X
2 0 X
3 1 X
3 0 X
4 1 X
4 0 X
5 1 X
5 0 X
6 1 X
6 0 X
7 1 X
7 0 X
8 1 X
8 0 (37)
*/

/* Test case XOR:
Tick Pulse Test_out
# SET 45 r1
memory ProgramMemory(0)=242;
memory ProgramMemory(1)=209;
# SET 38 r2
memory ProgramMemory(2)=242;
memory ProgramMemory(3)=98;
# XOR r1 r2
memory ProgramMemory(4)=4;
memory ProgramMemory(5)=33;
# SET 45 r1
1 1 X
1 0 X
2 1 X
2 0 X
3 1 X
3 0 X
4 1 X
4 0 X
5 1 X
5 0 X
6 1 X
6 0 X
7 1 X
7 0 X
8 1 X
8 0 X
# SET 38 r2
1 1 X
1 0 X
2 1 X
2 0 X
3 1 X
3 0 X
4 1 X
4 0 X
5 1 X
5 0 X
6 1 X
6 0 X
7 1 X
7 0 X
8 1 X
8 0 X
# XOR r1 r2
1 1 X
1 0 X
2 1 X
2 0 X
3 1 X
3 0 X
4 1 X
4 0 X
5 1 X
5 0 X
6 1 X
6 0 X
7 1 X
7 0 X
8 1 X
8 0 (11)
*/

/* Test case MOV:
Tick Pulse Test_out
# SET 68 r5
memory ProgramMemory(0)=244;
memory ProgramMemory(1)=69;
# SET -16 r3
memory ProgramMemory(2)=255;
memory ProgramMemory(3)=3;
# MOV r1 r5
memory ProgramMemory(4)=33;
memory ProgramMemory(5)=81;
# MOV r1 r3
memory ProgramMemory(6)=33;
memory ProgramMemory(7)=49;
# SET 68 r5
1 1 X
1 0 X
2 1 X
2 0 X
3 1 X
3 0 X
4 1 X
4 0 X
5 1 X
5 0 X
6 1 X
6 0 X
7 1 X
7 0 X
8 1 X
8 0 X
# SET -16 r3
1 1 X
1 0 X
2 1 X
2 0 X
3 1 X
3 0 X
4 1 X
4 0 X
5 1 X
5 0 X
6 1 X
6 0 X
7 1 X
7 0 X
8 1 X
8 0 X
# MOV r1 r5
1 1 X
1 0 X
2 1 X
2 0 X
3 1 X
3 0 X
4 1 X
4 0 X
5 1 X
5 0 X
6 1 X
6 0 X
7 1 X
7 0 X
8 1 X
8 0 (68)
# MOV r1 r3
1 1 X
1 0 X
2 1 X
2 0 X
3 1 X
3 0 X
4 1 X
4 0 X
5 1 X
5 0 X
6 1 X
6 0 X
7 1 X
7 0 X
8 1 X
8 0 (-16)
*/

/* Test case SET:
Tick Pulse Test_out
# SET 2 r1
memory ProgramMemory(0)=240;
memory ProgramMemory(1)=33;
# SET 87 r1
memory ProgramMemory(2)=245;
memory ProgramMemory(3)=113;
# SET -7 r1
memory ProgramMemory(4)=255;
memory ProgramMemory(5)=145;
# SET 55 r3
memory ProgramMemory(6)=243;
memory ProgramMemory(7)=115;
# SET 2 r1
1 1 X
1 0 X
2 1 X
2 0 X
3 1 X
3 0 X
4 1 X
4 0 X
5 1 X
5 0 X
6 1 X
6 0 X
7 1 X
7 0 X
8 1 X
8 0 (2)
# SET 87 r1
1 1 X
1 0 X
2 1 X
2 0 X
3 1 X
3 0 X
4 1 X
4 0 X
5 1 X
5 0 X
6 1 X
6 0 X
7 1 X
7 0 X
8 1 X
8 0 (87)
# SET -7 r1
1 1 X
1 0 X
2 1 X
2 0 X
3 1 X
3 0 X
4 1 X
4 0 X
5 1 X
5 0 X
6 1 X
6 0 X
7 1 X
7 0 X
8 1 X
8 0 (-7)
# SET 55 r3
1 1 X
1 0 X
2 1 X
2 0 X
3 1 X
3 0 X
4 1 X
4 0 X
5 1 X
5 0 X
6 1 X
6 0 X
7 1 X
7 0 X
8 1 X
8 0 (-7)
*/

/* Test case ADC:
Tick Pulse Test_out
# SET 100 r2
memory ProgramMemory(0)=246;
memory ProgramMemory(1)=66;
# SET 200 r3
memory ProgramMemory(2)=252;
memory ProgramMemory(3)=131;
# SET 2 r4
memory ProgramMemory(4)=240;
memory ProgramMemory(5)=36;
# SET 3 r5
memory ProgramMemory(6)=240;
memory ProgramMemory(7)=53;
# ADD r2 r3
memory ProgramMemory(8)=8;
memory ProgramMemory(9)=50;
# MOV r1 r2
memory ProgramMemory(10)=33;
memory ProgramMemory(11)=33;
# ADC r4 r5
memory ProgramMemory(12)=24;
memory ProgramMemory(13)=84;
# MOV r1 r4
memory ProgramMemory(14)=33;
memory ProgramMemory(15)=65;
# ADC r4 r5
memory ProgramMemory(16)=24;
memory ProgramMemory(17)=84;
# MOV r1 r4
memory ProgramMemory(18)=33;
memory ProgramMemory(19)=65;
# SET 100 r2
1 1 X
1 0 X
2 1 X
2 0 X
3 1 X
3 0 X
4 1 X
4 0 X
5 1 X
5 0 X
6 1 X
6 0 X
7 1 X
7 0 X
8 1 X
8 0 X
# SET 200 r3
1 1 X
1 0 X
2 1 X
2 0 X
3 1 X
3 0 X
4 1 X
4 0 X
5 1 X
5 0 X
6 1 X
6 0 X
7 1 X
7 0 X
8 1 X
8 0 X
# SET 2 r4
1 1 X
1 0 X
2 1 X
2 0 X
3 1 X
3 0 X
4 1 X
4 0 X
5 1 X
5 0 X
6 1 X
6 0 X
7 1 X
7 0 X
8 1 X
8 0 X
# SET 3 r5
1 1 X
1 0 X
2 1 X
2 0 X
3 1 X
3 0 X
4 1 X
4 0 X
5 1 X
5 0 X
6 1 X
6 0 X
7 1 X
7 0 X
8 1 X
8 0 X
# ADD r2 r3
1 1 X
1 0 X
2 1 X
2 0 X
3 1 X
3 0 X
4 1 X
4 0 X
5 1 X
5 0 X
6 1 X
6 0 X
7 1 X
7 0 X
8 1 X
8 0 X
# MOV r1 r2
1 1 X
1 0 X
2 1 X
2 0 X
3 1 X
3 0 X
4 1 X
4 0 X
5 1 X
5 0 X
6 1 X
6 0 X
7 1 X
7 0 X
8 1 X
8 0 (44)
# ADC r4 r5
1 1 X
1 0 X
2 1 X
2 0 X
3 1 X
3 0 X
4 1 X
4 0 X
5 1 X
5 0 X
6 1 X
6 0 X
7 1 X
7 0 X
8 1 X
8 0 X
# MOV r1 r4
1 1 X
1 0 X
2 1 X
2 0 X
3 1 X
3 0 X
4 1 X
4 0 X
5 1 X
5 0 X
6 1 X
6 0 X
7 1 X
7 0 X
8 1 X
8 0 (6)
# ADC r4 r5
1 1 X
1 0 X
2 1 X
2 0 X
3 1 X
3 0 X
4 1 X
4 0 X
5 1 X
5 0 X
6 1 X
6 0 X
7 1 X
7 0 X
8 1 X
8 0 X
# MOV r1 r4
1 1 X
1 0 X
2 1 X
2 0 X
3 1 X
3 0 X
4 1 X
4 0 X
5 1 X
5 0 X
6 1 X
6 0 X
7 1 X
7 0 X
8 1 X
8 0 (9)
*/

/* Test case AND:
Tick Pulse Test_out
# SET 45 r1
memory ProgramMemory(0)=242;
memory ProgramMemory(1)=209;
# SET 38 r2
memory ProgramMemory(2)=242;
memory ProgramMemory(3)=98;
# AND r1 r2
memory ProgramMemory(4)=20;
memory ProgramMemory(5)=33;
# SET 45 r1
1 1 X
1 0 X
2 1 X
2 0 X
3 1 X
3 0 X
4 1 X
4 0 X
5 1 X
5 0 X
6 1 X
6 0 X
7 1 X
7 0 X
8 1 X
8 0 X
# SET 38 r2
1 1 X
1 0 X
2 1 X
2 0 X
3 1 X
3 0 X
4 1 X
4 0 X
5 1 X
5 0 X
6 1 X
6 0 X
7 1 X
7 0 X
8 1 X
8 0 X
# AND r1 r2
1 1 X
1 0 X
2 1 X
2 0 X
3 1 X
3 0 X
4 1 X
4 0 X
5 1 X
5 0 X
6 1 X
6 0 X
7 1 X
7 0 X
8 1 X
8 0 (36)
*/

/* Test case STD|LDD:
Tick Pulse Test_out
# SET 0 r3
memory ProgramMemory(0)=240;
memory ProgramMemory(1)=3;
# SET 2 r4
memory ProgramMemory(2)=240;
memory ProgramMemory(3)=36;
# SET 23 r5
memory ProgramMemory(4)=241;
memory ProgramMemory(5)=117;
# SET 37 r1
memory ProgramMemory(6)=242;
memory ProgramMemory(7)=81;
# MTD r1
memory ProgramMemory(8)=49;
memory ProgramMemory(9)=1;
# STD r3 r5
memory ProgramMemory(10)=18;
memory ProgramMemory(11)=83;
# STD r4 r5
memory ProgramMemory(12)=18;
memory ProgramMemory(13)=84;
# SET 0 r1
memory ProgramMemory(14)=240;
memory ProgramMemory(15)=1;
# MTD r1
memory ProgramMemory(16)=49;
memory ProgramMemory(17)=1;
# LDD r3 r5
memory ProgramMemory(18)=2;
memory ProgramMemory(19)=83;
# MFD r1
memory ProgramMemory(20)=65;
memory ProgramMemory(21)=1;
# SET 0 r1
memory ProgramMemory(22)=240;
memory ProgramMemory(23)=1;
# MTD r1
memory ProgramMemory(24)=49;
memory ProgramMemory(25)=1;
# LDD r4 r5
memory ProgramMemory(26)=2;
memory ProgramMemory(27)=84;
# MFD r1
memory ProgramMemory(28)=65;
memory ProgramMemory(29)=1;
# SET 0 r3
1 1 X
1 0 X
2 1 X
2 0 X
3 1 X
3 0 X
4 1 X
4 0 X
5 1 X
5 0 X
6 1 X
6 0 X
7 1 X
7 0 X
8 1 X
8 0 X
# SET 2 r4
1 1 X
1 0 X
2 1 X
2 0 X
3 1 X
3 0 X
4 1 X
4 0 X
5 1 X
5 0 X
6 1 X
6 0 X
7 1 X
7 0 X
8 1 X
8 0 X
# SET 23 r5
1 1 X
1 0 X
2 1 X
2 0 X
3 1 X
3 0 X
4 1 X
4 0 X
5 1 X
5 0 X
6 1 X
6 0 X
7 1 X
7 0 X
8 1 X
8 0 X
# SET 37 r1
1 1 X
1 0 X
2 1 X
2 0 X
3 1 X
3 0 X
4 1 X
4 0 X
5 1 X
5 0 X
6 1 X
6 0 X
7 1 X
7 0 X
8 1 X
8 0 X
# MTD r1
1 1 X
1 0 X
2 1 X
2 0 X
3 1 X
3 0 X
4 1 X
4 0 X
5 1 X
5 0 X
6 1 X
6 0 X
7 1 X
7 0 X
8 1 X
8 0 X
# STD r3 r5
1 1 X
1 0 X
2 1 X
2 0 X
3 1 X
3 0 X
4 1 X
4 0 X
5 1 X
5 0 X
6 1 X
6 0 X
7 1 X
7 0 X
8 1 X
8 0 X
# STD r4 r5
1 1 X
1 0 X
2 1 X
2 0 X
3 1 X
3 0 X
4 1 X
4 0 X
5 1 X
5 0 X
6 1 X
6 0 X
7 1 X
7 0 X
8 1 X
8 0 X
# SET 0 r1
1 1 X
1 0 X
2 1 X
2 0 X
3 1 X
3 0 X
4 1 X
4 0 X
5 1 X
5 0 X
6 1 X
6 0 X
7 1 X
7 0 X
8 1 X
8 0 (0)
# MTD r1
1 1 X
1 0 X
2 1 X
2 0 X
3 1 X
3 0 X
4 1 X
4 0 X
5 1 X
5 0 X
6 1 X
6 0 X
7 1 X
7 0 X
8 1 X
8 0 X
# LDD r3 r5
1 1 X
1 0 X
2 1 X
2 0 X
3 1 X
3 0 X
4 1 X
4 0 X
5 1 X
5 0 X
6 1 X
6 0 X
7 1 X
7 0 X
8 1 X
8 0 X
# MFD r1
1 1 X
1 0 X
2 1 X
2 0 X
3 1 X
3 0 X
4 1 X
4 0 X
5 1 X
5 0 X
6 1 X
6 0 X
7 1 X
7 0 X
8 1 X
8 0 (37)
# SET 0 r1
1 1 X
1 0 X
2 1 X
2 0 X
3 1 X
3 0 X
4 1 X
4 0 X
5 1 X
5 0 X
6 1 X
6 0 X
7 1 X
7 0 X
8 1 X
8 0 (0)
# MTD r1
1 1 X
1 0 X
2 1 X
2 0 X
3 1 X
3 0 X
4 1 X
4 0 X
5 1 X
5 0 X
6 1 X
6 0 X
7 1 X
7 0 X
8 1 X
8 0 X
# LDD r4 r5
1 1 X
1 0 X
2 1 X
2 0 X
3 1 X
3 0 X
4 1 X
4 0 X
5 1 X
5 0 X
6 1 X
6 0 X
7 1 X
7 0 X
8 1 X
8 0 X
# MFD r1
1 1 X
1 0 X
2 1 X
2 0 X
3 1 X
3 0 X
4 1 X
4 0 X
5 1 X
5 0 X
6 1 X
6 0 X
7 1 X
7 0 X
8 1 X
8 0 (37)
*/

/* Test case MTD|MFD:
Tick Pulse Test_out
# SET 54 r1
memory ProgramMemory(0)=243;
memory ProgramMemory(1)=97;
# MTD r1
memory ProgramMemory(2)=49;
memory ProgramMemory(3)=1;
# SET 0 r1
memory ProgramMemory(4)=240;
memory ProgramMemory(5)=1;
# MFD r1
memory ProgramMemory(6)=65;
memory ProgramMemory(7)=1;
# SET 54 r1
1 1 X
1 0 X
2 1 X
2 0 X
3 1 X
3 0 X
4 1 X
4 0 X
5 1 X
5 0 X
6 1 X
6 0 X
7 1 X
7 0 X
8 1 X
8 0 X
# MTD r1
1 1 X
1 0 X
2 1 X
2 0 X
3 1 X
3 0 X
4 1 X
4 0 X
5 1 X
5 0 X
6 1 X
6 0 X
7 1 X
7 0 X
8 1 X
8 0 X
# SET 0 r1
1 1 X
1 0 X
2 1 X
2 0 X
3 1 X
3 0 X
4 1 X
4 0 X
5 1 X
5 0 X
6 1 X
6 0 X
7 1 X
7 0 X
8 1 X
8 0 (0)
# MFD r1
1 1 X
1 0 X
2 1 X
2 0 X
3 1 X
3 0 X
4 1 X
4 0 X
5 1 X
5 0 X
6 1 X
6 0 X
7 1 X
7 0 X
8 1 X
8 0 (54)
*/

/* Test case STI|LDI:
Tick Pulse Test_out
# SET 37 r1
memory ProgramMemory(0)=242;
memory ProgramMemory(1)=81;
# MTD r1
memory ProgramMemory(2)=49;
memory ProgramMemory(3)=1;
# STI 60
memory ProgramMemory(4)=144;
memory ProgramMemory(5)=60;
# STI 3000
memory ProgramMemory(6)=155;
memory ProgramMemory(7)=184;
# SET 0 r1
memory ProgramMemory(8)=240;
memory ProgramMemory(9)=1;
# MTD r1
memory ProgramMemory(10)=49;
memory ProgramMemory(11)=1;
# LDI 60
memory ProgramMemory(12)=128;
memory ProgramMemory(13)=60;
# MFD r1
memory ProgramMemory(14)=65;
memory ProgramMemory(15)=1;
# SET 0 r1
memory ProgramMemory(16)=240;
memory ProgramMemory(17)=1;
# MTD r1
memory ProgramMemory(18)=49;
memory ProgramMemory(19)=1;
# LDI 3000
memory ProgramMemory(20)=139;
memory ProgramMemory(21)=184;
# MFD r1
memory ProgramMemory(22)=65;
memory ProgramMemory(23)=1;
# SET 37 r1
1 1 X
1 0 X
2 1 X
2 0 X
3 1 X
3 0 X
4 1 X
4 0 X
5 1 X
5 0 X
6 1 X
6 0 X
7 1 X
7 0 X
8 1 X
8 0 X
# MTD r1
1 1 X
1 0 X
2 1 X
2 0 X
3 1 X
3 0 X
4 1 X
4 0 X
5 1 X
5 0 X
6 1 X
6 0 X
7 1 X
7 0 X
8 1 X
8 0 X
# STI 60
1 1 X
1 0 X
2 1 X
2 0 X
3 1 X
3 0 X
4 1 X
4 0 X
5 1 X
5 0 X
6 1 X
6 0 X
7 1 X
7 0 X
8 1 X
8 0 X
# STI 3000
1 1 X
1 0 X
2 1 X
2 0 X
3 1 X
3 0 X
4 1 X
4 0 X
5 1 X
5 0 X
6 1 X
6 0 X
7 1 X
7 0 X
8 1 X
8 0 X
# SET 0 r1
1 1 X
1 0 X
2 1 X
2 0 X
3 1 X
3 0 X
4 1 X
4 0 X
5 1 X
5 0 X
6 1 X
6 0 X
7 1 X
7 0 X
8 1 X
8 0 (0)
# MTD r1
1 1 X
1 0 X
2 1 X
2 0 X
3 1 X
3 0 X
4 1 X
4 0 X
5 1 X
5 0 X
6 1 X
6 0 X
7 1 X
7 0 X
8 1 X
8 0 X
# LDI 60
1 1 X
1 0 X
2 1 X
2 0 X
3 1 X
3 0 X
4 1 X
4 0 X
5 1 X
5 0 X
6 1 X
6 0 X
7 1 X
7 0 X
8 1 X
8 0 X
# MFD r1
1 1 X
1 0 X
2 1 X
2 0 X
3 1 X
3 0 X
4 1 X
4 0 X
5 1 X
5 0 X
6 1 X
6 0 X
7 1 X
7 0 X
8 1 X
8 0 (37)
# SET 0 r1
1 1 X
1 0 X
2 1 X
2 0 X
3 1 X
3 0 X
4 1 X
4 0 X
5 1 X
5 0 X
6 1 X
6 0 X
7 1 X
7 0 X
8 1 X
8 0 (0)
# MTD r1
1 1 X
1 0 X
2 1 X
2 0 X
3 1 X
3 0 X
4 1 X
4 0 X
5 1 X
5 0 X
6 1 X
6 0 X
7 1 X
7 0 X
8 1 X
8 0 X
# LDI 3000
1 1 X
1 0 X
2 1 X
2 0 X
3 1 X
3 0 X
4 1 X
4 0 X
5 1 X
5 0 X
6 1 X
6 0 X
7 1 X
7 0 X
8 1 X
8 0 X
# MFD r1
1 1 X
1 0 X
2 1 X
2 0 X
3 1 X
3 0 X
4 1 X
4 0 X
5 1 X
5 0 X
6 1 X
6 0 X
7 1 X
7 0 X
8 1 X
8 0 (37)
*/

/* Test case SUB:
Tick Pulse Test_out
# SET 6 r1
memory ProgramMemory(0)=240;
memory ProgramMemory(1)=97;
# SET 50 r6
memory ProgramMemory(2)=243;
memory ProgramMemory(3)=38;
# SUB r1 r6
memory ProgramMemory(4)=40;
memory ProgramMemory(5)=97;
# SET 72 r1
memory ProgramMemory(6)=244;
memory ProgramMemory(7)=129;
# SUB r1 r6
memory ProgramMemory(8)=40;
memory ProgramMemory(9)=97;
# SET 6 r1
1 1 X
1 0 X
2 1 X
2 0 X
3 1 X
3 0 X
4 1 X
4 0 X
5 1 X
5 0 X
6 1 X
6 0 X
7 1 X
7 0 X
8 1 X
8 0 X
# SET 50 r6
1 1 X
1 0 X
2 1 X
2 0 X
3 1 X
3 0 X
4 1 X
4 0 X
5 1 X
5 0 X
6 1 X
6 0 X
7 1 X
7 0 X
8 1 X
8 0 X
# SUB r1 r6
1 1 X
1 0 X
2 1 X
2 0 X
3 1 X
3 0 X
4 1 X
4 0 X
5 1 X
5 0 X
6 1 X
6 0 X
7 1 X
7 0 X
8 1 X
8 0 (-44)
# SET 72 r1
1 1 X
1 0 X
2 1 X
2 0 X
3 1 X
3 0 X
4 1 X
4 0 X
5 1 X
5 0 X
6 1 X
6 0 X
7 1 X
7 0 X
8 1 X
8 0 X
# SUB r1 r6
1 1 X
1 0 X
2 1 X
2 0 X
3 1 X
3 0 X
4 1 X
4 0 X
5 1 X
5 0 X
6 1 X
6 0 X
7 1 X
7 0 X
8 1 X
8 0 (22)
*/

/* Test case ORR:
Tick Pulse Test_out
# SET 45 r1
memory ProgramMemory(0)=242;
memory ProgramMemory(1)=209;
# SET 38 r2
memory ProgramMemory(2)=242;
memory ProgramMemory(3)=98;
# ORR r1 r2
memory ProgramMemory(4)=36;
memory ProgramMemory(5)=33;
# SET 45 r1
1 1 X
1 0 X
2 1 X
2 0 X
3 1 X
3 0 X
4 1 X
4 0 X
5 1 X
5 0 X
6 1 X
6 0 X
7 1 X
7 0 X
8 1 X
8 0 X
# SET 38 r2
1 1 X
1 0 X
2 1 X
2 0 X
3 1 X
3 0 X
4 1 X
4 0 X
5 1 X
5 0 X
6 1 X
6 0 X
7 1 X
7 0 X
8 1 X
8 0 X
# ORR r1 r2
1 1 X
1 0 X
2 1 X
2 0 X
3 1 X
3 0 X
4 1 X
4 0 X
5 1 X
5 0 X
6 1 X
6 0 X
7 1 X
7 0 X
8 1 X
8 0 (47)
*/

/* Test case BDU:
Tick Pulse Test_out
# SET 0 r1
memory ProgramMemory(0)=240;
memory ProgramMemory(1)=1;
# SET 8 r2
memory ProgramMemory(2)=240;
memory ProgramMemory(3)=130;
# BDU r1 r2
memory ProgramMemory(4)=34;
memory ProgramMemory(5)=33;
# SET 50 r1
memory ProgramMemory(6)=243;
memory ProgramMemory(7)=33;
# SET 30 r1
memory ProgramMemory(8)=241;
memory ProgramMemory(9)=225;
# SET 0 r1
1 1 X
1 0 X
2 1 X
2 0 X
3 1 X
3 0 X
4 1 X
4 0 X
5 1 X
5 0 X
6 1 X
6 0 X
7 1 X
7 0 X
8 1 X
8 0 X
# SET 8 r2
1 1 X
1 0 X
2 1 X
2 0 X
3 1 X
3 0 X
4 1 X
4 0 X
5 1 X
5 0 X
6 1 X
6 0 X
7 1 X
7 0 X
8 1 X
8 0 X
# BDU r1 r2
1 1 X
1 0 X
2 1 X
2 0 X
3 1 X
3 0 X
4 1 X
4 0 X
5 1 X
5 0 X
6 1 X
6 0 X
7 1 X
7 0 X
8 1 X
8 0 X
# SET 30 r1
1 1 X
1 0 X
2 1 X
2 0 X
3 1 X
3 0 X
4 1 X
4 0 X
5 1 X
5 0 X
6 1 X
6 0 X
7 1 X
7 0 X
8 1 X
8 0 (30)
*/

/* Test case CMP:
Tick Pulse Test_out
# SET 2 r2
memory ProgramMemory(0)=240;
memory ProgramMemory(1)=34;
# SET 5 r3
memory ProgramMemory(2)=240;
memory ProgramMemory(3)=83;
# CMP r3 r3
memory ProgramMemory(4)=81;
memory ProgramMemory(5)=51;
# BIE 10
memory ProgramMemory(6)=208;
memory ProgramMemory(7)=10;
# SET 50 r1
memory ProgramMemory(8)=243;
memory ProgramMemory(9)=33;
# SET 30 r1
memory ProgramMemory(10)=241;
memory ProgramMemory(11)=225;
# CMP r3 r2
memory ProgramMemory(12)=81;
memory ProgramMemory(13)=35;
# BIE 18
memory ProgramMemory(14)=208;
memory ProgramMemory(15)=18;
# SET 50 r1
memory ProgramMemory(16)=243;
memory ProgramMemory(17)=33;
# SET 30 r1
memory ProgramMemory(18)=241;
memory ProgramMemory(19)=225;
# SET 2 r2
1 1 X
1 0 X
2 1 X
2 0 X
3 1 X
3 0 X
4 1 X
4 0 X
5 1 X
5 0 X
6 1 X
6 0 X
7 1 X
7 0 X
8 1 X
8 0 X
# SET 5 r3
1 1 X
1 0 X
2 1 X
2 0 X
3 1 X
3 0 X
4 1 X
4 0 X
5 1 X
5 0 X
6 1 X
6 0 X
7 1 X
7 0 X
8 1 X
8 0 X
# CMP r3 r3
1 1 X
1 0 X
2 1 X
2 0 X
3 1 X
3 0 X
4 1 X
4 0 X
5 1 X
5 0 X
6 1 X
6 0 X
7 1 X
7 0 X
8 1 X
8 0 X
# BIE 10
1 1 X
1 0 X
2 1 X
2 0 X
3 1 X
3 0 X
4 1 X
4 0 X
5 1 X
5 0 X
6 1 X
6 0 X
7 1 X
7 0 X
8 1 X
8 0 X
# SET 30 r1
1 1 X
1 0 X
2 1 X
2 0 X
3 1 X
3 0 X
4 1 X
4 0 X
5 1 X
5 0 X
6 1 X
6 0 X
7 1 X
7 0 X
8 1 X
8 0 (30)
# CMP r3 r2
1 1 X
1 0 X
2 1 X
2 0 X
3 1 X
3 0 X
4 1 X
4 0 X
5 1 X
5 0 X
6 1 X
6 0 X
7 1 X
7 0 X
8 1 X
8 0 X
# BIE 18
1 1 X
1 0 X
2 1 X
2 0 X
3 1 X
3 0 X
4 1 X
4 0 X
5 1 X
5 0 X
6 1 X
6 0 X
7 1 X
7 0 X
8 1 X
8 0 X
# SET 30 r1
1 1 X
1 0 X
2 1 X
2 0 X
3 1 X
3 0 X
4 1 X
4 0 X
5 1 X
5 0 X
6 1 X
6 0 X
7 1 X
7 0 X
8 1 X
8 0 (50)
*/

/* Test case BIU:
Tick Pulse Test_out
# BIU 4
memory ProgramMemory(0)=160;
memory ProgramMemory(1)=4;
# SET 50 r1
memory ProgramMemory(2)=243;
memory ProgramMemory(3)=33;
# SET 30 r1
memory ProgramMemory(4)=241;
memory ProgramMemory(5)=225;
# BIU 4
1 1 X
1 0 X
2 1 X
2 0 X
3 1 X
3 0 X
4 1 X
4 0 X
5 1 X
5 0 X
6 1 X
6 0 X
7 1 X
7 0 X
8 1 X
8 0 X
# SET 30 r1
1 1 X
1 0 X
2 1 X
2 0 X
3 1 X
3 0 X
4 1 X
4 0 X
5 1 X
5 0 X
6 1 X
6 0 X
7 1 X
7 0 X
8 1 X
8 0 (30)
*/

/* Test case SBC:
Tick Pulse Test_out
# SET 50 r2
memory ProgramMemory(0)=243;
memory ProgramMemory(1)=34;
# SET 100 r3
memory ProgramMemory(2)=246;
memory ProgramMemory(3)=67;
# SET 4 r4
memory ProgramMemory(4)=240;
memory ProgramMemory(5)=68;
# SET 2 r5
memory ProgramMemory(6)=240;
memory ProgramMemory(7)=37;
# SUB r2 r3
memory ProgramMemory(8)=40;
memory ProgramMemory(9)=50;
# MOV r1 r2
memory ProgramMemory(10)=33;
memory ProgramMemory(11)=33;
# SBC r4 r5
memory ProgramMemory(12)=56;
memory ProgramMemory(13)=84;
# MOV r1 r4
memory ProgramMemory(14)=33;
memory ProgramMemory(15)=65;
# SBC r5 r4
memory ProgramMemory(16)=56;
memory ProgramMemory(17)=69;
# MOV r1 r5
memory ProgramMemory(18)=33;
memory ProgramMemory(19)=81;
# SET 50 r2
1 1 X
1 0 X
2 1 X
2 0 X
3 1 X
3 0 X
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*/

/* Test case NOT:
Tick Pulse Test_out
# SET 45 r1
memory ProgramMemory(0)=242;
memory ProgramMemory(1)=209;
# NOT r1 r1
memory ProgramMemory(2)=52;
memory ProgramMemory(3)=17;
# SET 45 r1
1 1 X
1 0 X
2 1 X
2 0 X
3 1 X
3 0 X
4 1 X
4 0 X
5 1 X
5 0 X
6 1 X
6 0 X
7 1 X
7 0 X
8 1 X
8 0 X
# NOT r1 r1
1 1 X
1 0 X
2 1 X
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*/

/* Test case BDG:
Tick Pulse Test_out
# SET 0 r4
memory ProgramMemory(0)=240;
memory ProgramMemory(1)=4;
# SET 18 r5
memory ProgramMemory(2)=241;
memory ProgramMemory(3)=37;
# SET 0 r6
memory ProgramMemory(4)=240;
memory ProgramMemory(5)=6;
# SET 26 r7
memory ProgramMemory(6)=241;
memory ProgramMemory(7)=167;
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*/

/* Test case TST:
Tick Pulse Test_out
# SET 2 r2
memory ProgramMemory(0)=240;
memory ProgramMemory(1)=34;
# SET -60 r3
memory ProgramMemory(2)=252;
memory ProgramMemory(3)=67;
# TST r2
memory ProgramMemory(4)=97;
memory ProgramMemory(5)=2;
# BIG 10
memory ProgramMemory(6)=176;
memory ProgramMemory(7)=10;
# SET 50 r1
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*/

/* Test case BIG:
Tick Pulse Test_out
# SET 2 r2
memory ProgramMemory(0)=240;
memory ProgramMemory(1)=34;
# SET 0 r3
memory ProgramMemory(2)=240;
memory ProgramMemory(3)=3;
# SUB r2 r3
memory ProgramMemory(4)=40;
memory ProgramMemory(5)=50;
# BIG 10
memory ProgramMemory(6)=176;
memory ProgramMemory(7)=10;
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*/

/* Test case INC:
Tick Pulse Test_out
# SET 3 r6
memory ProgramMemory(0)=240;
memory ProgramMemory(1)=54;
# INC r6
memory ProgramMemory(2)=72;
memory ProgramMemory(3)=6;
# MOV r1 r6
memory ProgramMemory(4)=33;
memory ProgramMemory(5)=97;
# SET -8 r3
memory ProgramMemory(6)=255;
memory ProgramMemory(7)=131;
# INC r3
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*/

/* Test case BDE:
Tick Pulse Test_out
# SET 0 r4
memory ProgramMemory(0)=240;
memory ProgramMemory(1)=4;
# SET 18 r5
memory ProgramMemory(2)=241;
memory ProgramMemory(3)=37;
# SET 0 r6
memory ProgramMemory(4)=240;
memory ProgramMemory(5)=6;
# SET 26 r7
memory ProgramMemory(6)=241;
memory ProgramMemory(7)=167;
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*/

/* Test case BIE:
Tick Pulse Test_out
# SET 2 r2
memory ProgramMemory(0)=240;
memory ProgramMemory(1)=34;
# SET 5 r3
memory ProgramMemory(2)=240;
memory ProgramMemory(3)=83;
# SUB r3 r3
memory ProgramMemory(4)=40;
memory ProgramMemory(5)=51;
# BIE 10
memory ProgramMemory(6)=208;
memory ProgramMemory(7)=10;
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*/

/* Test case DEC:
Tick Pulse Test_out
# SET 3 r6
memory ProgramMemory(0)=240;
memory ProgramMemory(1)=54;
# DEC r6
memory ProgramMemory(2)=88;
memory ProgramMemory(3)=6;
# MOV r1 r6
memory ProgramMemory(4)=33;
memory ProgramMemory(5)=97;
# SET -8 r3
memory ProgramMemory(6)=255;
memory ProgramMemory(7)=131;
# DEC r3
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*/

/* Test case BDN:
Tick Pulse Test_out
# SET 0 r4
memory ProgramMemory(0)=240;
memory ProgramMemory(1)=4;
# SET 18 r5
memory ProgramMemory(2)=241;
memory ProgramMemory(3)=37;
# SET 0 r6
memory ProgramMemory(4)=240;
memory ProgramMemory(5)=6;
# SET 26 r7
memory ProgramMemory(6)=241;
memory ProgramMemory(7)=167;
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*/

/* Test case BIN:
Tick Pulse Test_out
# SET 2 r2
memory ProgramMemory(0)=240;
memory ProgramMemory(1)=34;
# SET 5 r3
memory ProgramMemory(2)=240;
memory ProgramMemory(3)=83;
# SUB r3 r2
memory ProgramMemory(4)=40;
memory ProgramMemory(5)=35;
# BIN 10
memory ProgramMemory(6)=224;
memory ProgramMemory(7)=10;
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*/

/* Test case INV:
Tick Pulse Test_out
# SET -34 r8
memory ProgramMemory(0)=253;
memory ProgramMemory(1)=232;
# INV r1 r8
memory ProgramMemory(2)=104;
memory ProgramMemory(3)=129;
# SET 7 r1
memory ProgramMemory(4)=240;
memory ProgramMemory(5)=113;
# INV r1 r1
memory ProgramMemory(6)=104;
memory ProgramMemory(7)=17;
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*/
