// Digital circuit ControlUnit.dig as structural Verilog
module ControlUnit (
  input  [7:0] FirstByte,
  input  [7:0] SecondByte,
  input  F_Greater,
  input  F_Less,
  input  F_Equal,
  input  F_NotEqual,
  input  Clock_5,
  input  Clock_4,
  input  Clock_3,
  input  Clock_2,
  input  Clock_1,
  input  Carry,
  input  Clock_6,
  input  Clock_7,
  input  Clock_8,
  output D_WRT_MDR,
  output D_WRT_SRAM,
  output D_WRT_RegOutput,
  output D_WRT_RegBufferSecond,
  output D_WRT_RegBufferFirst,
  output D_WRT_Flags,
  output D_WRT_RPC,
  output D_WRT_CIRSecond,
  output D_WRT_CIRFirst,
  output D_RPC_Registers,
  output D_RPC_MemAdder,
  output D_ALU_Increment,
  output S_CTL_Halt,
  output S_ADR_Direct,
  output S_ADR_Immediate,
  output S_ALU_OrOut,
  output S_ALU_ResultOut,
  output S_ALU_Propagate,
  output S_ALU_Invert,
  output S_ALU_CarryOut,
  output S_MEM_Store,
  output S_MDR_WriteMEM,
  output S_MDR_WriteALU,
  output S_REG_WriteMDR,
  output S_REG_WriteALU,
  output [3:0] Select,
  output [11:0] Value,
  output S_REG_WriteVAL
);

  wire signalintegrator_1_d_sel_first, signalintegrator_1_d_sel_second, staticcontrolunit_1_p4, undriven,
       undriven_2, undriven_3, undriven_4, undriven_5, undriven_6, undriven_7, undriven_8, undriven_9,
       undriven_10;
  wire [3:0] undriven_11, undriven_12, undriven_13;

  // StaticControlUnit staticcontrolunit_1: pin names not known; wires that end beside it: FirstByte, SecondByte, S_CTL_Halt, staticcontrolunit_1_p4, S_ADR_Direct, S_ADR_Immediate, S_ALU_OrOut, S_ALU_ResultOut, S_ALU_Propagate, S_ALU_Invert, S_ALU_CarryOut, S_MDR_WriteMEM, S_MDR_WriteALU, S_MEM_Store
  SignalIntegrator signalintegrator_1 (
    .D_ALU_Increment(D_ALU_Increment), .D_RPC_MemAdder(D_RPC_MemAdder), .D_RPC_Registers(D_RPC_Registers),
    .D_WRT_CIRFirst(D_WRT_CIRFirst), .D_WRT_CIRSecond(D_WRT_CIRSecond), .D_WRT_RPC(D_WRT_RPC),
    .D_WRT_Flags(D_WRT_Flags), .D_WRT_BufferSecond(D_WRT_RegBufferSecond),
    .D_WRT_BufferFirst(D_WRT_RegBufferFirst), .D_SEL_Second(signalintegrator_1_d_sel_second),
    .D_SEL_First(signalintegrator_1_d_sel_first), .D_WRT_RegOutput(D_WRT_RegOutput), .D_WRT_SRAM(D_WRT_SRAM),
    .D_WRT_MDR(D_WRT_MDR), .S_ALU_Increment(undriven_10), .S_ALU_UseCarry(undriven_9), .F_Carry(Carry),
    .S_BRA_Unconditional(undriven_8), .S_BRA_Greater(undriven_7), .F_Greater(F_Greater),
    .S_BRA_Less(undriven_6), .F_Less(F_Less), .S_BRA_Equal(undriven_5), .F_Equal(F_Equal),
    .S_BRA_NotEqual(undriven_4), .F_NotEqual(F_NotEqual), .S_ALU_FlagWrite(undriven_3),
    .S_INS_RegReadSecond(undriven_2), .S_INS_RegReadFirst(undriven), .S_REG_WriteALU(S_REG_WriteALU),
    .S_REG_WriteMDR(S_REG_WriteMDR), .S_REG_WriteVAL(S_REG_WriteVAL), .S_MEM_Store(S_MEM_Store),
    .S_MDR_WriteALU(S_MDR_WriteALU), .S_MDR_WriteMem(S_MDR_WriteMEM), .Clock_1(Clock_1), .Clock_2(Clock_2),
    .Clock_3(Clock_3), .Clock_4(Clock_4), .Clock_5(Clock_5), .Clock_6(Clock_6), .Clock_7(Clock_7),
    .Clock_8(Clock_8));
  OperandIntegrator operandintegrator_1 (
    .Nibble_4(undriven_13), .Nibble_3(undriven_12), .Nibble_2(undriven_11),
    .S_INS_ValRead(staticcontrolunit_1_p4), .D_CLK_SelectSecond(signalintegrator_1_d_sel_second),
    .D_CLK_SelectFirst(signalintegrator_1_d_sel_first), .Value(Value), .Select(Select));
endmodule
