// Digital circuit Decoder.dig as structural Verilog
module Decoder (
  input  [2:0] In,
  output _0,
  output _1,
  output _2,
  output _3,
  output _4,
  output _5,
  output _6,
  output _7
);

  wire not_1_out, not_2_out, not_3_out;

  not not_1 (not_1_out, In[0]);
  not not_2 (not_2_out, In[1]);
  not not_3 (not_3_out, In[2]);
  and and_1 (_0, 1'b1, not_1_out, not_2_out, not_3_out);
  and and_2 (_1, 1'b1, In[0], not_2_out, not_3_out);
  and and_3 (_2, 1'b1, not_1_out, In[1], not_3_out);
  and and_4 (_3, 1'b1, In[0], In[1], not_3_out);
  and and_5 (_4, 1'b1, not_1_out, not_2_out, In[2]);
  and and_6 (_5, 1'b1, In[0], not_2_out, In[2]);
  and and_7 (_6, 1'b1, not_1_out, In[1], In[2]);
  and and_8 (_7, 1'b1, In[0], In[1], In[2]);
endmodule
