// Digital circuit InstructionSplitter.dig as structural Verilog
module InstructionSplitter (
  input  [15:0] Instruction,
  output IsOpcodeNibble,
  output [2:0] Counter,
  output [3:0] Nibble2,
  output [3:0] Nibble3,
  output [3:0] Nibble4
);


  assign Counter = Instruction[14:12];
  assign IsOpcodeNibble = Instruction[15];
  assign Nibble2 = Instruction[11:8];
  assign Nibble3 = Instruction[7:4];
  assign Nibble4 = Instruction[3:0];
endmodule
