// Digital circuit OperandIntegrator.dig as structural Verilog
module OperandIntegrator (
  input  [3:0] Nibble_2,
  input  [3:0] Nibble_3,
  input  [3:0] Nibble_4,
  input  D_CLK_SelectFirst,
  input  D_CLK_SelectSecond,
  input  S_INS_ValRead,
  output [3:0] Select,
  output [11:0] Value
);

  assign Select = D_CLK_SelectSecond ? Nibble_4 : 4'bz;  // Driver driver_1
  assign Select = D_CLK_SelectFirst ? Nibble_3 : 4'bz;  // Driver driver_2
  assign Value = S_INS_ValRead ? {Nibble_2, Nibble_3, Nibble_4} : 12'bz;  // Driver driver_3
  PullDown #(.Bits(4)) pulldown_1 (.out(Select));
endmodule
