// Digital circuit SignalIntegrator.dig as structural Verilog
module SignalIntegrator (
  input  S_ALU_Increment,
  input  S_ALU_UseCarry,
  input  Clock_1,
  input  Clock_2,
  input  S_BRA_Unconditional,
  input  Clock_5,
  input  Clock_3,
  input  Clock_4,
  input  S_ALU_FlagWrite,
  input  S_BRA_Greater,
  input  F_Greater,
  input  S_BRA_Less,
  input  F_Less,
  input  S_BRA_Equal,
  input  F_Equal,
  input  S_BRA_NotEqual,
  input  F_NotEqual,
  input  S_INS_RegReadFirst,
  input  S_INS_RegReadSecond,
  input  S_REG_WriteALU,
  input  S_REG_WriteMDR,
  input  S_MEM_Store,
  input  S_MDR_WriteALU,
  input  S_MDR_WriteMem,
  input  F_Carry,
  input  S_REG_WriteVAL,
  input  Clock_6,
  input  Clock_7,
  input  Clock_8,
  output D_ALU_Increment,
  output D_RPC_MemAdder,
  output D_RPC_Registers,
  output D_WRT_CIRFirst,
  output D_WRT_CIRSecond,
  output D_WRT_RPC,
  output D_WRT_Flags,
  output D_SEL_First,
  output D_SEL_Second,
  output D_WRT_RegOutput,
  output D_WRT_SRAM,
  output D_WRT_MDR,
  output D_WRT_BufferFirst,
  output D_WRT_BufferSecond
);

  wire and_1_out, and_2_out, and_3_out, and_4_out, and_5_out, and_6_out, and_8_out, and_10_out, and_11_out,
       not_1_out, or_2_out, or_3_out, or_4_out, or_5_out, or_6_out, or_7_out, or_8_out, or_9_out, or_10_out,
       or_13_out, or_14_out;

  not not_1 (not_1_out, S_ALU_UseCarry);
  and and_1 (and_1_out, S_ALU_Increment, not_1_out);
  and and_2 (and_2_out, S_ALU_UseCarry, F_Carry);
  and and_3 (and_3_out, S_BRA_Greater, F_Greater);
  and and_4 (and_4_out, S_BRA_Less, F_Less);
  and and_5 (and_5_out, S_BRA_Equal, F_Equal);
  and and_6 (and_6_out, S_BRA_NotEqual, F_NotEqual);
  or or_1 (D_ALU_Increment, and_1_out, and_2_out);
  or or_2 (or_2_out, and_3_out, and_4_out);
  or or_3 (or_3_out, and_5_out, and_6_out);
  or or_4 (or_4_out, or_2_out, or_3_out);
  or or_5 (or_5_out, Clock_5, Clock_6);
  or or_6 (or_6_out, Clock_7, Clock_8);
  or or_7 (or_7_out, S_REG_WriteMDR, S_REG_WriteVAL);
  or or_8 (or_8_out, Clock_7, Clock_6);
  or or_9 (or_9_out, S_BRA_Unconditional, or_4_out);
  or or_10 (or_10_out, Clock_1, Clock_3);
  or or_11 (D_SEL_Second, or_5_out, or_6_out);
  or or_12 (D_SEL_First, Clock_3, Clock_4);
  or or_13 (or_13_out, S_REG_WriteALU, or_7_out);
  or or_14 (or_14_out, S_MDR_WriteALU, S_MDR_WriteMem);
  and and_7 (D_RPC_Registers, or_8_out, or_9_out);
  and and_8 (and_8_out, or_9_out, Clock_7);
  and and_9 (D_WRT_Flags, S_ALU_FlagWrite, Clock_8);
  and and_10 (and_10_out, Clock_6, S_INS_RegReadSecond);
  and and_11 (and_11_out, Clock_4, S_INS_RegReadFirst);
  and and_12 (D_WRT_RegOutput, Clock_8, or_13_out);
  and and_13 (D_WRT_SRAM, S_MEM_Store, Clock_8);
  and and_14 (D_WRT_MDR, or_14_out, Clock_8);
  or or_15 (D_WRT_RPC, or_10_out, and_8_out);
  or or_16 (D_WRT_BufferSecond, Clock_2, and_10_out);
  or or_17 (D_WRT_BufferFirst, Clock_2, and_11_out);
  not not_2 (D_RPC_MemAdder, D_RPC_Registers);

  assign D_WRT_CIRFirst = Clock_1;
  assign D_WRT_CIRSecond = Clock_2;
endmodule
