// Digital circuit Branch Combinator.dig as structural Verilog
module Branch_Combinator (
  input  [7:0] Counter,
  input  Active_Group3,
  input  Active_Nibble,
  output BRA_Less,
  output BRA_Equal,
  output BRA_NotEqual,
  output BRA_Unconditional,
  output BRA_Greater
);

  wire or_1_out;

  or or_1 (or_1_out, Active_Group3, Active_Nibble);
  and and_1 (BRA_Unconditional, Counter[2], or_1_out);
  and and_2 (BRA_Greater, Counter[3], or_1_out);
  and and_3 (BRA_Less, Counter[4], or_1_out);
  and and_4 (BRA_Equal, Counter[5], or_1_out);
  and and_5 (BRA_NotEqual, Counter[6], or_1_out);
endmodule
