// Digital circuit Group1 Combinator.dig as structural Verilog
module Group1_Combinator (
  input  [7:0] Counter,
  input  Active,
  output ALU_UseCarry,
  output ALU_Increment,
  output ALU_Invert,
  output ALU_Propagate,
  output ALU_ResultOut,
  output ALU_FlagWrite,
  output INS_RegReadSecond,
  output INS_RegReadFirst,
  output REG_WriteALU
);

  wire not_1_out, not_2_out, or_1_out, or_2_out, or_3_out, or_4_out, or_5_out, or_6_out;

  or or_1 (or_1_out, Counter[2], Counter[3]);
  or or_2 (or_2_out, or_1_out, Counter[6]);
  or or_3 (or_3_out, Counter[1], Counter[3]);
  or or_4 (or_4_out, or_2_out, Counter[4]);
  or or_5 (or_5_out, or_2_out, Counter[5]);
  or or_6 (or_6_out, Counter[4], Counter[5]);
  not not_1 (not_1_out, Counter[6]);
  not not_2 (not_2_out, or_6_out);
  and and_1 (ALU_UseCarry, or_3_out, Active);
  and and_2 (ALU_Increment, or_4_out, Active);
  and and_3 (ALU_Invert, or_5_out, Active);
  and and_4 (INS_RegReadSecond, not_1_out, Active);
  and and_5 (INS_RegReadFirst, not_2_out, Active);

  assign ALU_FlagWrite = Active;
  assign ALU_Propagate = Active;
  assign ALU_ResultOut = Active;
  assign REG_WriteALU = Active;
endmodule
