// Digital circuit Group2 Combinator.dig as structural Verilog
module Group2_Combinator (
  input  [7:0] Counter,
  input  Active,
  output ALU_Invert,
  output ALU_ResultOut,
  output ALU_FlagWrite,
  output INS_RegReadSecond,
  output INS_RegReadFirst,
  output REG_WriteALU,
  output ALU_CarryOut,
  output ALU_OrOut
);

  wire or_1_out, or_2_out, or_3_out;

  or or_1 (or_1_out, Counter[1], Counter[2]);
  or or_2 (or_2_out, Counter[0], Counter[3]);
  or or_3 (or_3_out, Counter[0], or_1_out);
  and and_1 (ALU_Invert, Counter[3], Active);
  and and_2 (ALU_ResultOut, or_2_out, Active);
  and and_3 (ALU_CarryOut, Counter[1], Active);
  and and_4 (ALU_OrOut, Counter[2], Active);
  and and_5 (INS_RegReadSecond, or_3_out, Active);

  assign ALU_FlagWrite = Active;
  assign INS_RegReadFirst = Active;
  assign REG_WriteALU = Active;
endmodule
