// Digital circuit Group3 Combinator.dig as structural Verilog
module Group3_Combinator (
  input  [7:0] Counter,
  input  Active,
  output ADR_Direct,
  output INS_RegReadSecond,
  output INS_RegReadFirst,
  output MEM_Store,
  output MDR_WriteMem
);

  and and_1 (MDR_WriteMem, Counter[0], Active);
  and and_2 (MEM_Store, Counter[1], Active);

  assign ADR_Direct = Active;
  assign INS_RegReadFirst = Active;
  assign INS_RegReadSecond = Active;
endmodule
