// Digital circuit ALU.dig as structural Verilog
module ALU (
  input  [7:0] Data_2_in,
  input  [7:0] Data_1_in,
  input  Invert,
  input  Increment,
  input  Out_carry,
  input  Propagate,
  input  Out_or,
  input  Out_result,
  output [7:0] Data_out,
  output Carry,
  output Equal,
  output Greater,
  output Less,
  output NotEqual
);

  wire not_1_out;
  wire [6:0] or_2_out, pulldown_1_out;
  wire [7:0] and_1_out, and_2_out, or_1_out, xor_1_out, xor_2_out, xor_3_out;

  assign or_1_out = Data_2_in | Data_1_in;  // Or or_1, 8 bits wide
  assign xor_1_out = {8{Invert}} ^ Data_2_in;  // XOr xor_1, 8 bits wide
  assign xor_2_out = Data_1_in ^ xor_1_out;  // XOr xor_2, 8 bits wide
  assign and_1_out = xor_1_out & Data_1_in;  // And and_1, 8 bits wide
  assign xor_3_out = xor_2_out ^ {pulldown_1_out, Increment};  // XOr xor_3, 8 bits wide
  assign and_2_out = xor_2_out & {pulldown_1_out, Increment};  // And and_2, 8 bits wide
  assign {Carry, or_2_out} = and_2_out | and_1_out;  // Or or_2, 8 bits wide
  PullDown #(.Bits(7)) pulldown_1 (.out(pulldown_1_out));
  assign pulldown_1_out = Propagate ? or_2_out : 7'bz;  // Driver driver_1
  assign Data_out = Out_carry ? {Carry, or_2_out} : 8'bz;  // Driver driver_2
  assign Data_out = Out_result ? xor_3_out : 8'bz;  // Driver driver_3
  assign Data_out = Out_or ? or_1_out : 8'bz;  // Driver driver_4
  or or_3 (NotEqual, xor_3_out[7], xor_3_out[6], xor_3_out[5], xor_3_out[4], xor_3_out[0], xor_3_out[1], xor_3_out[2], xor_3_out[3]);
  not not_1 (not_1_out, xor_3_out[7]);
  and and_3 (Greater, NotEqual, not_1_out);
  and and_4 (Less, xor_3_out[7], NotEqual);
  not not_2 (Equal, NotEqual);

  // Notes on the sheet:
  //   Data_2_in: pin 2
  //   Data_1_in: pin 1
  //   Data_out: pin 9
  //   Carry: pin 10
  //   Invert: pin 3
  //   Increment: pin 4
  //   Equal: pin 12
  //   Greater: pin 14
  //   Less: pin 13
  //   Out_carry: pin 6
  //   Propagate: pin 5
  //   Out_or: pin 8
  //   Out_result: pin 7
  //   NotEqual: pin 11
  //   Add
  //   Subtract
  //   Increment
  //   Decrement
  //   Compare
  //   Test
  //   Invert
  //   NOT
  //   XOR
  //   AND
  //   OR
  //   In_1
  //   A
  //   0
  //   In_2
  //   Inc
  //   B
  //   1
  //   Inv
  //   Prop
  //   Out_c
  //   Bitwise Or
  //   Out_o
  //   Out_r
  //   Full Adder
  //   When a 'Compare' operation is carried out between inputs A and B
  //   -> Out is set to A - B (and is probably unused)
  //   -> Carry is set to |A - B| > 128 (and is also probably unused
  //   -> Equal is set to A == B
  //   -> Greater is set to A > B
  //   -> Less is set to A < B
  //   When a 'Compare' operation is carried out between input A and 0
  //   -> Out is set to A (and is probably unused)
  //   -> Carry is set to 0 (and is also probably unused
  //   -> Equal is set to A == 0
  //   -> Greater is set to A > 0
  //   -> Less is set to A < 0
  //   Flag Combinator
  //   Output Selector
  //   In_1 > In_2
  //   In_1 < In_2
  //   In_1 == In_2
  //   In_1 != In_2
  //   |Out| > 128
endmodule

/* Test case Add:
	Data-1_in Data-2_in Increment Invert Propagate Out_carry Out_or Out_result Data_out
loop(i, 512)
	let a = random(1<<8) - 128;
	let b = random(1<<8) - 128;
	(a)	  (b)	    0	      0      1         0         0      1          (a+b)
end loop
*/

/* Test case Decrement:
	Data-1_in Data-2_in Increment Invert Propagate Out_carry Out_or Out_result Data_out
loop(i, 512)
	let a = random(1<<8)-128;
	(a)	  0	    0	      1      1         0         0      1          (a-1)
end loop
*/

/* Test case Invert:
	Data-1_in Data-2_in Increment Invert Propagate Out_carry Out_or Out_result Data_out
loop(i, 512)
	let b = random(1<<8)-128;
	0	  (b)	    1	      1      1         0         0      1          (-b)
end loop
*/

/* Test case AND:
	Data-1_in Data-2_in Increment Invert Propagate Out_carry Out_or Out_result Data_out
loop(i, 512)
	let a = random(1<<8)-128;
	let b = random(1<<8)-128;
	(a)	  (b)	    0	      0      0         1         0      0          (a&b)
end loop
*/

/* Test case Sub:
	Data-1_in Data-2_in Increment Invert Propagate Out_carry Out_or Out_result Data_out
loop(i, 512)
	let a = random(1<<8) - 128;
	let b = random(1<<8) - 128;
	(a)	  (b)	    1	      1      1         0         0      1          (a-b)
end loop
*/

/* Test case Compare:
	Data-1_in Data-2_in Increment Invert Propagate Out_carry Out_or Out_result Data_out Greater Less  Equal
loop(i, 512)
	let a = random(1<<7)-128;
	let b = random(1<<7)-128;
	(a)	  (b)	    1	      1      1         0         0      0          Z        (a>b)   (a<b) (a=b)
end loop
*/

/* Test case NOT:
	Data-1_in Data-2_in Increment Invert Propagate Out_carry Out_or Out_result Data_out
loop(i, 512)
	let b = random(1<<8)-128;
	0	  (b)	    0	      1      0         0         0      1          (-b-1)
end loop
*/

/* Test case OR:
	Data-1_in Data-2_in Increment Invert Propagate Out_carry Out_or Out_result Data_out
loop(i, 512)
	let a = random(1<<8)-128;
	let b = random(1<<8)-128;
	(a)	  (b)	    0	      0      0         0         1      0          (a|b)
end loop
*/

/* Test case Increment:
	Data-1_in Data-2_in Increment Invert Propagate Out_carry Out_or Out_result Data_out
loop(i, 512)
	let a = random(1<<8)-128;
	(a)	  0	    1	      0      1         0         0      1          (a+1)
end loop
*/

/* Test case Test:
	Data-1_in Data-2_in Increment Invert Propagate Out_carry Out_or Out_result Data_out Greater Less  Equal
loop(i, 512)
	let a = random(1<<8);
	(a)	  0	    0	      0      0         0         0      0          Z        (a<128 & a>0)   (a>127) (a=0)
end loop
*/

/* Test case XOR:
	Data-1_in Data-2_in Increment Invert Propagate Out_carry Out_or Out_result Data_out
loop(i, 512)
	let a = random(1<<8)-128;
	let b = random(1<<8)-128;
	(a)	  (b)	    0	      0      0         0         0      1          (a^b)
end loop
*/
