// Digital circuit MemoryAdder.dig as structural Verilog
module MemoryAdder (
  input  [11:0] Data_in,
  output [11:0] Data_out
);

  wire [11:1] and_1_out;
  wire [11:11] and_1_out_2;

  assign Data_out = Data_in ^ {and_1_out, 1'b1};  // XOr xor_1, 12 bits wide
  assign {and_1_out_2[11], and_1_out} = Data_in & {and_1_out, 1'b1};  // And and_1, 12 bits wide

  // Notes on the sheet:
  //   Data_in: pin 1
  //   Data_out: pin 12
  //   Data_out = Data_in + 1
endmodule

/* Test case:
	     Data_in Data_out
loop(a, 1024)
	(a) (a+1)
end loop
*/
