// Digital circuit Buffer.dig as structural Verilog
module Buffer (
  input  [7:0] Data_in,
  input  Clk_R1_write,
  input  Clk_R2_write,
  output [7:0] R1_out,
  output [7:0] R2_out
);

  D_FF #(.Bits(8)) d_ff_1 (.D(Data_in), .C(Clk_R1_write), .Q(R1_out));  // open: nQ
  D_FF #(.Bits(8)) d_ff_2 (.D(Data_in), .C(Clk_R2_write), .Q(R2_out));  // open: nQ

  // Notes on the sheet:
  //   R1_out: pin 6
  //   R2_out: pin 5
  //   Data_in: pin 3
  //   Clk_R1_write: pin 1
  //   Clk_R2_write: pin 2
  //   Used to store 16-bit outputs from 8-bit storages
  //   For example, to read two registers in a single cycle
  //   [1] Select the first register in the register file
  //   [2] Send the output value of the register file to Input
  //   [3] Send a signal to Write_1
  //   [4] Select the second register in the register file
  //   [5] Send the output value of the register file to Input
  //   [6] Send a signal to Write_2
  //   [7] Now, Out_1 will output the first value and Out_2 the second value
endmodule
