// Digital circuit CIR.dig as structural Verilog
module CIR (
  input  [15:0] In,
  input  Clock,
  output [15:0] Out
);

  // MemoryRegister memoryregister_1: pin names not known; wires that end beside it: Clock, In, Out

  // Notes on the sheet:
  //   Out: pin 4
  //   In: pin 1
  //   Clock: pin 2
endmodule
