// Digital circuit Decoder Right.dig as structural Verilog
module Decoder_Right (
  input  [3:0] In_1,
  output _0,
  output _1,
  output _2,
  output _3,
  output _4,
  output _5,
  output _6,
  output _7,
  output _8,
  output _9,
  output _10,
  output _11,
  output _12,
  output _13,
  output _14,
  output _15
);

  wire [3:0] not_1_out;

  and and_1 (_0, not_1_out[0], not_1_out[1], not_1_out[2], not_1_out[3]);
  and and_2 (_1, In_1[0], not_1_out[1], not_1_out[2], not_1_out[3]);
  and and_3 (_2, not_1_out[0], In_1[1], not_1_out[2], not_1_out[3]);
  and and_4 (_3, In_1[0], In_1[1], not_1_out[2], not_1_out[3]);
  and and_5 (_4, not_1_out[0], not_1_out[1], In_1[2], not_1_out[3]);
  and and_6 (_5, In_1[0], not_1_out[1], In_1[2], not_1_out[3]);
  and and_7 (_6, not_1_out[0], In_1[1], In_1[2], not_1_out[3]);
  and and_8 (_7, In_1[0], In_1[1], In_1[2], not_1_out[3]);
  and and_9 (_8, not_1_out[0], not_1_out[1], not_1_out[2], In_1[3]);
  and and_10 (_9, In_1[0], not_1_out[1], not_1_out[2], In_1[3]);
  and and_11 (_10, not_1_out[0], In_1[1], not_1_out[2], In_1[3]);
  and and_12 (_11, In_1[0], In_1[1], not_1_out[2], In_1[3]);
  and and_13 (_12, not_1_out[0], not_1_out[1], In_1[2], In_1[3]);
  and and_14 (_13, In_1[0], not_1_out[1], In_1[2], In_1[3]);
  and and_15 (_14, not_1_out[0], In_1[1], In_1[2], In_1[3]);
  and and_16 (_15, In_1[0], In_1[1], In_1[2], In_1[3]);
  assign not_1_out = ~In_1;  // Not not_1, 4 bits wide
endmodule
