// Digital circuit MDR.dig as structural Verilog
module MDR (
  input  [7:0] Data_mem,
  input  Clk_write,
  input  [7:0] Data_ALU,
  input  Write_mem,
  input  Write_ALU,
  output [7:0] Data_out
);

  wire [7:0] driver_1_out;

  assign driver_1_out = Write_ALU ? Data_ALU : 8'bz;  // Driver driver_1
  assign driver_1_out = Write_mem ? Data_mem : 8'bz;  // Driver driver_2
  PullDown #(.Bits(8)) pulldown_1 (.out(driver_1_out));
  D_FF #(.Bits(8)) MDR (.D(driver_1_out), .C(Clk_write), .Q(Data_out));  // open: nQ

  // Notes on the sheet:
  //   Data_mem: pin 5
  //   Clk_write: pin 1
  //   Data_out: pin 6
  //   Data_ALU: pin 4
  //   Write_mem: pin 3
  //   Write_ALU: pin 2
endmodule

/* Test case Write None:
	Clk_write Write_reg Write_mem Data_reg Data_mem Data_out
loop(a, 512)
	0	  0	    0	      Z        Z	0
	1	  0	    0	      Z        Z	0
end loop
*/

/* Test case Write Mem:
	Clk_write Write_reg Write_mem Data_reg Data_mem Data_out
loop(a, 512)
	let b = random(1<<16);
	0	  1	    0	      (b)      Z	X
	1	  1	    0	      (b)      Z	(b)
end loop
*/

/* Test case Write Data:
	Clk_write Write_reg Write_mem Data_reg Data_mem Data_out
loop(a, 512)
	let b = random(1<<16);
	0	  0	    1	      0        (b)	X
	1	  0	    1	      0        (b)	(b)
end loop
*/
