// Digital circuit RPC.dig as structural Verilog
module RPC (
  input  [11:0] Reg_in,
  input  Clk_write,
  input  [11:0] Add_in,
  input  Reg_write,
  input  Add_write,
  output [11:0] Data_out
);

  wire [11:0] driver_1_out;

  assign driver_1_out = Reg_write ? Reg_in : 12'bz;  // Driver driver_1
  assign driver_1_out = Add_write ? Add_in : 12'bz;  // Driver driver_2
  D_FF #(.Bits(12)) d_ff_1 (.D(driver_1_out), .C(Clk_write), .Q(Data_out));  // open: nQ
  PullDown #(.Bits(12)) pulldown_1 (.out(driver_1_out));

  // Notes on the sheet:
  //   Reg_in: pin 4
  //   Clk_write: pin 5
  //   Add_in: pin 1
  //   Reg_write: pin 2
  //   Add_write: pin 3
  //   Data_out: pin 8
  //   If Reg_write is high
  //   -> When Clk_Write is triggered...
  //   -> ...Reg_in will be written to the register
  //   If Add_write is high
  //   -> When Clk_Write is triggered...
  //   -> ...Add_in will be written to the register
endmodule

/* Test case Write REG (none):
	Clk_write Reg_write Reg_in Data_out
loop(a, 512)
	let b = random(1<<16);
	0	  0	    (b)    X
	1         0	    (b)    0
end loop
*/

/* Test case Write REG:
	Clk_write Reg_write Reg_in Data_out
loop(a, 512)
	let b = random(1<<16);
	0	  1	    (b)    X
	1         1	    (b)    (b)
end loop
*/

/* Test case Write ADD (none):
	Clk_write Add_write Add_in Data_out
loop(a, 512)
	let b = random(1<<16);
	0	  0	    (b)    X
	1         0	    (b)    0
end loop
*/

/* Test case Write ADD:
	Clk_write Add_write Add_in Data_out
loop(a, 512)
	let b = random(1<<16);
	0	  1	    (b)    X
	1         1	    (b)    (b)
end loop
*/
