// Digital circuit Register File.dig as structural Verilog
module Register_File (
  input  [3:0] Select,
  input  Clk_write,
  input  [7:0] Data_alu,
  input  [7:0] Data_mdr,
  input  Write_mdr,
  input  Write_alu,
  input  [11:0] Data_val,
  input  Write_val,
  output [7:0] Data_out,
  output [7:0] Test_out
);

  wire decoder_right_1__1, decoder_right_1__2, decoder_right_1__3, decoder_right_1__4, decoder_right_1__5,
       decoder_right_1__6, decoder_right_1__7, decoder_right_1__8, decoder_right_1__9, decoder_right_1__10,
       decoder_right_1__11, decoder_right_1__12, decoder_right_1__13, decoder_right_1__14,
       decoder_right_1__15;
  wire [7:0] d_ff_2_q, d_ff_3_q, d_ff_4_q, d_ff_5_q, d_ff_6_q, d_ff_7_q, d_ff_8_q, d_ff_9_q, d_ff_10_q,
       d_ff_11_q, d_ff_12_q, d_ff_13_q, d_ff_14_q, d_ff_15_q, driver_1_out, driver_5_out, driver_6_out,
       driver_7_out, driver_8_out, driver_9_out, driver_10_out, driver_11_out, driver_12_out, driver_13_out,
       driver_14_out, driver_15_out, driver_16_out, driver_17_out, driver_18_out, driver_19_out;
  wire [15:0] decoder_left_1__0, driver_4_out;

  Decoder_Left decoder_left_1 (
    .In_1(Select), ._0(decoder_left_1__0[0]), ._1(decoder_left_1__0[1]), ._2(decoder_left_1__0[2]),
    ._3(decoder_left_1__0[3]), ._4(decoder_left_1__0[4]), ._5(decoder_left_1__0[5]),
    ._6(decoder_left_1__0[6]), ._7(decoder_left_1__0[7]), ._8(decoder_left_1__0[8]),
    ._9(decoder_left_1__0[9]), ._10(decoder_left_1__0[10]), ._11(decoder_left_1__0[11]),
    ._12(decoder_left_1__0[12]), ._13(decoder_left_1__0[13]), ._14(decoder_left_1__0[14]),
    ._15(decoder_left_1__0[15]));
  assign driver_1_out = Write_mdr ? Data_mdr : 8'bz;  // Driver driver_1
  assign driver_1_out = Write_alu ? Data_alu : 8'bz;  // Driver driver_2
  assign driver_1_out = Write_val ? Data_val[11:4] : 8'bz;  // Driver driver_3
  assign driver_4_out = Clk_write ? decoder_left_1__0 : 16'bz;  // Driver driver_4
  PullDown #(.Bits(16)) pulldown_1 (.out(driver_4_out));
  D_FF #(.Bits(8)) d_ff_1 (.D(driver_1_out), .C(driver_4_out[1]), .Q(Test_out));  // open: nQ
  D_FF #(.Bits(8)) d_ff_2 (.D(driver_1_out), .C(driver_4_out[2]), .Q(d_ff_2_q));  // open: nQ
  D_FF #(.Bits(8)) d_ff_3 (.D(driver_1_out), .C(driver_4_out[3]), .Q(d_ff_3_q));  // open: nQ
  D_FF #(.Bits(8)) d_ff_4 (.D(driver_1_out), .C(driver_4_out[4]), .Q(d_ff_4_q));  // open: nQ
  D_FF #(.Bits(8)) d_ff_5 (.D(driver_1_out), .C(driver_4_out[5]), .Q(d_ff_5_q));  // open: nQ
  D_FF #(.Bits(8)) d_ff_6 (.D(driver_1_out), .C(driver_4_out[6]), .Q(d_ff_6_q));  // open: nQ
  D_FF #(.Bits(8)) d_ff_7 (.D(driver_1_out), .C(driver_4_out[7]), .Q(d_ff_7_q));  // open: nQ
  D_FF #(.Bits(8)) d_ff_8 (.D(driver_1_out), .C(driver_4_out[8]), .Q(d_ff_8_q));  // open: nQ
  D_FF #(.Bits(8)) d_ff_9 (.D(driver_1_out), .C(driver_4_out[9]), .Q(d_ff_9_q));  // open: nQ
  D_FF #(.Bits(8)) d_ff_10 (.D(driver_1_out), .C(driver_4_out[10]), .Q(d_ff_10_q));  // open: nQ
  D_FF #(.Bits(8)) d_ff_11 (.D(driver_1_out), .C(driver_4_out[11]), .Q(d_ff_11_q));  // open: nQ
  D_FF #(.Bits(8)) d_ff_12 (.D(driver_1_out), .C(driver_4_out[12]), .Q(d_ff_12_q));  // open: nQ
  D_FF #(.Bits(8)) d_ff_13 (.D(driver_1_out), .C(driver_4_out[13]), .Q(d_ff_13_q));  // open: nQ
  D_FF #(.Bits(8)) d_ff_14 (.D(driver_1_out), .C(driver_4_out[14]), .Q(d_ff_14_q));  // open: nQ
  D_FF #(.Bits(8)) d_ff_15 (.D(driver_1_out), .C(driver_4_out[15]), .Q(d_ff_15_q));  // open: nQ
  assign Data_out = driver_5_out | driver_6_out | driver_7_out | driver_8_out | driver_9_out | driver_10_out | driver_11_out | driver_12_out | driver_13_out | driver_14_out | driver_15_out | driver_16_out | driver_17_out | driver_18_out | driver_19_out;  // Or or_1, 8 bits wide
  assign driver_5_out = decoder_right_1__1 ? Test_out : 8'bz;  // Driver driver_5
  assign driver_6_out = decoder_right_1__2 ? d_ff_2_q : 8'bz;  // Driver driver_6
  assign driver_7_out = decoder_right_1__3 ? d_ff_3_q : 8'bz;  // Driver driver_7
  assign driver_8_out = decoder_right_1__4 ? d_ff_4_q : 8'bz;  // Driver driver_8
  assign driver_9_out = decoder_right_1__5 ? d_ff_5_q : 8'bz;  // Driver driver_9
  assign driver_10_out = decoder_right_1__6 ? d_ff_6_q : 8'bz;  // Driver driver_10
  assign driver_11_out = decoder_right_1__7 ? d_ff_7_q : 8'bz;  // Driver driver_11
  assign driver_12_out = decoder_right_1__8 ? d_ff_8_q : 8'bz;  // Driver driver_12
  assign driver_13_out = decoder_right_1__9 ? d_ff_9_q : 8'bz;  // Driver driver_13
  assign driver_14_out = decoder_right_1__10 ? d_ff_10_q : 8'bz;  // Driver driver_14
  assign driver_15_out = decoder_right_1__11 ? d_ff_11_q : 8'bz;  // Driver driver_15
  assign driver_16_out = decoder_right_1__12 ? d_ff_12_q : 8'bz;  // Driver driver_16
  assign driver_17_out = decoder_right_1__13 ? d_ff_13_q : 8'bz;  // Driver driver_17
  assign driver_18_out = decoder_right_1__14 ? d_ff_14_q : 8'bz;  // Driver driver_18
  assign driver_19_out = decoder_right_1__15 ? d_ff_15_q : 8'bz;  // Driver driver_19
  PullDown #(.Bits(8)) pulldown_2 (.out(driver_5_out));
  PullDown #(.Bits(8)) pulldown_3 (.out(driver_6_out));
  PullDown #(.Bits(8)) pulldown_4 (.out(driver_7_out));
  PullDown #(.Bits(8)) pulldown_5 (.out(driver_8_out));
  PullDown #(.Bits(8)) pulldown_6 (.out(driver_9_out));
  PullDown #(.Bits(8)) pulldown_7 (.out(driver_10_out));
  PullDown #(.Bits(8)) pulldown_8 (.out(driver_11_out));
  PullDown #(.Bits(8)) pulldown_9 (.out(driver_12_out));
  PullDown #(.Bits(8)) pulldown_10 (.out(driver_13_out));
  PullDown #(.Bits(8)) pulldown_11 (.out(driver_14_out));
  PullDown #(.Bits(8)) pulldown_12 (.out(driver_15_out));
  PullDown #(.Bits(8)) pulldown_13 (.out(driver_16_out));
  PullDown #(.Bits(8)) pulldown_14 (.out(driver_17_out));
  PullDown #(.Bits(8)) pulldown_15 (.out(driver_18_out));
  Decoder_Right decoder_right_1 (
    .In_1(Select), ._1(decoder_right_1__1), ._2(decoder_right_1__2), ._3(decoder_right_1__3),
    ._4(decoder_right_1__4), ._5(decoder_right_1__5), ._6(decoder_right_1__6), ._7(decoder_right_1__7),
    ._8(decoder_right_1__8), ._9(decoder_right_1__9), ._10(decoder_right_1__10), ._11(decoder_right_1__11),
    ._12(decoder_right_1__12), ._13(decoder_right_1__13), ._14(decoder_right_1__14), ._15(decoder_right_1__15));  // open: _0
  PullDown #(.Bits(8)) pulldown_16 (.out(driver_19_out));

  // Notes on the sheet:
  //   Select: pin 11
  //   Clk_write: pin 12
  //   Data_alu: pin 5
  //   Data_out: pin 10
  //   Data_mdr: pin 4
  //   Write_mdr: pin 1
  //   Write_alu: pin 2
  //   Test_out: pin 7
  //   Data_val: pin 6
  //   Write_val: pin 3
  //   Data_Out will never be high Z
  //   Writing will only occur on CLOCK
  //   When Select is set to zero
  //   -> Data_Out is zero (not high Z)
  //   -> Writing is disabled
  //   When SELECT is set to a value x
  //   -> Data_out is the value in register x
  //   -> If write_MDR is high, Data_MDR will be written to register x
  //   -> If write_ALU is high, Data_ALU will be written to register x
  //   DIGITAL BOILERPLATE
endmodule

/* Test case:
	Clk_write Select Write_mdr Write_alu Data_mdr Data_alu Data_out
loop(a, 128)
	let r1 = random(1<<2)*2+1;
	let r2 = random(1<<2)*2+2;

	let v1 = random(1<<8);
	let v2 = random(1<<8);

	0	  (r1)	 1	   0         (v1)     0	       X
	1	  (r1)	 1	   0         (v1)     0	       (v1)

	0	  (r2)	 0	   1         0	      (v2)     X
	1	  (r2)	 0	   1         0	      (v2)     (v2)

	0	  (r1)	 0	   0         0        0	       (v1)
	0	  (r2)	 0	   0         0        0	       (v2)
end loop
*/
