// Digital circuit CPU.dig as structural Verilog
module CPU (
  input  Pulse,
  output [7:0] Test_out,
  output [3:0] out_3
);

  wire alu_1_carry, alu_1_equal, alu_1_greater, alu_1_less, alu_1_notequal, clock_1_clock_1, clock_1_clock_2,
       clock_1_clock_3, clock_1_clock_4, clock_1_clock_5, clock_1_clock_6, clock_1_clock_7, clock_1_clock_8,
       controlunit_1_d_alu_increment, controlunit_1_d_rpc_memadder, controlunit_1_d_rpc_registers,
       controlunit_1_d_wrt_cirfirst, controlunit_1_d_wrt_cirsecond, controlunit_1_d_wrt_flags,
       controlunit_1_d_wrt_mdr, controlunit_1_d_wrt_regbufferfirst, controlunit_1_d_wrt_regbuffersecond,
       controlunit_1_d_wrt_regoutput, controlunit_1_d_wrt_rpc, controlunit_1_d_wrt_sram,
       controlunit_1_s_adr_direct, controlunit_1_s_adr_immediate, controlunit_1_s_alu_carryout,
       controlunit_1_s_alu_invert, controlunit_1_s_alu_orout, controlunit_1_s_alu_propagate,
       controlunit_1_s_alu_resultout, controlunit_1_s_ctl_halt, controlunit_1_s_mdr_writealu,
       controlunit_1_s_mdr_writemem, controlunit_1_s_mem_store, controlunit_1_s_reg_writealu,
       controlunit_1_s_reg_writemdr, controlunit_1_s_reg_writeval, flags_1_carry_out, flags_1_equal_out,
       flags_1_greater_out, flags_1_less_out, flags_1_notequal_out;
  wire [7:0] alu_1_data_out, buffer_1_r1_out, buffer_1_r2_out, buffer_2_r1_out, buffer_2_r2_out,
       eeprom_1_data_out, mdr_1_data_out, registers_1_data_out, sram_1_data_out;
  wire [11:0] controlunit_1_value;
  wire [15:0] addressor_1_p6, memoryadder_1_data_out, rpc_1_data_out;

  RPC rpc_1 (
    .Reg_in(addressor_1_p6), .Clk_write(controlunit_1_d_wrt_rpc), .Add_in(memoryadder_1_data_out),
    .Reg_write(controlunit_1_d_rpc_registers), .Add_write(controlunit_1_d_rpc_memadder),
    .Data_out(rpc_1_data_out));
  EEPROM eeprom_1 (.Address_in(rpc_1_data_out), .Data_out(eeprom_1_data_out));
  MemoryAdder memoryadder_1 (.Data_in(rpc_1_data_out), .Data_out(memoryadder_1_data_out));
  // Probe on rpc_1_data_out
  // Probe on eeprom_1_data_out
  Buffer buffer_1 (
    .R1_out(buffer_1_r1_out), .R2_out(buffer_1_r2_out), .Data_in(eeprom_1_data_out),
    .Clk_R1_write(controlunit_1_d_wrt_cirfirst), .Clk_R2_write(controlunit_1_d_wrt_cirsecond));
  Clock clock_1 (
    .Halt(controlunit_1_s_ctl_halt), .Pulse(Pulse), .Clock_1(clock_1_clock_1), .Clock_2(clock_1_clock_2),
    .Clock_3(clock_1_clock_3), .Clock_4(clock_1_clock_4), .Clock_5(clock_1_clock_5),
    .Clock_6(clock_1_clock_6), .Clock_7(clock_1_clock_7), .Clock_8(clock_1_clock_8));
  // Probe on buffer_1_r2_out
  // Probe on buffer_1_r1_out
  ControlUnit controlunit_1 (
    .FirstByte(buffer_1_r1_out), .SecondByte(buffer_1_r2_out), .Clock_1(clock_1_clock_1),
    .Clock_2(clock_1_clock_2), .Clock_3(clock_1_clock_3), .Clock_4(clock_1_clock_4),
    .Clock_5(clock_1_clock_5), .Clock_6(clock_1_clock_6), .Clock_7(clock_1_clock_7),
    .Clock_8(clock_1_clock_8), .S_CTL_Halt(controlunit_1_s_ctl_halt),
    .S_ADR_Direct(controlunit_1_s_adr_direct), .S_ADR_Immediate(controlunit_1_s_adr_immediate),
    .S_ALU_OrOut(controlunit_1_s_alu_orout), .S_ALU_ResultOut(controlunit_1_s_alu_resultout),
    .S_ALU_Propagate(controlunit_1_s_alu_propagate), .S_ALU_Invert(controlunit_1_s_alu_invert),
    .S_ALU_CarryOut(controlunit_1_s_alu_carryout), .S_MDR_WriteMEM(controlunit_1_s_mdr_writemem),
    .S_MDR_WriteALU(controlunit_1_s_mdr_writealu), .S_MEM_Store(controlunit_1_s_mem_store),
    .S_REG_WriteVAL(controlunit_1_s_reg_writeval), .S_REG_WriteMDR(controlunit_1_s_reg_writemdr),
    .S_REG_WriteALU(controlunit_1_s_reg_writealu), .D_WRT_MDR(controlunit_1_d_wrt_mdr),
    .D_WRT_SRAM(controlunit_1_d_wrt_sram), .D_WRT_RegOutput(controlunit_1_d_wrt_regoutput),
    .D_WRT_RegBufferFirst(controlunit_1_d_wrt_regbufferfirst),
    .D_WRT_RegBufferSecond(controlunit_1_d_wrt_regbuffersecond), .D_WRT_Flags(controlunit_1_d_wrt_flags),
    .D_WRT_RPC(controlunit_1_d_wrt_rpc), .D_WRT_CIRSecond(controlunit_1_d_wrt_cirsecond),
    .D_WRT_CIRFirst(controlunit_1_d_wrt_cirfirst), .D_RPC_Registers(controlunit_1_d_rpc_registers),
    .D_RPC_MemAdder(controlunit_1_d_rpc_memadder), .D_ALU_Increment(controlunit_1_d_alu_increment),
    .Select(out_3), .Value(controlunit_1_value), .F_NotEqual(flags_1_notequal_out),
    .F_Equal(flags_1_equal_out), .F_Less(flags_1_less_out), .F_Greater(flags_1_greater_out),
    .Carry(flags_1_carry_out));
  SRAM sram_1 (
    .Address_in(addressor_1_p6), .Store(controlunit_1_s_mem_store), .Clk_write(controlunit_1_d_wrt_sram),
    .Data_out(sram_1_data_out), .Data_in(mdr_1_data_out));
  MDR mdr_1 (
    .Data_mem(sram_1_data_out), .Clk_write(controlunit_1_d_wrt_mdr), .Data_out(mdr_1_data_out),
    .Data_reg(alu_1_data_out), .Write_mem(controlunit_1_s_mdr_writemem),
    .Write_reg(controlunit_1_s_mdr_writealu));
  Registers registers_1 (
    .Select(out_3), .Clk_write(controlunit_1_d_wrt_regoutput), .Data_alu(alu_1_data_out),
    .Data_out(registers_1_data_out), .Data_mdr(mdr_1_data_out), .Write_mdr(controlunit_1_s_reg_writemdr),
    .Write_alu(controlunit_1_s_reg_writealu), .Test_out(Test_out), .Data_val(controlunit_1_value),
    .Write_val(controlunit_1_s_reg_writeval));
  Buffer buffer_2 (
    .R1_out(buffer_2_r1_out), .R2_out(buffer_2_r2_out), .Data_in(registers_1_data_out),
    .Clk_R1_write(controlunit_1_d_wrt_regbuffersecond), .Clk_R2_write(controlunit_1_d_wrt_regbufferfirst));
  // Probe on buffer_2_r2_out
  // Probe on buffer_2_r1_out
  // Addressor addressor_1: pin names not known; wires that end beside it: buffer_2_r1_out, buffer_2_r2_out, controlunit_1_value, controlunit_1_s_adr_direct, controlunit_1_s_adr_immediate, addressor_1_p6
  // Probe on alu_1_data_out
  ALU alu_1 (
    .Data_2_in(buffer_2_r2_out), .Data_1_in(buffer_2_r1_out), .Data_out(alu_1_data_out), .Carry(alu_1_carry),
    .Invert(controlunit_1_s_alu_invert), .Increment(controlunit_1_d_alu_increment), .Equal(alu_1_equal),
    .Greater(alu_1_greater), .Less(alu_1_less), .Out_carry(controlunit_1_s_alu_carryout),
    .Propagate(controlunit_1_s_alu_propagate), .Out_or(controlunit_1_s_alu_orout),
    .Out_result(controlunit_1_s_alu_resultout), .NotEqual(alu_1_notequal));
  Flags flags_1 (
    .Less_out(flags_1_less_out), .Less_in(alu_1_less), .Greater_in(alu_1_greater), .Equal_in(alu_1_equal),
    .Carry_in(alu_1_carry), .Greater_out(flags_1_greater_out), .Equal_out(flags_1_equal_out),
    .Carry_out(flags_1_carry_out), .Clock(controlunit_1_d_wrt_flags), .NotEqual_out(flags_1_notequal_out),
    .NotEqual_in(alu_1_notequal));

  // Notes on the sheet:
  //   TICK 1
  //   -> First byte of instruction fetched
  //   -> Program counter incremented
  //   TICK 2
  //   -> Second byte of instruction fetched
  //   TICK 3
  //   -> First register selected
  //   -> Program counter incremented
  //   TICK 4
  //   -> First register fetched
  //   TICK 5
  //   -> Second register selected
  //   TICK 6
  //   -> Second register fetched
  //   TICK 7
  //   -> Flag register written to
  //   -> Output register written to
  //   -> Program counter written to
  //   -> Memory written to
endmodule

/* Test case SET:
Pulse Test_out

# SET #2 $1
memory ProgramMemory(0)=240;
memory ProgramMemory(1)=33;

# SET #87 $1
memory ProgramMemory(2)=245;
memory ProgramMemory(3)=113;

1 X
0 X
1 X
0 X
1 X
0 X
1 X
0 X
1 X
0 X
1 X
0 X
1 X
0 X
1 X
0 2

1 X
0 X
1 X
0 X
1 X
0 X
1 X
0 X
1 X
0 X
1 X
0 X
1 X
0 X
1 X
0 87
*/

/* Test case MOV:
Pulse Test_out

# SET #2 $4
memory ProgramMemory(0)=240;
memory ProgramMemory(1)=36;

# MOV $4 $1
memory ProgramMemory(2)=33;
memory ProgramMemory(3)=65;

1 X
0 X
1 X
0 X
1 X
0 X
1 X
0 X
1 X
0 X
1 X
0 X
1 X
0 X
1 X
0 0

1 X
0 X
1 X
0 X
1 X
0 X
1 X
0 X
1 X
0 X
1 X
0 X
1 X
0 X
1 X
0 2
*/
