// Digital circuit Addressor.dig as structural Verilog
module Addressor (
  input  nEnable_direct,
  input  nEnable_imm,
  input  [11:0] Data_imm,
  input  Enable_direct,
  input  [7:0] Data_direct1,
  input  [7:0] Data_direct2,
  output [11:0] Data_out
);

  Buffer_8_1 buffer_8_1_1 (
    .OE1(nEnable_direct), ._1_Y(Data_out[11]), .VCC(1'b1), .GND(1'b0), ._1_A(Data_direct2[3]),
    ._2_A(Data_direct2[2]), ._2_Y(Data_out[10]), ._4_A(Data_direct2[0]), ._5_A(Data_direct1[7]),
    ._3_Y(Data_out[9]), ._3_A(Data_direct2[1]), .OE2(1'b0), ._4_Y(Data_out[8]), ._6_A(Data_direct1[6]),
    ._7_A(Data_direct1[5]), ._8_A(Data_direct1[4]), ._5_Y(Data_out[7]), ._6_Y(Data_out[6]),
    ._7_Y(Data_out[5]), ._8_Y(Data_out[4]));
  Buffer_4_1 buffer_4_1_1 (
    .n1OE(nEnable_direct), ._11_Y(Data_out[0]), .VCC(1'b1), .GND(1'b0), ._11_A(Data_direct1[0]),
    ._12_A(Data_direct1[1]), ._12_Y(Data_out[1]), ._14_A(Data_direct1[3]), ._21_A(Data_imm[0]),
    ._13_Y(Data_out[2]), ._13_A(Data_direct1[2]), ._2OE(Enable_direct), ._14_Y(Data_out[3]),
    ._22_A(Data_imm[1]), ._23_A(Data_imm[2]), ._24_A(Data_imm[3]), ._21_Y(Data_out[0]), ._22_Y(Data_out[1]),
    ._23_Y(Data_out[2]), ._24_Y(Data_out[3]));
  Buffer_8_1 buffer_8_1_2 (
    .OE1(1'b0), ._1_Y(Data_out[4]), .VCC(1'b1), .GND(1'b0), ._1_A(Data_imm[4]), ._2_A(Data_imm[5]),
    ._2_Y(Data_out[5]), ._4_A(Data_imm[7]), ._5_A(Data_imm[8]), ._3_Y(Data_out[6]), ._3_A(Data_imm[6]),
    .OE2(nEnable_imm), ._4_Y(Data_out[7]), ._6_A(Data_imm[9]), ._7_A(Data_imm[10]), ._8_A(Data_imm[11]),
    ._5_Y(Data_out[8]), ._6_Y(Data_out[9]), ._7_Y(Data_out[10]), ._8_Y(Data_out[11]));
  LED _2 (.in(Data_imm[2]));
  LED _3 (.in(Data_imm[3]));
  LED _0 (.in(Data_imm[0]));
  LED _1 (.in(Data_imm[1]));

  // Notes on the sheet:
  //   nEnable_direct: pin 5
  //   nEnable_imm: pin 6
  //   Data_imm: pin 14
  //   Enable_direct: pin 8
  //   Data_direct1: pin 2
  //   Data_out: pin 1
  //   Data_direct2: pin 3
  //   Width
  //   36 holes
  //   9 cm
  //   Height
  //   32 holes
  //   8 cm
endmodule

/* Test case:
Data_direct1 Data_direct2 Data_imm Enable_direct ~{Enable_direct} ~{Enable_imm} Data_out
48           1            200      1             0                1             304
57           0            205      1             0                1             57
48           1            200      0             1                0             200
57           0            205      0             1                0             205
*/
