// Digital circuit Clock.dig as structural Verilog
module Clock (
  input  S_CTL_HLT,
  input  TestPulse
);

  wire _1k_2_out, _1k_out, _10k_2_out, _10k_3_out, _10k_4_out, _10k_out, _555_1_control, _555_1_output,
       and_2_1_1__4_y, d_flip_flop_1__1_q, d_flip_flop_1__2_q, d_flip_flop_1__3_q, d_flip_flop_1__4_q,
       d_flip_flop_1__5_q, d_flip_flop_1__6_q, d_flip_flop_1__7_q, not_1_1_1__5_y, not_1_1_1__6_y,
       or_3_1_1__1_y, or_3_1_1__2_y, or_3_1_1__3_y, resistor_1_out, resistor_2_out, resistor_3_out,
       resistor_4_out, resistor_5_out, resistor_6_out, resistor_7_out, resistor_8_out, resistor_9_out,
       resistor_10_out;

  _555 _555_1 (
    .GND(1'b0), .VCC(1'b1), .Trigger(_10k_3_out), .Reset(1'b1), .Threshold(_10k_3_out), .Dischrg(_10k_4_out),
    .Output(_555_1_output), .Control(_555_1_control));
  Capacitor capacitor_1 (.In(1'b0), .Out(resistor_6_out));
  Capacitor capacitor_2 (.In(1'b0), .Out(resistor_7_out));
  Capacitor _0_01uF (.In(_1k_2_out), .Out(1'b0));
  D_Flip_Flop d_flip_flop_1 (
    .EN(1'b0), ._1_Q(d_flip_flop_1__1_q), .VCC(1'b1), .GND(1'b0), ._1_D(and_2_1_1__4_y), ._2_D(_10k_2_out),
    ._3_Q(d_flip_flop_1__3_q), .CLK(TestPulse), ._2_Q(d_flip_flop_1__2_q), ._3_D(resistor_10_out),
    ._4_D(resistor_9_out), ._4_Q(d_flip_flop_1__4_q), ._5_Q(d_flip_flop_1__5_q), ._5_D(resistor_8_out),
    ._6_D(_10k_out), ._7_Q(d_flip_flop_1__7_q), ._6_Q(d_flip_flop_1__6_q), ._7_D(resistor_1_out),
    ._8_D(resistor_2_out));  // open: _8_Q
  OR_3_1 or_3_1_1 (
    ._1_B(d_flip_flop_1__2_q), ._1_Y(or_3_1_1__1_y), .VCC(1'b1), .GND(1'b0), ._1_C(d_flip_flop_1__1_q),
    ._3_A(d_flip_flop_1__5_q), ._3_Y(or_3_1_1__3_y), ._2_C(or_3_1_1__3_y), ._3_C(d_flip_flop_1__7_q),
    ._2_Y(or_3_1_1__2_y), ._3_B(d_flip_flop_1__6_q), ._1_A(d_flip_flop_1__3_q), ._2_B(d_flip_flop_1__4_q),
    ._2_A(or_3_1_1__1_y));
  NOT_1_1 not_1_1_1 (
    ._1_A(1'b0), ._2_A(1'b0), ._3_A(1'b0), ._4_A(1'b0), .VCC(1'b1), .GND(1'b0), ._5_A(S_CTL_HLT),
    ._5_Y(not_1_1_1__5_y), ._6_A(or_3_1_1__2_y), ._6_Y(not_1_1_1__6_y));  // open: _1_Y, _2_Y, _3_Y, _4_Y
  AND_2_1 and_2_1_1 (
    ._1_A(1'b0), .VCC(1'b1), .GND(1'b0), ._1_B(1'b0), ._2_A(1'b0), ._2_B(1'b0), ._3_B(1'b0), ._3_A(1'b0),
    ._4_B(not_1_1_1__6_y), ._4_Y(and_2_1_1__4_y), ._4_A(not_1_1_1__5_y));  // open: _1_Y, _2_Y, _3_Y
  Resistor _10k (.In(resistor_6_out), .Out(_10k_out));
  Resistor resistor_1 (.In(resistor_7_out), .Out(resistor_1_out));
  Resistor resistor_2 (.In(_1k_2_out), .Out(resistor_2_out));
  Resistor _1k (.In(d_flip_flop_1__4_q), .Out(_1k_out));
  Resistor resistor_3 (.In(d_flip_flop_1__3_q), .Out(resistor_3_out));
  Resistor resistor_4 (.In(d_flip_flop_1__2_q), .Out(resistor_4_out));
  Resistor resistor_5 (.In(d_flip_flop_1__1_q), .Out(resistor_5_out));
  Resistor resistor_6 (.In(d_flip_flop_1__5_q), .Out(resistor_6_out));
  Resistor resistor_7 (.In(d_flip_flop_1__6_q), .Out(resistor_7_out));
  Resistor _1k_2 (.In(d_flip_flop_1__7_q), .Out(_1k_2_out));
  Resistor resistor_8 (.In(_1k_out), .Out(resistor_8_out));
  Resistor resistor_9 (.In(resistor_3_out), .Out(resistor_9_out));
  Resistor resistor_10 (.In(resistor_4_out), .Out(resistor_10_out));
  Resistor _10k_2 (.In(resistor_5_out), .Out(_10k_2_out));
  Resistor _10k_3 (.In(_10k_4_out), .Out(_10k_3_out));
  Capacitor _1uF (.In(1'b0), .Out(_10k_4_out));
  Resistor _10k_4 (.In(1'b1), .Out(_10k_4_out));
  Capacitor _1uF_2 (.In(1'b0), .Out(_555_1_control));
  Capacitor capacitor_3 (.In(1'b0), .Out(_1k_out));
  Capacitor capacitor_4 (.In(1'b0), .Out(resistor_3_out));
  Capacitor capacitor_5 (.In(1'b0), .Out(resistor_4_out));
  Capacitor _0_01uF_2 (.In(1'b0), .Out(resistor_5_out));

  // Notes on the sheet:
  //   S_CTL_HLT: pin 20
endmodule
