// Digital circuit ControlUnit.dig as structural Verilog
module ControlUnit (
  input  [7:0] FirstByte,
  input  [7:0] SecondByte,
  output ALU_UseCarry,
  output ALU_Increment,
  output ALU_Invert,
  output ALU_Propagate,
  output ALU_ResultOut,
  output ALU_CarryOut,
  output ALU_FlagWrite,
  output ALU_OrOut,
  output ADR_Immediate,
  output ADR_Direct,
  output BRA_Branch,
  output BRA_Unconditional,
  output BRA_Greater,
  output BRA_Less,
  output BRA_Equal,
  output BRA_NotEqual,
  output INS_RegReadFirst,
  output INS_RegReadSecond,
  output INS_ValReadCenter,
  output INS_ValReadEnd,
  output REG_WriteALU,
  output REG_WriteMDR,
  output MEM_Load,
  output MEM_Store,
  output MDR_WriteALU,
  output MDR_WriteMEM,
  output CTL_Halt
);

  wire auxiliary_combinator_1__2_3_4_5_6, group1_combinator_1_p4, group1_combinator_1_p5,
       group1_combinator_1_p6, group1_combinator_1_p7, group1_combinator_1_p8, group1_combinator_1_p9,
       group1_combinator_1_p10, group1_combinator_1_p11, group2_combinator_1_p3, group2_combinator_1_p4,
       group2_combinator_1_p5, group2_combinator_1_p6, group2_combinator_1_p7, group2_combinator_1_p8,
       group3_combinator_1_ins_regreadfirst, group3_combinator_1_ins_regreadsecond,
       group3_combinator_1_mdr_writemem, group3_combinator_1_mem_load, group3_combinator_1_mem_store,
       group4_combinator_1_alu_flagwrite, group4_combinator_1_alu_increment, group4_combinator_1_alu_invert,
       group4_combinator_1_alu_propagate, group4_combinator_1_alu_resultout,
       group4_combinator_1_ins_regreadfirst, group4_combinator_1_ins_regreadsecond,
       group4_combinator_1_reg_writealu, instructionsplitter_1_isopcodenibble,
       nibble_combinator_1_ins_regreadfirst, nibble_combinator_1_mdr_writemem, nibble_combinator_1_mem_load,
       nibble_combinator_1_mem_store, not_1_out, or_4_out, or_6_out, or_7_out, or_9_out, or_10_out,
       or_11_out, or_13_out, or_15_out, or_18_out;
  wire [2:0] instructionsplitter_1_counter;
  wire [3:0] driver_1_out, instructionsplitter_1_nibble2, instructionsplitter_1_nibble3,
       instructionsplitter_1_nibble4;
  wire [7:0] decoder_1__0;

  InstructionSplitter instructionsplitter_1 (
    .Instruction({FirstByte, SecondByte}), .Nibble4(instructionsplitter_1_nibble4),
    .Nibble3(instructionsplitter_1_nibble3), .Nibble2(instructionsplitter_1_nibble2),
    .Counter(instructionsplitter_1_counter), .IsOpcodeNibble(instructionsplitter_1_isopcodenibble));
  // ControlUnit controlunit_1: pin names not known
  not not_1 (not_1_out, instructionsplitter_1_isopcodenibble);
  assign driver_1_out = not_1_out ? instructionsplitter_1_nibble2 : 4'bz;  // Driver driver_1
  PullDown #(.Bits(4)) pulldown_1 (.out(driver_1_out));
  Decoder decoder_1 (
    .In(instructionsplitter_1_counter), ._0(decoder_1__0[0]), ._1(decoder_1__0[1]), ._2(decoder_1__0[2]),
    ._3(decoder_1__0[3]), ._4(decoder_1__0[4]), ._5(decoder_1__0[5]), ._6(decoder_1__0[6]),
    ._7(decoder_1__0[7]));
  Auxiliary_Combinator auxiliary_combinator_1 (.Counter(decoder_1__0), ._2_3_4_5_6(auxiliary_combinator_1__2_3_4_5_6));
  // Group1_Combinator group1_combinator_1: pin names not known; wires that end beside it: decoder_1__0, driver_1_out[3], ALU_UseCarry, group1_combinator_1_p4, group1_combinator_1_p5, group1_combinator_1_p6, group1_combinator_1_p7, group1_combinator_1_p8, group1_combinator_1_p9, group1_combinator_1_p10, group1_combinator_1_p11
  // Group2_Combinator group2_combinator_1: pin names not known; wires that end beside it: decoder_1__0, driver_1_out[2], group2_combinator_1_p3, group2_combinator_1_p4, group2_combinator_1_p5, group2_combinator_1_p6, group2_combinator_1_p7, group2_combinator_1_p8, ALU_CarryOut, ALU_OrOut
  Group3_Combinator group3_combinator_1 (
    .Counter(decoder_1__0), .Active(driver_1_out[1]), .ADR_Direct(ADR_Direct),
    .INS_RegReadFirst(group3_combinator_1_ins_regreadfirst),
    .INS_RegReadSecond(group3_combinator_1_ins_regreadsecond), .MEM_Load(group3_combinator_1_mem_load),
    .MEM_Store(group3_combinator_1_mem_store), .MDR_WriteMem(group3_combinator_1_mdr_writemem));
  Group4_Combinator group4_combinator_1 (
    .Counter(decoder_1__0), .Active(driver_1_out[0]), ._2_3_4_5_6(auxiliary_combinator_1__2_3_4_5_6),
    .ALU_Increment(group4_combinator_1_alu_increment), .ALU_FlagWrite(group4_combinator_1_alu_flagwrite),
    .ALU_Invert(group4_combinator_1_alu_invert), .ALU_Propagate(group4_combinator_1_alu_propagate),
    .ALU_ResultOut(group4_combinator_1_alu_resultout),
    .INS_RegReadFirst(group4_combinator_1_ins_regreadfirst),
    .INS_RegReadSecond(group4_combinator_1_ins_regreadsecond),
    .REG_WriteALU(group4_combinator_1_reg_writealu), .REG_WriteMDR(REG_WriteMDR),
    .MDR_WriteALU(MDR_WriteALU), .CTL_Halt(CTL_Halt));
  Nibble_Combinator nibble_combinator_1 (
    .Counter(decoder_1__0), .Active(instructionsplitter_1_isopcodenibble), .ADR_Immediate(ADR_Immediate),
    .INS_RegReadFirst(nibble_combinator_1_ins_regreadfirst), .INS_ValReadCenter(INS_ValReadCenter),
    .INS_ValReadEnd(INS_ValReadEnd), .MEM_Load(nibble_combinator_1_mem_load),
    .MEM_Store(nibble_combinator_1_mem_store), .MDR_WriteMem(nibble_combinator_1_mdr_writemem));
  Branch_Combinator branch_combinator_1 (
    .Counter(decoder_1__0), .Active_Group3(driver_1_out[1]),
    .Active_Nibble(instructionsplitter_1_isopcodenibble), ._2_3_4_5_6(auxiliary_combinator_1__2_3_4_5_6),
    .BRA_Branch(BRA_Branch), .BRA_Less(BRA_Less), .BRA_Equal(BRA_Equal), .BRA_NotEqual(BRA_NotEqual),
    .BRA_Unconditional(BRA_Unconditional), .BRA_Greater(BRA_Greater));
  or or_1 (MDR_WriteMEM, group3_combinator_1_mdr_writemem, nibble_combinator_1_mdr_writemem);
  or or_2 (MEM_Store, group3_combinator_1_mem_store, nibble_combinator_1_mem_store);
  or or_3 (MEM_Load, group3_combinator_1_mem_load, nibble_combinator_1_mem_load);
  or or_4 (or_4_out, group2_combinator_1_p8, group4_combinator_1_reg_writealu);
  or or_5 (REG_WriteALU, group1_combinator_1_p11, or_4_out);
  or or_6 (or_6_out, group3_combinator_1_ins_regreadsecond, group4_combinator_1_ins_regreadsecond);
  or or_7 (or_7_out, group2_combinator_1_p7, or_6_out);
  or or_8 (INS_RegReadSecond, group1_combinator_1_p10, or_7_out);
  or or_9 (or_9_out, group4_combinator_1_ins_regreadfirst, nibble_combinator_1_ins_regreadfirst);
  or or_10 (or_10_out, group3_combinator_1_ins_regreadfirst, or_9_out);
  or or_11 (or_11_out, group1_combinator_1_p9, or_10_out);
  or or_12 (INS_RegReadFirst, group2_combinator_1_p6, or_11_out);
  or or_13 (or_13_out, group2_combinator_1_p5, group4_combinator_1_alu_flagwrite);
  or or_14 (ALU_FlagWrite, group1_combinator_1_p8, or_13_out);
  or or_15 (or_15_out, group2_combinator_1_p4, group4_combinator_1_alu_resultout);
  or or_16 (ALU_ResultOut, group1_combinator_1_p7, or_15_out);
  or or_17 (ALU_Propagate, group1_combinator_1_p6, group4_combinator_1_alu_propagate);
  or or_18 (or_18_out, group2_combinator_1_p3, group4_combinator_1_alu_invert);
  or or_19 (ALU_Invert, group1_combinator_1_p5, or_18_out);
  or or_20 (ALU_Increment, group1_combinator_1_p4, group4_combinator_1_alu_increment);
endmodule

/* Test case ALU:
FirstByte ALU-UseCarry ALU-Increment ALU-Invert ALU-Propagate ALU-ResultOut ALU-CarryOut ALU-OrOut ALU-FlagWrite

8         0            0             0          1             1             0            0         1
24        1            0             0          1             1             0            0         1
40        0            1             1          1             1             0            0         1
56        1            1             1          1             1             0            0         1
72        0            1             0          1             1             0            0         1
88        0            0             1          1             1             0            0         1
104       0            1             1          1             1             0            0         1

4         0            0             0          0             1             0            0         1
20        0            0             0          0             0             1            0         1
36        0            0             0          0             0             0            1         1
52        0            0             1          0             1             0            0         1

2         0            0             0          0             0             0            0         0
18        0            0             0          0             0             0            0         0
34        0            0             0          0             0             0            0         0
50        0            0             0          0             0             0            0         0
66        0            0             0          0             0             0            0         0
82        0            0             0          0             0             0            0         0
98        0            0             0          0             0             0            0         0

1         0            0             0          0             0             0            0         0
17        0            0             0          0             0             0            0         0
33        0            0             0          0             1             0            0         0
49        0            0             0          0             1             0            0         0
65        0            0             0          0             0             0            0         0
81        0            1             1          1             0             0            0         1
97        0            0             0          0             0             0            0         1

128       0            0             0          0             0             0            0         0
144       0            0             0          0             0             0            0         0
160       0            0             0          0             0             0            0         0
176       0            0             0          0             0             0            0         0
192       0            0             0          0             0             0            0         0
208       0            0             0          0             0             0            0         0
224       0            0             0          0             0             0            0         0
240       0            0             0          0             0             0            0         0
*/

/* Test case ADR:
FirstByte ADR-Immediate ADR-Direct

8         0             0
24        0             0
40        0             0
56        0             0
72        0             0
88        0             0
104       0             0

4         0             0
20        0             0
36        0             0
52        0             0

2         0             1
18        0             1
34        0             1
50        0             1
66        0             1
82        0             1
98        0             1

1         0             0
17        0             0
33        0             0
49        0             0
65        0             0
81        0             0
97        0             0

128       1             0
144       1             0
160       1             0
176       1             0
192       1             0
208       1             0
224       1             0
240       0             0
*/

/* Test case BRA:
FirstByte BRA-Branch BRA-Unconditional BRA-Greater BRA-Less BRA-Equal BRA-NotEqual

8         0          0                 0           0        0         0
24        0          0                 0           0        0         0
40        0          0                 0           0        0         0
56        0          0                 0           0        0         0
72        0          0                 0           0        0         0
88        0          0                 0           0        0         0
104       0          0                 0           0        0         0

4         0          0                 0           0        0         0
20        0          0                 0           0        0         0
36        0          0                 0           0        0         0
52        0          0                 0           0        0         0

2         0          0                 0           0        0         0
18        0          0                 0           0        0         0
34        1          1                 0           0        0         0
50        1          0                 1           0        0         0
66        1          0                 0           1        0         0
82        1          0                 0           0        1         0
98        1          0                 0           0        0         1

1         0          0                 0           0        0         0
17        0          0                 0           0        0         0
33        0          0                 0           0        0         0
49        0          0                 0           0        0         0
65        0          0                 0           0        0         0
81        0          0                 0           0        0         0
97        0          0                 0           0        0         0

128       0          0                 0           0        0         0
144       0          0                 0           0        0         0
160       1          1                 0           0        0         0
176       1          0                 1           0        0         0
192       1          0                 0           1        0         0
208       1          0                 0           0        1         0
224       1          0                 0           0        0         1
240       0          0                 0           0        0         0
*/

/* Test case INS:
FirstByte INS-RegReadFirst INS-RegReadSecond INS-ValReadCenter INS-ValReadEnd

8         1                1                 0                 0
24        1                1                 0                 0
40        1                1                 0                 0
56        1                1                 0                 0
72        1                0                 0                 0
88        1                0                 0                 0
104       1                0                 0                 0
              
4         1                1                 0                 0
20        1                1                 0                 0
36        1                1                 0                 0
52        1                0                 0                 0
              
2         1                1                 0                 0
18        1                1                 0                 0
34        1                1                 0                 0
50        1                1                 0                 0
66        1                1                 0                 0
82        1                1                 0                 0
98        1                1                 0                 0
              
1         0                0                 0                 0
17        0                0                 0                 0
33        1                1                 0                 0
49        1                0                 0                 0
65        1                0                 0                 0
81        1                1                 0                 0
97        1                0                 0                 0
              
128       0                0                 1                 1
144       0                0                 1                 1
160       0                0                 1                 1
176       0                0                 1                 1
192       0                0                 1                 1
208       0                0                 1                 1
224       0                0                 1                 1
240       1                0                 1                 0
*/

/* Test case REG:
FirstByte REG-WriteALU REG-WriteMDR

8         1                0
24        1                0
40        1                0
56        1                0
72        1                0
88        1                0
104       1                0
              
4         1                0
20        1                0
36        1                0
52        1                0
              
2         0                0
18        0                0
34        0                0
50        0                0
66        0                0
82        0                0
98        0                0
              
1         0                0
17        0                0
33        1                0
49        0                0
65        0                1
81        0                0
97        0                0
              
128       0                0
144       0                0
160       0                0
176       0                0
192       0                0
208       0                0
224       0                0
240       0                0
*/

/* Test case MEM:
FirstByte MEM-Load MEM-Store

8         0        0
24        0        0
40        0        0
56        0        0
72        0        0
88        0        0
104       0        0
              
4         0        0
20        0        0
36        0        0
52        0        0
              
2         1        0
18        0        1
34        0        0
50        0        0
66        0        0
82        0        0
98        0        0
              
1         0        0
17        0        0
33        0        0
49        0        0
65        0        0
81        0        0
97        0        0
              
128       1        0
144       0        1
160       0        0
176       0        0
192       0        0
208       0        0
224       0        0
240       0        0
*/

/* Test case MDR:
FirstByte MDR-WriteALU MDR-WriteMEM

8         0            0
24        0            0
40        0            0
56        0            0
72        0            0
88        0            0
104       0            0
              
4         0            0
20        0            0
36        0            0
52        0            0
              
2         0            1
18        0            0
34        0            0
50        0            0
66        0            0
82        0            0
98        0            0
              
1         0            0
17        0            0
33        0            0
49        1            0
65        0            0
81        0            0
97        0            0
              
128       0            1
144       0            0
160       0            0
176       0            0
192       0            0
208       0            0
224       0            0
240       0            0
*/

/* Test case CTL:
FirstByte CTL-Halt

8         0
24        0
40        0
56        0
72        0
88        0
104       0
              
4         0
20        0
36        0
52        0
              
2         0
18        0
34        0
50        0
66        0
82        0
98        0
              
1         0
17        1
33        0
49        0
65        0
81        0
97        0
              
128       0
144       0
160       0
176       0
192       0
208       0
224       0
240       0
*/
