// Digital circuit Decoder-16.dig as structural Verilog
module Decoder_16 (
  input  [3:0] In,
  output [15:0] Out
);

  wire and_4_1_1__1_y, and_4_1_1__2_y, and_4_1_2__1_y, and_4_1_2__2_y, and_4_1_3__1_y, and_4_1_3__2_y,
       and_4_1_4__1_y, and_4_1_4__2_y, and_4_1_5__1_y, and_4_1_5__2_y, and_4_1_6__1_y, and_4_1_6__2_y,
       and_4_1_7__1_y, and_4_1_7__2_y, and_4_1_8__1_y, and_4_1_8__2_y, not_1_1_1__1_y, not_1_1_1__4_y,
       not_1_1_1__5_y, not_1_1_1__6_y;

  NOT_1_1 not_1_1_1 (
    ._1_A(In[3]), ._1_Y(not_1_1_1__1_y), ._2_A(1'b0), ._3_A(1'b0), ._4_A(In[0]), ._4_Y(not_1_1_1__4_y),
    .VCC(1'b1), .GND(1'b0), ._5_A(In[1]), ._5_Y(not_1_1_1__5_y), ._6_A(In[2]), ._6_Y(not_1_1_1__6_y));  // open: _2_Y, _3_Y
  AND_4_1 and_4_1_1 (
    ._1_B(not_1_1_1__5_y), ._1_Y(and_4_1_1__1_y), .VCC(1'b1), .GND(1'b0), ._1_C(not_1_1_1__6_y), .NC_2(1'b0),
    ._2_A(In[0]), ._2_D(not_1_1_1__1_y), ._2_Y(and_4_1_1__2_y), ._2_C(not_1_1_1__6_y), ._1_A(not_1_1_1__4_y),
    .NC_1(1'b0), ._1_D(not_1_1_1__1_y), ._2_B(not_1_1_1__5_y));
  AND_4_1 and_4_1_2 (
    ._1_B(In[1]), ._1_Y(and_4_1_2__1_y), .VCC(1'b1), .GND(1'b0), ._1_C(not_1_1_1__6_y), .NC_2(1'b0),
    ._2_A(In[0]), ._2_D(not_1_1_1__1_y), ._2_Y(and_4_1_2__2_y), ._2_C(not_1_1_1__6_y), ._1_A(not_1_1_1__4_y),
    .NC_1(1'b0), ._1_D(not_1_1_1__1_y), ._2_B(In[1]));
  AND_4_1 and_4_1_3 (
    ._1_B(not_1_1_1__5_y), ._1_Y(and_4_1_3__1_y), .VCC(1'b1), .GND(1'b0), ._1_C(In[2]), .NC_2(1'b0),
    ._2_A(In[0]), ._2_D(not_1_1_1__1_y), ._2_Y(and_4_1_3__2_y), ._2_C(In[2]), ._1_A(not_1_1_1__4_y),
    .NC_1(1'b0), ._1_D(not_1_1_1__1_y), ._2_B(not_1_1_1__5_y));
  AND_4_1 and_4_1_4 (
    ._1_B(In[1]), ._1_Y(and_4_1_4__1_y), .VCC(1'b1), .GND(1'b0), ._1_C(In[2]), .NC_2(1'b0), ._2_A(In[0]),
    ._2_D(not_1_1_1__1_y), ._2_Y(and_4_1_4__2_y), ._2_C(In[2]), ._1_A(not_1_1_1__4_y), .NC_1(1'b0),
    ._1_D(not_1_1_1__1_y), ._2_B(In[1]));
  AND_4_1 and_4_1_5 (
    ._1_B(not_1_1_1__5_y), ._1_Y(and_4_1_5__1_y), .VCC(1'b1), .GND(1'b0), ._1_C(not_1_1_1__6_y), .NC_2(1'b0),
    ._2_A(In[0]), ._2_D(In[3]), ._2_Y(and_4_1_5__2_y), ._2_C(not_1_1_1__6_y), ._1_A(not_1_1_1__4_y),
    .NC_1(1'b0), ._1_D(In[3]), ._2_B(not_1_1_1__5_y));
  AND_4_1 and_4_1_6 (
    ._1_B(In[1]), ._1_Y(and_4_1_6__1_y), .VCC(1'b1), .GND(1'b0), ._1_C(not_1_1_1__6_y), .NC_2(1'b0),
    ._2_A(In[0]), ._2_D(In[3]), ._2_Y(and_4_1_6__2_y), ._2_C(not_1_1_1__6_y), ._1_A(not_1_1_1__4_y),
    .NC_1(1'b0), ._1_D(In[3]), ._2_B(In[1]));
  AND_4_1 and_4_1_7 (
    ._1_B(not_1_1_1__5_y), ._1_Y(and_4_1_7__1_y), .VCC(1'b1), .GND(1'b0), ._1_C(In[2]), .NC_2(1'b0),
    ._2_A(In[0]), ._2_D(In[3]), ._2_Y(and_4_1_7__2_y), ._2_C(In[2]), ._1_A(not_1_1_1__4_y), .NC_1(1'b0),
    ._1_D(In[3]), ._2_B(not_1_1_1__5_y));
  AND_4_1 and_4_1_8 (
    ._1_B(In[1]), ._1_Y(and_4_1_8__1_y), .VCC(1'b1), .GND(1'b0), ._1_C(In[2]), .NC_2(1'b0), ._2_A(In[0]),
    ._2_D(In[3]), ._2_Y(and_4_1_8__2_y), ._2_C(In[2]), ._1_A(not_1_1_1__4_y), .NC_1(1'b0), ._1_D(In[3]),
    ._2_B(In[1]));
  NOT_1_1 not_1_1_2 (
    ._1_A(and_4_1_1__1_y), ._1_Y(Out[0]), ._2_A(and_4_1_1__2_y), ._2_Y(Out[1]), ._3_A(and_4_1_2__1_y),
    ._3_Y(Out[2]), ._4_A(and_4_1_2__2_y), ._4_Y(Out[3]), .VCC(1'b1), .GND(1'b0), ._5_A(and_4_1_3__1_y),
    ._5_Y(Out[4]), ._6_A(and_4_1_3__2_y), ._6_Y(Out[5]));
  NOT_1_1 not_1_1_3 (
    ._1_A(and_4_1_4__1_y), ._1_Y(Out[6]), ._2_A(and_4_1_4__2_y), ._2_Y(Out[7]), ._3_A(and_4_1_5__1_y),
    ._3_Y(Out[8]), ._4_A(and_4_1_5__2_y), ._4_Y(Out[9]), .VCC(1'b1), .GND(1'b0), ._5_A(and_4_1_6__1_y),
    ._5_Y(Out[10]), ._6_A(and_4_1_6__2_y), ._6_Y(Out[11]));
  NOT_1_1 not_1_1_4 (
    ._1_A(and_4_1_7__1_y), ._1_Y(Out[12]), ._2_A(and_4_1_7__2_y), ._2_Y(Out[13]), ._3_A(and_4_1_8__1_y),
    ._3_Y(Out[14]), ._4_A(1'b0), .VCC(1'b1), .GND(1'b0), ._5_A(1'b0), ._6_A(and_4_1_8__2_y), ._6_Y(Out[15]));  // open: _4_Y, _5_Y
  LED _3 (.in(In[2]));
  LED _2 (.in(In[1]));
  LED _1 (.in(In[0]));
  LED _2_2 (.in(not_1_1_1__5_y));
  LED _1_2 (.in(not_1_1_1__4_y));
  LED _4 (.in(In[3]));
  LED _3_2 (.in(not_1_1_1__6_y));
  LED _4_2 (.in(not_1_1_1__1_y));

  // Notes on the sheet:
  //   In: pin 50
  //   Out: pin 25
  //   Width
  //   22 holes
  //   5.5 cm
  //   Height
  //   142 holes
  //   35.5 cm
endmodule

/* Test case:
In       Out
0	 (-2)
1	 (-3)
2	 (-5)
3	 (-9)
4	 (-17)
5	 (-33)
6	 (-65)
7	 (-129)
8	 (-257)
9	 (-513)
10	 (-1025)
11	 (-2049)
12	 (-4097)
13	 (-8193)
14	 (-16385)
15	 (-32769)
*/
