// Digital circuit Decoder-8.dig as structural Verilog
module Decoder_8 (
  input  [2:0] In,
  output [7:0] Out
);

  wire not_1_1_1__4_y, not_1_1_1__5_y, not_1_1_1__6_y;

  NOT_1_1 not_1_1_1 (
    ._1_A(1'b0), ._2_A(1'b0), ._3_A(1'b0), ._4_A(In[0]), ._4_Y(not_1_1_1__4_y), .VCC(1'b1), .GND(1'b0),
    ._5_A(In[1]), ._5_Y(not_1_1_1__5_y), ._6_A(In[2]), ._6_Y(not_1_1_1__6_y));  // open: _1_Y, _2_Y, _3_Y
  AND_4_1 and_4_1_1 (
    ._1_B(not_1_1_1__5_y), ._1_Y(Out[0]), .VCC(1'b1), .GND(1'b0), ._1_C(not_1_1_1__6_y), .NC_2(1'b0),
    ._2_A(In[0]), ._2_D(1'b1), ._2_Y(Out[1]), ._2_C(not_1_1_1__6_y), ._1_A(not_1_1_1__4_y), .NC_1(1'b0),
    ._1_D(1'b1), ._2_B(not_1_1_1__5_y));
  AND_4_1 and_4_1_2 (
    ._1_B(In[1]), ._1_Y(Out[2]), .VCC(1'b1), .GND(1'b0), ._1_C(not_1_1_1__6_y), .NC_2(1'b0), ._2_A(In[0]),
    ._2_D(1'b1), ._2_Y(Out[3]), ._2_C(not_1_1_1__6_y), ._1_A(not_1_1_1__4_y), .NC_1(1'b0), ._1_D(1'b1),
    ._2_B(In[1]));
  AND_4_1 and_4_1_3 (
    ._1_B(not_1_1_1__5_y), ._1_Y(Out[4]), .VCC(1'b1), .GND(1'b0), ._1_C(In[2]), .NC_2(1'b0), ._2_A(In[0]),
    ._2_D(1'b1), ._2_Y(Out[5]), ._2_C(In[2]), ._1_A(not_1_1_1__4_y), .NC_1(1'b0), ._1_D(1'b1),
    ._2_B(not_1_1_1__5_y));
  AND_4_1 and_4_1_4 (
    ._1_B(In[1]), ._1_Y(Out[6]), .VCC(1'b1), .GND(1'b0), ._1_C(In[2]), .NC_2(1'b0), ._2_A(In[0]),
    ._2_D(1'b1), ._2_Y(Out[7]), ._2_C(In[2]), ._1_A(not_1_1_1__4_y), .NC_1(1'b0), ._1_D(1'b1), ._2_B(In[1]));
  LED _3 (.in(In[2]));
  LED _2 (.in(In[1]));
  LED _1 (.in(In[0]));
  LED _3_2 (.in(not_1_1_1__6_y));
  LED _2_2 (.in(not_1_1_1__5_y));
  LED _1_2 (.in(not_1_1_1__4_y));

  // Notes on the sheet:
  //   In: pin 28
  //   Out: pin 14
  //   Width
  //   24 holes
  //   6 cm
  //   Height
  //   52 holes
  //   13 cm
endmodule

/* Test case:
In       Out
0	 1
1	 2
2	 4
3	 8
4	 16
5	 32
6	 64
7	 128
*/
