// Digital circuit EEPROM.dig as structural Verilog
module EEPROM (
  input  [11:0] Address,
  input  D_CLK_CIRFirst,
  input  D_CLK_CIRSecond,
  output [7:0] Out_MSB,
  output [7:0] Out_LSB
);

  wire sram_1_d_0, sram_1_d_1, sram_1_d_2, sram_1_d_3, sram_1_d_4, sram_1_d_5, sram_1_d_6, sram_1_d_7;

  D_Flip_Flop d_flip_flop_1 (
    .EN(1'b0), ._1_Q(Out_MSB[0]), .VCC(1'b1), .GND(1'b0), ._1_D(sram_1_d_0), ._2_D(sram_1_d_1),
    ._3_Q(Out_MSB[2]), .CLK(D_CLK_CIRFirst), ._2_Q(Out_MSB[1]), ._3_D(sram_1_d_2), ._4_D(sram_1_d_3),
    ._4_Q(Out_MSB[3]), ._5_Q(Out_MSB[4]), ._5_D(sram_1_d_4), ._6_D(sram_1_d_5), ._7_Q(Out_MSB[6]),
    ._6_Q(Out_MSB[5]), ._7_D(sram_1_d_6), ._8_D(sram_1_d_7), ._8_Q(Out_MSB[7]));
  D_Flip_Flop d_flip_flop_2 (
    .EN(1'b0), ._1_Q(Out_LSB[0]), .VCC(1'b1), .GND(1'b0), ._1_D(sram_1_d_0), ._2_D(sram_1_d_1),
    ._3_Q(Out_LSB[2]), .CLK(D_CLK_CIRSecond), ._2_Q(Out_LSB[1]), ._3_D(sram_1_d_2), ._4_D(sram_1_d_3),
    ._4_Q(Out_LSB[3]), ._5_Q(Out_LSB[4]), ._5_D(sram_1_d_4), ._6_D(sram_1_d_5), ._7_Q(Out_LSB[6]),
    ._6_Q(Out_LSB[5]), ._7_D(sram_1_d_6), ._8_D(sram_1_d_7), ._8_Q(Out_LSB[7]));
  SRAM sram_1 (
    .NC(1'b0), .A_0(Address[0]), .A_1(Address[1]), .A_2(Address[2]), .A_3(Address[3]), .A_4(Address[4]),
    .A_5(Address[5]), .A_6(Address[6]), .A_7(Address[7]), .A_8(Address[8]), .A_9(Address[9]),
    .A_10(Address[10]), .A_11(Address[11]), .OE(1'b0), .GND(1'b0), .VCC(1'b1), .WE(1'b1), .A_12(1'b0),
    .CS_2(1'b1), .CS_1(1'b0), .D_0(sram_1_d_0), .D_1(sram_1_d_1), .D_2(sram_1_d_2), .D_3(sram_1_d_3),
    .D_4(sram_1_d_4), .D_5(sram_1_d_5), .D_6(sram_1_d_6), .D_7(sram_1_d_7));

  // Notes on the sheet:
  //   Address: pin 5
  //   Out_MSB: pin 11
  //   Out_LSB: pin 12
  //   D_CLK_CIRFirst: pin 16
  //   D_CLK_CIRSecond: pin 13
endmodule
