// Digital circuit FlagUnit.dig as structural Verilog
module FlagUnit (
  input  ALU_usecarry,
  input  ALU_increment,
  input  BRA_unconditional,
  input  BRA_less,
  input  BRA_greater,
  input  BRA_equal,
  input  BRA_notequal,
  input  Clock_1,
  input  Clock_2,
  input  Clock_5,
  input  Greater,
  input  Less,
  input  Equal,
  input  Carry,
  output ALU_Increment_2,
  output PC_Write,
  output PC_Registers,
  output PC_MemAdder
);

  wire and_1_out, and_2_out, and_3_out, and_4_out, and_5_out, and_6_out, not_1_out, or_1_out;

  not not_1 (not_1_out, Equal);
  and and_1 (and_1_out, BRA_less, Less);
  and and_2 (and_2_out, BRA_greater, Greater);
  and and_3 (and_3_out, BRA_equal, Equal);
  and and_4 (and_4_out, BRA_notequal, not_1_out);
  and and_5 (and_5_out, Carry, ALU_usecarry);
  xor xor_1 (ALU_Increment_2, ALU_increment, and_5_out);
  or or_1 (or_1_out, and_2_out, and_3_out, and_4_out);
  or or_2 (PC_Registers, BRA_unconditional, and_1_out, or_1_out);
  and and_6 (and_6_out, Clock_5, PC_Registers);
  or or_3 (PC_Write, Clock_1, Clock_2, and_6_out);
  not not_2 (PC_MemAdder, ALU_Increment_2);

  // Notes on the sheet:
  //   ALU_usecarry: pin 21
  //   ALU_increment: pin 22
  //   BRA_unconditional: pin 13
  //   BRA_less: pin 12
  //   BRA_greater: pin 14
  //   BRA_equal: pin 15
  //   BRA_notequal: pin 16
  //   Clock_1: pin 1
  //   Clock_2: pin 2
  //   Clock_5: pin 3
  //   Greater: pin 5
  //   Less: pin 4
  //   Equal: pin 6
  //   Carry: pin 7
  //   ALU_Increment_2: pin 8
  //   PC_Write: pin 9
  //   PC_Registers: pin 11
  //   PC_MemAdder: pin 10
endmodule

/* Test case:
BRA-Less Less RegistersToPC
0 0 0
0 1 0
1 0 0
1 1 1
*/
