// Digital circuit MEM Adder.dig as structural Verilog
module MEM_Adder (
  input  [11:0] Data_in,
  output [11:0] Data_out
);

  wire and_2_1_1__1_y, and_2_1_1__2_y, and_2_1_1__3_y, and_2_1_1__4_y, and_2_1_2__1_y, and_2_1_2__2_y,
       and_2_1_2__3_y, and_2_1_2__4_y, and_2_1_3__1_y, and_2_1_3__2_y, and_2_1_3__3_y;

  XOR_2_1 xor_2_1_1 (
    ._1_A(Data_in[0]), ._1_Y(Data_out[0]), .VCC(1'b1), .GND(1'b0), ._1_B(1'b1), ._2_A(Data_in[1]),
    ._2_Y(Data_out[1]), ._2_B(and_2_1_1__1_y), ._3_B(Data_in[2]), ._3_Y(Data_out[2]), ._3_A(and_2_1_1__2_y),
    ._4_B(Data_in[3]), ._4_Y(Data_out[3]), ._4_A(and_2_1_1__3_y));
  XOR_2_1 xor_2_1_2 (
    ._1_A(Data_in[4]), ._1_Y(Data_out[4]), .VCC(1'b1), .GND(1'b0), ._1_B(and_2_1_1__4_y), ._2_A(Data_in[5]),
    ._2_Y(Data_out[5]), ._2_B(and_2_1_2__1_y), ._3_B(Data_in[6]), ._3_Y(Data_out[6]), ._3_A(and_2_1_2__2_y),
    ._4_B(Data_in[7]), ._4_Y(Data_out[7]), ._4_A(and_2_1_2__3_y));
  XOR_2_1 xor_2_1_3 (
    ._1_A(Data_in[8]), ._1_Y(Data_out[8]), .VCC(1'b1), .GND(1'b0), ._1_B(and_2_1_2__4_y), ._2_A(Data_in[9]),
    ._2_Y(Data_out[9]), ._2_B(and_2_1_3__1_y), ._3_B(Data_in[10]), ._3_Y(Data_out[10]),
    ._3_A(and_2_1_3__2_y), ._4_B(Data_in[11]), ._4_Y(Data_out[11]), ._4_A(and_2_1_3__3_y));
  AND_2_1 and_2_1_1 (
    ._1_A(Data_in[0]), ._1_Y(and_2_1_1__1_y), .VCC(1'b1), .GND(1'b0), ._1_B(1'b1), ._2_A(Data_in[1]),
    ._2_Y(and_2_1_1__2_y), ._2_B(and_2_1_1__1_y), ._3_B(Data_in[2]), ._3_Y(and_2_1_1__3_y),
    ._3_A(and_2_1_1__2_y), ._4_B(Data_in[3]), ._4_Y(and_2_1_1__4_y), ._4_A(and_2_1_1__3_y));
  AND_2_1 and_2_1_2 (
    ._1_A(Data_in[4]), ._1_Y(and_2_1_2__1_y), .VCC(1'b1), .GND(1'b0), ._1_B(and_2_1_1__4_y),
    ._2_A(Data_in[5]), ._2_Y(and_2_1_2__2_y), ._2_B(and_2_1_2__1_y), ._3_B(Data_in[6]),
    ._3_Y(and_2_1_2__3_y), ._3_A(and_2_1_2__2_y), ._4_B(Data_in[7]), ._4_Y(and_2_1_2__4_y),
    ._4_A(and_2_1_2__3_y));
  AND_2_1 and_2_1_3 (
    ._1_A(Data_in[8]), ._1_Y(and_2_1_3__1_y), .VCC(1'b1), .GND(1'b0), ._1_B(and_2_1_2__4_y),
    ._2_A(Data_in[9]), ._2_Y(and_2_1_3__2_y), ._2_B(and_2_1_3__1_y), ._3_B(Data_in[10]),
    ._3_Y(and_2_1_3__3_y), ._3_A(and_2_1_3__2_y), ._4_B(Data_in[11]), ._4_A(and_2_1_3__3_y));  // open: _4_Y

  // Notes on the sheet:
  //   Data_in: pin 10
  //   Data_out: pin 9
  //   Width
  //   38 holes
  //   9.5 cm
  //   Height
  //   42 holes
  //   10.5 cm
endmodule

/* Test case:
	     Data_in Data_out
loop(a, 1024)
	(a) (a+1)
end loop
*/
