// Digital circuit ProgramMemory.dig as structural Verilog
module ProgramMemory (
  input  [11:0] Address,
  input  D_CLK_CIRFirst,
  input  D_CLK_CIRSecond,
  output [3:0] Nibble_2,
  output [7:0] LSB,
  output [2:0] Counter,
  output [2:0] IsOpcodeNibble
);

  wire eeprom_1_d_0, eeprom_1_d_1, eeprom_1_d_2, eeprom_1_d_3, eeprom_1_d_4, eeprom_1_d_5, eeprom_1_d_6,
       eeprom_1_d_7;

  EEPROM eeprom_1 (
    .NC(1'b0), .A_0(Address[0]), .A_1(Address[1]), .A_2(Address[2]), .A_3(Address[3]), .A_4(Address[4]),
    .A_5(Address[5]), .A_6(Address[6]), .A_7(Address[7]), .A_8(Address[8]), .A_9(Address[9]),
    .A_10(Address[10]), .A_11(Address[11]), .nOE(1'b0), .GND(1'b0), .VCC(1'b1), .nWE(1'b1), .A_12(1'b0),
    .CS_2(1'b1), .nCS_1(1'b0), .D_0(eeprom_1_d_0), .D_1(eeprom_1_d_1), .D_2(eeprom_1_d_2),
    .D_3(eeprom_1_d_3), .D_4(eeprom_1_d_4), .D_5(eeprom_1_d_5), .D_6(eeprom_1_d_6), .D_7(eeprom_1_d_7));
  // D_Flip_Flop d_flip_flop_1: pin names not known; wires that end beside it: 1'b0, Nibble_2[0], eeprom_1_d_0, eeprom_1_d_1, Nibble_2[1], Nibble_2[2], eeprom_1_d_2, eeprom_1_d_3, Nibble_2[3], 1'b0, 1'b1, IsOpcodeNibble, eeprom_1_d_7, eeprom_1_d_6, Counter[2], Counter[1], eeprom_1_d_5, eeprom_1_d_4, Counter[0], D_CLK_CIRFirst
  D_Flip_Flop d_flip_flop_2 (
    .EN(1'b0), ._1_Q(LSB[0]), .VCC(1'b1), .GND(1'b0), ._1_D(eeprom_1_d_0), ._2_D(eeprom_1_d_1),
    ._3_Q(LSB[2]), .CLK(D_CLK_CIRSecond), ._2_Q(LSB[1]), ._3_D(eeprom_1_d_2), ._4_D(eeprom_1_d_3),
    ._4_Q(LSB[3]), ._5_Q(LSB[4]), ._5_D(eeprom_1_d_4), ._6_D(eeprom_1_d_5), ._7_Q(LSB[6]), ._6_Q(LSB[5]),
    ._7_D(eeprom_1_d_6), ._8_D(eeprom_1_d_7), ._8_Q(LSB[7]));

  // Notes on the sheet:
  //   Address: pin 5
  //   Nibble_2: pin 9
  //   LSB: pin 12
  //   D_CLK_CIRFirst: pin 16
  //   D_CLK_CIRSecond: pin 14
  //   Counter: pin 10
  //   IsOpcodeNibble: pin 11
  //   Width
  //   28 holes
  //   7 cm
  //   Height
  //   44 holes
  //   11 cm
endmodule

/* Test case:
Address	D-CLK-CIRFirst D-CLK-CIRSecond Out_MSB Out_LSB

memory ProgramMemory(50)=20;
memory ProgramMemory(51)=62;

memory ProgramMemory(1204)=13;
memory ProgramMemory(1205)=136;

50   0 0 X   X
50   1 0 20  X

51   0 0 20  X
51   0 1 20  62

1204 0 0 X   X
1204 1 0 13  X

1205 0 0 13  X
1205 0 1 13  136
*/
