// Digital circuit RegisterBuffer.dig as structural Verilog
module RegisterBuffer (
  input  [7:0] Data_in,
  input  Clk_R2_write,
  input  Clk_R1_write,
  output [7:0] R2_out,
  output [7:0] R1_out
);

  D_Flip_Flop d_flip_flop_1 (
    .EN(1'b0), ._1_Q(R2_out[0]), .VCC(1'b1), .GND(1'b0), ._1_D(Data_in[0]), ._2_D(Data_in[1]),
    ._3_Q(R2_out[2]), .CLK(Clk_R2_write), ._2_Q(R2_out[1]), ._3_D(Data_in[2]), ._4_D(Data_in[3]),
    ._4_Q(R2_out[3]), ._5_Q(R2_out[4]), ._5_D(Data_in[4]), ._6_D(Data_in[5]), ._7_Q(R2_out[6]),
    ._6_Q(R2_out[5]), ._7_D(Data_in[6]), ._8_D(Data_in[7]), ._8_Q(R2_out[7]));
  D_Flip_Flop d_flip_flop_2 (
    .EN(1'b0), ._1_Q(R1_out[0]), .VCC(1'b1), .GND(1'b0), ._1_D(Data_in[0]), ._2_D(Data_in[1]),
    ._3_Q(R1_out[2]), .CLK(Clk_R1_write), ._2_Q(R1_out[1]), ._3_D(Data_in[2]), ._4_D(Data_in[3]),
    ._4_Q(R1_out[3]), ._5_Q(R1_out[4]), ._5_D(Data_in[4]), ._6_D(Data_in[5]), ._7_Q(R1_out[6]),
    ._6_Q(R1_out[5]), ._7_D(Data_in[6]), ._8_D(Data_in[7]), ._8_Q(R1_out[7]));

  // Notes on the sheet:
  //   Data_in: pin 1
  //   Clk_R2_write: pin 3
  //   Clk_R1_write: pin 5
  //   R2_out: pin 8
  //   R1_out: pin 6
  //   Width
  //   16 holes
  //   4 cm
  //   Height
  //   32 holes
  //   8 cm
endmodule
