// Digital circuit SCU.dig as structural Verilog
module SCU (
  input  [3:0] Nibble_2,
  input  IsOpcodeNibble,
  input  [7:0] Counter,
  input  [7:0] Clock,
  input  F_Carry,
  input  F_Greater,
  input  F_Less,
  input  F_Equal,
  input  F_NotEqual,
  output S_CTL_Halt,
  output S_ADR_Direct,
  output S_ADR_Immediate,
  output nS_ALU_CarryOut,
  output nS_ALU_OrOut,
  output S_ALU_Propagate,
  output nS_ALU_ResultOut,
  output S_ALU_Invert,
  output nS_REG_WriteALU,
  output D_ALU_Increment,
  output D_RPC_Registers,
  output D_RPC_MemAdder,
  output D_WRT_CIRFirst,
  output D_WRT_CIRSecond,
  output D_WRT_RPC,
  output D_WRT_Flags,
  output D_WRT_BufferSecond,
  output D_WRT_BufferFirst,
  output D_SEL_Second,
  output D_SEL_First,
  output nD_WRT_SRAM,
  output D_WRT_MDR,
  output D_WRT_RegOutput,
  output nS_REG_WriteMDR,
  output nS_REG_WriteVAL,
  output S_INS_ValRead,
  output nS_INS_ValRead,
  output nD_RPC_Registers,
  output nD_RPC_MemAdder,
  output nS_ADR_Direct,
  output nS_ADR_Immediate,
  output nS_MDR_WriteMEM,
  output nS_MDR_WriteALU
);

  wire and_2_1_1__1_y, and_2_1_1__3_y, and_2_1_1__4_y, and_2_1_2__1_y, and_2_1_2__2_y, and_2_1_2__3_y,
       and_2_1_2__4_y, and_2_1_3__1_y, and_2_1_3__2_y, and_2_1_3__3_y, and_2_1_3__4_y, and_2_1_4__1_y,
       and_2_1_4__2_y, and_2_1_4__3_y, and_2_1_4__4_y, and_2_1_5__1_y, and_2_1_5__2_y, and_2_1_5__3_y,
       and_2_1_5__4_y, and_2_1_6__1_y, and_2_1_6__2_y, and_2_1_6__4_y, and_2_1_7__2_y, and_2_1_7__3_y,
       and_2_1_7__4_y, and_2_1_8__1_y, and_2_1_8__2_y, and_2_1_8__3_y, and_2_1_8__4_y, and_2_1_9__1_y,
       and_2_1_9__2_y, and_2_1_10__1_y, and_2_1_10__2_y, and_2_1_10__3_y, and_2_1_10__4_y, and_2_1_11__1_y,
       and_2_1_11__2_y, and_2_1_12__2_y, and_2_1_12__4_y, and_2_1_13__2_y, and_2_1_13__4_y, not_1_1_1__1_y,
       not_1_1_1__2_y, not_1_1_1__3_y, not_1_1_1__5_y, not_1_1_1__6_y, or_2_1_1__1_y, or_2_1_1__2_y,
       or_2_1_1__3_y, or_2_1_1__4_y, or_2_1_2__1_y, or_2_1_2__2_y, or_2_1_2__3_y, or_2_1_2__4_y,
       or_2_1_3__1_y, or_2_1_3__2_y, or_2_1_3__3_y, or_2_1_3__4_y, or_2_1_4__1_y, or_2_1_4__2_y,
       or_2_1_4__3_y, or_2_1_4__4_y, or_2_1_5__1_y, or_2_1_5__3_y, or_2_1_5__4_y, or_2_1_6__1_y,
       or_2_1_6__2_y, or_2_1_6__3_y, or_2_1_6__4_y, or_2_1_7__1_y, or_2_1_7__2_y, or_2_1_7__4_y,
       or_2_1_8__1_y, or_2_1_8__2_y, or_2_1_8__3_y, or_2_1_8__4_y, or_2_1_9__1_y, or_2_1_9__2_y,
       or_2_1_9__3_y, or_2_1_10__2_y, or_2_1_10__4_y, or_2_1_11__1_y, or_2_1_11__2_y, or_2_1_12__3_y,
       or_2_1_12__4_y, or_2_1_13__1_y, or_2_1_13__2_y, or_2_1_13__3_y, or_2_1_13__4_y;

  Decoder #(.Selector_Bits(3)) decoder_1 (.sel(3'b000));  // open: out_0, out_1, out_2, out_3, out_4, out_5, out_6, out_7
  AND_2_1 and_2_1_1 (
    ._1_A(not_1_1_1__5_y), ._1_Y(and_2_1_1__1_y), .VCC(1'b1), .GND(1'b0), ._1_B(Nibble_2[0]),
    ._2_A(not_1_1_1__5_y), ._2_Y(S_ADR_Direct), ._2_B(Nibble_2[1]), ._3_B(not_1_1_1__5_y),
    ._3_Y(and_2_1_1__3_y), ._3_A(Nibble_2[2]), ._4_B(not_1_1_1__5_y), ._4_Y(and_2_1_1__4_y),
    ._4_A(Nibble_2[3]));
  OR_2_1 or_2_1_1 (
    ._1_A(Counter[1]), ._1_Y(or_2_1_1__1_y), .VCC(1'b1), .GND(1'b0), ._1_B(Counter[3]), ._2_A(Counter[2]),
    ._2_Y(or_2_1_1__2_y), ._2_B(Counter[3]), ._3_B(Counter[6]), ._3_Y(or_2_1_1__3_y), ._3_A(or_2_1_1__2_y),
    ._4_B(or_2_1_1__3_y), ._4_Y(or_2_1_1__4_y), ._4_A(Counter[4]));
  OR_2_1 or_2_1_2 (
    ._1_A(Counter[4]), ._1_Y(or_2_1_2__1_y), .VCC(1'b1), .GND(1'b0), ._1_B(Counter[5]), ._2_A(Counter[0]),
    ._2_Y(or_2_1_2__2_y), ._2_B(Counter[3]), ._3_B(Counter[1]), ._3_Y(or_2_1_2__3_y), ._3_A(Counter[2]),
    ._4_B(or_2_1_1__3_y), ._4_Y(or_2_1_2__4_y), ._4_A(Counter[5]));
  NOT_1_1 not_1_1_1 (
    ._1_A(Counter[6]), ._1_Y(not_1_1_1__1_y), ._2_A(or_2_1_2__1_y), ._2_Y(not_1_1_1__2_y), ._3_A(Counter[7]),
    ._3_Y(not_1_1_1__3_y), ._4_A(1'b0), .VCC(1'b1), .GND(1'b0), ._5_A(IsOpcodeNibble), ._5_Y(not_1_1_1__5_y),
    ._6_A(and_2_1_2__1_y), ._6_Y(not_1_1_1__6_y));  // open: _4_Y
  OR_2_1 or_2_1_3 (
    ._1_A(or_2_1_2__3_y), ._1_Y(or_2_1_3__1_y), .VCC(1'b1), .GND(1'b0), ._1_B(Counter[0]), ._2_A(Counter[2]),
    ._2_Y(or_2_1_3__2_y), ._2_B(Counter[3]), ._3_B(Counter[6]), ._3_Y(or_2_1_3__3_y), ._3_A(Counter[5]),
    ._4_B(Counter[2]), ._4_Y(or_2_1_3__4_y), ._4_A(Counter[5]));
  OR_2_1 or_2_1_4 (
    ._1_A(Counter[3]), ._1_Y(or_2_1_4__1_y), .VCC(1'b1), .GND(1'b0), ._1_B(Counter[4]), ._2_A(Counter[5]),
    ._2_Y(or_2_1_4__2_y), ._2_B(Counter[6]), ._3_B(S_ADR_Direct), ._3_Y(or_2_1_4__3_y),
    ._3_A(IsOpcodeNibble), ._4_B(or_2_1_4__1_y), ._4_Y(or_2_1_4__4_y), ._4_A(or_2_1_4__2_y));
  AND_2_1 and_2_1_2 (
    ._1_A(or_2_1_1__1_y), ._1_Y(and_2_1_2__1_y), .VCC(1'b1), .GND(1'b0), ._1_B(and_2_1_1__4_y),
    ._2_A(or_2_1_1__4_y), ._2_Y(and_2_1_2__2_y), ._2_B(and_2_1_1__4_y), ._3_B(and_2_1_1__4_y),
    ._3_Y(and_2_1_2__3_y), ._3_A(or_2_1_2__4_y), ._4_B(and_2_1_1__4_y), ._4_Y(and_2_1_2__4_y),
    ._4_A(not_1_1_1__1_y));
  AND_2_1 and_2_1_3 (
    ._1_A(and_2_1_1__4_y), ._1_Y(and_2_1_3__1_y), .VCC(1'b1), .GND(1'b0), ._1_B(not_1_1_1__2_y),
    ._2_A(Counter[3]), ._2_Y(and_2_1_3__2_y), ._2_B(and_2_1_1__3_y), ._3_B(and_2_1_1__3_y),
    ._3_Y(and_2_1_3__3_y), ._3_A(or_2_1_2__2_y), ._4_B(and_2_1_1__3_y), ._4_Y(and_2_1_3__4_y),
    ._4_A(Counter[1]));
  AND_2_1 and_2_1_4 (
    ._1_A(and_2_1_1__3_y), ._1_Y(and_2_1_4__1_y), .VCC(1'b1), .GND(1'b0), ._1_B(Counter[2]),
    ._2_A(S_ADR_Direct), ._2_Y(and_2_1_4__2_y), ._2_B(Counter[0]), ._3_B(S_ADR_Direct),
    ._3_Y(and_2_1_4__3_y), ._3_A(Counter[1]), ._4_B(and_2_1_1__1_y), ._4_Y(and_2_1_4__4_y), ._4_A(Counter[5]));
  AND_2_1 and_2_1_5 (
    ._1_A(or_2_1_3__1_y), ._1_Y(and_2_1_5__1_y), .VCC(1'b1), .GND(1'b0), ._1_B(and_2_1_1__3_y),
    ._2_A(and_2_1_1__1_y), ._2_Y(and_2_1_5__2_y), ._2_B(or_2_1_3__3_y), ._3_B(and_2_1_1__1_y),
    ._3_Y(and_2_1_5__3_y), ._3_A(or_2_1_3__4_y), ._4_B(and_2_1_1__1_y), ._4_Y(and_2_1_5__4_y),
    ._4_A(Counter[2]));
  AND_2_1 and_2_1_6 (
    ._1_A(or_2_1_3__2_y), ._1_Y(and_2_1_6__1_y), .VCC(1'b1), .GND(1'b0), ._1_B(and_2_1_1__1_y),
    ._2_A(and_2_1_1__1_y), ._2_Y(and_2_1_6__2_y), ._2_B(Counter[4]), ._3_B(and_2_1_1__1_y),
    ._3_Y(S_CTL_Halt), ._3_A(Counter[1]), ._4_B(or_2_1_4__4_y), ._4_Y(and_2_1_6__4_y), ._4_A(and_2_1_1__1_y));
  AND_2_1 and_2_1_7 (
    ._1_A(not_1_1_1__3_y), ._1_Y(S_ADR_Immediate), .VCC(1'b1), .GND(1'b0), ._1_B(IsOpcodeNibble),
    ._2_A(and_2_1_1__1_y), ._2_Y(and_2_1_7__2_y), ._2_B(Counter[3]), ._3_B(Counter[0]),
    ._3_Y(and_2_1_7__3_y), ._3_A(IsOpcodeNibble), ._4_B(IsOpcodeNibble), ._4_Y(and_2_1_7__4_y),
    ._4_A(Counter[7]));
  AND_2_1 and_2_1_8 (
    ._1_A(Counter[2]), ._1_Y(and_2_1_8__1_y), .VCC(1'b1), .GND(1'b0), ._1_B(or_2_1_4__3_y),
    ._2_A(IsOpcodeNibble), ._2_Y(and_2_1_8__2_y), ._2_B(Counter[1]), ._3_B(or_2_1_4__3_y),
    ._3_Y(and_2_1_8__3_y), ._3_A(Counter[4]), ._4_B(or_2_1_4__3_y), ._4_Y(and_2_1_8__4_y), ._4_A(Counter[5]));
  AND_2_1 and_2_1_9 (
    ._1_A(Counter[3]), ._1_Y(and_2_1_9__1_y), .VCC(1'b1), .GND(1'b0), ._1_B(or_2_1_4__3_y),
    ._2_A(or_2_1_4__3_y), ._2_Y(and_2_1_9__2_y), ._2_B(Counter[6]), ._3_B(1'b0), ._3_A(1'b0), ._4_B(1'b0),
    ._4_A(1'b0));  // open: _3_Y, _4_Y
  LED ALU_Increment (.in(and_2_1_2__2_y));
  LED ALU_UseCarry (.in(and_2_1_2__1_y));
  LED nS_ALU_UseCarry (.in(not_1_1_1__6_y));
  LED ALU_Invert (.in(and_2_1_2__3_y));
  LED REG_WriteALU (.in(and_2_1_1__4_y));
  LED INS_RegReadFirst (.in(and_2_1_1__3_y));
  LED REG_WriteALU_2 (.in(and_2_1_1__3_y));
  LED ALU_FlagWrite (.in(and_2_1_1__3_y));
  LED INS_RegReadSecond (.in(S_ADR_Direct));
  LED MDR_WriteALU (.in(and_2_1_7__2_y));
  LED MEM_Store (.in(and_2_1_8__2_y));
  LED BRA_Unconditional (.in(and_2_1_8__1_y));
  LED ALU_Propagate (.in(and_2_1_1__4_y));
  LED ALU_ResultOut (.in(and_2_1_1__4_y));
  LED ALU_FlagWrite_2 (.in(and_2_1_1__4_y));
  LED INS_RegReadSecond_2 (.in(and_2_1_2__4_y));
  LED ALU_Invert_2 (.in(and_2_1_3__2_y));
  LED INS_RegReadFirst_2 (.in(and_2_1_3__1_y));
  LED ALU_CarryOut (.in(and_2_1_3__4_y));
  LED ALU_ResultOut_2 (.in(and_2_1_3__3_y));
  LED INS_RegReadFirst_3 (.in(S_ADR_Direct));
  LED ADR_Direct (.in(S_ADR_Direct));
  LED MDR_WriteMem (.in(and_2_1_4__2_y));
  LED ALU_OrOut (.in(and_2_1_4__1_y));
  LED ALU_Increment_2 (.in(and_2_1_4__4_y));
  LED ALU_Invert_3 (.in(and_2_1_4__4_y));
  LED ALU_Propagate_2 (.in(and_2_1_4__4_y));
  LED MEM_Store_2 (.in(and_2_1_4__3_y));
  LED INS_RegReadSecond_3 (.in(and_2_1_5__1_y));
  LED ALU_FlagWrite_3 (.in(and_2_1_5__2_y));
  LED INS_RegReadFirst_4 (.in(and_2_1_5__3_y));
  LED REG_WriteALU_3 (.in(and_2_1_5__4_y));
  LED ALU_ResultOut_3 (.in(and_2_1_6__1_y));
  LED REG_WriteMDR (.in(and_2_1_6__2_y));
  LED INS_RegReadSecond_4 (.in(and_2_1_6__4_y));
  LED CTL_Halt (.in(S_CTL_Halt));
  LED MDR_WriteMem_2 (.in(and_2_1_7__3_y));
  LED REG_WriteVAL (.in(and_2_1_7__4_y));
  LED ADR_Immediate (.in(S_ADR_Immediate));
  LED INS_ValRead (.in(IsOpcodeNibble));
  LED BRA_NotEqual (.in(and_2_1_9__2_y));
  LED BRA_Less (.in(and_2_1_8__3_y));
  LED BRA_Equal (.in(and_2_1_8__4_y));
  LED BRA_Greater (.in(and_2_1_9__1_y));
  OR_2_1 or_2_1_5 (
    ._1_A(and_2_1_2__2_y), ._1_Y(or_2_1_5__1_y), .VCC(1'b1), .GND(1'b0), ._1_B(and_2_1_4__4_y),
    ._2_A(and_2_1_1__4_y), ._2_Y(S_ALU_Propagate), ._2_B(and_2_1_4__4_y), ._3_B(or_2_1_5__4_y),
    ._3_Y(or_2_1_5__3_y), ._3_A(and_2_1_1__4_y), ._4_B(and_2_1_6__1_y), ._4_Y(or_2_1_5__4_y),
    ._4_A(and_2_1_3__3_y));
  OR_2_1 or_2_1_6 (
    ._1_A(and_2_1_1__4_y), ._1_Y(or_2_1_6__1_y), .VCC(1'b1), .GND(1'b0), ._1_B(and_2_1_5__2_y),
    ._2_A(or_2_1_6__1_y), ._2_Y(or_2_1_6__2_y), ._2_B(and_2_1_1__3_y), ._3_B(or_2_1_6__4_y),
    ._3_Y(or_2_1_6__3_y), ._3_A(and_2_1_2__4_y), ._4_B(S_ADR_Direct), ._4_Y(or_2_1_6__4_y),
    ._4_A(and_2_1_5__1_y));
  OR_2_1 or_2_1_7 (
    ._1_A(or_2_1_6__3_y), ._1_Y(or_2_1_7__1_y), .VCC(1'b1), .GND(1'b0), ._1_B(and_2_1_6__4_y),
    ._2_A(and_2_1_2__3_y), ._2_Y(or_2_1_7__2_y), ._2_B(and_2_1_3__2_y), ._3_B(and_2_1_4__4_y),
    ._3_Y(S_ALU_Invert), ._3_A(or_2_1_7__2_y), ._4_B(and_2_1_1__3_y), ._4_Y(or_2_1_7__4_y),
    ._4_A(and_2_1_3__1_y));
  OR_2_1 or_2_1_8 (
    ._1_A(S_ADR_Direct), ._1_Y(or_2_1_8__1_y), .VCC(1'b1), .GND(1'b0), ._1_B(or_2_1_7__4_y),
    ._2_A(or_2_1_8__1_y), ._2_Y(or_2_1_8__2_y), ._2_B(and_2_1_5__3_y), ._3_B(or_2_1_8__4_y),
    ._3_Y(or_2_1_8__3_y), ._3_A(and_2_1_1__3_y), ._4_B(and_2_1_5__4_y), ._4_Y(or_2_1_8__4_y),
    ._4_A(and_2_1_1__4_y));
  OR_2_1 or_2_1_9 (
    ._1_A(and_2_1_4__2_y), ._1_Y(or_2_1_9__1_y), .VCC(1'b1), .GND(1'b0), ._1_B(and_2_1_7__3_y),
    ._2_A(and_2_1_4__3_y), ._2_Y(or_2_1_9__2_y), ._2_B(and_2_1_8__2_y), ._3_B(or_2_1_9__1_y),
    ._3_Y(or_2_1_9__3_y), ._3_A(and_2_1_7__2_y), ._4_B(1'b0), ._4_A(1'b0));  // open: _4_Y
  AND_2_1 and_2_1_10 (
    ._1_A(and_2_1_9__1_y), ._1_Y(and_2_1_10__1_y), .VCC(1'b1), .GND(1'b0), ._1_B(F_Greater), ._2_A(F_Less),
    ._2_Y(and_2_1_10__2_y), ._2_B(and_2_1_8__3_y), ._3_B(F_Equal), ._3_Y(and_2_1_10__3_y),
    ._3_A(and_2_1_8__4_y), ._4_B(F_NotEqual), ._4_Y(and_2_1_10__4_y), ._4_A(and_2_1_9__2_y));
  AND_2_1 and_2_1_11 (
    ._1_A(not_1_1_1__6_y), ._1_Y(and_2_1_11__1_y), .VCC(1'b1), .GND(1'b0), ._1_B(or_2_1_5__1_y),
    ._2_A(and_2_1_2__1_y), ._2_Y(and_2_1_11__2_y), ._2_B(F_Carry), ._3_B(1'b0), ._3_A(1'b0), ._4_B(1'b0),
    ._4_A(1'b0));  // open: _3_Y, _4_Y
  OR_2_1 or_2_1_10 (
    ._1_A(and_2_1_11__2_y), ._1_Y(D_ALU_Increment), .VCC(1'b1), .GND(1'b0), ._1_B(and_2_1_11__1_y),
    ._2_A(Clock[6]), ._2_Y(or_2_1_10__2_y), ._2_B(Clock[5]), ._3_B(or_2_1_10__4_y), ._3_Y(D_WRT_RPC),
    ._3_A(and_2_1_12__2_y), ._4_B(Clock[0]), ._4_Y(or_2_1_10__4_y), ._4_A(Clock[2]));
  OR_2_1 or_2_1_11 (
    ._1_A(or_2_1_8__3_y), ._1_Y(or_2_1_11__1_y), .VCC(1'b1), .GND(1'b0), ._1_B(and_2_1_6__2_y),
    ._2_A(or_2_1_11__1_y), ._2_Y(or_2_1_11__2_y), ._2_B(and_2_1_7__4_y), ._3_B(Clock[1]),
    ._3_Y(D_WRT_BufferFirst), ._3_A(and_2_1_13__2_y), ._4_B(and_2_1_12__4_y), ._4_Y(D_WRT_BufferSecond),
    ._4_A(Clock[1]));
  OR_2_1 or_2_1_12 (
    ._1_A(Clock[2]), ._1_Y(D_SEL_First), .VCC(1'b1), .GND(1'b0), ._1_B(Clock[3]), ._2_A(or_2_1_12__4_y),
    ._2_Y(D_SEL_Second), ._2_B(or_2_1_12__3_y), ._3_B(Clock[5]), ._3_Y(or_2_1_12__3_y), ._3_A(Clock[4]),
    ._4_B(Clock[7]), ._4_Y(or_2_1_12__4_y), ._4_A(Clock[6]));
  OR_2_1 or_2_1_13 (
    ._1_A(and_2_1_10__2_y), ._1_Y(or_2_1_13__1_y), .VCC(1'b1), .GND(1'b0), ._1_B(and_2_1_10__1_y),
    ._2_A(or_2_1_13__1_y), ._2_Y(or_2_1_13__2_y), ._2_B(and_2_1_10__4_y), ._3_B(or_2_1_13__4_y),
    ._3_Y(or_2_1_13__3_y), ._3_A(and_2_1_10__3_y), ._4_B(or_2_1_13__2_y), ._4_Y(or_2_1_13__4_y),
    ._4_A(and_2_1_8__1_y));
  AND_2_1 and_2_1_12 (
    ._1_A(or_2_1_10__2_y), ._1_Y(D_RPC_Registers), .VCC(1'b1), .GND(1'b0), ._1_B(or_2_1_13__3_y),
    ._2_A(Clock[6]), ._2_Y(and_2_1_12__2_y), ._2_B(or_2_1_13__3_y), ._3_B(or_2_1_11__2_y),
    ._3_Y(D_WRT_RegOutput), ._3_A(Clock[7]), ._4_B(Clock[5]), ._4_Y(and_2_1_12__4_y), ._4_A(or_2_1_7__1_y));
  AND_2_1 and_2_1_13 (
    ._1_A(or_2_1_6__2_y), ._1_Y(D_WRT_Flags), .VCC(1'b1), .GND(1'b0), ._1_B(Clock[7]), ._2_A(Clock[3]),
    ._2_Y(and_2_1_13__2_y), ._2_B(or_2_1_8__2_y), ._3_B(Clock[7]), ._3_Y(D_WRT_MDR), ._3_A(or_2_1_9__3_y),
    ._4_B(Clock[7]), ._4_Y(and_2_1_13__4_y), ._4_A(or_2_1_9__2_y));
  LED Branch_Happening (.in(or_2_1_13__3_y));
  NOT_1_1 not_1_1_2 (
    ._1_A(D_RPC_Registers), ._1_Y(D_RPC_MemAdder), ._2_A(IsOpcodeNibble), ._2_Y(nS_INS_ValRead),
    ._3_A(S_ADR_Direct), ._3_Y(nS_ADR_Direct), ._4_A(or_2_1_5__3_y), ._4_Y(nS_ALU_ResultOut), .VCC(1'b1),
    .GND(1'b0), ._5_A(or_2_1_9__1_y), ._5_Y(nS_MDR_WriteMEM), ._6_A(S_ADR_Immediate), ._6_Y(nS_ADR_Immediate));
  NOT_1_1 not_1_1_3 (
    ._1_A(and_2_1_7__2_y), ._1_Y(nS_MDR_WriteALU), ._2_A(and_2_1_13__4_y), ._2_Y(nD_WRT_SRAM),
    ._3_A(and_2_1_4__1_y), ._3_Y(nS_ALU_OrOut), ._4_A(1'b0), .VCC(1'b1), .GND(1'b0), ._5_A(1'b0),
    ._6_A(and_2_1_3__4_y), ._6_Y(nS_ALU_CarryOut));  // open: _4_Y, _5_Y
  NOT_1_1 not_1_1_4 (
    ._1_A(and_2_1_7__4_y), ._1_Y(nS_REG_WriteVAL), ._2_A(and_2_1_6__2_y), ._2_Y(nS_REG_WriteMDR),
    ._3_A(or_2_1_8__3_y), ._3_Y(nS_REG_WriteALU), ._4_A(1'b0), .VCC(1'b1), .GND(1'b0), ._5_A(1'b0),
    ._6_A(1'b0));  // open: _4_Y, _5_Y, _6_Y

  assign D_WRT_CIRFirst = Clock[0];
  assign D_WRT_CIRSecond = Clock[1];
  assign nD_RPC_MemAdder = D_RPC_Registers;
  assign nD_RPC_Registers = D_RPC_MemAdder;
  assign S_INS_ValRead = IsOpcodeNibble;

  // Notes on the sheet:
  //   Nibble_2: pin 2
  //   IsOpcodeNibble: pin 70
  //   Counter: pin 1
  //   S_CTL_Halt: pin 59
  //   S_ADR_Direct: pin 58
  //   S_ADR_Immediate: pin 57
  //   nS_ALU_CarryOut: pin 52
  //   nS_ALU_OrOut: pin 56
  //   S_ALU_Propagate: pin 54
  //   nS_ALU_ResultOut: pin 55
  //   S_ALU_Invert: pin 53
  //   nS_REG_WriteALU: pin 46
  //   Clock: pin 69
  //   D_ALU_Increment: pin 62
  //   D_RPC_Registers: pin 36
  //   D_RPC_MemAdder: pin 63
  //   D_WRT_CIRFirst: pin 37
  //   D_WRT_CIRSecond: pin 38
  //   D_WRT_RPC: pin 39
  //   D_WRT_Flags: pin 40
  //   D_WRT_BufferSecond: pin 41
  //   D_WRT_BufferFirst: pin 42
  //   D_SEL_Second: pin 68
  //   D_SEL_First: pin 67
  //   nD_WRT_SRAM: pin 44
  //   D_WRT_MDR: pin 45
  //   D_WRT_RegOutput: pin 43
  //   nS_REG_WriteMDR: pin 47
  //   nS_REG_WriteVAL: pin 48
  //   S_INS_ValRead: pin 60
  //   nS_INS_ValRead: pin 61
  //   nD_RPC_Registers: pin 35
  //   nD_RPC_MemAdder: pin 34
  //   nS_ADR_Direct: pin 62
  //   nS_ADR_Immediate: pin 63
  //   nS_MDR_WriteMEM: pin 51
  //   nS_MDR_WriteALU: pin 50
  //   Testing
  //   SecondByte
  //   FirstByte
  //   Width
  //   144 holes
  //   36 cm
  //   Height
  //   112 holes
  //   28 cm
endmodule

/* Test case S-ALU:
FirstByte S-ALU-Invert S-ALU-Propagate S-ALU-ResultOut S-ALU-CarryOut S-ALU-OrOut

8         0          1             1             0            0
24        0          1             1             0            0
40        1          1             1             0            0
56        1          1             1             0            0
72        0          1             1             0            0
88        1          1             1             0            0
104       1          1             1             0            0

4         0          0             1             0            0
20        0          0             0             1            0
36        0          0             0             0            1
52        1          0             1             0            0

2         0          0             0             0            0
18        0          0             0             0            0
34        0          0             0             0            0
50        0          0             0             0            0
66        0          0             0             0            0
82        0          0             0             0            0
98        0          0             0             0            0

1         0          0             0             0            0
17        0          0             0             0            0
33        0          0             1             0            0
49        0          0             1             0            0
65        0          0             0             0            0
81        1          1             0             0            0
97        0          0             0             0            0
*/

/* Test case S-ADR:
FirstByte S-ADR-Immediate S-ADR-Direct

8         0             0
24        0             0
40        0             0
56        0             0
72        0             0
88        0             0
104       0             0

4         0             0
20        0             0
36        0             0
52        0             0

2         0             1
18        0             1
34        0             1
50        0             1
66        0             1
82        0             1
98        0             1

1         0             0
17        0             0
33        0             0
49        0             0
65        0             0
81        0             0
97        0             0

128       1             0
144       1             0
160       1             0
176       1             0
192       1             0
208       1             0
224       1             0
240       0             0
*/

/* Test case S-REG:
FirstByte S-REG-WriteALU S-REG-WriteMDR S-REG-WriteVAL

8         1                0		0
24        1                0		0
40        1                0		0
56        1                0		0
72        1                0		0
88        1                0		0
104       1                0		0
              
4         1                0		0
20        1                0		0
36        1                0		0
52        1                0		0
              
2         0                0		0
18        0                0		0
34        0                0		0
50        0                0		0
66        0                0		0
82        0                0		0
98        0                0		0
              
1         0                0		0
17        0                0		0
33        1                0		0
49        0                0		0
65        0                1		0
81        0                0		0
97        0                0		0
              
128       0                0		0
144       0                0		0
160       0                0		0
176       0                0		0
192       0                0		0
208       0                0		0
224       0                0		0
240       0                0		1
*/

/* Test case S-MEM:
FirstByte S-MEM-Store

8         0
24        0
40        0
56        0
72        0
88        0
104       0
              
4         0
20        0
36        0
52        0
              
2         0
18        1
34        0
50        0
66        0
82        0
98        0
              
1         0
17        0
33        0
49        0
65        0
81        0
97        0
              
128       0
144       1
160       0
176       0
192       0
208       0
224       0
240       0
*/

/* Test case S-MDR:
FirstByte S-MDR-WriteALU S-MDR-WriteMEM

8         0            0
24        0            0
40        0            0
56        0            0
72        0            0
88        0            0
104       0            0
              
4         0            0
20        0            0
36        0            0
52        0            0
              
2         0            1
18        0            0
34        0            0
50        0            0
66        0            0
82        0            0
98        0            0
              
1         0            0
17        0            0
33        0            0
49        1            0
65        0            0
81        0            0
97        0            0
              
128       0            1
144       0            0
160       0            0
176       0            0
192       0            0
208       0            0
224       0            0
240       0            0
*/

/* Test case S-CTL:
FirstByte S-CTL-Halt

8         0
24        0
40        0
56        0
72        0
88        0
104       0
              
4         0
20        0
36        0
52        0
              
2         0
18        0
34        0
50        0
66        0
82        0
98        0
              
1         0
17        1
33        0
49        0
65        0
81        0
97        0
              
128       0
144       0
160       0
176       0
192       0
208       0
224       0
240       0
*/
