// Digital circuit SignalIntegrator.dig as structural Verilog
module SignalIntegrator (
  input  S_ALU_Increment,
  input  S_ALU_UseCarry,
  input  Clock_1,
  input  Clock_2,
  input  S_BRA_Unconditional,
  input  Clock_5,
  input  Clock_3,
  input  Clock_4,
  input  S_ALU_FlagWrite,
  input  S_BRA_Greater,
  input  F_Greater,
  input  S_BRA_Less,
  input  F_Less,
  input  S_BRA_Equal,
  input  F_Equal,
  input  S_BRA_NotEqual,
  input  F_NotEqual,
  input  S_INS_RegReadFirst,
  input  S_INS_RegReadSecond,
  input  S_REG_WriteALU,
  input  S_REG_WriteMDR,
  input  S_MEM_Store,
  input  S_MDR_WriteALU,
  input  S_MDR_WriteMem,
  input  F_Carry,
  input  S_REG_WriteVAL,
  input  Clock_6,
  input  Clock_7,
  input  Clock_8,
  output D_ALU_Increment,
  output D_RPC_MemAdder,
  output D_RPC_Registers,
  output D_CLK_CIRFirst,
  output D_CLK_CIRSecond,
  output D_CLK_RPC,
  output D_CLK_Flags,
  output D_CLK_SelectFirst,
  output D_CLK_SelectSecond,
  output D_CLK_RegOutput,
  output D_CLK_SRAM,
  output D_CLK_MDR
);

  wire and_1_out, and_2_out, and_3_out, and_4_out, and_5_out, or_1_out, or_2_out, or_3_out, or_4_out,
       or_5_out, or_6_out, or_8_out, or_9_out, or_10_out, or_11_out;

  and and_1 (and_1_out, S_ALU_UseCarry, F_Carry);
  and and_2 (and_2_out, S_BRA_Greater, F_Greater);
  and and_3 (and_3_out, S_BRA_Less, F_Less);
  and and_4 (and_4_out, S_BRA_Equal, F_Equal);
  and and_5 (and_5_out, S_BRA_NotEqual, F_NotEqual);
  xor xor_1 (D_ALU_Increment, S_ALU_Increment, and_1_out);
  or or_1 (or_1_out, and_2_out, and_3_out);
  or or_2 (or_2_out, and_4_out, and_5_out);
  or or_3 (or_3_out, S_REG_WriteMDR, S_REG_WriteVAL);
  or or_4 (or_4_out, S_REG_WriteALU, or_3_out);
  or or_5 (or_5_out, or_1_out, or_2_out);
  or or_6 (or_6_out, S_BRA_Unconditional, or_5_out);
  or or_7 (D_CLK_RPC, Clock_1, Clock_3);
  or or_8 (or_8_out, Clock_3, Clock_4);
  or or_9 (or_9_out, Clock_5, Clock_6);
  or or_10 (or_10_out, S_INS_RegReadSecond, or_4_out);
  or or_11 (or_11_out, S_MDR_WriteALU, S_MDR_WriteMem);
  and and_6 (D_RPC_Registers, Clock_5, or_6_out);
  and and_7 (D_CLK_Flags, S_ALU_FlagWrite, Clock_5);
  and and_8 (D_CLK_SelectFirst, or_8_out, S_INS_RegReadFirst);
  and and_9 (D_CLK_SelectSecond, or_9_out, or_10_out);
  and and_10 (D_CLK_RegOutput, Clock_6, or_4_out);
  and and_11 (D_CLK_SRAM, S_MEM_Store, Clock_5);
  and and_12 (D_CLK_MDR, or_11_out, Clock_5);
  not not_1 (D_RPC_MemAdder, D_RPC_Registers);

  assign D_CLK_CIRFirst = Clock_1;
  assign D_CLK_CIRSecond = Clock_2;
endmodule
