// Digital circuit StaticControlUnit.dig as structural Verilog
module StaticControlUnit (
  input  [7:0] FirstByte,
  input  [7:0] SecondByte,
  output S_ALU_CarryOut,
  output S_ALU_Invert,
  output S_ALU_Propagate,
  output S_ALU_ResultOut,
  output S_ALU_OrOut,
  output S_ADR_Immediate,
  output S_ADR_Direct,
  output S_INS_ValReadCenter,
  output S_INS_ValReadEnd,
  output S_CTL_Halt,
  output S_MDR_WriteMEM,
  output S_MDR_WriteALU,
  output S_MEM_Store,
  output S_REG_WriteMDR,
  output S_REG_WriteALU,
  output S_INS_RegReadSecond,
  output S_INS_RegReadFirst,
  output S_ALU_FlagWrite,
  output S_BRA_NotEqual,
  output S_BRA_Equal,
  output S_BRA_Less,
  output S_BRA_Greater,
  output S_BRA_Unconditional,
  output S_ALU_UseCarry,
  output S_ALU_Increment,
  output [3:0] Nibble_2,
  output [3:0] Nibble_3,
  output [3:0] Nibble_4
);

  wire group1_combinator_1_p4, group1_combinator_1_p5, group1_combinator_1_p6, group1_combinator_1_p7,
       group1_combinator_1_p8, group1_combinator_1_p9, group1_combinator_1_p10, group1_combinator_1_p11,
       group2_combinator_1_p3, group2_combinator_1_p4, group2_combinator_1_p5, group2_combinator_1_p6,
       group2_combinator_1_p7, group2_combinator_1_p8, group3_combinator_1_p4, group3_combinator_1_p5,
       group3_combinator_1_p6, group3_combinator_1_p7, group4_combinator_1_p3, group4_combinator_1_p4,
       group4_combinator_1_p5, group4_combinator_1_p6, group4_combinator_1_p7, group4_combinator_1_p8,
       group4_combinator_1_p9, group4_combinator_1_p10, instructionsplitter_1_isopcodenibble,
       nibble_combinator_1_ins_regreadfirst, nibble_combinator_1_mdr_writemem, nibble_combinator_1_mem_store,
       not_1_out, or_3_out, or_5_out, or_6_out, or_8_out, or_9_out, or_10_out, or_12_out, or_14_out,
       or_17_out;
  wire [2:0] instructionsplitter_1_counter;
  wire [3:0] driver_1_out;
  wire [7:0] decoder_1__0;

  InstructionSplitter instructionsplitter_1 (
    .Instruction({FirstByte, SecondByte}), .Nibble4(Nibble_4), .Nibble3(Nibble_3), .Nibble2(Nibble_2),
    .Counter(instructionsplitter_1_counter), .IsOpcodeNibble(instructionsplitter_1_isopcodenibble));
  not not_1 (not_1_out, instructionsplitter_1_isopcodenibble);
  assign driver_1_out = not_1_out ? Nibble_2 : 4'bz;  // Driver driver_1
  PullDown #(.Bits(4)) pulldown_1 (.out(driver_1_out));
  Decoder decoder_1 (
    .In(instructionsplitter_1_counter), ._0(decoder_1__0[0]), ._1(decoder_1__0[1]), ._2(decoder_1__0[2]),
    ._3(decoder_1__0[3]), ._4(decoder_1__0[4]), ._5(decoder_1__0[5]), ._6(decoder_1__0[6]),
    ._7(decoder_1__0[7]));
  // Group1_Combinator group1_combinator_1: pin names not known; wires that end beside it: decoder_1__0, driver_1_out[3], S_ALU_UseCarry, group1_combinator_1_p4, group1_combinator_1_p5, group1_combinator_1_p6, group1_combinator_1_p7, group1_combinator_1_p8, group1_combinator_1_p9, group1_combinator_1_p10, group1_combinator_1_p11
  // Group2_Combinator group2_combinator_1: pin names not known; wires that end beside it: decoder_1__0, driver_1_out[2], group2_combinator_1_p3, group2_combinator_1_p4, group2_combinator_1_p5, group2_combinator_1_p6, group2_combinator_1_p7, group2_combinator_1_p8, S_ALU_CarryOut, S_ALU_OrOut
  // Group3_Combinator group3_combinator_1: pin names not known; wires that end beside it: decoder_1__0, driver_1_out[1], S_ADR_Direct, group3_combinator_1_p4, group3_combinator_1_p5, group3_combinator_1_p6, group3_combinator_1_p7
  // Group4_Combinator group4_combinator_1: pin names not known; wires that end beside it: decoder_1__0, driver_1_out[0], group4_combinator_1_p3, group4_combinator_1_p4, group4_combinator_1_p5, group4_combinator_1_p6, group4_combinator_1_p7, group4_combinator_1_p8, group4_combinator_1_p9, group4_combinator_1_p10, S_REG_WriteMDR, S_MDR_WriteALU, S_CTL_Halt
  Nibble_Combinator nibble_combinator_1 (
    .Counter(decoder_1__0), .Active(instructionsplitter_1_isopcodenibble), .ADR_Immediate(S_ADR_Immediate),
    .INS_RegReadFirst(nibble_combinator_1_ins_regreadfirst), .INS_ValReadCenter(S_INS_ValReadCenter),
    .INS_ValReadEnd(S_INS_ValReadEnd), .MEM_Store(nibble_combinator_1_mem_store),
    .MDR_WriteMem(nibble_combinator_1_mdr_writemem));
  Branch_Combinator branch_combinator_1 (
    .Counter(decoder_1__0), .Active_Group3(driver_1_out[1]),
    .Active_Nibble(instructionsplitter_1_isopcodenibble), .BRA_Less(S_BRA_Less), .BRA_Equal(S_BRA_Equal),
    .BRA_NotEqual(S_BRA_NotEqual), .BRA_Unconditional(S_BRA_Unconditional), .BRA_Greater(S_BRA_Greater));
  or or_1 (S_MDR_WriteMEM, group3_combinator_1_p7, nibble_combinator_1_mdr_writemem);
  or or_2 (S_MEM_Store, group3_combinator_1_p6, nibble_combinator_1_mem_store);
  or or_3 (or_3_out, group2_combinator_1_p8, group4_combinator_1_p10);
  or or_4 (S_REG_WriteALU, group1_combinator_1_p11, or_3_out);
  or or_5 (or_5_out, group3_combinator_1_p5, group4_combinator_1_p9);
  or or_6 (or_6_out, group2_combinator_1_p7, or_5_out);
  or or_7 (S_INS_RegReadSecond, group1_combinator_1_p10, or_6_out);
  or or_8 (or_8_out, group4_combinator_1_p8, nibble_combinator_1_ins_regreadfirst);
  or or_9 (or_9_out, group3_combinator_1_p4, or_8_out);
  or or_10 (or_10_out, group1_combinator_1_p9, or_9_out);
  or or_11 (S_INS_RegReadFirst, group2_combinator_1_p6, or_10_out);
  or or_12 (or_12_out, group2_combinator_1_p5, group4_combinator_1_p4);
  or or_13 (S_ALU_FlagWrite, group1_combinator_1_p8, or_12_out);
  or or_14 (or_14_out, group2_combinator_1_p4, group4_combinator_1_p7);
  or or_15 (S_ALU_ResultOut, group1_combinator_1_p7, or_14_out);
  or or_16 (S_ALU_Propagate, group1_combinator_1_p6, group4_combinator_1_p6);
  or or_17 (or_17_out, group2_combinator_1_p3, group4_combinator_1_p5);
  or or_18 (S_ALU_Invert, group1_combinator_1_p5, or_17_out);
  or or_19 (S_ALU_Increment, group1_combinator_1_p4, group4_combinator_1_p3);
  // Pins of 1 and 4 bits meet at Nibble_4
  // Pins of 1 and 4 bits meet at Nibble_3
  // Pins of 1 and 4 bits meet at Nibble_2
endmodule

/* Test case ALU:
FirstByte S-ALU-UseCarry S-ALU-Increment S-ALU-Invert S-ALU-Propagate S-ALU-ResultOut S-ALU-CarryOut S-ALU-OrOut S-ALU-FlagWrite

8         0            0             0          1             1             0            0         1
24        1            0             0          1             1             0            0         1
40        0            1             1          1             1             0            0         1
56        1            1             1          1             1             0            0         1
72        0            1             0          1             1             0            0         1
88        0            0             1          1             1             0            0         1
104       0            1             1          1             1             0            0         1

4         0            0             0          0             1             0            0         1
20        0            0             0          0             0             1            0         1
36        0            0             0          0             0             0            1         1
52        0            0             1          0             1             0            0         1

2         0            0             0          0             0             0            0         0
18        0            0             0          0             0             0            0         0
34        0            0             0          0             0             0            0         0
50        0            0             0          0             0             0            0         0
66        0            0             0          0             0             0            0         0
82        0            0             0          0             0             0            0         0
98        0            0             0          0             0             0            0         0

1         0            0             0          0             0             0            0         0
17        0            0             0          0             0             0            0         0
33        0            0             0          0             1             0            0         0
49        0            0             0          0             1             0            0         0
65        0            0             0          0             0             0            0         0
81        0            1             1          1             0             0            0         1
97        0            0             0          0             0             0            0         1

128       0            0             0          0             0             0            0         0
144       0            0             0          0             0             0            0         0
160       0            0             0          0             0             0            0         0
176       0            0             0          0             0             0            0         0
192       0            0             0          0             0             0            0         0
208       0            0             0          0             0             0            0         0
224       0            0             0          0             0             0            0         0
240       0            0             0          0             0             0            0         0
*/

/* Test case ADR:
FirstByte S-ADR-Immediate S-ADR-Direct

8         0             0
24        0             0
40        0             0
56        0             0
72        0             0
88        0             0
104       0             0

4         0             0
20        0             0
36        0             0
52        0             0

2         0             1
18        0             1
34        0             1
50        0             1
66        0             1
82        0             1
98        0             1

1         0             0
17        0             0
33        0             0
49        0             0
65        0             0
81        0             0
97        0             0

128       1             0
144       1             0
160       1             0
176       1             0
192       1             0
208       1             0
224       1             0
240       0             0
*/

/* Test case BRA:
FirstByte S-BRA-Unconditional S-BRA-Greater S-BRA-Less S-BRA-Equal S-BRA-NotEqual

8         0                 0           0        0         0
24        0                 0           0        0         0
40        0                 0           0        0         0
56        0                 0           0        0         0
72        0                 0           0        0         0
88        0                 0           0        0         0
104       0                 0           0        0         0

4         0                 0           0        0         0
20        0                 0           0        0         0
36        0                 0           0        0         0
52        0                 0           0        0         0

2         0                 0           0        0         0
18        0                 0           0        0         0
34        1                 0           0        0         0
50        0                 1           0        0         0
66        0                 0           1        0         0
82        0                 0           0        1         0
98        0                 0           0        0         1

1         0                 0           0        0         0
17        0                 0           0        0         0
33        0                 0           0        0         0
49        0                 0           0        0         0
65        0                 0           0        0         0
81        0                 0           0        0         0
97        0                 0           0        0         0

128       0                 0           0        0         0
144       0                 0           0        0         0
160       1                 0           0        0         0
176       0                 1           0        0         0
192       0                 0           1        0         0
208       0                 0           0        1         0
224       0                 0           0        0         1
240       0                 0           0        0         0
*/

/* Test case INS:
FirstByte S-INS-RegReadFirst S-INS-RegReadSecond S-INS-ValReadCenter S-INS-ValReadEnd

8         1                1                 0                 0
24        1                1                 0                 0
40        1                1                 0                 0
56        1                1                 0                 0
72        1                0                 0                 0
88        1                0                 0                 0
104       1                0                 0                 0
              
4         1                1                 0                 0
20        1                1                 0                 0
36        1                1                 0                 0
52        1                0                 0                 0
              
2         1                1                 0                 0
18        1                1                 0                 0
34        1                1                 0                 0
50        1                1                 0                 0
66        1                1                 0                 0
82        1                1                 0                 0
98        1                1                 0                 0
              
1         0                0                 0                 0
17        0                0                 0                 0
33        1                1                 0                 0
49        1                0                 0                 0
65        1                0                 0                 0
81        1                1                 0                 0
97        1                0                 0                 0
              
128       0                0                 1                 1
144       0                0                 1                 1
160       0                0                 1                 1
176       0                0                 1                 1
192       0                0                 1                 1
208       0                0                 1                 1
224       0                0                 1                 1
240       1                0                 1                 0
*/

/* Test case REG:
FirstByte S-REG-WriteALU S-REG-WriteMDR

8         1                0
24        1                0
40        1                0
56        1                0
72        1                0
88        1                0
104       1                0
              
4         1                0
20        1                0
36        1                0
52        1                0
              
2         0                0
18        0                0
34        0                0
50        0                0
66        0                0
82        0                0
98        0                0
              
1         0                0
17        0                0
33        1                0
49        0                0
65        0                1
81        0                0
97        0                0
              
128       0                0
144       0                0
160       0                0
176       0                0
192       0                0
208       0                0
224       0                0
240       0                0
*/

/* Test case MEM:
FirstByte S-MEM-Store

8         0
24        0
40        0
56        0
72        0
88        0
104       0
              
4         0
20        0
36        0
52        0
              
2         0
18        1
34        0
50        0
66        0
82        0
98        0
              
1         0
17        0
33        0
49        0
65        0
81        0
97        0
              
128       0
144       1
160       0
176       0
192       0
208       0
224       0
240       0
*/

/* Test case MDR:
FirstByte S-MDR-WriteALU S-MDR-WriteMEM

8         0            0
24        0            0
40        0            0
56        0            0
72        0            0
88        0            0
104       0            0
              
4         0            0
20        0            0
36        0            0
52        0            0
              
2         0            1
18        0            0
34        0            0
50        0            0
66        0            0
82        0            0
98        0            0
              
1         0            0
17        0            0
33        0            0
49        1            0
65        0            0
81        0            0
97        0            0
              
128       0            1
144       0            0
160       0            0
176       0            0
192       0            0
208       0            0
224       0            0
240       0            0
*/

/* Test case CTL:
FirstByte S-CTL-Halt

8         0
24        0
40        0
56        0
72        0
88        0
104       0
              
4         0
20        0
36        0
52        0
              
2         0
18        0
34        0
50        0
66        0
82        0
98        0
              
1         0
17        1
33        0
49        0
65        0
81        0
97        0
              
128       0
144       0
160       0
176       0
192       0
208       0
224       0
240       0
*/
