// Digital circuit Auxiliary Combinator.dig as structural Verilog
module Auxiliary_Combinator (
  input  [7:0] Counter,
  output _2_3_4_5_6
);

  wire or_1_out, or_2_out, or_3_out;

  or or_1 (or_1_out, Counter[2], Counter[3]);
  or or_2 (or_2_out, or_1_out, Counter[4]);
  or or_3 (or_3_out, or_2_out, Counter[5]);
  or or_4 (_2_3_4_5_6, or_3_out, Counter[6]);
endmodule
