// Digital circuit Branch Combinator.dig as structural Verilog
module Branch_Combinator (
  input  [7:0] Counter,
  input  Active_Group3,
  input  Active_Nibble,
  input  _2_3_4_5_6,
  output BRA_Branch,
  output BRA_Less,
  output BRA_Equal,
  output BRA_NotEqual,
  output BRA_Unconditional,
  output BRA_Greater
);

  wire or_1_out;

  or or_1 (or_1_out, Active_Group3, Active_Nibble);
  and and_1 (BRA_Branch, _2_3_4_5_6, or_1_out);
  and and_2 (BRA_Unconditional, Counter[2], or_1_out);
  and and_3 (BRA_Greater, Counter[3], or_1_out);
  and and_4 (BRA_Less, Counter[4], or_1_out);
  and and_5 (BRA_Equal, Counter[5], or_1_out);
  and and_6 (BRA_NotEqual, Counter[6], or_1_out);
endmodule
