// Digital circuit Group1 Combinator.dig as structural Verilog
module Group1_Combinator (
  input  [7:0] Counter,
  input  Active,
  output ALU_UseCarry,
  output ALU_Increment,
  output ALU_Invert,
  output ALU_Propagate,
  output ALU_ResultOut,
  output ALU_FlagWrite,
  output INS_RegReadFirst,
  output INS_RegReadSecond,
  output REG_WriteALU
);

  wire or_1_out, or_2_out, or_3_out, or_4_out, or_5_out, or_6_out, or_7_out, or_8_out;

  or or_1 (or_1_out, Counter[2], Counter[3]);
  or or_2 (or_2_out, Counter[0], Counter[1]);
  or or_3 (or_3_out, or_1_out, Counter[6]);
  or or_4 (or_4_out, or_2_out, Counter[2]);
  or or_5 (or_5_out, Counter[1], Counter[3]);
  or or_6 (or_6_out, or_3_out, Counter[4]);
  or or_7 (or_7_out, or_3_out, Counter[5]);
  or or_8 (or_8_out, or_4_out, Counter[3]);
  and and_1 (ALU_UseCarry, or_5_out, Active);
  and and_2 (ALU_Increment, or_6_out, Active);
  and and_3 (ALU_Invert, or_7_out, Active);
  and and_4 (INS_RegReadSecond, or_8_out, Active);

  assign ALU_FlagWrite = Active;
  assign ALU_Propagate = Active;
  assign ALU_ResultOut = Active;
  assign INS_RegReadFirst = Active;
  assign REG_WriteALU = Active;
endmodule
