// Digital circuit Group4 Combinator.dig as structural Verilog
module Group4_Combinator (
  input  [7:0] Counter,
  input  Active,
  output ALU_Increment,
  output ALU_FlagWrite,
  output ALU_Invert,
  output ALU_Propagate,
  output ALU_ResultOut,
  output INS_RegReadFirst,
  output INS_RegReadSecond,
  output REG_WriteALU,
  output REG_WriteMDR,
  output MDR_WriteALU,
  output CTL_Halt
);

  wire or_1_out, or_2_out, or_3_out, or_4_out, or_5_out, or_6_out, or_7_out;

  or or_1 (or_1_out, Counter[2], Counter[3]);
  or or_2 (or_2_out, Counter[5], Counter[6]);
  or or_3 (or_3_out, Counter[2], Counter[5]);
  or or_4 (or_4_out, Counter[2], Counter[3]);
  or or_5 (or_5_out, or_4_out, Counter[4]);
  or or_6 (or_6_out, or_5_out, Counter[5]);
  or or_7 (or_7_out, or_6_out, Counter[6]);
  and and_1 (ALU_Increment, Counter[5], Active);
  and and_2 (ALU_Invert, Counter[5], Active);
  and and_3 (ALU_Propagate, Counter[5], Active);
  and and_4 (ALU_ResultOut, or_1_out, Active);
  and and_5 (ALU_FlagWrite, or_2_out, Active);
  and and_6 (INS_RegReadSecond, or_3_out, Active);
  and and_7 (REG_WriteALU, Counter[2], Active);
  and and_8 (REG_WriteMDR, Counter[4], Active);
  and and_9 (MDR_WriteALU, Counter[3], Active);
  and and_10 (CTL_Halt, Counter[1], Active);
  and and_11 (INS_RegReadFirst, or_7_out, Active);
endmodule
