// Digital circuit Nibble Combinator.dig as structural Verilog
module Nibble_Combinator (
  input  [7:0] Counter,
  input  Active,
  output ADR_Immediate,
  output INS_RegReadFirst,
  output INS_ValReadCenter,
  output INS_ValReadEnd,
  output MEM_Load,
  output MEM_Store,
  output MDR_WriteMem
);

  wire not_1_out;

  not not_1 (not_1_out, Counter[7]);
  and and_1 (ADR_Immediate, not_1_out, Active);
  and and_2 (INS_RegReadFirst, Counter[7], Active);
  and and_3 (INS_ValReadEnd, not_1_out, Active);
  and and_4 (MEM_Load, Counter[0], Active);
  and and_5 (MEM_Store, Counter[1], Active);
  and and_6 (MDR_WriteMem, Counter[0], Active);

  assign INS_ValReadCenter = Active;
endmodule
