// Digital circuit 555.dig as structural Verilog
module _555 (
  input  GND,
  input  VCC,
  input  Trigger,
  input  Reset,
  input  Threshold,
  input  Dischrg,
  output Output,
  output Control
);

  PowerSupply powersupply_1 (.VDD(VCC), .GND(GND));

  assign Control = 1'b0;
  assign Output = 1'b0;

  // Notes on the sheet:
  //   GND: pin 1
  //   VCC: pin 8
  //   Trigger: pin 2
  //   Reset: pin 4
  //   Threshold: pin 6
  //   Dischrg: pin 7
  //   Output: pin 3
  //   Control: pin 5
endmodule
