// Digital circuit AND 4-1.dig as structural Verilog
module AND_4_1 (
  input  _1_B,
  input  VCC,
  input  GND,
  input  _1_C,
  input  NC_2,
  input  _2_A,
  input  _2_D,
  input  _2_C,
  input  _1_A,
  input  NC_1,
  input  _1_D,
  input  _2_B,
  output _1_Y,
  output _2_Y
);

  PowerSupply powersupply_1 (.VDD(VCC), .GND(GND));
  PullDown pulldown_1 (.out(NC_1));
  PullDown pulldown_2 (.out(NC_2));
  and and_1 (_1_Y, _1_A, _1_B, _1_C, _1_D);
  and and_2 (_2_Y, _2_A, _2_B, _2_C, _2_D);

  // Notes on the sheet:
  //   _1_B: pin 2
  //   _1_Y: pin 6
  //   VCC: pin 14
  //   GND: pin 7
  //   _1_C: pin 4
  //   NC_2: pin 11
  //   _2_A: pin 9
  //   _2_D: pin 13
  //   _2_Y: pin 8
  //   _2_C: pin 12
  //   _1_A: pin 1
  //   NC_1: pin 3
  //   _1_D: pin 5
  //   _2_B: pin 10
endmodule
