// Digital circuit Buffer 4-1.dig as structural Verilog
module Buffer_4_1 (
  input  n1OE,
  input  VCC,
  input  GND,
  input  _11_A,
  input  _12_A,
  input  _14_A,
  input  _21_A,
  input  _13_A,
  input  _2OE,
  input  _22_A,
  input  _23_A,
  input  _24_A,
  output _11_Y,
  output _12_Y,
  output _13_Y,
  output _14_Y,
  output _21_Y,
  output _22_Y,
  output _23_Y,
  output _24_Y
);

  wire not_1_out;

  PowerSupply powersupply_1 (.VDD(VCC), .GND(GND));
  not not_1 (not_1_out, n1OE);
  assign {_14_Y, _13_Y, _12_Y, _11_Y} = not_1_out ? {_14_A, _13_A, _12_A, _11_A} : 4'bz;  // Driver driver_1
  assign {_24_Y, _23_Y, _22_Y, _21_Y} = _2OE ? {_24_A, _23_A, _22_A, _21_A} : 4'bz;  // Driver driver_2

  // Notes on the sheet:
  //   n1OE: pin 1
  //   _11_Y: pin 18
  //   VCC: pin 20
  //   GND: pin 10
  //   _11_A: pin 2
  //   _12_A: pin 4
  //   _12_Y: pin 16
  //   _14_A: pin 8
  //   _21_A: pin 11
  //   _13_Y: pin 14
  //   _13_A: pin 6
  //   _2OE: pin 19
  //   _14_Y: pin 12
  //   _22_A: pin 13
  //   _23_A: pin 15
  //   _24_A: pin 17
  //   _21_Y: pin 9
  //   _22_Y: pin 7
  //   _23_Y: pin 5
  //   _24_Y: pin 3
endmodule
