// Digital circuit Buffer 8-1.dig as structural Verilog
module Buffer_8_1 (
  input  nOE1,
  input  VCC,
  input  GND,
  input  _1_A,
  input  _2_A,
  input  _4_A,
  input  _5_A,
  input  _3_A,
  input  nOE2,
  input  _6_A,
  input  _7_A,
  input  _8_A,
  output _1_Y,
  output _2_Y,
  output _3_Y,
  output _4_Y,
  output _5_Y,
  output _6_Y,
  output _7_Y,
  output _8_Y
);

  wire and_1_out, not_1_out, not_2_out;

  PowerSupply powersupply_1 (.VDD(VCC), .GND(GND));
  not not_1 (not_1_out, nOE1);
  not not_2 (not_2_out, nOE2);
  and and_1 (and_1_out, not_1_out, not_2_out);
  assign {_8_Y, _7_Y, _6_Y, _5_Y, _4_Y, _3_Y, _2_Y, _1_Y} = and_1_out ? {_8_A, _7_A, _6_A, _5_A, _4_A, _3_A, _2_A, _1_A} : 8'bz;  // Driver driver_1

  // Notes on the sheet:
  //   nOE1: pin 1
  //   _1_Y: pin 18
  //   VCC: pin 20
  //   GND: pin 10
  //   _1_A: pin 2
  //   _2_A: pin 3
  //   _2_Y: pin 17
  //   _4_A: pin 5
  //   _5_A: pin 6
  //   _3_Y: pin 16
  //   _3_A: pin 4
  //   nOE2: pin 19
  //   _4_Y: pin 15
  //   _6_A: pin 7
  //   _7_A: pin 8
  //   _8_A: pin 9
  //   _5_Y: pin 14
  //   _6_Y: pin 13
  //   _7_Y: pin 12
  //   _8_Y: pin 11
endmodule
