// Digital circuit OR 3-1.dig as structural Verilog
module OR_3_1 (
  input  _1_B,
  input  VCC,
  input  GND,
  input  _1_C,
  input  _3_A,
  input  _2_C,
  input  _3_C,
  input  _3_B,
  input  _1_A,
  input  _2_B,
  input  _2_A,
  output _1_Y,
  output _3_Y,
  output _2_Y
);

  PowerSupply powersupply_1 (.VDD(VCC), .GND(GND));
  or or_1 (_2_Y, _2_A, _2_B, _2_C);
  or or_2 (_1_Y, _1_A, _1_B, _1_C);
  or or_3 (_3_Y, _3_A, _3_B, _3_C);

  // Notes on the sheet:
  //   _1_B: pin 4
  //   _1_Y: pin 6
  //   VCC: pin 14
  //   GND: pin 7
  //   _1_C: pin 5
  //   _3_A: pin 11
  //   _3_Y: pin 10
  //   _2_C: pin 8
  //   _3_C: pin 13
  //   _2_Y: pin 9
  //   _3_B: pin 12
  //   _1_A: pin 3
  //   _2_B: pin 2
  //   _2_A: pin 1
endmodule
