// Digital circuit XOR 2-1.dig as structural Verilog
module XOR_2_1 (
  input  _1_A,
  input  VCC,
  input  GND,
  input  _1_B,
  input  _2_A,
  input  _2_B,
  input  _3_B,
  input  _3_A,
  input  _4_B,
  input  _4_A,
  output _1_Y,
  output _2_Y,
  output _3_Y,
  output _4_Y
);

  PowerSupply powersupply_1 (.VDD(VCC), .GND(GND));
  xor xor_1 (_1_Y, _1_A, _1_B);
  xor xor_2 (_2_Y, _2_A, _2_B);
  xor xor_3 (_3_Y, _3_A, _3_B);
  xor xor_4 (_4_Y, _4_A, _4_B);

  // Notes on the sheet:
  //   _1_A: pin 1
  //   _1_Y: pin 3
  //   VCC: pin 14
  //   GND: pin 7
  //   _1_B: pin 2
  //   _2_A: pin 4
  //   _2_Y: pin 6
  //   _2_B: pin 5
  //   _3_B: pin 10
  //   _3_Y: pin 8
  //   _3_A: pin 9
  //   _4_B: pin 13
  //   _4_Y: pin 11
  //   _4_A: pin 12
endmodule
