// Digital circuit NOT 1-1.dig as structural Verilog
module NOT_1_1 (
  input  _1_A,
  input  _2_A,
  input  _3_A,
  input  _4_A,
  input  VCC,
  input  GND,
  input  _5_A,
  input  _6_A,
  output _1_Y,
  output _2_Y,
  output _3_Y,
  output _4_Y,
  output _5_Y,
  output _6_Y
);

  PowerSupply powersupply_1 (.VDD(VCC), .GND(GND));
  assign {_6_Y, _5_Y, _4_Y, _3_Y, _2_Y, _1_Y} = ~{_6_A, _5_A, _4_A, _3_A, _2_A, _1_A};  // Not not_1, 6 bits wide

  // Notes on the sheet:
  //   _1_A: pin 1
  //   _1_Y: pin 2
  //   _2_A: pin 3
  //   _2_Y: pin 4
  //   _3_A: pin 5
  //   _3_Y: pin 6
  //   _4_A: pin 9
  //   _4_Y: pin 8
  //   VCC: pin 14
  //   GND: pin 7
  //   _5_A: pin 11
  //   _5_Y: pin 10
  //   _6_A: pin 13
  //   _6_Y: pin 12
endmodule
