// Digital circuit new_SCU.dig as structural Verilog
module new_SCU (
  input  [3:0] Nibble_2,
  input  IsOpcodeNibble,
  input  [7:0] Counter,
  input  F_Carry,
  input  F_Greater,
  input  F_Less,
  input  F_Equal,
  input  F_NotEqual,
  input  [7:0] Clock,
  input  [7:0] FirstByte,
  input  [7:0] SecondByte,
  output S_CTL_Halt,
  output S_ALU_Propagate,
  output S_ALU_Invert,
  output nS_INS_ValRead,
  output nS_ADR_Direct,
  output S_ADR_Direct,
  output S_INS_ValRead,
  output S_ADR_Immediate,
  output nS_ALU_ResultOut,
  output nS_ADR_Immediate,
  output nS_MDR_WriteMEM,
  output nS_MDR_WriteALU,
  output nS_ALU_CarryOut,
  output nS_ALU_OrOut,
  output nS_REG_WriteALU,
  output nS_REG_WriteMDR,
  output nS_REG_WriteVAL,
  output D_ALU_Increment,
  output D_WRT_RPC,
  output D_SEL_Second,
  output D_SEL_First,
  output D_WRT_CIRFirst,
  output D_WRT_CIRSecond,
  output D_WRT_Flags,
  output D_WRT_BufferSecond,
  output D_WRT_BufferFirst,
  output D_WRT_MDR,
  output D_WRT_RegOutput,
  output D_RPC_MemAdder,
  output D_RPC_Registers,
  output nD_RPC_MemAdder,
  output nD_RPC_Registers,
  output nD_WRT_SRAM
);

  wire and_2_1_1__1_y, and_2_1_1__2_y, and_2_1_1__3_y, and_2_1_1__4_y, and_2_1_2__1_y, and_2_1_2__2_y,
       and_2_1_3__1_y, and_2_1_3__2_y, and_2_1_3__4_y, and_2_1_4__4_y, buffer_4_1_1__11_y,
       buffer_4_1_1__13_y, buffer_4_1_1__14_y, buffer_4_1_2__22_y, buffer_4_1_2__23_y, buffer_4_1_2__24_y,
       buffer_4_1_3__23_y, buffer_4_1_3__24_y, buffer_4_1_4__21_y, buffer_4_1_4__22_y, buffer_4_1_5__21_y,
       buffer_4_1_5__22_y, buffer_4_1_5__23_y, buffer_4_1_5__24_y, buffer_4_1_6__22_y, buffer_4_1_6__23_y,
       buffer_4_1_6__24_y, buffer_8_1_1__4_y, buffer_8_1_1__5_y, buffer_8_1_1__6_y, buffer_8_1_1__7_y,
       buffer_8_1_1__8_y, buffer_8_1_2__2_y, buffer_8_1_2__3_y, buffer_8_1_2__4_y, buffer_8_1_2__5_y,
       buffer_8_1_3__1_y, buffer_8_1_3__2_y, buffer_8_1_3__3_y, buffer_8_1_3__4_y, buffer_8_1_3__5_y,
       decoder_1_out_0, decoder_1_out_1, decoder_1_out_2, decoder_1_out_3, decoder_1_out_4, decoder_1_out_5,
       decoder_1_out_6, decoder_1_out_7, not_1_1_1__1_y, not_1_1_1__2_y, not_1_1_1__3_y, not_1_1_1__4_y,
       not_1_1_1__6_y, not_1_1_2__6_y, not_1_1_6__1_y, or_2_1_1__1_y, or_2_1_1__2_y, or_2_1_1__3_y,
       or_2_1_1__4_y, or_2_1_2__1_y, or_2_1_2__2_y, or_2_1_2__3_y, or_2_1_3__1_y, or_2_1_3__2_y,
       or_2_1_3__3_y, or_2_1_3__4_y, or_2_1_4__1_y, or_2_1_4__2_y, or_2_1_4__3_y, or_2_1_4__4_y,
       or_2_1_5__1_y, or_2_1_5__3_y, or_2_1_6__1_y, or_2_1_6__2_y, or_2_1_6__3_y, or_2_1_6__4_y,
       or_2_1_7__1_y, or_2_1_7__2_y, or_2_1_7__3_y, or_2_1_7__4_y, or_2_1_8__1_y, or_2_1_8__2_y,
       or_2_1_8__3_y, or_2_1_8__4_y, or_2_1_9__1_y, or_2_1_9__2_y, or_2_1_9__3_y, or_2_1_9__4_y,
       or_2_1_10__3_y, or_2_1_10__4_y, or_2_1_11__3_y, or_2_1_11__4_y, or_2_1_12__2_y, or_2_1_13__1_y,
       or_2_1_13__2_y, or_2_1_13__3_y, or_2_1_13__4_y;

  Decoder #(.Selector_Bits(3)) decoder_1 (
    .sel(FirstByte[6:4]), .out_0(decoder_1_out_0), .out_1(decoder_1_out_1), .out_2(decoder_1_out_2),
    .out_3(decoder_1_out_3), .out_4(decoder_1_out_4), .out_5(decoder_1_out_5), .out_6(decoder_1_out_6),
    .out_7(decoder_1_out_7));
  Buffer_4_1 buffer_4_1_1 (
    .n1OE(FirstByte[7]), ._11_Y(buffer_4_1_1__11_y), .VCC(1'b1), .GND(1'b0), ._11_A(FirstByte[0]),
    ._12_A(FirstByte[1]), ._12_Y(S_ADR_Direct), ._14_A(FirstByte[3]), ._21_A(1'b0),
    ._13_Y(buffer_4_1_1__13_y), ._13_A(FirstByte[2]), ._2OE(1'b0), ._14_Y(buffer_4_1_1__14_y), ._22_A(1'b0),
    ._23_A(1'b0), ._24_A(1'b0));  // open: _21_Y, _22_Y, _23_Y, _24_Y
  OR_2_1 or_2_1_1 (
    ._1_A(decoder_1_out_2), ._1_Y(or_2_1_1__1_y), .VCC(1'b1), .GND(1'b0), ._1_B(decoder_1_out_3),
    ._2_A(or_2_1_1__1_y), ._2_Y(or_2_1_1__2_y), ._2_B(decoder_1_out_6), ._3_B(decoder_1_out_4),
    ._3_Y(or_2_1_1__3_y), ._3_A(or_2_1_1__2_y), ._4_B(decoder_1_out_5), ._4_Y(or_2_1_1__4_y),
    ._4_A(or_2_1_1__2_y));
  OR_2_1 or_2_1_2 (
    ._1_A(decoder_1_out_1), ._1_Y(or_2_1_2__1_y), .VCC(1'b1), .GND(1'b0), ._1_B(decoder_1_out_3),
    ._2_A(decoder_1_out_0), ._2_Y(or_2_1_2__2_y), ._2_B(decoder_1_out_3), ._3_B(decoder_1_out_5),
    ._3_Y(or_2_1_2__3_y), ._3_A(decoder_1_out_4), ._4_B(1'b0), ._4_A(1'b0));  // open: _4_Y
  NOT_1_1 not_1_1_1 (
    ._1_A(decoder_1_out_6), ._1_Y(not_1_1_1__1_y), ._2_A(decoder_1_out_7), ._2_Y(not_1_1_1__2_y),
    ._3_A(buffer_4_1_1__11_y), ._3_Y(not_1_1_1__3_y), ._4_A(buffer_4_1_1__13_y), ._4_Y(not_1_1_1__4_y),
    .VCC(1'b1), .GND(1'b0), ._5_A(1'b0), ._6_A(or_2_1_2__3_y), ._6_Y(not_1_1_1__6_y));  // open: _5_Y
  OR_2_1 or_2_1_3 (
    ._1_A(decoder_1_out_0), ._1_Y(or_2_1_3__1_y), .VCC(1'b1), .GND(1'b0), ._1_B(decoder_1_out_1),
    ._2_A(or_2_1_3__1_y), ._2_Y(or_2_1_3__2_y), ._2_B(decoder_1_out_2), ._3_B(decoder_1_out_6),
    ._3_Y(or_2_1_3__3_y), ._3_A(decoder_1_out_5), ._4_B(decoder_1_out_2), ._4_Y(or_2_1_3__4_y),
    ._4_A(decoder_1_out_5));
  OR_2_1 or_2_1_4 (
    ._1_A(decoder_1_out_3), ._1_Y(or_2_1_4__1_y), .VCC(1'b1), .GND(1'b0), ._1_B(decoder_1_out_4),
    ._2_A(decoder_1_out_5), ._2_Y(or_2_1_4__2_y), ._2_B(decoder_1_out_6), ._3_B(FirstByte[7]),
    ._3_Y(or_2_1_4__3_y), ._3_A(S_ADR_Direct), ._4_B(or_2_1_4__1_y), ._4_Y(or_2_1_4__4_y),
    ._4_A(or_2_1_4__2_y));
  NOT_1_1 not_1_1_2 (
    ._1_A(1'b0), ._2_A(1'b0), ._3_A(1'b0), ._4_A(1'b0), .VCC(1'b1), .GND(1'b0), ._5_A(1'b0),
    ._6_A(or_2_1_4__3_y), ._6_Y(not_1_1_2__6_y));  // open: _1_Y, _2_Y, _3_Y, _4_Y, _5_Y
  PullDown pulldown_1 (.out(buffer_4_1_1__11_y));
  PullDown pulldown_2 (.out(S_ADR_Direct));
  PullDown pulldown_3 (.out(buffer_4_1_1__13_y));
  PullDown pulldown_4 (.out(buffer_4_1_1__14_y));
  Buffer_8_1 buffer_8_1_1 (
    .nOE1(not_1_1_1__4_y), .VCC(1'b1), .GND(1'b0), ._1_A(1'b0), ._2_A(1'b0), ._4_A(or_2_1_2__2_y),
    ._5_A(decoder_1_out_3), ._3_A(1'b0), .nOE2(1'b0), ._4_Y(buffer_8_1_1__4_y), ._6_A(decoder_1_out_2),
    ._7_A(decoder_1_out_1), ._8_A(or_2_1_3__2_y), ._5_Y(buffer_8_1_1__5_y), ._6_Y(buffer_8_1_1__6_y),
    ._7_Y(buffer_8_1_1__7_y), ._8_Y(buffer_8_1_1__8_y));  // open: _1_Y, _2_Y, _3_Y
  Buffer_8_1 buffer_8_1_2 (
    .nOE1(not_1_1_1__3_y), ._1_Y(S_CTL_Halt), .VCC(1'b1), .GND(1'b0), ._1_A(decoder_1_out_1),
    ._2_A(decoder_1_out_2), ._2_Y(buffer_8_1_2__2_y), ._4_A(decoder_1_out_3), ._5_A(or_2_1_4__4_y),
    ._3_Y(buffer_8_1_2__3_y), ._3_A(decoder_1_out_4), .nOE2(1'b0), ._4_Y(buffer_8_1_2__4_y), ._6_A(1'b0),
    ._7_A(1'b0), ._8_A(1'b0), ._5_Y(buffer_8_1_2__5_y));  // open: _6_Y, _7_Y, _8_Y
  Buffer_8_1 buffer_8_1_3 (
    .nOE1(not_1_1_2__6_y), ._1_Y(buffer_8_1_3__1_y), .VCC(1'b1), .GND(1'b0), ._1_A(decoder_1_out_2),
    ._2_A(decoder_1_out_3), ._2_Y(buffer_8_1_3__2_y), ._4_A(decoder_1_out_5), ._5_A(decoder_1_out_6),
    ._3_Y(buffer_8_1_3__3_y), ._3_A(decoder_1_out_4), .nOE2(1'b0), ._4_Y(buffer_8_1_3__4_y), ._6_A(1'b0),
    ._7_A(1'b0), ._8_A(1'b0), ._5_Y(buffer_8_1_3__5_y));  // open: _6_Y, _7_Y, _8_Y
  Buffer_4_1 buffer_4_1_2 (
    .n1OE(1'b1), .VCC(1'b1), .GND(1'b0), ._11_A(1'b0), ._12_A(1'b0), ._14_A(1'b0), ._21_A(1'b0),
    ._13_A(1'b0), ._2OE(buffer_4_1_1__14_y), ._22_A(or_2_1_1__4_y), ._23_A(or_2_1_1__3_y),
    ._24_A(or_2_1_2__1_y), ._22_Y(buffer_4_1_2__22_y), ._23_Y(buffer_4_1_2__23_y), ._24_Y(buffer_4_1_2__24_y));  // open: _11_Y, _12_Y, _13_Y, _14_Y, _21_Y
  Buffer_4_1 buffer_4_1_3 (
    .n1OE(1'b1), .VCC(1'b1), .GND(1'b0), ._11_A(1'b0), ._12_A(1'b0), ._14_A(1'b0), ._21_A(1'b0),
    ._13_A(1'b0), ._2OE(buffer_4_1_1__14_y), ._22_A(1'b0), ._23_A(not_1_1_1__1_y), ._24_A(not_1_1_1__6_y),
    ._23_Y(buffer_4_1_3__23_y), ._24_Y(buffer_4_1_3__24_y));  // open: _11_Y, _12_Y, _13_Y, _14_Y, _21_Y, _22_Y
  Buffer_4_1 buffer_4_1_4 (
    .n1OE(1'b1), .VCC(1'b1), .GND(1'b0), ._11_A(1'b0), ._12_A(1'b0), ._14_A(1'b0), ._21_A(decoder_1_out_1),
    ._13_A(1'b0), ._2OE(S_ADR_Direct), ._22_A(decoder_1_out_0), ._23_A(1'b0), ._24_A(1'b0),
    ._21_Y(buffer_4_1_4__21_y), ._22_Y(buffer_4_1_4__22_y));  // open: _11_Y, _12_Y, _13_Y, _14_Y, _23_Y, _24_Y
  Buffer_4_1 buffer_4_1_5 (
    .n1OE(1'b1), .VCC(1'b1), .GND(1'b0), ._11_A(1'b0), ._12_A(1'b0), ._14_A(1'b0), ._21_A(or_2_1_1__1_y),
    ._13_A(1'b0), ._2OE(buffer_4_1_1__11_y), ._22_A(or_2_1_3__4_y), ._23_A(or_2_1_3__3_y),
    ._24_A(decoder_1_out_5), ._21_Y(buffer_4_1_5__21_y), ._22_Y(buffer_4_1_5__22_y),
    ._23_Y(buffer_4_1_5__23_y), ._24_Y(buffer_4_1_5__24_y));  // open: _11_Y, _12_Y, _13_Y, _14_Y
  Buffer_4_1 buffer_4_1_6 (
    .n1OE(1'b1), .VCC(1'b1), .GND(1'b0), ._11_A(1'b0), ._12_A(1'b0), ._14_A(1'b0), ._21_A(not_1_1_1__2_y),
    ._13_A(1'b0), ._2OE(FirstByte[7]), ._22_A(decoder_1_out_0), ._23_A(decoder_1_out_1),
    ._24_A(decoder_1_out_7), ._21_Y(S_ADR_Immediate), ._22_Y(buffer_4_1_6__22_y), ._23_Y(buffer_4_1_6__23_y),
    ._24_Y(buffer_4_1_6__24_y));  // open: _11_Y, _12_Y, _13_Y, _14_Y
  LED ALU_Increment (.in(buffer_4_1_2__23_y));
  LED ALU_Invert (.in(buffer_4_1_2__22_y));
  PullDown pulldown_5 (.out(buffer_4_1_2__22_y));
  PullDown pulldown_6 (.out(buffer_4_1_2__23_y));
  LED INS_RegReadSecond (.in(buffer_4_1_3__23_y));
  LED INS_RegReadFirst (.in(buffer_4_1_3__24_y));
  PullDown pulldown_7 (.out(buffer_4_1_3__23_y));
  PullDown pulldown_8 (.out(buffer_4_1_3__24_y));
  LED ALU_Invert_2 (.in(buffer_8_1_1__5_y));
  LED ALU_ResultOut (.in(buffer_8_1_1__4_y));
  PullDown pulldown_9 (.out(buffer_8_1_1__4_y));
  PullDown pulldown_10 (.out(buffer_8_1_1__5_y));
  LED ALU_ResultOut_2 (.in(buffer_4_1_5__21_y));
  LED INS_RegReadFirst_2 (.in(buffer_4_1_5__22_y));
  LED REG_WriteALU (.in(buffer_8_1_2__2_y));
  LED CTL_Halt (.in(S_CTL_Halt));
  PullDown pulldown_11 (.out(S_CTL_Halt));
  PullDown pulldown_12 (.out(buffer_8_1_2__2_y));
  LED BRA_Unconditional (.in(buffer_8_1_3__1_y));
  LED BRA_Greater (.in(buffer_8_1_3__2_y));
  PullDown pulldown_13 (.out(buffer_8_1_3__1_y));
  PullDown pulldown_14 (.out(buffer_8_1_3__2_y));
  LED ALU_UseCarry (.in(buffer_4_1_2__24_y));
  LED ALU_Propagate (.in(buffer_4_1_1__14_y));
  LED ALU_ResultOut_3 (.in(buffer_4_1_1__14_y));
  LED ALU_FlagWrite (.in(buffer_4_1_1__14_y));
  PullDown pulldown_15 (.out(buffer_4_1_2__24_y));
  LED INS_RegReadFirst_3 (.in(buffer_4_1_1__13_y));
  LED REG_WriteALU_2 (.in(buffer_4_1_1__13_y));
  LED ALU_FlagWrite_2 (.in(buffer_4_1_1__13_y));
  LED INS_RegReadSecond_2 (.in(S_ADR_Direct));
  LED ALU_CarryOut (.in(buffer_8_1_1__7_y));
  LED ALU_OrOut (.in(buffer_8_1_1__6_y));
  LED MEM_Store (.in(buffer_4_1_4__21_y));
  LED INS_RegReadSecond_3 (.in(buffer_8_1_1__8_y));
  PullDown pulldown_16 (.out(buffer_8_1_1__6_y));
  PullDown pulldown_17 (.out(buffer_8_1_1__7_y));
  PullDown pulldown_18 (.out(buffer_8_1_1__8_y));
  PullDown pulldown_19 (.out(buffer_4_1_4__21_y));
  LED ALU_Increment_2 (.in(buffer_4_1_5__24_y));
  LED ALU_Invert_3 (.in(buffer_4_1_5__24_y));
  LED ALU_Propagate_2 (.in(buffer_4_1_5__24_y));
  LED ALU_FlagWrite_3 (.in(buffer_4_1_5__23_y));
  LED MDR_WriteALU (.in(buffer_8_1_2__4_y));
  LED REG_WriteMDR (.in(buffer_8_1_2__3_y));
  LED INS_RegReadSecond_4 (.in(buffer_8_1_2__5_y));
  LED INS_ValRead (.in(FirstByte[7]));
  PullDown pulldown_20 (.out(buffer_8_1_2__3_y));
  PullDown pulldown_21 (.out(buffer_8_1_2__4_y));
  PullDown pulldown_22 (.out(buffer_8_1_2__5_y));
  LED BRA_NotEqual (.in(buffer_8_1_3__5_y));
  LED BRA_Less (.in(buffer_8_1_3__3_y));
  LED BRA_Equal (.in(buffer_8_1_3__4_y));
  PullDown pulldown_23 (.out(buffer_8_1_3__5_y));
  PullDown pulldown_24 (.out(buffer_8_1_3__4_y));
  PullDown pulldown_25 (.out(buffer_8_1_3__3_y));
  LED ADR_Immediate (.in(S_ADR_Immediate));
  PullDown pulldown_26 (.out(S_ADR_Immediate));
  LED REG_WriteALU_3 (.in(buffer_4_1_1__14_y));
  LED INS_RegReadFirst_4 (.in(S_ADR_Direct));
  LED ADR_Direct (.in(S_ADR_Direct));
  LED MDR_WriteMem (.in(buffer_4_1_4__22_y));
  PullDown pulldown_27 (.out(buffer_4_1_4__22_y));
  PullDown pulldown_28 (.out(FirstByte[7]));
  LED MDR_WriteMem_2 (.in(buffer_4_1_6__22_y));
  LED REG_WriteVAL (.in(buffer_4_1_6__24_y));
  LED MEM_Store_2 (.in(buffer_4_1_6__23_y));
  PullDown pulldown_29 (.out(buffer_4_1_6__22_y));
  PullDown pulldown_30 (.out(buffer_4_1_6__23_y));
  PullDown pulldown_31 (.out(buffer_4_1_6__24_y));
  PullDown pulldown_32 (.out(buffer_4_1_5__21_y));
  PullDown pulldown_33 (.out(buffer_4_1_5__22_y));
  PullDown pulldown_34 (.out(buffer_4_1_5__23_y));
  PullDown pulldown_35 (.out(buffer_4_1_5__24_y));
  OR_2_1 or_2_1_5 (
    ._1_A(buffer_4_1_2__22_y), ._1_Y(or_2_1_5__1_y), .VCC(1'b1), .GND(1'b0), ._1_B(buffer_8_1_1__5_y),
    ._2_A(or_2_1_5__1_y), ._2_Y(S_ALU_Invert), ._2_B(buffer_4_1_5__24_y), ._3_B(buffer_4_1_5__24_y),
    ._3_Y(or_2_1_5__3_y), ._3_A(buffer_4_1_2__23_y), ._4_B(buffer_4_1_5__24_y), ._4_Y(S_ALU_Propagate),
    ._4_A(buffer_4_1_1__14_y));
  OR_2_1 or_2_1_6 (
    ._1_A(buffer_4_1_1__13_y), ._1_Y(or_2_1_6__1_y), .VCC(1'b1), .GND(1'b0), ._1_B(S_ADR_Direct),
    ._2_A(or_2_1_6__1_y), ._2_Y(or_2_1_6__2_y), ._2_B(buffer_4_1_3__24_y), ._3_B(S_ADR_Direct),
    ._3_Y(or_2_1_6__3_y), ._3_A(buffer_4_1_3__23_y), ._4_B(or_2_1_6__2_y), ._4_Y(or_2_1_6__4_y),
    ._4_A(buffer_4_1_5__22_y));
  OR_2_1 or_2_1_7 (
    ._1_A(buffer_4_1_1__14_y), ._1_Y(or_2_1_7__1_y), .VCC(1'b1), .GND(1'b0), ._1_B(buffer_8_1_1__4_y),
    ._2_A(or_2_1_7__1_y), ._2_Y(or_2_1_7__2_y), ._2_B(buffer_4_1_5__21_y), ._3_B(or_2_1_7__4_y),
    ._3_Y(or_2_1_7__3_y), ._3_A(buffer_4_1_1__13_y), ._4_B(buffer_4_1_1__14_y), ._4_Y(or_2_1_7__4_y),
    ._4_A(buffer_4_1_5__23_y));
  OR_2_1 or_2_1_8 (
    ._1_A(buffer_4_1_1__14_y), ._1_Y(or_2_1_8__1_y), .VCC(1'b1), .GND(1'b0), ._1_B(buffer_4_1_1__13_y),
    ._2_A(or_2_1_8__1_y), ._2_Y(or_2_1_8__2_y), ._2_B(buffer_8_1_2__2_y), ._3_B(or_2_1_8__4_y),
    ._3_Y(or_2_1_8__3_y), ._3_A(buffer_8_1_2__5_y), ._4_B(buffer_8_1_1__8_y), ._4_Y(or_2_1_8__4_y),
    ._4_A(or_2_1_6__3_y));
  OR_2_1 or_2_1_9 (
    ._1_A(buffer_4_1_4__21_y), ._1_Y(or_2_1_9__1_y), .VCC(1'b1), .GND(1'b0), ._1_B(buffer_4_1_6__23_y),
    ._2_A(buffer_4_1_4__22_y), ._2_Y(or_2_1_9__2_y), ._2_B(buffer_4_1_6__22_y), ._3_B(or_2_1_9__4_y),
    ._3_Y(or_2_1_9__3_y), ._3_A(or_2_1_8__2_y), ._4_B(buffer_4_1_6__24_y), ._4_Y(or_2_1_9__4_y),
    ._4_A(buffer_8_1_2__3_y));
  AND_2_1 and_2_1_1 (
    ._1_A(buffer_8_1_3__2_y), ._1_Y(and_2_1_1__1_y), .VCC(1'b1), .GND(1'b0), ._1_B(F_Greater),
    ._2_A(buffer_8_1_3__3_y), ._2_Y(and_2_1_1__2_y), ._2_B(F_Less), ._3_B(F_Equal), ._3_Y(and_2_1_1__3_y),
    ._3_A(buffer_8_1_3__4_y), ._4_B(buffer_8_1_3__5_y), ._4_Y(and_2_1_1__4_y), ._4_A(F_NotEqual));
  LED ALU_Invert_4 (.in(S_ALU_Invert));
  LED ADR_Direct_2 (.in(S_ADR_Direct));
  LED ALU_FlagWrite_4 (.in(or_2_1_7__3_y));
  LED INS_RegReadSecond_5 (.in(or_2_1_8__3_y));
  LED INS_ValRead_2 (.in(FirstByte[7]));
  LED CTL_Halt_2 (.in(S_CTL_Halt));
  LED ADR_Immediate_2 (.in(S_ADR_Immediate));
  LED ALU_Increment_3 (.in(or_2_1_5__3_y));
  LED ALU_Propagate_3 (.in(S_ALU_Propagate));
  LED ALU_UseCarry_2 (.in(buffer_4_1_2__24_y));
  LED INS_RegReadFirst_5 (.in(or_2_1_6__4_y));
  LED ALU_ResultOut_4 (.in(or_2_1_7__2_y));
  LED ALU_OrOut_2 (.in(buffer_8_1_1__6_y));
  LED ALU_CarryOut_2 (.in(buffer_8_1_1__7_y));
  LED REG_WriteALU_4 (.in(or_2_1_8__2_y));
  LED REG_WriteVal_2 (.in(buffer_4_1_6__24_y));
  LED REG_WriteMDR_2 (.in(buffer_8_1_2__3_y));
  LED MDR_WriteALU_2 (.in(buffer_8_1_2__4_y));
  LED MDR_WriteMem_3 (.in(or_2_1_9__2_y));
  LED MEM_Store_3 (.in(or_2_1_9__1_y));
  NOT_1_1 not_1_1_3 (
    ._1_A(S_ADR_Immediate), ._1_Y(nS_ADR_Immediate), ._2_A(FirstByte[7]), ._2_Y(nS_INS_ValRead),
    ._3_A(or_2_1_6__4_y), ._3_Y(nS_ADR_Direct), ._4_A(or_2_1_7__2_y), ._4_Y(nS_ALU_ResultOut), .VCC(1'b1),
    .GND(1'b0), ._5_A(buffer_8_1_1__6_y), ._5_Y(nS_ALU_OrOut), ._6_A(buffer_8_1_1__7_y),
    ._6_Y(nS_ALU_CarryOut));
  NOT_1_1 not_1_1_4 (
    ._1_A(or_2_1_8__2_y), ._1_Y(nS_REG_WriteALU), ._2_A(buffer_4_1_6__24_y), ._2_Y(nS_REG_WriteVAL),
    ._3_A(buffer_8_1_2__3_y), ._3_Y(nS_REG_WriteMDR), ._4_A(and_2_1_4__4_y), ._4_Y(nD_WRT_SRAM), .VCC(1'b1),
    .GND(1'b0), ._5_A(D_RPC_Registers), ._5_Y(nD_RPC_Registers), ._6_A(D_RPC_MemAdder), ._6_Y(nD_RPC_MemAdder));
  NOT_1_1 not_1_1_5 (
    ._1_A(buffer_8_1_2__4_y), ._1_Y(nS_MDR_WriteALU), ._2_A(or_2_1_9__2_y), ._2_Y(nS_MDR_WriteMEM),
    ._3_A(1'b0), ._4_A(1'b0), .VCC(1'b1), .GND(1'b0), ._5_A(1'b0), ._6_A(1'b0));  // open: _3_Y, _4_Y, _5_Y, _6_Y
  LED ALU_Increment_4 (.in(D_ALU_Increment));
  LED RPC_Registers (.in(D_RPC_Registers));
  LED RPC_MemAdder (.in(D_RPC_MemAdder));
  LED WRT_PC (.in(D_WRT_RPC));
  LED WRT_Flags (.in(D_WRT_Flags));
  LED WRT_BufferSecond (.in(D_WRT_BufferSecond));
  LED WRT_BufferFirst (.in(D_WRT_BufferFirst));
  LED SEL_Second (.in(D_SEL_Second));
  LED SEL_First (.in(D_SEL_First));
  LED WRT_RegOutput (.in(D_WRT_RegOutput));
  LED WRT_MDR (.in(D_WRT_MDR));
  LED WRT_SRAM (.in(and_2_1_4__4_y));
  LED nALU_UseCarry (.in(not_1_1_6__1_y));
  NOT_1_1 not_1_1_6 (
    ._1_A(buffer_4_1_2__24_y), ._1_Y(not_1_1_6__1_y), ._2_A(1'b0), ._3_A(1'b0), ._4_A(D_RPC_Registers),
    ._4_Y(D_RPC_MemAdder), .VCC(1'b1), .GND(1'b0), ._5_A(1'b0), ._6_A(1'b0));  // open: _2_Y, _3_Y, _5_Y, _6_Y
  AND_2_1 and_2_1_2 (
    ._1_A(not_1_1_6__1_y), ._1_Y(and_2_1_2__1_y), .VCC(1'b1), .GND(1'b0), ._1_B(or_2_1_5__3_y),
    ._2_A(F_Carry), ._2_Y(and_2_1_2__2_y), ._2_B(buffer_4_1_2__24_y), ._3_B(or_2_1_13__3_y),
    ._3_Y(D_RPC_Registers), ._3_A(or_2_1_10__4_y), ._4_B(1'b0), ._4_A(1'b0));  // open: _4_Y
  OR_2_1 or_2_1_10 (
    ._1_A(and_2_1_2__2_y), ._1_Y(D_ALU_Increment), .VCC(1'b1), .GND(1'b0), ._1_B(and_2_1_2__1_y),
    ._2_A(and_2_1_3__4_y), ._2_Y(D_WRT_RPC), ._2_B(or_2_1_10__3_y), ._3_B(Clock[2]), ._3_Y(or_2_1_10__3_y),
    ._3_A(Clock[0]), ._4_B(Clock[6]), ._4_Y(or_2_1_10__4_y), ._4_A(Clock[5]));
  AND_2_1 and_2_1_3 (
    ._1_A(Clock[3]), ._1_Y(and_2_1_3__1_y), .VCC(1'b1), .GND(1'b0), ._1_B(S_ADR_Direct), ._2_A(Clock[5]),
    ._2_Y(and_2_1_3__2_y), ._2_B(or_2_1_8__3_y), ._3_B(or_2_1_7__3_y), ._3_Y(D_WRT_Flags), ._3_A(Clock[7]),
    ._4_B(Clock[6]), ._4_Y(and_2_1_3__4_y), ._4_A(or_2_1_13__3_y));
  OR_2_1 or_2_1_11 (
    ._1_A(and_2_1_3__2_y), ._1_Y(D_WRT_BufferSecond), .VCC(1'b1), .GND(1'b0), ._1_B(Clock[1]),
    ._2_A(and_2_1_3__1_y), ._2_Y(D_WRT_BufferFirst), ._2_B(Clock[1]), ._3_B(or_2_1_11__4_y),
    ._3_Y(or_2_1_11__3_y), ._3_A(Clock[5]), ._4_B(Clock[7]), ._4_Y(or_2_1_11__4_y), ._4_A(Clock[6]));
  OR_2_1 or_2_1_12 (
    ._1_A(1'b0), .VCC(1'b1), .GND(1'b0), ._1_B(1'b0), ._2_A(buffer_8_1_2__4_y), ._2_Y(or_2_1_12__2_y),
    ._2_B(or_2_1_9__2_y), ._3_B(Clock[2]), ._3_Y(D_SEL_First), ._3_A(Clock[3]), ._4_B(or_2_1_11__3_y),
    ._4_Y(D_SEL_Second), ._4_A(Clock[4]));  // open: _1_Y
  AND_2_1 and_2_1_4 (
    ._1_A(or_2_1_12__2_y), ._1_Y(D_WRT_MDR), .VCC(1'b1), .GND(1'b0), ._1_B(Clock[7]), ._2_A(or_2_1_9__3_y),
    ._2_Y(D_WRT_RegOutput), ._2_B(Clock[7]), ._3_B(1'b0), ._3_A(1'b0), ._4_B(or_2_1_9__1_y),
    ._4_Y(and_2_1_4__4_y), ._4_A(Clock[7]));  // open: _3_Y
  OR_2_1 or_2_1_13 (
    ._1_A(and_2_1_1__4_y), ._1_Y(or_2_1_13__1_y), .VCC(1'b1), .GND(1'b0), ._1_B(and_2_1_1__3_y),
    ._2_A(or_2_1_13__1_y), ._2_Y(or_2_1_13__2_y), ._2_B(and_2_1_1__2_y), ._3_B(or_2_1_13__4_y),
    ._3_Y(or_2_1_13__3_y), ._3_A(or_2_1_13__2_y), ._4_B(buffer_8_1_3__1_y), ._4_Y(or_2_1_13__4_y),
    ._4_A(and_2_1_1__1_y));
  LED Should_Branch (.in(or_2_1_13__3_y));

  assign D_WRT_CIRFirst = Clock[0];
  assign D_WRT_CIRSecond = Clock[1];
  assign S_INS_ValRead = FirstByte[7];

  // Notes on the sheet:
  //   Nibble_2: pin 2
  //   IsOpcodeNibble: pin 70
  //   Counter: pin 1
  //   Clock: pin 69
  //   S_CTL_Halt: pin 59
  //   S_ALU_Propagate: pin 54
  //   S_ALU_Invert: pin 53
  //   nS_INS_ValRead: pin 61
  //   nS_ADR_Direct: pin 62
  //   S_ADR_Direct: pin 58
  //   S_INS_ValRead: pin 60
  //   S_ADR_Immediate: pin 57
  //   nS_ALU_ResultOut: pin 55
  //   nS_ADR_Immediate: pin 63
  //   nS_MDR_WriteMEM: pin 51
  //   nS_MDR_WriteALU: pin 50
  //   nS_ALU_CarryOut: pin 52
  //   nS_ALU_OrOut: pin 56
  //   nS_REG_WriteALU: pin 46
  //   nS_REG_WriteMDR: pin 47
  //   nS_REG_WriteVAL: pin 48
  //   D_ALU_Increment: pin 62
  //   D_WRT_RPC: pin 39
  //   D_SEL_Second: pin 68
  //   D_SEL_First: pin 67
  //   D_WRT_CIRFirst: pin 37
  //   D_WRT_CIRSecond: pin 38
  //   D_WRT_Flags: pin 40
  //   D_WRT_BufferSecond: pin 41
  //   D_WRT_BufferFirst: pin 42
  //   D_WRT_MDR: pin 45
  //   D_WRT_RegOutput: pin 43
  //   D_RPC_MemAdder: pin 63
  //   D_RPC_Registers: pin 36
  //   nD_RPC_MemAdder: pin 34
  //   nD_RPC_Registers: pin 35
  //   nD_WRT_SRAM: pin 44
  //   Testing
  //   Width
  //   144 holes
  //   36 cm
  //   Height
  //   112 holes
  //   28 cm
endmodule

/* Test case S-ALU:
FirstByte S-ALU-Invert S-ALU-Propagate ~{S-ALU-ResultOut} ~{S-ALU-CarryOut} ~{S-ALU-OrOut}

8         0            1               0                  1                 1
24        0            1               0                  1                 1
40        1            1               0                  1                 1
56        1            1               0                  1                 1
72        0            1               0                  1                 1
88        1            1               0                  1                 1
104       1            1               0                  1                 1
            
4         0            0               0                  1                 1
20        0            0               1                  0                 1
36        0            0               1                  1                 0
52        1            0               0                  1                 1
              
2         0            0               1                  1                 1
18        0            0               1                  1                 1
34        0            0               1                  1                 1
50        0            0               1                  1                 1
66        0            0               1                  1                 1
82        0            0               1                  1                 1
98        0            0               1                  1                 1
              
1         0            0               1                  1                 1
17        0            0               1                  1                 1
33        0            0               0                  1                 1
49        0            0               0                  1                 1
65        0            0               1                  1                 1
81        1            1               1                  1                 1
97        0            0               1                  1                 1
     
*/

/* Test case S-ADR:
FirstByte S-ADR-Immediate S-ADR-Direct

8         0             0
24        0             0
40        0             0
56        0             0
72        0             0
88        0             0
104       0             0

4         0             0
20        0             0
36        0             0
52        0             0

2         0             1
18        0             1
34        0             1
50        0             1
66        0             1
82        0             1
98        0             1

1         0             0
17        0             0
33        0             0
49        0             0
65        0             0
81        0             0
97        0             0

128       1             0
144       1             0
160       1             0
176       1             0
192       1             0
208       1             0
224       1             0
240       0             0
*/

/* Test case S-REG:
FirstByte ~{S-REG-WriteALU} ~{S-REG-WriteMDR} ~{S-REG-WriteVAL}

8         0                 1                 1
24        0                 1                 1
40        0                 1                 1
56        0                 1                 1
72        0                 1                 1
88        0                 1                 1
104       0                 1                 1
              
4         0                 1                 1
20        0                 1                 1
36        0                 1                 1
52        0                 1                 1
              
2         1                 1                 1
18        1                 1                 1
34        1                 1                 1
50        1                 1                 1
66        1                 1                 1
82        1                 1                 1
98        1                 1                 1
              
1         1                 1                 1
17        1                 1                 1
33        0                 1                 1
49        1                 1                 1
65        1                 0                 1
81        1                 1                 1
97        1                 1                 1

128       1                 1                 1
144       1                 1                 1
160       1                 1                 1
176       1                 1                 1
192       1                 1                 1
208       1                 1                 1
224       1                 1                 1
240       1                 1                 0
*/

/* Test case S-MEM:
FirstByte S-MEM-Store

8         0
24        0
40        0
56        0
72        0
88        0
104       0
              
4         0
20        0
36        0
52        0
              
2         0
18        1
34        0
50        0
66        0
82        0
98        0
              
1         0
17        0
33        0
49        0
65        0
81        0
97        0
              
128       0
144       1
160       0
176       0
192       0
208       0
224       0
240       0
*/

/* Test case S-MDR:
FirstByte ~{S-MDR-WriteALU} ~{S-MDR-WriteMEM}

8         1            1
24        1            1
40        1            1
56        1            1
72        1            1
88        1            1
104       1            1
              
4         1            1
20        1            1
36        1            1
52        1            1
              
2         1            0
18        1            1
34        1            1
50        1            1
66        1            1
82        1            1
98        1            1
              
1         1            1
17        1            1
33        1            1
49        0            1
65        1            1
81        1            1
97        1            1
              
128       1            0
144       1            1
160       1            1
176       1            1
192       1            1
208       1            1
224       1            1
240       1            1
*/

/* Test case S-CTL:
FirstByte S-CTL-Halt

8         0
24        0
40        0
56        0
72        0
88        0
104       0
              
4         0
20        0
36        0
52        0
              
2         0
18        0
34        0
50        0
66        0
82        0
98        0
              
1         0
17        1
33        0
49        0
65        0
81        0
97        0
              
128       0
144       0
160       0
176       0
192       0
208       0
224       0
240       0
*/
