// Digital circuit old_RPC.dig as structural Verilog
module old_RPC (
  input  Clk_write,
  input  Reg_write,
  input  nReg_write,
  input  Add_write,
  input  nAdd_write,
  input  [11:0] Add_in,
  input  [11:0] Reg_in,
  output [11:0] Address
);

  wire and_2_1_1__1_y, and_2_1_1__2_y, and_2_1_1__3_y, and_2_1_1__4_y, and_2_1_2__1_y, and_2_1_2__2_y,
       and_2_1_2__3_y, and_2_1_2__4_y, buffer_8_1_1__1_y, buffer_8_1_1__2_y, buffer_8_1_1__3_y,
       buffer_8_1_1__4_y, buffer_8_1_1__5_y, buffer_8_1_1__6_y, buffer_8_1_1__7_y, buffer_8_1_1__8_y,
       or_2_1_1__1_y, or_2_1_1__2_y, or_2_1_1__3_y, or_2_1_1__4_y;

  Buffer_8_1 buffer_8_1_1 (
    .nOE1(nAdd_write), ._1_Y(buffer_8_1_1__1_y), .VCC(1'b1), .GND(1'b0), ._1_A(Add_in[11]),
    ._2_A(Add_in[10]), ._2_Y(buffer_8_1_1__2_y), ._4_A(Add_in[8]), ._5_A(Add_in[7]),
    ._3_Y(buffer_8_1_1__3_y), ._3_A(Add_in[9]), .nOE2(1'b0), ._4_Y(buffer_8_1_1__4_y), ._6_A(Add_in[6]),
    ._7_A(Add_in[5]), ._8_A(Add_in[4]), ._5_Y(buffer_8_1_1__5_y), ._6_Y(buffer_8_1_1__6_y),
    ._7_Y(buffer_8_1_1__7_y), ._8_Y(buffer_8_1_1__8_y));
  D_Flip_Flop d_flip_flop_1 (
    .EN(1'b0), ._1_Q(Address[4]), .VCC(1'b1), .GND(1'b0), ._1_D(buffer_8_1_1__8_y), ._2_D(buffer_8_1_1__7_y),
    ._3_Q(Address[6]), .CLK(Clk_write), ._2_Q(Address[5]), ._3_D(buffer_8_1_1__6_y),
    ._4_D(buffer_8_1_1__5_y), ._4_Q(Address[7]), ._5_Q(Address[8]), ._5_D(buffer_8_1_1__4_y),
    ._6_D(buffer_8_1_1__3_y), ._7_Q(Address[10]), ._6_Q(Address[9]), ._7_D(buffer_8_1_1__2_y),
    ._8_D(buffer_8_1_1__1_y), ._8_Q(Address[11]));
  AND_2_1 and_2_1_1 (
    ._1_A(Add_in[3]), ._1_Y(and_2_1_1__1_y), .VCC(1'b1), .GND(1'b0), ._1_B(Add_write), ._2_A(Add_in[2]),
    ._2_Y(and_2_1_1__2_y), ._2_B(Add_write), ._3_B(Add_in[1]), ._3_Y(and_2_1_1__3_y), ._3_A(Add_write),
    ._4_B(Add_in[0]), ._4_Y(and_2_1_1__4_y), ._4_A(Add_write));
  LED _7 (.in(buffer_8_1_1__5_y));
  LED _4 (.in(buffer_8_1_1__8_y));
  LED _5 (.in(buffer_8_1_1__7_y));
  LED _6 (.in(buffer_8_1_1__6_y));
  LED _0 (.in(and_2_1_1__4_y));
  LED _1 (.in(and_2_1_1__3_y));
  LED _2 (.in(and_2_1_1__2_y));
  LED _3 (.in(and_2_1_1__1_y));
  LED _11 (.in(buffer_8_1_1__1_y));
  LED _10 (.in(buffer_8_1_1__2_y));
  LED _9 (.in(buffer_8_1_1__3_y));
  LED _8 (.in(buffer_8_1_1__4_y));
  LED _0_2 (.in(or_2_1_1__4_y));
  LED _1_2 (.in(or_2_1_1__3_y));
  LED _2_2 (.in(or_2_1_1__2_y));
  LED _3_2 (.in(or_2_1_1__1_y));
  D_Flip_Flop d_flip_flop_2 (
    .EN(1'b0), ._1_Q(Address[0]), .VCC(1'b1), .GND(1'b0), ._1_D(or_2_1_1__4_y), ._2_D(or_2_1_1__3_y),
    ._3_Q(Address[2]), .CLK(Clk_write), ._2_Q(Address[1]), ._3_D(or_2_1_1__2_y), ._4_D(or_2_1_1__1_y),
    ._4_Q(Address[3]), ._5_D(1'b0), ._6_D(1'b0), ._7_D(1'b0), ._8_D(1'b0));  // open: _5_Q, _7_Q, _6_Q, _8_Q
  OR_2_1 or_2_1_1 (
    ._1_A(and_2_1_2__1_y), ._1_Y(or_2_1_1__1_y), .VCC(1'b1), .GND(1'b0), ._1_B(and_2_1_1__1_y),
    ._2_A(and_2_1_2__2_y), ._2_Y(or_2_1_1__2_y), ._2_B(and_2_1_1__2_y), ._3_B(and_2_1_2__3_y),
    ._3_Y(or_2_1_1__3_y), ._3_A(and_2_1_1__3_y), ._4_B(and_2_1_2__4_y), ._4_Y(or_2_1_1__4_y),
    ._4_A(and_2_1_1__4_y));
  AND_2_1 and_2_1_2 (
    ._1_A(Reg_in[3]), ._1_Y(and_2_1_2__1_y), .VCC(1'b1), .GND(1'b0), ._1_B(Reg_write), ._2_A(Reg_in[2]),
    ._2_Y(and_2_1_2__2_y), ._2_B(Reg_write), ._3_B(Reg_in[1]), ._3_Y(and_2_1_2__3_y), ._3_A(Reg_write),
    ._4_B(Reg_in[0]), ._4_Y(and_2_1_2__4_y), ._4_A(Reg_write));
  Buffer_8_1 buffer_8_1_2 (
    .nOE1(1'b0), ._1_Y(buffer_8_1_1__8_y), .VCC(1'b1), .GND(1'b0), ._1_A(Reg_in[4]), ._2_A(Reg_in[5]),
    ._2_Y(buffer_8_1_1__7_y), ._4_A(Reg_in[7]), ._5_A(Reg_in[8]), ._3_Y(buffer_8_1_1__6_y), ._3_A(Reg_in[6]),
    .nOE2(nReg_write), ._4_Y(buffer_8_1_1__5_y), ._6_A(Reg_in[9]), ._7_A(Reg_in[10]), ._8_A(Reg_in[11]),
    ._5_Y(buffer_8_1_1__4_y), ._6_Y(buffer_8_1_1__3_y), ._7_Y(buffer_8_1_1__2_y), ._8_Y(buffer_8_1_1__1_y));
  LED _1_3 (.in(Reg_in[1]));
  LED _2_3 (.in(Reg_in[2]));
  LED _3_3 (.in(Reg_in[3]));
  LED _0_3 (.in(Reg_in[0]));

  // Notes on the sheet:
  //   Add_in: pin 1
  //   Reg_in: pin 19
  //   Address: pin 20
  //   Width
  //   44 holes
  //   11 cm
  //   Height
  //   52 holes
  //   13 cm
endmodule
