// Digital circuit old_SCU.dig as structural Verilog
module old_SCU (
  input  [3:0] Nibble_2,
  input  IsOpcodeNibble,
  input  [7:0] Counter,
  input  [7:0] FirstByte,
  input  [7:0] SecondByte,
  output S_ALU_Increment,
  output S_ALU_UseCarry,
  output S_BRA_Unconditional,
  output S_BRA_Greater,
  output S_BRA_Equal,
  output S_BRA_Less,
  output S_BRA_NotEqual,
  output S_CTL_Halt,
  output S_MDR_WriteALU,
  output S_REG_WriteVAL,
  output S_REG_WriteMDR,
  output S_INS_ValRead,
  output S_ADR_Direct,
  output S_ADR_Immediate,
  output S_ALU_CarryOut,
  output S_ALU_OrOut,
  output S_ALU_Propagate,
  output S_ALU_ResultOut,
  output S_ALU_FlagWrite,
  output S_INS_RegReadSecond,
  output S_ALU_Invert,
  output S_INS_RegReadFirst,
  output S_REG_WriteALU,
  output S_MDR_WriteMEM,
  output S_MEM_Store
);

  wire and_2_1_1__2_y, and_2_1_1__3_y, and_2_1_1__4_y, and_2_1_2__1_y, and_2_1_2__2_y, and_2_1_2__3_y,
       and_2_1_3__2_y, and_2_1_3__3_y, and_2_1_3__4_y, and_2_1_4__1_y, and_2_1_4__2_y, and_2_1_4__3_y,
       and_2_1_4__4_y, and_2_1_5__1_y, and_2_1_5__4_y, and_2_1_6__3_y, and_2_1_7__2_y, decoder_1_out_0,
       decoder_1_out_1, decoder_1_out_2, decoder_1_out_3, decoder_1_out_4, decoder_1_out_5, decoder_1_out_6,
       decoder_1_out_7, not_1_1_1__1_y, not_1_1_1__2_y, not_1_1_1__3_y, or_2_1_1__1_y, or_2_1_1__2_y,
       or_2_1_1__3_y, or_2_1_1__4_y, or_2_1_2__1_y, or_2_1_2__2_y, or_2_1_2__3_y, or_2_1_2__4_y,
       or_2_1_3__1_y, or_2_1_3__2_y, or_2_1_3__3_y, or_2_1_3__4_y, or_2_1_4__1_y, or_2_1_4__2_y,
       or_2_1_4__3_y, or_2_1_4__4_y, or_2_1_5__4_y, or_2_1_6__1_y, or_2_1_6__3_y, or_2_1_6__4_y,
       or_2_1_7__2_y, or_2_1_7__4_y, or_2_1_8__1_y, or_2_1_8__4_y;

  Decoder #(.Selector_Bits(3)) decoder_1 (
    .sel(FirstByte[6:4]), .out_0(decoder_1_out_0), .out_1(decoder_1_out_1), .out_2(decoder_1_out_2),
    .out_3(decoder_1_out_3), .out_4(decoder_1_out_4), .out_5(decoder_1_out_5), .out_6(decoder_1_out_6),
    .out_7(decoder_1_out_7));
  OR_2_1 or_2_1_1 (
    ._1_A(decoder_1_out_1), ._1_Y(or_2_1_1__1_y), .VCC(1'b1), .GND(1'b0), ._1_B(decoder_1_out_3),
    ._2_A(decoder_1_out_2), ._2_Y(or_2_1_1__2_y), ._2_B(decoder_1_out_3), ._3_B(decoder_1_out_6),
    ._3_Y(or_2_1_1__3_y), ._3_A(or_2_1_1__2_y), ._4_B(or_2_1_1__3_y), ._4_Y(or_2_1_1__4_y),
    ._4_A(decoder_1_out_4));
  OR_2_1 or_2_1_2 (
    ._1_A(decoder_1_out_4), ._1_Y(or_2_1_2__1_y), .VCC(1'b1), .GND(1'b0), ._1_B(decoder_1_out_5),
    ._2_A(decoder_1_out_0), ._2_Y(or_2_1_2__2_y), ._2_B(decoder_1_out_3), ._3_B(decoder_1_out_1),
    ._3_Y(or_2_1_2__3_y), ._3_A(decoder_1_out_2), ._4_B(or_2_1_1__3_y), ._4_Y(or_2_1_2__4_y),
    ._4_A(decoder_1_out_5));
  NOT_1_1 not_1_1_1 (
    ._1_A(decoder_1_out_6), ._1_Y(not_1_1_1__1_y), ._2_A(or_2_1_2__1_y), ._2_Y(not_1_1_1__2_y),
    ._3_A(decoder_1_out_7), ._3_Y(not_1_1_1__3_y), ._4_A(1'b0), .VCC(1'b1), .GND(1'b0), ._5_A(1'b0),
    ._6_A(1'b0));  // open: _4_Y, _5_Y, _6_Y
  OR_2_1 or_2_1_3 (
    ._1_A(or_2_1_2__3_y), ._1_Y(or_2_1_3__1_y), .VCC(1'b1), .GND(1'b0), ._1_B(decoder_1_out_0),
    ._2_A(decoder_1_out_2), ._2_Y(or_2_1_3__2_y), ._2_B(decoder_1_out_3), ._3_B(decoder_1_out_6),
    ._3_Y(or_2_1_3__3_y), ._3_A(decoder_1_out_5), ._4_B(decoder_1_out_2), ._4_Y(or_2_1_3__4_y),
    ._4_A(decoder_1_out_5));
  OR_2_1 or_2_1_4 (
    ._1_A(decoder_1_out_3), ._1_Y(or_2_1_4__1_y), .VCC(1'b1), .GND(1'b0), ._1_B(decoder_1_out_4),
    ._2_A(decoder_1_out_5), ._2_Y(or_2_1_4__2_y), ._2_B(decoder_1_out_6), ._3_B(FirstByte[1]),
    ._3_Y(or_2_1_4__3_y), ._3_A(FirstByte[7]), ._4_B(or_2_1_4__1_y), ._4_Y(or_2_1_4__4_y),
    ._4_A(or_2_1_4__2_y));
  AND_2_1 and_2_1_1 (
    ._1_A(or_2_1_1__1_y), ._1_Y(S_ALU_UseCarry), .VCC(1'b1), .GND(1'b0), ._1_B(FirstByte[3]),
    ._2_A(or_2_1_1__4_y), ._2_Y(and_2_1_1__2_y), ._2_B(FirstByte[3]), ._3_B(FirstByte[3]),
    ._3_Y(and_2_1_1__3_y), ._3_A(or_2_1_2__4_y), ._4_B(FirstByte[3]), ._4_Y(and_2_1_1__4_y),
    ._4_A(not_1_1_1__1_y));
  AND_2_1 and_2_1_2 (
    ._1_A(FirstByte[3]), ._1_Y(and_2_1_2__1_y), .VCC(1'b1), .GND(1'b0), ._1_B(not_1_1_1__2_y),
    ._2_A(decoder_1_out_3), ._2_Y(and_2_1_2__2_y), ._2_B(FirstByte[2]), ._3_B(FirstByte[2]),
    ._3_Y(and_2_1_2__3_y), ._3_A(or_2_1_2__2_y), ._4_B(FirstByte[2]), ._4_Y(S_ALU_CarryOut),
    ._4_A(decoder_1_out_1));
  AND_2_1 and_2_1_3 (
    ._1_A(FirstByte[2]), ._1_Y(S_ALU_OrOut), .VCC(1'b1), .GND(1'b0), ._1_B(decoder_1_out_2),
    ._2_A(FirstByte[1]), ._2_Y(and_2_1_3__2_y), ._2_B(decoder_1_out_0), ._3_B(FirstByte[1]),
    ._3_Y(and_2_1_3__3_y), ._3_A(decoder_1_out_1), ._4_B(FirstByte[0]), ._4_Y(and_2_1_3__4_y),
    ._4_A(decoder_1_out_5));
  AND_2_1 and_2_1_4 (
    ._1_A(or_2_1_3__1_y), ._1_Y(and_2_1_4__1_y), .VCC(1'b1), .GND(1'b0), ._1_B(FirstByte[2]),
    ._2_A(FirstByte[0]), ._2_Y(and_2_1_4__2_y), ._2_B(or_2_1_3__3_y), ._3_B(FirstByte[0]),
    ._3_Y(and_2_1_4__3_y), ._3_A(or_2_1_3__4_y), ._4_B(FirstByte[0]), ._4_Y(and_2_1_4__4_y),
    ._4_A(decoder_1_out_2));
  AND_2_1 and_2_1_5 (
    ._1_A(or_2_1_3__2_y), ._1_Y(and_2_1_5__1_y), .VCC(1'b1), .GND(1'b0), ._1_B(FirstByte[0]),
    ._2_A(FirstByte[0]), ._2_Y(S_REG_WriteMDR), ._2_B(decoder_1_out_4), ._3_B(FirstByte[0]),
    ._3_Y(S_CTL_Halt), ._3_A(decoder_1_out_1), ._4_B(or_2_1_4__4_y), ._4_Y(and_2_1_5__4_y),
    ._4_A(FirstByte[0]));
  AND_2_1 and_2_1_6 (
    ._1_A(not_1_1_1__3_y), ._1_Y(S_ADR_Immediate), .VCC(1'b1), .GND(1'b0), ._1_B(FirstByte[7]),
    ._2_A(FirstByte[0]), ._2_Y(S_MDR_WriteALU), ._2_B(decoder_1_out_3), ._3_B(decoder_1_out_0),
    ._3_Y(and_2_1_6__3_y), ._3_A(FirstByte[7]), ._4_B(FirstByte[7]), ._4_Y(S_REG_WriteVAL),
    ._4_A(decoder_1_out_7));
  AND_2_1 and_2_1_7 (
    ._1_A(decoder_1_out_2), ._1_Y(S_BRA_Unconditional), .VCC(1'b1), .GND(1'b0), ._1_B(or_2_1_4__3_y),
    ._2_A(FirstByte[7]), ._2_Y(and_2_1_7__2_y), ._2_B(decoder_1_out_1), ._3_B(or_2_1_4__3_y),
    ._3_Y(S_BRA_Less), ._3_A(decoder_1_out_4), ._4_B(or_2_1_4__3_y), ._4_Y(S_BRA_Equal),
    ._4_A(decoder_1_out_5));
  AND_2_1 and_2_1_8 (
    ._1_A(decoder_1_out_3), ._1_Y(S_BRA_Greater), .VCC(1'b1), .GND(1'b0), ._1_B(or_2_1_4__3_y),
    ._2_A(or_2_1_4__3_y), ._2_Y(S_BRA_NotEqual), ._2_B(decoder_1_out_6), ._3_B(1'b0), ._3_A(1'b0),
    ._4_B(1'b0), ._4_A(1'b0));  // open: _3_Y, _4_Y
  LED INS_RegReadFirst (.in(FirstByte[2]));
  LED REG_WriteALU (.in(FirstByte[2]));
  LED ALU_Increment (.in(and_2_1_1__2_y));
  LED ALU_UseCarry (.in(S_ALU_UseCarry));
  LED ALU_Propagate (.in(FirstByte[3]));
  LED ALU_ResultOut (.in(FirstByte[3]));
  LED ALU_Invert (.in(and_2_1_1__3_y));
  LED REG_WriteALU_2 (.in(FirstByte[3]));
  LED ALU_Invert_2 (.in(and_2_1_2__2_y));
  LED INS_RegReadFirst_2 (.in(and_2_1_2__1_y));
  LED ALU_FlagWrite (.in(FirstByte[2]));
  LED INS_RegReadSecond (.in(FirstByte[1]));
  LED INS_RegReadFirst_3 (.in(FirstByte[1]));
  LED ADR_Direct (.in(FirstByte[1]));
  LED ALU_Increment_2 (.in(and_2_1_3__4_y));
  LED ALU_Invert_3 (.in(and_2_1_3__4_y));
  LED INS_RegReadSecond_2 (.in(and_2_1_4__1_y));
  LED ALU_FlagWrite_2 (.in(and_2_1_4__2_y));
  LED ALU_ResultOut_2 (.in(and_2_1_5__1_y));
  LED MDR_WriteALU (.in(S_MDR_WriteALU));
  LED REG_WriteMDR (.in(S_REG_WriteMDR));
  LED ADR_Immediate (.in(S_ADR_Immediate));
  LED INS_ValRead (.in(FirstByte[7]));
  LED MEM_Store (.in(and_2_1_7__2_y));
  LED BRA_Less (.in(S_BRA_Less));
  LED BRA_Equal (.in(S_BRA_Equal));
  LED BRA_Unconditional (.in(S_BRA_Unconditional));
  LED ALU_FlagWrite_3 (.in(FirstByte[3]));
  LED INS_RegReadSecond_3 (.in(and_2_1_1__4_y));
  LED ALU_CarryOut (.in(S_ALU_CarryOut));
  LED ALU_ResultOut_3 (.in(and_2_1_2__3_y));
  LED MDR_WriteMem (.in(and_2_1_3__2_y));
  LED ALU_OrOut (.in(S_ALU_OrOut));
  LED ALU_Propagate_2 (.in(and_2_1_3__4_y));
  LED MEM_Store_2 (.in(and_2_1_3__3_y));
  LED INS_RegReadFirst_4 (.in(and_2_1_4__3_y));
  LED REG_WriteALU_3 (.in(and_2_1_4__4_y));
  LED INS_RegReadSecond_4 (.in(and_2_1_5__4_y));
  LED CTL_Halt (.in(S_CTL_Halt));
  LED MDR_WriteMem_2 (.in(and_2_1_6__3_y));
  LED REG_WriteVAL (.in(S_REG_WriteVAL));
  LED BRA_NotEqual (.in(S_BRA_NotEqual));
  LED BRA_Greater (.in(S_BRA_Greater));
  OR_2_1 or_2_1_5 (
    ._1_A(and_2_1_1__2_y), ._1_Y(S_ALU_Increment), .VCC(1'b1), .GND(1'b0), ._1_B(and_2_1_3__4_y),
    ._2_A(FirstByte[3]), ._2_Y(S_ALU_Propagate), ._2_B(and_2_1_3__4_y), ._3_B(or_2_1_5__4_y),
    ._3_Y(S_ALU_ResultOut), ._3_A(FirstByte[3]), ._4_B(and_2_1_5__1_y), ._4_Y(or_2_1_5__4_y),
    ._4_A(and_2_1_2__3_y));
  OR_2_1 or_2_1_6 (
    ._1_A(FirstByte[3]), ._1_Y(or_2_1_6__1_y), .VCC(1'b1), .GND(1'b0), ._1_B(and_2_1_4__2_y),
    ._2_A(or_2_1_6__1_y), ._2_Y(S_ALU_FlagWrite), ._2_B(FirstByte[2]), ._3_B(or_2_1_6__4_y),
    ._3_Y(or_2_1_6__3_y), ._3_A(and_2_1_1__4_y), ._4_B(FirstByte[1]), ._4_Y(or_2_1_6__4_y),
    ._4_A(and_2_1_4__1_y));
  OR_2_1 or_2_1_7 (
    ._1_A(or_2_1_6__3_y), ._1_Y(S_INS_RegReadSecond), .VCC(1'b1), .GND(1'b0), ._1_B(and_2_1_5__4_y),
    ._2_A(and_2_1_1__3_y), ._2_Y(or_2_1_7__2_y), ._2_B(and_2_1_2__2_y), ._3_B(and_2_1_3__4_y),
    ._3_Y(S_ALU_Invert), ._3_A(or_2_1_7__2_y), ._4_B(FirstByte[2]), ._4_Y(or_2_1_7__4_y),
    ._4_A(and_2_1_2__1_y));
  OR_2_1 or_2_1_8 (
    ._1_A(FirstByte[1]), ._1_Y(or_2_1_8__1_y), .VCC(1'b1), .GND(1'b0), ._1_B(or_2_1_7__4_y),
    ._2_A(or_2_1_8__1_y), ._2_Y(S_INS_RegReadFirst), ._2_B(and_2_1_4__3_y), ._3_B(or_2_1_8__4_y),
    ._3_Y(S_REG_WriteALU), ._3_A(FirstByte[2]), ._4_B(and_2_1_4__4_y), ._4_Y(or_2_1_8__4_y),
    ._4_A(FirstByte[3]));
  OR_2_1 or_2_1_9 (
    ._1_A(and_2_1_3__2_y), ._1_Y(S_MDR_WriteMEM), .VCC(1'b1), .GND(1'b0), ._1_B(and_2_1_6__3_y),
    ._2_A(and_2_1_3__3_y), ._2_Y(S_MEM_Store), ._2_B(and_2_1_7__2_y), ._3_B(1'b0), ._3_A(1'b0), ._4_B(1'b0),
    ._4_A(1'b0));  // open: _3_Y, _4_Y
  AND_2_1 and_2_1_9 ();  // open: _1_A, _1_Y, VCC, GND, _1_B, _2_A, _2_Y, _2_B, _3_B, _3_Y, _3_A, _4_B, _4_Y, _4_A
  AND_2_1 and_2_1_10 ();  // open: _1_A, _1_Y, VCC, GND, _1_B, _2_A, _2_Y, _2_B, _3_B, _3_Y, _3_A, _4_B, _4_Y, _4_A
  OR_2_1 or_2_1_10 ();  // open: _1_A, _1_Y, VCC, GND, _1_B, _2_A, _2_Y, _2_B, _3_B, _3_Y, _3_A, _4_B, _4_Y, _4_A
  OR_2_1 or_2_1_11 ();  // open: _1_A, _1_Y, VCC, GND, _1_B, _2_A, _2_Y, _2_B, _3_B, _3_Y, _3_A, _4_B, _4_Y, _4_A
  OR_2_1 or_2_1_12 ();  // open: _1_A, _1_Y, VCC, GND, _1_B, _2_A, _2_Y, _2_B, _3_B, _3_Y, _3_A, _4_B, _4_Y, _4_A
  OR_2_1 or_2_1_13 ();  // open: _1_A, _1_Y, VCC, GND, _1_B, _2_A, _2_Y, _2_B, _3_B, _3_Y, _3_A, _4_B, _4_Y, _4_A
  OR_2_1 or_2_1_14 ();  // open: _1_A, _1_Y, VCC, GND, _1_B, _2_A, _2_Y, _2_B, _3_B, _3_Y, _3_A, _4_B, _4_Y, _4_A
  AND_2_1 and_2_1_11 ();  // open: _1_A, _1_Y, VCC, GND, _1_B, _2_A, _2_Y, _2_B, _3_B, _3_Y, _3_A, _4_B, _4_Y, _4_A
  AND_2_1 and_2_1_12 ();  // open: _1_A, _1_Y, VCC, GND, _1_B, _2_A, _2_Y, _2_B, _3_B, _3_Y, _3_A, _4_B, _4_Y, _4_A
  OR_2_1 or_2_1_15 ();  // open: _1_A, _1_Y, VCC, GND, _1_B, _2_A, _2_Y, _2_B, _3_B, _3_Y, _3_A, _4_B, _4_Y, _4_A
  NOT_1_1 not_1_1_2 ();  // open: _1_A, _1_Y, _2_A, _2_Y, _3_A, _3_Y, _4_A, _4_Y, VCC, GND, _5_A, _5_Y, _6_A, _6_Y
  NOT_1_1 not_1_1_3 ();  // open: _1_A, _1_Y, _2_A, _2_Y, _3_A, _3_Y, _4_A, _4_Y, VCC, GND, _5_A, _5_Y, _6_A, _6_Y
  NOT_1_1 not_1_1_4 ();  // open: _1_A, _1_Y, _2_A, _2_Y, _3_A, _3_Y, _4_A, _4_Y, VCC, GND, _5_A, _5_Y, _6_A, _6_Y

  assign S_ADR_Direct = FirstByte[1];
  assign S_INS_ValRead = FirstByte[7];

  // Notes on the sheet:
  //   Nibble_2: pin 2
  //   IsOpcodeNibble: pin 40
  //   Counter: pin 1
  //   Testing
endmodule

/* Test case ALU:
FirstByte S-ALU-UseCarry S-ALU-Increment S-ALU-Invert S-ALU-Propagate S-ALU-ResultOut S-ALU-CarryOut S-ALU-OrOut S-ALU-FlagWrite

8         0            0             0          1             1             0            0         1
24        1            0             0          1             1             0            0         1
40        0            1             1          1             1             0            0         1
56        1            1             1          1             1             0            0         1
72        0            1             0          1             1             0            0         1
88        0            0             1          1             1             0            0         1
104       0            1             1          1             1             0            0         1

4         0            0             0          0             1             0            0         1
20        0            0             0          0             0             1            0         1
36        0            0             0          0             0             0            1         1
52        0            0             1          0             1             0            0         1

2         0            0             0          0             0             0            0         0
18        0            0             0          0             0             0            0         0
34        0            0             0          0             0             0            0         0
50        0            0             0          0             0             0            0         0
66        0            0             0          0             0             0            0         0
82        0            0             0          0             0             0            0         0
98        0            0             0          0             0             0            0         0

1         0            0             0          0             0             0            0         0
17        0            0             0          0             0             0            0         0
33        0            0             0          0             1             0            0         0
49        0            0             0          0             1             0            0         0
65        0            0             0          0             0             0            0         0
81        0            1             1          1             0             0            0         1
97        0            0             0          0             0             0            0         1

128       0            0             0          0             0             0            0         0
144       0            0             0          0             0             0            0         0
160       0            0             0          0             0             0            0         0
176       0            0             0          0             0             0            0         0
192       0            0             0          0             0             0            0         0
208       0            0             0          0             0             0            0         0
224       0            0             0          0             0             0            0         0
240       0            0             0          0             0             0            0         0
*/

/* Test case ADR:
FirstByte S-ADR-Immediate S-ADR-Direct

8         0             0
24        0             0
40        0             0
56        0             0
72        0             0
88        0             0
104       0             0

4         0             0
20        0             0
36        0             0
52        0             0

2         0             1
18        0             1
34        0             1
50        0             1
66        0             1
82        0             1
98        0             1

1         0             0
17        0             0
33        0             0
49        0             0
65        0             0
81        0             0
97        0             0

128       1             0
144       1             0
160       1             0
176       1             0
192       1             0
208       1             0
224       1             0
240       0             0
*/

/* Test case BRA:
FirstByte S-BRA-Unconditional S-BRA-Greater S-BRA-Less S-BRA-Equal S-BRA-NotEqual

8         0                 0           0        0         0
24        0                 0           0        0         0
40        0                 0           0        0         0
56        0                 0           0        0         0
72        0                 0           0        0         0
88        0                 0           0        0         0
104       0                 0           0        0         0

4         0                 0           0        0         0
20        0                 0           0        0         0
36        0                 0           0        0         0
52        0                 0           0        0         0

2         0                 0           0        0         0
18        0                 0           0        0         0
34        1                 0           0        0         0
50        0                 1           0        0         0
66        0                 0           1        0         0
82        0                 0           0        1         0
98        0                 0           0        0         1

1         0                 0           0        0         0
17        0                 0           0        0         0
33        0                 0           0        0         0
49        0                 0           0        0         0
65        0                 0           0        0         0
81        0                 0           0        0         0
97        0                 0           0        0         0

128       0                 0           0        0         0
144       0                 0           0        0         0
160       1                 0           0        0         0
176       0                 1           0        0         0
192       0                 0           1        0         0
208       0                 0           0        1         0
224       0                 0           0        0         1
240       0                 0           0        0         0
*/

/* Test case INS:
FirstByte S-INS-RegReadSecond S-INS-RegReadFirst S-INS-ValRead

8         1                1                 0
24        1                1                 0
40        1                1                 0
56        1                1                 0
72        1                0                 0
88        1                0                 0
104       0                1                 0
              
4         1                1                 0
20        1                1                 0
36        1                1                 0
52        0                1                 0
              
2         1                1                 0
18        1                1                 0
34        1                1                 0
50        1                1                 0
66        1                1                 0
82        1                1                 0
98        1                1                 0
              
1         0                0                 0
17        0                0                 0
33        0                1                 0
49        1                0                 0
65        1                0                 0
81        1                1                 0
97        1                0                 0
              
128       0                0                 1
144       0                0                 1
160       0                0                 1
176       0                0                 1
192       0                0                 1
208       0                0                 1
224       0                0                 1
240       0                0                 1
*/

/* Test case REG:
FirstByte S-REG-WriteALU S-REG-WriteMDR S-REG-WriteVAL

8         1                0		0
24        1                0		0
40        1                0		0
56        1                0		0
72        1                0		0
88        1                0		0
104       1                0		0
              
4         1                0		0
20        1                0		0
36        1                0		0
52        1                0		0
              
2         0                0		0
18        0                0		0
34        0                0		0
50        0                0		0
66        0                0		0
82        0                0		0
98        0                0		0
              
1         0                0		0
17        0                0		0
33        1                0		0
49        0                0		0
65        0                1		0
81        0                0		0
97        0                0		0
              
128       0                0		0
144       0                0		0
160       0                0		0
176       0                0		0
192       0                0		0
208       0                0		0
224       0                0		0
240       0                0		1
*/

/* Test case MEM:
FirstByte S-MEM-Store

8         0
24        0
40        0
56        0
72        0
88        0
104       0
              
4         0
20        0
36        0
52        0
              
2         0
18        1
34        0
50        0
66        0
82        0
98        0
              
1         0
17        0
33        0
49        0
65        0
81        0
97        0
              
128       0
144       1
160       0
176       0
192       0
208       0
224       0
240       0
*/

/* Test case MDR:
FirstByte S-MDR-WriteALU S-MDR-WriteMEM

8         0            0
24        0            0
40        0            0
56        0            0
72        0            0
88        0            0
104       0            0
              
4         0            0
20        0            0
36        0            0
52        0            0
              
2         0            1
18        0            0
34        0            0
50        0            0
66        0            0
82        0            0
98        0            0
              
1         0            0
17        0            0
33        0            0
49        1            0
65        0            0
81        0            0
97        0            0
              
128       0            1
144       0            0
160       0            0
176       0            0
192       0            0
208       0            0
224       0            0
240       0            0
*/

/* Test case CTL:
FirstByte S-CTL-Halt

8         0
24        0
40        0
56        0
72        0
88        0
104       0
              
4         0
20        0
36        0
52        0
              
2         0
18        0
34        0
50        0
66        0
82        0
98        0
              
1         0
17        1
33        0
49        0
65        0
81        0
97        0
              
128       0
144       0
160       0
176       0
192       0
208       0
224       0
240       0
*/
