// Digital circuit Addressor.dig as structural Verilog
module Addressor (
  input  [7:0] Data_direct1,
  input  [11:0] Data_imm,
  input  Enable_direct,
  input  Enable_imm,
  input  [7:0] Data_direct2,
  output [11:0] Data_out
);

  assign Data_out = Enable_direct ? {Data_direct2[3:0], Data_direct1} : 12'bz;  // Driver driver_1
  assign Data_out = Enable_imm ? Data_imm : 12'bz;  // Driver driver_2

  // Notes on the sheet:
  //   Data_direct1: pin 1
  //   Data_imm: pin 3
  //   Data_out: pin 5
  //   Enable_direct: pin 8
  //   Enable_imm: pin 7
  //   Data_direct2: pin 2
endmodule
