// Digital circuit SRAM.dig as structural Verilog
module SRAM (
  input  [15:0] Address_in,
  input  Store,
  input  Clk_write,
  input  [7:0] Data_in,
  output [7:0] Data_out
);

  wire not_1_out;
  wire [7:0] ramsingleport_1_d;

  not not_1 (not_1_out, Store);
  RAMSinglePort #(.AddrBits(13), .Bits(8)) ramsingleport_1 (
    .A(Address_in[12:0]), .str(Store), .C(Clk_write), .ld(not_1_out), .D(ramsingleport_1_d));
  assign ramsingleport_1_d = Store ? Data_in : 8'bz;  // Driver driver_1
  assign Data_out = not_1_out ? ramsingleport_1_d : 8'bz;  // Driver driver_2

  // Notes on the sheet:
  //   Address_in: pin 6
  //   Store: pin 3
  //   Clk_write: pin 1
  //   Data_out: pin 4
  //   Data_in: pin 5
endmodule

/* Test case:
	Clk_write Store Load Address_in Data_in Data_out
loop(a, 256)
	let data = random(1<<8);
	let address = random(1<<16);

	0	  1 	0    (address)  (data)  X
	1	  1 	0    (address)  (data)  X

	0	  0 	1    (address)  0       X
	1	  0 	1    (address)  0       (data)
end loop
*/
