// Digital circuit Flags.dig as structural Verilog
module Flags (
  input  Less_in,
  input  Greater_in,
  input  Equal_in,
  input  Carry_in,
  input  Clock,
  input  NotEqual_in,
  output Less_out,
  output Greater_out,
  output Equal_out,
  output Carry_out,
  output NotEqual_out
);

  D_FF #(.Bits(4)) d_ff_1 (
    .D({NotEqual_in, Equal_in, Less_in, Greater_in}), .C(Clock),
    .Q({NotEqual_out, Equal_out, Less_out, Greater_out}));  // open: nQ
  // Pins of 4 and 5 bits meet at {Carry_in, NotEqual_in, Equal_in, Less_in, Greater_in}
  // Pins of 4 and 5 bits meet at {Carry_out, NotEqual_out, Equal_out, Less_out, Greater_out}

  // Notes on the sheet:
  //   Less_out: pin 10
  //   Less_in: pin 3
  //   Greater_in: pin 2
  //   Equal_in: pin 4
  //   Carry_in: pin 6
  //   Greater_out: pin 11
  //   Equal_out: pin 9
  //   Carry_out: pin 7
  //   Clock: pin 1
  //   NotEqual_out: pin 8
  //   NotEqual_in: pin 5
endmodule
