// Digital circuit ALU.dig as structural Verilog
module ALU (
  input  [7:0] Data_1_in,
  input  [7:0] Data_2_in,
  input  S_ALU_Invert,
  input  D_ALU_Increment,
  input  S_ALU_Propagate,
  input  nS_ALU_CarryOut,
  input  nS_ALU_ResultOut,
  input  nS_ALU_OrOut,
  input  D_WRT_Flags,
  output [7:0] Data_out,
  output F_Carry,
  output F_Greater,
  output F_Less,
  output F_Equal,
  output F_NotEqual
);

  wire and_2_1_1__1_y, and_2_1_1__2_y, and_2_1_2__1_y, and_2_1_2__2_y, and_2_1_2__3_y, and_2_1_2__4_y,
       and_2_1_3__1_y, and_2_1_3__2_y, and_2_1_3__3_y, and_2_1_3__4_y, and_2_1_4__1_y, and_2_1_4__2_y,
       and_2_1_4__3_y, and_2_1_4__4_y, and_2_1_5__1_y, and_2_1_5__2_y, and_2_1_5__3_y, and_2_1_5__4_y,
       and_2_1_6__1_y, and_2_1_6__2_y, and_2_1_6__3_y, and_2_1_6__4_y, and_2_1_7__1_y, and_2_1_7__2_y,
       and_2_1_7__3_y, not_1_1_1__1_y, not_1_1_1__2_y, or_2_1_1__1_y, or_2_1_1__2_y, or_2_1_1__3_y,
       or_2_1_1__4_y, or_2_1_2__1_y, or_2_1_2__2_y, or_2_1_2__3_y, or_2_1_2__4_y, or_2_1_3__1_y,
       or_2_1_3__2_y, or_2_1_3__3_y, or_2_1_3__4_y, or_2_1_4__1_y, or_2_1_4__3_y, or_2_1_4__4_y,
       or_2_1_5__1_y, or_2_1_5__2_y, or_2_1_5__3_y, or_2_1_5__4_y, or_2_1_6__1_y, or_2_1_6__2_y,
       or_2_1_6__3_y, or_2_1_6__4_y, xor_2_1_1__1_y, xor_2_1_1__2_y, xor_2_1_1__3_y, xor_2_1_1__4_y,
       xor_2_1_2__1_y, xor_2_1_2__2_y, xor_2_1_2__3_y, xor_2_1_2__4_y, xor_2_1_3__1_y, xor_2_1_3__2_y,
       xor_2_1_3__3_y, xor_2_1_3__4_y, xor_2_1_4__1_y, xor_2_1_4__2_y, xor_2_1_4__3_y, xor_2_1_4__4_y,
       xor_2_1_5__1_y, xor_2_1_5__2_y, xor_2_1_5__3_y, xor_2_1_5__4_y, xor_2_1_6__1_y, xor_2_1_6__2_y,
       xor_2_1_6__3_y, xor_2_1_6__4_y;

  OR_2_1 or_2_1_1 (
    ._1_A(Data_2_in[7]), ._1_Y(or_2_1_1__1_y), .VCC(1'b1), .GND(1'b0), ._1_B(Data_1_in[7]),
    ._2_A(Data_2_in[6]), ._2_Y(or_2_1_1__2_y), ._2_B(Data_1_in[6]), ._3_B(Data_2_in[1]),
    ._3_Y(or_2_1_1__3_y), ._3_A(Data_1_in[1]), ._4_B(Data_2_in[0]), ._4_Y(or_2_1_1__4_y), ._4_A(Data_1_in[0]));
  OR_2_1 or_2_1_2 (
    ._1_A(Data_2_in[5]), ._1_Y(or_2_1_2__1_y), .VCC(1'b1), .GND(1'b0), ._1_B(Data_1_in[5]),
    ._2_A(Data_2_in[4]), ._2_Y(or_2_1_2__2_y), ._2_B(Data_1_in[4]), ._3_B(Data_2_in[3]),
    ._3_Y(or_2_1_2__3_y), ._3_A(Data_1_in[3]), ._4_B(Data_2_in[2]), ._4_Y(or_2_1_2__4_y), ._4_A(Data_1_in[2]));
  OR_2_1 or_2_1_3 (
    ._1_A(or_2_1_4__3_y), ._1_Y(or_2_1_3__1_y), .VCC(1'b1), .GND(1'b0), ._1_B(xor_2_1_6__2_y),
    ._2_A(or_2_1_3__1_y), ._2_Y(or_2_1_3__2_y), ._2_B(xor_2_1_6__3_y), ._3_B(or_2_1_3__4_y),
    ._3_Y(or_2_1_3__3_y), ._3_A(xor_2_1_3__3_y), ._4_B(xor_2_1_6__1_y), ._4_Y(or_2_1_3__4_y),
    ._4_A(xor_2_1_3__4_y));
  OR_2_1 or_2_1_4 (
    ._1_A(or_2_1_3__2_y), ._1_Y(or_2_1_4__1_y), .VCC(1'b1), .GND(1'b0), ._1_B(xor_2_1_6__4_y), ._2_A(1'b0),
    ._2_B(1'b0), ._3_B(or_2_1_4__4_y), ._3_Y(or_2_1_4__3_y), ._3_A(xor_2_1_3__1_y), ._4_B(or_2_1_3__3_y),
    ._4_Y(or_2_1_4__4_y), ._4_A(xor_2_1_3__2_y));  // open: _2_Y
  NOT_1_1 not_1_1_1 (
    ._1_A(xor_2_1_6__4_y), ._1_Y(not_1_1_1__1_y), ._2_A(or_2_1_4__1_y), ._2_Y(not_1_1_1__2_y), ._3_A(1'b0),
    ._4_A(1'b0), .VCC(1'b1), .GND(1'b0), ._5_A(1'b0), ._6_A(1'b0));  // open: _3_Y, _4_Y, _5_Y, _6_Y
  AND_2_1 and_2_1_1 (
    ._1_A(not_1_1_1__1_y), ._1_Y(and_2_1_1__1_y), .VCC(1'b1), .GND(1'b0), ._1_B(or_2_1_4__1_y),
    ._2_A(or_2_1_4__1_y), ._2_Y(and_2_1_1__2_y), ._2_B(xor_2_1_6__4_y), ._3_B(1'b0), ._3_A(1'b0),
    ._4_B(1'b0), ._4_A(1'b0));  // open: _3_Y, _4_Y
  D_Flip_Flop d_flip_flop_1 (
    .nEN(1'b0), ._1_Q(F_Carry), .VCC(1'b1), .GND(1'b0), ._1_D(or_2_1_6__4_y), ._2_D(and_2_1_1__1_y),
    ._3_Q(F_Less), .CLK(D_WRT_Flags), ._2_Q(F_Greater), ._3_D(and_2_1_1__2_y), ._4_D(not_1_1_1__2_y),
    ._4_Q(F_Equal), ._5_Q(F_NotEqual), ._5_D(or_2_1_4__1_y), ._6_D(1'b0), ._7_D(1'b0), ._8_D(1'b0));  // open: _7_Q, _6_Q, _8_Q
  Buffer_8_1 buffer_8_1_1 (
    .OE1(1'b0), ._1_Y(Data_out[0]), .VCC(1'b1), .GND(1'b0), ._1_A(or_2_1_1__4_y), ._2_A(or_2_1_1__3_y),
    ._2_Y(Data_out[1]), ._4_A(or_2_1_2__3_y), ._5_A(or_2_1_2__2_y), ._3_Y(Data_out[2]), ._3_A(or_2_1_2__4_y),
    .OE2(nS_ALU_OrOut), ._4_Y(Data_out[3]), ._6_A(or_2_1_2__1_y), ._7_A(or_2_1_1__2_y), ._8_A(or_2_1_1__1_y),
    ._5_Y(Data_out[4]), ._6_Y(Data_out[5]), ._7_Y(Data_out[6]), ._8_Y(Data_out[7]));
  Buffer_8_1 buffer_8_1_2 (
    .OE1(1'b0), ._1_Y(Data_out[0]), .VCC(1'b1), .GND(1'b0), ._1_A(xor_2_1_3__1_y), ._2_A(xor_2_1_3__2_y),
    ._2_Y(Data_out[1]), ._4_A(xor_2_1_3__4_y), ._5_A(xor_2_1_6__1_y), ._3_Y(Data_out[2]),
    ._3_A(xor_2_1_3__3_y), .OE2(nS_ALU_ResultOut), ._4_Y(Data_out[3]), ._6_A(xor_2_1_6__2_y),
    ._7_A(xor_2_1_6__3_y), ._8_A(xor_2_1_6__4_y), ._5_Y(Data_out[4]), ._6_Y(Data_out[5]), ._7_Y(Data_out[6]),
    ._8_Y(Data_out[7]));
  Buffer_8_1 buffer_8_1_3 (
    .OE1(1'b0), ._1_Y(Data_out[0]), .VCC(1'b1), .GND(1'b0), ._1_A(or_2_1_5__1_y), ._2_A(or_2_1_5__2_y),
    ._2_Y(Data_out[1]), ._4_A(or_2_1_5__4_y), ._5_A(or_2_1_6__1_y), ._3_Y(Data_out[2]), ._3_A(or_2_1_5__3_y),
    .OE2(nS_ALU_CarryOut), ._4_Y(Data_out[3]), ._6_A(or_2_1_6__2_y), ._7_A(or_2_1_6__3_y),
    ._8_A(or_2_1_6__4_y), ._5_Y(Data_out[4]), ._6_Y(Data_out[5]), ._7_Y(Data_out[6]), ._8_Y(Data_out[7]));
  LED S_1 (.in(xor_2_1_3__1_y));
  LED S_2 (.in(xor_2_1_3__2_y));
  LED C_1 (.in(or_2_1_5__1_y));
  LED C_2 (.in(or_2_1_5__2_y));
  XOR_2_1 xor_2_1_1 (
    ._1_A(S_ALU_Invert), ._1_Y(xor_2_1_1__1_y), .VCC(1'b1), .GND(1'b0), ._1_B(Data_2_in[0]),
    ._2_A(S_ALU_Invert), ._2_Y(xor_2_1_1__2_y), ._2_B(Data_2_in[1]), ._3_B(S_ALU_Invert),
    ._3_Y(xor_2_1_1__3_y), ._3_A(Data_2_in[2]), ._4_B(S_ALU_Invert), ._4_Y(xor_2_1_1__4_y),
    ._4_A(Data_2_in[3]));
  XOR_2_1 xor_2_1_2 (
    ._1_A(xor_2_1_1__1_y), ._1_Y(xor_2_1_2__1_y), .VCC(1'b1), .GND(1'b0), ._1_B(Data_1_in[0]),
    ._2_A(xor_2_1_1__2_y), ._2_Y(xor_2_1_2__2_y), ._2_B(Data_1_in[1]), ._3_B(xor_2_1_1__3_y),
    ._3_Y(xor_2_1_2__3_y), ._3_A(Data_1_in[2]), ._4_B(xor_2_1_1__4_y), ._4_Y(xor_2_1_2__4_y),
    ._4_A(Data_1_in[3]));
  AND_2_1 and_2_1_2 (
    ._1_A(xor_2_1_1__1_y), ._1_Y(and_2_1_2__1_y), .VCC(1'b1), .GND(1'b0), ._1_B(Data_1_in[0]),
    ._2_A(xor_2_1_1__2_y), ._2_Y(and_2_1_2__2_y), ._2_B(Data_1_in[1]), ._3_B(xor_2_1_1__3_y),
    ._3_Y(and_2_1_2__3_y), ._3_A(Data_1_in[2]), ._4_B(xor_2_1_1__4_y), ._4_Y(and_2_1_2__4_y),
    ._4_A(Data_1_in[3]));
  XOR_2_1 xor_2_1_3 (
    ._1_A(xor_2_1_2__1_y), ._1_Y(xor_2_1_3__1_y), .VCC(1'b1), .GND(1'b0), ._1_B(D_ALU_Increment),
    ._2_A(xor_2_1_2__2_y), ._2_Y(xor_2_1_3__2_y), ._2_B(and_2_1_4__1_y), ._3_B(xor_2_1_2__3_y),
    ._3_Y(xor_2_1_3__3_y), ._3_A(and_2_1_4__2_y), ._4_B(xor_2_1_2__4_y), ._4_Y(xor_2_1_3__4_y),
    ._4_A(and_2_1_4__3_y));
  AND_2_1 and_2_1_3 (
    ._1_A(D_ALU_Increment), ._1_Y(and_2_1_3__1_y), .VCC(1'b1), .GND(1'b0), ._1_B(xor_2_1_2__1_y),
    ._2_A(and_2_1_4__1_y), ._2_Y(and_2_1_3__2_y), ._2_B(xor_2_1_2__2_y), ._3_B(and_2_1_4__2_y),
    ._3_Y(and_2_1_3__3_y), ._3_A(xor_2_1_2__3_y), ._4_B(and_2_1_4__3_y), ._4_Y(and_2_1_3__4_y),
    ._4_A(xor_2_1_2__4_y));
  AND_2_1 and_2_1_4 (
    ._1_A(S_ALU_Propagate), ._1_Y(and_2_1_4__1_y), .VCC(1'b1), .GND(1'b0), ._1_B(or_2_1_5__1_y),
    ._2_A(S_ALU_Propagate), ._2_Y(and_2_1_4__2_y), ._2_B(or_2_1_5__2_y), ._3_B(S_ALU_Propagate),
    ._3_Y(and_2_1_4__3_y), ._3_A(or_2_1_5__3_y), ._4_B(S_ALU_Propagate), ._4_Y(and_2_1_4__4_y),
    ._4_A(or_2_1_5__4_y));
  OR_2_1 or_2_1_5 (
    ._1_A(and_2_1_3__1_y), ._1_Y(or_2_1_5__1_y), .VCC(1'b1), .GND(1'b0), ._1_B(and_2_1_2__1_y),
    ._2_A(and_2_1_3__2_y), ._2_Y(or_2_1_5__2_y), ._2_B(and_2_1_2__2_y), ._3_B(and_2_1_3__3_y),
    ._3_Y(or_2_1_5__3_y), ._3_A(and_2_1_2__3_y), ._4_B(and_2_1_3__4_y), ._4_Y(or_2_1_5__4_y),
    ._4_A(and_2_1_2__4_y));
  LED S_4 (.in(xor_2_1_3__4_y));
  LED S_3 (.in(xor_2_1_3__3_y));
  LED C_4 (.in(or_2_1_5__4_y));
  LED C_3 (.in(or_2_1_5__3_y));
  LED S_5 (.in(xor_2_1_6__1_y));
  LED S_6 (.in(xor_2_1_6__2_y));
  LED C_5 (.in(or_2_1_6__1_y));
  LED C_6 (.in(or_2_1_6__2_y));
  XOR_2_1 xor_2_1_4 (
    ._1_A(S_ALU_Invert), ._1_Y(xor_2_1_4__1_y), .VCC(1'b1), .GND(1'b0), ._1_B(Data_2_in[4]),
    ._2_A(S_ALU_Invert), ._2_Y(xor_2_1_4__2_y), ._2_B(Data_2_in[5]), ._3_B(S_ALU_Invert),
    ._3_Y(xor_2_1_4__3_y), ._3_A(Data_2_in[6]), ._4_B(S_ALU_Invert), ._4_Y(xor_2_1_4__4_y),
    ._4_A(Data_2_in[7]));
  XOR_2_1 xor_2_1_5 (
    ._1_A(xor_2_1_4__1_y), ._1_Y(xor_2_1_5__1_y), .VCC(1'b1), .GND(1'b0), ._1_B(Data_1_in[4]),
    ._2_A(xor_2_1_4__2_y), ._2_Y(xor_2_1_5__2_y), ._2_B(Data_1_in[5]), ._3_B(xor_2_1_4__3_y),
    ._3_Y(xor_2_1_5__3_y), ._3_A(Data_1_in[6]), ._4_B(xor_2_1_4__4_y), ._4_Y(xor_2_1_5__4_y),
    ._4_A(Data_1_in[7]));
  AND_2_1 and_2_1_5 (
    ._1_A(xor_2_1_4__1_y), ._1_Y(and_2_1_5__1_y), .VCC(1'b1), .GND(1'b0), ._1_B(Data_1_in[4]),
    ._2_A(xor_2_1_4__2_y), ._2_Y(and_2_1_5__2_y), ._2_B(Data_1_in[5]), ._3_B(xor_2_1_4__3_y),
    ._3_Y(and_2_1_5__3_y), ._3_A(Data_1_in[6]), ._4_B(xor_2_1_4__4_y), ._4_Y(and_2_1_5__4_y),
    ._4_A(Data_1_in[7]));
  XOR_2_1 xor_2_1_6 (
    ._1_A(xor_2_1_5__1_y), ._1_Y(xor_2_1_6__1_y), .VCC(1'b1), .GND(1'b0), ._1_B(and_2_1_4__4_y),
    ._2_A(xor_2_1_5__2_y), ._2_Y(xor_2_1_6__2_y), ._2_B(and_2_1_7__1_y), ._3_B(xor_2_1_5__3_y),
    ._3_Y(xor_2_1_6__3_y), ._3_A(and_2_1_7__2_y), ._4_B(xor_2_1_5__4_y), ._4_Y(xor_2_1_6__4_y),
    ._4_A(and_2_1_7__3_y));
  AND_2_1 and_2_1_6 (
    ._1_A(and_2_1_4__4_y), ._1_Y(and_2_1_6__1_y), .VCC(1'b1), .GND(1'b0), ._1_B(xor_2_1_5__1_y),
    ._2_A(and_2_1_7__1_y), ._2_Y(and_2_1_6__2_y), ._2_B(xor_2_1_5__2_y), ._3_B(and_2_1_7__2_y),
    ._3_Y(and_2_1_6__3_y), ._3_A(xor_2_1_5__3_y), ._4_B(and_2_1_7__3_y), ._4_Y(and_2_1_6__4_y),
    ._4_A(xor_2_1_5__4_y));
  AND_2_1 and_2_1_7 (
    ._1_A(S_ALU_Propagate), ._1_Y(and_2_1_7__1_y), .VCC(1'b1), .GND(1'b0), ._1_B(or_2_1_6__1_y),
    ._2_A(S_ALU_Propagate), ._2_Y(and_2_1_7__2_y), ._2_B(or_2_1_6__2_y), ._3_B(S_ALU_Propagate),
    ._3_Y(and_2_1_7__3_y), ._3_A(or_2_1_6__3_y), ._4_B(1'b0), ._4_A(1'b0));  // open: _4_Y
  OR_2_1 or_2_1_6 (
    ._1_A(and_2_1_6__1_y), ._1_Y(or_2_1_6__1_y), .VCC(1'b1), .GND(1'b0), ._1_B(and_2_1_5__1_y),
    ._2_A(and_2_1_6__2_y), ._2_Y(or_2_1_6__2_y), ._2_B(and_2_1_5__2_y), ._3_B(and_2_1_6__3_y),
    ._3_Y(or_2_1_6__3_y), ._3_A(and_2_1_5__3_y), ._4_B(and_2_1_6__4_y), ._4_Y(or_2_1_6__4_y),
    ._4_A(and_2_1_5__4_y));
  LED S_8 (.in(xor_2_1_6__4_y));
  LED S_7 (.in(xor_2_1_6__3_y));
  LED C_8 (.in(or_2_1_6__4_y));
  LED C_7 (.in(or_2_1_6__3_y));

  // Notes on the sheet:
  //   Data_1_in: pin 1
  //   Data_2_in: pin 2
  //   S_ALU_Invert: pin 3
  //   D_ALU_Increment: pin 7
  //   S_ALU_Propagate: pin 8
  //   nS_ALU_CarryOut: pin 9
  //   nS_ALU_ResultOut: pin 6
  //   nS_ALU_OrOut: pin 5
  //   Data_out: pin 4
  //   F_Carry: pin 10
  //   F_Greater: pin 11
  //   F_Less: pin 12
  //   F_Equal: pin 13
  //   F_NotEqual: pin 14
  //   D_WRT_Flags: pin 15
  //   Width
  //   52 holes
  //   13 cm
  //   Height
  //   110 holes
  //   27.5 cm
endmodule

/* Test case Add:
	Data-1_in Data-2_in Increment Invert Propagate ~{Out_carry} ~{Out_or} ~{Out_result} Data_out
loop(i, 512)
	let a = random(1<<8) - 128;
	let b = random(1<<8) - 128;
	(a)	  (b)	    0	      0      1         1            1         0             (a+b)
end loop
*/

/* Test case Decrement:
	Data-1_in Data-2_in Increment Invert Propagate ~{Out_carry} ~{Out_or} ~{Out_result} Data_out
loop(i, 512)
	let a = random(1<<8)-128;
	(a)	  0	    0	      1      1         1            1         0             (a-1)
end loop
*/

/* Test case Invert:
	Data-1_in Data-2_in Increment Invert Propagate ~{Out_carry} ~{Out_or} ~{Out_result} Data_out
loop(i, 512)
	let b = random(1<<8)-128;
	0	  (b)	    1	      1      1         1            1         0             (-b)
end loop
*/

/* Test case AND:
	Data-1_in Data-2_in Increment Invert Propagate ~{Out_carry} ~{Out_or} ~{Out_result} Data_out
loop(i, 512)
	let a = random(1<<8)-128;
	let b = random(1<<8)-128;
	(a)	  (b)	    0	      0      0         0            1         1             (a&b)
end loop
*/

/* Test case Sub:
	Data-1_in Data-2_in Increment Invert Propagate ~{Out_carry} ~{Out_or} ~{Out_result} Data_out
loop(i, 512)
	let a = random(1<<8) - 128;
	let b = random(1<<8) - 128;
	(a)	  (b)	    1	      1      1         1            1         0             (a-b)
end loop
*/

/* Test case Compare:
	Data-1_in Data-2_in D-WRT-Flags Increment Invert Propagate ~{Out_carry} ~{Out_or} ~{Out_result} Data_out Greater Less  Equal
loop(i, 512)
	let a = random(1<<7)-128;
	let b = random(1<<7)-128;
	(a)	  (b)       0		1	  1	 1	   1		1	  1		Z	 X	 X     X
	(a)	  (b)	    1           1	  1      1         1            1         1             Z        (a>b)   (a<b) (a=b)
end loop
*/

/* Test case NOT:
	Data-1_in Data-2_in Increment Invert Propagate ~{Out_carry} ~{Out_or} ~{Out_result} Data_out
loop(i, 512)
	let b = random(1<<8)-128;
	0	  (b)	    0	      1      0         1            1         0             (-b-1)
end loop
*/

/* Test case OR:
	Data-1_in Data-2_in Increment Invert Propagate ~{Out_carry} ~{Out_or} ~{Out_result} Data_out
loop(i, 512)
	let a = random(1<<8)-128;
	let b = random(1<<8)-128;
	(a)	  (b)	    0	      0      0         1            0         1             (a|b)
end loop
*/

/* Test case Increment:
	Data-1_in Data-2_in Increment Invert Propagate ~{Out_carry} ~{Out_or} ~{Out_result} Data_out
loop(i, 512)
	let a = random(1<<8)-128;
	(a)	  0	    1	      0      1         1            1         0             (a+1)
end loop
*/

/* Test case Test:
	Data-1_in Data-2_in D-WRT-Flags Increment Invert Propagate ~{Out_carry} ~{Out_or} ~{Out_result} Data_out Greater          Less    Equal
loop(i, 512)
	let a = random(1<<8);
	(a)	  0	    0           0	  0      0         1            1         1             Z        X                X       X
	(a)	  0	    1           0	  0      0         1            1         1             Z        (a<128 & a>0)   (a>127) (a=0)
end loop
*/

/* Test case XOR:
	Data-1_in Data-2_in Increment Invert Propagate ~{Out_carry} ~{Out_or} ~{Out_result} Data_out
loop(i, 512)
	let a = random(1<<8)-128;
	let b = random(1<<8)-128;
	(a)	  (b)	    0	      0      0         1            1         0             (a^b)
end loop
*/
