// Digital circuit CPU.dig as structural Verilog
module CPU (
  input  Pulse,
  input  Tick,
  output [7:0] Test_out
);

  wire alu_1_f_carry, alu_1_f_equal, alu_1_f_greater, alu_1_f_less, alu_1_f_notequal,
       programmemory_1_isopcodenibble, scu_1_d_alu_increment, scu_1_d_rpc_registers, scu_1_d_sel_first,
       scu_1_d_sel_second, scu_1_d_wrt_bufferfirst, scu_1_d_wrt_buffersecond, scu_1_d_wrt_cirfirst,
       scu_1_d_wrt_cirsecond, scu_1_d_wrt_flags, scu_1_d_wrt_mdr, scu_1_d_wrt_regoutput, scu_1_d_wrt_rpc,
       scu_1_nd_rpc_memadder, scu_1_nd_rpc_registers, scu_1_nd_wrt_sram, scu_1_ns_adr_direct,
       scu_1_ns_adr_immediate, scu_1_ns_alu_carryout, scu_1_ns_alu_orout, scu_1_ns_alu_resultout,
       scu_1_ns_ins_valread, scu_1_ns_mdr_writealu, scu_1_ns_mdr_writemem, scu_1_ns_reg_writealu,
       scu_1_ns_reg_writemdr, scu_1_ns_reg_writeval, scu_1_s_adr_immediate, scu_1_s_alu_invert,
       scu_1_s_alu_propagate, scu_1_s_ctl_halt, scu_1_s_ins_valread;
  wire [2:0] programmemory_1_counter;
  wire [3:0] operandintegrator_1_select, programmemory_1_nibble_2;
  wire [7:0] alu_1_data_out, clock_1_clock, decoder_8_1_out, mdr_1_data_out, programmemory_1_lsb, ram_1_out,
       register_file_1_data_out, registerbuffer_1_r1_out, registerbuffer_1_r2_out;
  wire [11:0] addressor_1_data_out, mem_adder_1_data_out, operandintegrator_1_value, rpc_1_address;
  wire [15:0] decoder_16_1_out;

  MEM_Adder mem_adder_1 (.Data_in(rpc_1_address), .Data_out(mem_adder_1_data_out));
  RPC rpc_1 (
    .D_WRT_RPC(scu_1_d_wrt_rpc), .D_RPC_Registers(scu_1_d_rpc_registers),
    .nD_RPC_Registers(scu_1_nd_rpc_registers), .nD_RPC_MemAdder(scu_1_nd_rpc_memadder),
    .Add_in(mem_adder_1_data_out), .Reg_in(addressor_1_data_out), .Address(rpc_1_address));
  RAM ram_1 (.Address(addressor_1_data_out), .Data(mdr_1_data_out), .nD_WRT_SRAM(scu_1_nd_wrt_sram), .Out(ram_1_out));
  ProgramMemory programmemory_1 (
    .Address(rpc_1_address), .Nibble_2(programmemory_1_nibble_2), .LSB(programmemory_1_lsb),
    .D_WRT_CIRFirst(scu_1_d_wrt_cirfirst), .D_WRT_CIRSecond(scu_1_d_wrt_cirsecond),
    .Counter(programmemory_1_counter), .IsOpcodeNibble(programmemory_1_isopcodenibble));
  Decoder_8 decoder_8_1 (.In(programmemory_1_counter), .Out(decoder_8_1_out));
  MDR mdr_1 (
    .Data_alu(alu_1_data_out), .nS_MDR_WriteALU(scu_1_ns_mdr_writealu),
    .nS_MDR_WriteMEM(scu_1_ns_mdr_writemem), .Data_mem(ram_1_out), .D_WRT_MDR(scu_1_d_wrt_mdr),
    .Data_out(mdr_1_data_out));
  SCU scu_1 (
    .Counter(decoder_8_1_out), .Nibble_2(programmemory_1_nibble_2),
    .IsOpcodeNibble(programmemory_1_isopcodenibble), .S_ALU_Invert(scu_1_s_alu_invert),
    .S_ALU_Propagate(scu_1_s_alu_propagate), .S_CTL_Halt(scu_1_s_ctl_halt),
    .S_INS_ValRead(scu_1_s_ins_valread), .S_ADR_Immediate(scu_1_s_adr_immediate),
    .nS_MDR_WriteMEM(scu_1_ns_mdr_writemem), .nS_MDR_WriteALU(scu_1_ns_mdr_writealu),
    .nS_REG_WriteMDR(scu_1_ns_reg_writemdr), .nS_REG_WriteVAL(scu_1_ns_reg_writeval),
    .nS_REG_WriteALU(scu_1_ns_reg_writealu), .nS_ADR_Direct(scu_1_ns_adr_direct),
    .nS_INS_ValRead(scu_1_ns_ins_valread), .nS_ADR_Immediate(scu_1_ns_adr_immediate),
    .nS_ALU_CarryOut(scu_1_ns_alu_carryout), .nS_ALU_OrOut(scu_1_ns_alu_orout),
    .nS_ALU_ResultOut(scu_1_ns_alu_resultout), .nD_RPC_MemAdder(scu_1_nd_rpc_memadder),
    .nD_RPC_Registers(scu_1_nd_rpc_registers), .nD_WRT_SRAM(scu_1_nd_wrt_sram),
    .D_WRT_RegOutput(scu_1_d_wrt_regoutput), .D_WRT_MDR(scu_1_d_wrt_mdr), .D_SEL_Second(scu_1_d_sel_second),
    .D_SEL_First(scu_1_d_sel_first), .D_WRT_BufferFirst(scu_1_d_wrt_bufferfirst),
    .D_WRT_BufferSecond(scu_1_d_wrt_buffersecond), .D_WRT_Flags(scu_1_d_wrt_flags),
    .D_WRT_RPC(scu_1_d_wrt_rpc), .D_ALU_Increment(scu_1_d_alu_increment),
    .D_RPC_Registers(scu_1_d_rpc_registers), .D_WRT_CIRFirst(scu_1_d_wrt_cirfirst),
    .D_WRT_CIRSecond(scu_1_d_wrt_cirsecond), .Clock(clock_1_clock), .F_Carry(alu_1_f_carry),
    .F_NotEqual(alu_1_f_notequal), .F_Equal(alu_1_f_equal), .F_Less(alu_1_f_less), .F_Greater(alu_1_f_greater));  // open: S_ADR_Direct, D_RPC_MemAdder
  OperandIntegrator operandintegrator_1 (
    .Nibble_2(programmemory_1_nibble_2), .LSB(programmemory_1_lsb), .D_SEL_First(scu_1_d_sel_first),
    .D_SEL_Second(scu_1_d_sel_second), .S_INS_ValRead(scu_1_s_ins_valread),
    .Select(operandintegrator_1_select), .Value(operandintegrator_1_value),
    .nS_INS_ValRead(scu_1_ns_ins_valread));
  Clock clock_1 (.S_CTL_HLT(scu_1_s_ctl_halt), .TestPulse(Pulse), .Clock(clock_1_clock));
  Decoder_16 decoder_16_1 (.In(operandintegrator_1_select), .Out(decoder_16_1_out));
  Register_File register_file_1 (
    .Select(decoder_16_1_out), .D_WRT_RegOutput(scu_1_d_wrt_regoutput), .Data_alu(alu_1_data_out),
    .nS_REG_WriteALU(scu_1_ns_reg_writealu), .Data_val(operandintegrator_1_value),
    .nS_REG_WriteVal(scu_1_ns_reg_writeval), .Data_out(register_file_1_data_out), .Test_out(Test_out),
    .nS_REG_WriteMDR(scu_1_ns_reg_writemdr), .Data_mdr(mdr_1_data_out));
  Addressor addressor_1 (
    .nS_ADR_Direct(scu_1_ns_adr_direct), .nS_ADR_Immediate(scu_1_ns_adr_immediate),
    .Data_imm(operandintegrator_1_value), .S_ADR_Immediate(scu_1_s_adr_immediate),
    .Data_direct1(registerbuffer_1_r1_out), .Data_out(addressor_1_data_out),
    .Data_direct2(registerbuffer_1_r2_out));
  ALU alu_1 (
    .Data_1_in(registerbuffer_1_r2_out), .Data_2_in(registerbuffer_1_r1_out),
    .S_ALU_Invert(scu_1_s_alu_invert), .D_ALU_Increment(scu_1_d_alu_increment),
    .S_ALU_Propagate(scu_1_s_alu_propagate), .nS_ALU_CarryOut(scu_1_ns_alu_carryout),
    .nS_ALU_ResultOut(scu_1_ns_alu_resultout), .nS_ALU_OrOut(scu_1_ns_alu_orout), .Data_out(alu_1_data_out),
    .F_Carry(alu_1_f_carry), .F_Greater(alu_1_f_greater), .F_Less(alu_1_f_less), .F_Equal(alu_1_f_equal),
    .F_NotEqual(alu_1_f_notequal), .D_WRT_Flags(scu_1_d_wrt_flags));
  RegisterBuffer registerbuffer_1 (
    .Data_in(register_file_1_data_out), .D_WRT_BufferSecond(scu_1_d_wrt_buffersecond),
    .D_WRT_BufferFirst(scu_1_d_wrt_bufferfirst), .R2_out(registerbuffer_1_r2_out),
    .R1_out(registerbuffer_1_r1_out));
endmodule

/* Test case ADD:
Tick Pulse Test_out
# SET 3 r1
memory ProgramMemory(0)=240;
memory ProgramMemory(1)=49;
# SET 45 r6
memory ProgramMemory(2)=242;
memory ProgramMemory(3)=214;
# ADD r1 r6
memory ProgramMemory(4)=8;
memory ProgramMemory(5)=97;
# SET -8 r1
memory ProgramMemory(6)=255;
memory ProgramMemory(7)=129;
# ADD r1 r6
memory ProgramMemory(8)=8;
memory ProgramMemory(9)=97;
# SET 3 r1
1 1 X
1 0 X
2 1 X
2 0 X
3 1 X
3 0 X
4 1 X
4 0 X
5 1 X
5 0 X
6 1 X
6 0 X
7 1 X
7 0 X
8 1 X
8 0 X
# SET 45 r6
1 1 X
1 0 X
2 1 X
2 0 X
3 1 X
3 0 X
4 1 X
4 0 X
5 1 X
5 0 X
6 1 X
6 0 X
7 1 X
7 0 X
8 1 X
8 0 X
# ADD r1 r6
1 1 X
1 0 X
2 1 X
2 0 X
3 1 X
3 0 X
4 1 X
4 0 X
5 1 X
5 0 X
6 1 X
6 0 X
7 1 X
7 0 X
8 1 X
8 0 (48)
# SET -8 r1
1 1 X
1 0 X
2 1 X
2 0 X
3 1 X
3 0 X
4 1 X
4 0 X
5 1 X
5 0 X
6 1 X
6 0 X
7 1 X
7 0 X
8 1 X
8 0 X
# ADD r1 r6
1 1 X
1 0 X
2 1 X
2 0 X
3 1 X
3 0 X
4 1 X
4 0 X
5 1 X
5 0 X
6 1 X
6 0 X
7 1 X
7 0 X
8 1 X
8 0 (37)
*/

/* Test case XOR:
Tick Pulse Test_out
# SET 45 r1
memory ProgramMemory(0)=242;
memory ProgramMemory(1)=209;
# SET 38 r2
memory ProgramMemory(2)=242;
memory ProgramMemory(3)=98;
# XOR r1 r2
memory ProgramMemory(4)=4;
memory ProgramMemory(5)=33;
# SET 45 r1
1 1 X
1 0 X
2 1 X
2 0 X
3 1 X
3 0 X
4 1 X
4 0 X
5 1 X
5 0 X
6 1 X
6 0 X
7 1 X
7 0 X
8 1 X
8 0 X
# SET 38 r2
1 1 X
1 0 X
2 1 X
2 0 X
3 1 X
3 0 X
4 1 X
4 0 X
5 1 X
5 0 X
6 1 X
6 0 X
7 1 X
7 0 X
8 1 X
8 0 X
# XOR r1 r2
1 1 X
1 0 X
2 1 X
2 0 X
3 1 X
3 0 X
4 1 X
4 0 X
5 1 X
5 0 X
6 1 X
6 0 X
7 1 X
7 0 X
8 1 X
8 0 (11)
*/

/* Test case MOV:
Tick Pulse Test_out
# SET 68 r5
memory ProgramMemory(0)=244;
memory ProgramMemory(1)=69;
# SET -16 r3
memory ProgramMemory(2)=255;
memory ProgramMemory(3)=3;
# MOV r1 r5
memory ProgramMemory(4)=33;
memory ProgramMemory(5)=81;
# MOV r1 r3
memory ProgramMemory(6)=33;
memory ProgramMemory(7)=49;
# SET 68 r5
1 1 X
1 0 X
2 1 X
2 0 X
3 1 X
3 0 X
4 1 X
4 0 X
5 1 X
5 0 X
6 1 X
6 0 X
7 1 X
7 0 X
8 1 X
8 0 X
# SET -16 r3
1 1 X
1 0 X
2 1 X
2 0 X
3 1 X
3 0 X
4 1 X
4 0 X
5 1 X
5 0 X
6 1 X
6 0 X
7 1 X
7 0 X
8 1 X
8 0 X
# MOV r1 r5
1 1 X
1 0 X
2 1 X
2 0 X
3 1 X
3 0 X
4 1 X
4 0 X
5 1 X
5 0 X
6 1 X
6 0 X
7 1 X
7 0 X
8 1 X
8 0 (68)
# MOV r1 r3
1 1 X
1 0 X
2 1 X
2 0 X
3 1 X
3 0 X
4 1 X
4 0 X
5 1 X
5 0 X
6 1 X
6 0 X
7 1 X
7 0 X
8 1 X
8 0 (-16)
*/

/* Test case SET:
Tick Pulse Test_out
# SET 2 r1
memory ProgramMemory(0)=240;
memory ProgramMemory(1)=33;
# SET 87 r1
memory ProgramMemory(2)=245;
memory ProgramMemory(3)=113;
# SET -7 r1
memory ProgramMemory(4)=255;
memory ProgramMemory(5)=145;
# SET 55 r3
memory ProgramMemory(6)=243;
memory ProgramMemory(7)=115;
# SET 2 r1
1 1 X
1 0 X
2 1 X
2 0 X
3 1 X
3 0 X
4 1 X
4 0 X
5 1 X
5 0 X
6 1 X
6 0 X
7 1 X
7 0 X
8 1 X
8 0 (2)
# SET 87 r1
1 1 X
1 0 X
2 1 X
2 0 X
3 1 X
3 0 X
4 1 X
4 0 X
5 1 X
5 0 X
6 1 X
6 0 X
7 1 X
7 0 X
8 1 X
8 0 (87)
# SET -7 r1
1 1 X
1 0 X
2 1 X
2 0 X
3 1 X
3 0 X
4 1 X
4 0 X
5 1 X
5 0 X
6 1 X
6 0 X
7 1 X
7 0 X
8 1 X
8 0 (-7)
# SET 55 r3
1 1 X
1 0 X
2 1 X
2 0 X
3 1 X
3 0 X
4 1 X
4 0 X
5 1 X
5 0 X
6 1 X
6 0 X
7 1 X
7 0 X
8 1 X
8 0 (-7)
*/

/* Test case ADC:
Tick Pulse Test_out
# SET 100 r2
memory ProgramMemory(0)=246;
memory ProgramMemory(1)=66;
# SET 200 r3
memory ProgramMemory(2)=252;
memory ProgramMemory(3)=131;
# SET 2 r4
memory ProgramMemory(4)=240;
memory ProgramMemory(5)=36;
# SET 3 r5
memory ProgramMemory(6)=240;
memory ProgramMemory(7)=53;
# ADD r2 r3
memory ProgramMemory(8)=8;
memory ProgramMemory(9)=50;
# MOV r1 r2
memory ProgramMemory(10)=33;
memory ProgramMemory(11)=33;
# ADC r4 r5
memory ProgramMemory(12)=24;
memory ProgramMemory(13)=84;
# MOV r1 r4
memory ProgramMemory(14)=33;
memory ProgramMemory(15)=65;
# ADC r4 r5
memory ProgramMemory(16)=24;
memory ProgramMemory(17)=84;
# MOV r1 r4
memory ProgramMemory(18)=33;
memory ProgramMemory(19)=65;
# SET 100 r2
1 1 X
1 0 X
2 1 X
2 0 X
3 1 X
3 0 X
4 1 X
4 0 X
5 1 X
5 0 X
6 1 X
6 0 X
7 1 X
7 0 X
8 1 X
8 0 X
# SET 200 r3
1 1 X
1 0 X
2 1 X
2 0 X
3 1 X
3 0 X
4 1 X
4 0 X
5 1 X
5 0 X
6 1 X
6 0 X
7 1 X
7 0 X
8 1 X
8 0 X
# SET 2 r4
1 1 X
1 0 X
2 1 X
2 0 X
3 1 X
3 0 X
4 1 X
4 0 X
5 1 X
5 0 X
6 1 X
6 0 X
7 1 X
7 0 X
8 1 X
8 0 X
# SET 3 r5
1 1 X
1 0 X
2 1 X
2 0 X
3 1 X
3 0 X
4 1 X
4 0 X
5 1 X
5 0 X
6 1 X
6 0 X
7 1 X
7 0 X
8 1 X
8 0 X
# ADD r2 r3
1 1 X
1 0 X
2 1 X
2 0 X
3 1 X
3 0 X
4 1 X
4 0 X
5 1 X
5 0 X
6 1 X
6 0 X
7 1 X
7 0 X
8 1 X
8 0 X
# MOV r1 r2
1 1 X
1 0 X
2 1 X
2 0 X
3 1 X
3 0 X
4 1 X
4 0 X
5 1 X
5 0 X
6 1 X
6 0 X
7 1 X
7 0 X
8 1 X
8 0 (44)
# ADC r4 r5
1 1 X
1 0 X
2 1 X
2 0 X
3 1 X
3 0 X
4 1 X
4 0 X
5 1 X
5 0 X
6 1 X
6 0 X
7 1 X
7 0 X
8 1 X
8 0 X
# MOV r1 r4
1 1 X
1 0 X
2 1 X
2 0 X
3 1 X
3 0 X
4 1 X
4 0 X
5 1 X
5 0 X
6 1 X
6 0 X
7 1 X
7 0 X
8 1 X
8 0 (6)
# ADC r4 r5
1 1 X
1 0 X
2 1 X
2 0 X
3 1 X
3 0 X
4 1 X
4 0 X
5 1 X
5 0 X
6 1 X
6 0 X
7 1 X
7 0 X
8 1 X
8 0 X
# MOV r1 r4
1 1 X
1 0 X
2 1 X
2 0 X
3 1 X
3 0 X
4 1 X
4 0 X
5 1 X
5 0 X
6 1 X
6 0 X
7 1 X
7 0 X
8 1 X
8 0 (9)
*/

/* Test case AND:
Tick Pulse Test_out
# SET 45 r1
memory ProgramMemory(0)=242;
memory ProgramMemory(1)=209;
# SET 38 r2
memory ProgramMemory(2)=242;
memory ProgramMemory(3)=98;
# AND r1 r2
memory ProgramMemory(4)=20;
memory ProgramMemory(5)=33;
# SET 45 r1
1 1 X
1 0 X
2 1 X
2 0 X
3 1 X
3 0 X
4 1 X
4 0 X
5 1 X
5 0 X
6 1 X
6 0 X
7 1 X
7 0 X
8 1 X
8 0 X
# SET 38 r2
1 1 X
1 0 X
2 1 X
2 0 X
3 1 X
3 0 X
4 1 X
4 0 X
5 1 X
5 0 X
6 1 X
6 0 X
7 1 X
7 0 X
8 1 X
8 0 X
# AND r1 r2
1 1 X
1 0 X
2 1 X
2 0 X
3 1 X
3 0 X
4 1 X
4 0 X
5 1 X
5 0 X
6 1 X
6 0 X
7 1 X
7 0 X
8 1 X
8 0 (36)
*/

/* Test case STD|LDD:
Tick Pulse Test_out
# SET 0 r3
memory ProgramMemory(0)=240;
memory ProgramMemory(1)=3;
# SET 2 r4
memory ProgramMemory(2)=240;
memory ProgramMemory(3)=36;
# SET 23 r5
memory ProgramMemory(4)=241;
memory ProgramMemory(5)=117;
# SET 37 r1
memory ProgramMemory(6)=242;
memory ProgramMemory(7)=81;
# MTD r1
memory ProgramMemory(8)=49;
memory ProgramMemory(9)=1;
# STD r3 r5
memory ProgramMemory(10)=18;
memory ProgramMemory(11)=83;
# STD r4 r5
memory ProgramMemory(12)=18;
memory ProgramMemory(13)=84;
# SET 0 r1
memory ProgramMemory(14)=240;
memory ProgramMemory(15)=1;
# MTD r1
memory ProgramMemory(16)=49;
memory ProgramMemory(17)=1;
# LDD r3 r5
memory ProgramMemory(18)=2;
memory ProgramMemory(19)=83;
# MFD r1
memory ProgramMemory(20)=65;
memory ProgramMemory(21)=1;
# SET 0 r1
memory ProgramMemory(22)=240;
memory ProgramMemory(23)=1;
# MTD r1
memory ProgramMemory(24)=49;
memory ProgramMemory(25)=1;
# LDD r4 r5
memory ProgramMemory(26)=2;
memory ProgramMemory(27)=84;
# MFD r1
memory ProgramMemory(28)=65;
memory ProgramMemory(29)=1;
# SET 0 r3
1 1 X
1 0 X
2 1 X
2 0 X
3 1 X
3 0 X
4 1 X
4 0 X
5 1 X
5 0 X
6 1 X
6 0 X
7 1 X
7 0 X
8 1 X
8 0 X
# SET 2 r4
1 1 X
1 0 X
2 1 X
2 0 X
3 1 X
3 0 X
4 1 X
4 0 X
5 1 X
5 0 X
6 1 X
6 0 X
7 1 X
7 0 X
8 1 X
8 0 X
# SET 23 r5
1 1 X
1 0 X
2 1 X
2 0 X
3 1 X
3 0 X
4 1 X
4 0 X
5 1 X
5 0 X
6 1 X
6 0 X
7 1 X
7 0 X
8 1 X
8 0 X
# SET 37 r1
1 1 X
1 0 X
2 1 X
2 0 X
3 1 X
3 0 X
4 1 X
4 0 X
5 1 X
5 0 X
6 1 X
6 0 X
7 1 X
7 0 X
8 1 X
8 0 X
# MTD r1
1 1 X
1 0 X
2 1 X
2 0 X
3 1 X
3 0 X
4 1 X
4 0 X
5 1 X
5 0 X
6 1 X
6 0 X
7 1 X
7 0 X
8 1 X
8 0 X
# STD r3 r5
1 1 X
1 0 X
2 1 X
2 0 X
3 1 X
3 0 X
4 1 X
4 0 X
5 1 X
5 0 X
6 1 X
6 0 X
7 1 X
7 0 X
8 1 X
8 0 X
# STD r4 r5
1 1 X
1 0 X
2 1 X
2 0 X
3 1 X
3 0 X
4 1 X
4 0 X
5 1 X
5 0 X
6 1 X
6 0 X
7 1 X
7 0 X
8 1 X
8 0 X
# SET 0 r1
1 1 X
1 0 X
2 1 X
2 0 X
3 1 X
3 0 X
4 1 X
4 0 X
5 1 X
5 0 X
6 1 X
6 0 X
7 1 X
7 0 X
8 1 X
8 0 (0)
# MTD r1
1 1 X
1 0 X
2 1 X
2 0 X
3 1 X
3 0 X
4 1 X
4 0 X
5 1 X
5 0 X
6 1 X
6 0 X
7 1 X
7 0 X
8 1 X
8 0 X
# LDD r3 r5
1 1 X
1 0 X
2 1 X
2 0 X
3 1 X
3 0 X
4 1 X
4 0 X
5 1 X
5 0 X
6 1 X
6 0 X
7 1 X
7 0 X
8 1 X
8 0 X
# MFD r1
1 1 X
1 0 X
2 1 X
2 0 X
3 1 X
3 0 X
4 1 X
4 0 X
5 1 X
5 0 X
6 1 X
6 0 X
7 1 X
7 0 X
8 1 X
8 0 (37)
# SET 0 r1
1 1 X
1 0 X
2 1 X
2 0 X
3 1 X
3 0 X
4 1 X
4 0 X
5 1 X
5 0 X
6 1 X
6 0 X
7 1 X
7 0 X
8 1 X
8 0 (0)
# MTD r1
1 1 X
1 0 X
2 1 X
2 0 X
3 1 X
3 0 X
4 1 X
4 0 X
5 1 X
5 0 X
6 1 X
6 0 X
7 1 X
7 0 X
8 1 X
8 0 X
# LDD r4 r5
1 1 X
1 0 X
2 1 X
2 0 X
3 1 X
3 0 X
4 1 X
4 0 X
5 1 X
5 0 X
6 1 X
6 0 X
7 1 X
7 0 X
8 1 X
8 0 X
# MFD r1
1 1 X
1 0 X
2 1 X
2 0 X
3 1 X
3 0 X
4 1 X
4 0 X
5 1 X
5 0 X
6 1 X
6 0 X
7 1 X
7 0 X
8 1 X
8 0 (37)
*/

/* Test case MTD|MFD:
Tick Pulse Test_out
# SET 54 r1
memory ProgramMemory(0)=243;
memory ProgramMemory(1)=97;
# MTD r1
memory ProgramMemory(2)=49;
memory ProgramMemory(3)=1;
# SET 0 r1
memory ProgramMemory(4)=240;
memory ProgramMemory(5)=1;
# MFD r1
memory ProgramMemory(6)=65;
memory ProgramMemory(7)=1;
# SET 54 r1
1 1 X
1 0 X
2 1 X
2 0 X
3 1 X
3 0 X
4 1 X
4 0 X
5 1 X
5 0 X
6 1 X
6 0 X
7 1 X
7 0 X
8 1 X
8 0 X
# MTD r1
1 1 X
1 0 X
2 1 X
2 0 X
3 1 X
3 0 X
4 1 X
4 0 X
5 1 X
5 0 X
6 1 X
6 0 X
7 1 X
7 0 X
8 1 X
8 0 X
# SET 0 r1
1 1 X
1 0 X
2 1 X
2 0 X
3 1 X
3 0 X
4 1 X
4 0 X
5 1 X
5 0 X
6 1 X
6 0 X
7 1 X
7 0 X
8 1 X
8 0 (0)
# MFD r1
1 1 X
1 0 X
2 1 X
2 0 X
3 1 X
3 0 X
4 1 X
4 0 X
5 1 X
5 0 X
6 1 X
6 0 X
7 1 X
7 0 X
8 1 X
8 0 (54)
*/

/* Test case STI|LDI:
Tick Pulse Test_out
# SET 37 r1
memory ProgramMemory(0)=242;
memory ProgramMemory(1)=81;
# MTD r1
memory ProgramMemory(2)=49;
memory ProgramMemory(3)=1;
# STI 60
memory ProgramMemory(4)=144;
memory ProgramMemory(5)=60;
# STI 3000
memory ProgramMemory(6)=155;
memory ProgramMemory(7)=184;
# SET 0 r1
memory ProgramMemory(8)=240;
memory ProgramMemory(9)=1;
# MTD r1
memory ProgramMemory(10)=49;
memory ProgramMemory(11)=1;
# LDI 60
memory ProgramMemory(12)=128;
memory ProgramMemory(13)=60;
# MFD r1
memory ProgramMemory(14)=65;
memory ProgramMemory(15)=1;
# SET 0 r1
memory ProgramMemory(16)=240;
memory ProgramMemory(17)=1;
# MTD r1
memory ProgramMemory(18)=49;
memory ProgramMemory(19)=1;
# LDI 3000
memory ProgramMemory(20)=139;
memory ProgramMemory(21)=184;
# MFD r1
memory ProgramMemory(22)=65;
memory ProgramMemory(23)=1;
# SET 37 r1
1 1 X
1 0 X
2 1 X
2 0 X
3 1 X
3 0 X
4 1 X
4 0 X
5 1 X
5 0 X
6 1 X
6 0 X
7 1 X
7 0 X
8 1 X
8 0 X
# MTD r1
1 1 X
1 0 X
2 1 X
2 0 X
3 1 X
3 0 X
4 1 X
4 0 X
5 1 X
5 0 X
6 1 X
6 0 X
7 1 X
7 0 X
8 1 X
8 0 X
# STI 60
1 1 X
1 0 X
2 1 X
2 0 X
3 1 X
3 0 X
4 1 X
4 0 X
5 1 X
5 0 X
6 1 X
6 0 X
7 1 X
7 0 X
8 1 X
8 0 X
# STI 3000
1 1 X
1 0 X
2 1 X
2 0 X
3 1 X
3 0 X
4 1 X
4 0 X
5 1 X
5 0 X
6 1 X
6 0 X
7 1 X
7 0 X
8 1 X
8 0 X
# SET 0 r1
1 1 X
1 0 X
2 1 X
2 0 X
3 1 X
3 0 X
4 1 X
4 0 X
5 1 X
5 0 X
6 1 X
6 0 X
7 1 X
7 0 X
8 1 X
8 0 (0)
# MTD r1
1 1 X
1 0 X
2 1 X
2 0 X
3 1 X
3 0 X
4 1 X
4 0 X
5 1 X
5 0 X
6 1 X
6 0 X
7 1 X
7 0 X
8 1 X
8 0 X
# LDI 60
1 1 X
1 0 X
2 1 X
2 0 X
3 1 X
3 0 X
4 1 X
4 0 X
5 1 X
5 0 X
6 1 X
6 0 X
7 1 X
7 0 X
8 1 X
8 0 X
# MFD r1
1 1 X
1 0 X
2 1 X
2 0 X
3 1 X
3 0 X
4 1 X
4 0 X
5 1 X
5 0 X
6 1 X
6 0 X
7 1 X
7 0 X
8 1 X
8 0 (37)
# SET 0 r1
1 1 X
1 0 X
2 1 X
2 0 X
3 1 X
3 0 X
4 1 X
4 0 X
5 1 X
5 0 X
6 1 X
6 0 X
7 1 X
7 0 X
8 1 X
8 0 (0)
# MTD r1
1 1 X
1 0 X
2 1 X
2 0 X
3 1 X
3 0 X
4 1 X
4 0 X
5 1 X
5 0 X
6 1 X
6 0 X
7 1 X
7 0 X
8 1 X
8 0 X
# LDI 3000
1 1 X
1 0 X
2 1 X
2 0 X
3 1 X
3 0 X
4 1 X
4 0 X
5 1 X
5 0 X
6 1 X
6 0 X
7 1 X
7 0 X
8 1 X
8 0 X
# MFD r1
1 1 X
1 0 X
2 1 X
2 0 X
3 1 X
3 0 X
4 1 X
4 0 X
5 1 X
5 0 X
6 1 X
6 0 X
7 1 X
7 0 X
8 1 X
8 0 (37)
*/

/* Test case SUB:
Tick Pulse Test_out
# SET 6 r1
memory ProgramMemory(0)=240;
memory ProgramMemory(1)=97;
# SET 50 r6
memory ProgramMemory(2)=243;
memory ProgramMemory(3)=38;
# SUB r1 r6
memory ProgramMemory(4)=40;
memory ProgramMemory(5)=97;
# SET 72 r1
memory ProgramMemory(6)=244;
memory ProgramMemory(7)=129;
# SUB r1 r6
memory ProgramMemory(8)=40;
memory ProgramMemory(9)=97;
# SET 6 r1
1 1 X
1 0 X
2 1 X
2 0 X
3 1 X
3 0 X
4 1 X
4 0 X
5 1 X
5 0 X
6 1 X
6 0 X
7 1 X
7 0 X
8 1 X
8 0 X
# SET 50 r6
1 1 X
1 0 X
2 1 X
2 0 X
3 1 X
3 0 X
4 1 X
4 0 X
5 1 X
5 0 X
6 1 X
6 0 X
7 1 X
7 0 X
8 1 X
8 0 X
# SUB r1 r6
1 1 X
1 0 X
2 1 X
2 0 X
3 1 X
3 0 X
4 1 X
4 0 X
5 1 X
5 0 X
6 1 X
6 0 X
7 1 X
7 0 X
8 1 X
8 0 (-44)
# SET 72 r1
1 1 X
1 0 X
2 1 X
2 0 X
3 1 X
3 0 X
4 1 X
4 0 X
5 1 X
5 0 X
6 1 X
6 0 X
7 1 X
7 0 X
8 1 X
8 0 X
# SUB r1 r6
1 1 X
1 0 X
2 1 X
2 0 X
3 1 X
3 0 X
4 1 X
4 0 X
5 1 X
5 0 X
6 1 X
6 0 X
7 1 X
7 0 X
8 1 X
8 0 (22)
*/

/* Test case ORR:
Tick Pulse Test_out
# SET 45 r1
memory ProgramMemory(0)=242;
memory ProgramMemory(1)=209;
# SET 38 r2
memory ProgramMemory(2)=242;
memory ProgramMemory(3)=98;
# ORR r1 r2
memory ProgramMemory(4)=36;
memory ProgramMemory(5)=33;
# SET 45 r1
1 1 X
1 0 X
2 1 X
2 0 X
3 1 X
3 0 X
4 1 X
4 0 X
5 1 X
5 0 X
6 1 X
6 0 X
7 1 X
7 0 X
8 1 X
8 0 X
# SET 38 r2
1 1 X
1 0 X
2 1 X
2 0 X
3 1 X
3 0 X
4 1 X
4 0 X
5 1 X
5 0 X
6 1 X
6 0 X
7 1 X
7 0 X
8 1 X
8 0 X
# ORR r1 r2
1 1 X
1 0 X
2 1 X
2 0 X
3 1 X
3 0 X
4 1 X
4 0 X
5 1 X
5 0 X
6 1 X
6 0 X
7 1 X
7 0 X
8 1 X
8 0 (47)
*/

/* Test case BDU:
Tick Pulse Test_out
# SET 0 r1
memory ProgramMemory(0)=240;
memory ProgramMemory(1)=1;
# SET 8 r2
memory ProgramMemory(2)=240;
memory ProgramMemory(3)=130;
# BDU r1 r2
memory ProgramMemory(4)=34;
memory ProgramMemory(5)=33;
# SET 50 r1
memory ProgramMemory(6)=243;
memory ProgramMemory(7)=33;
# SET 30 r1
memory ProgramMemory(8)=241;
memory ProgramMemory(9)=225;
# SET 0 r1
1 1 X
1 0 X
2 1 X
2 0 X
3 1 X
3 0 X
4 1 X
4 0 X
5 1 X
5 0 X
6 1 X
6 0 X
7 1 X
7 0 X
8 1 X
8 0 X
# SET 8 r2
1 1 X
1 0 X
2 1 X
2 0 X
3 1 X
3 0 X
4 1 X
4 0 X
5 1 X
5 0 X
6 1 X
6 0 X
7 1 X
7 0 X
8 1 X
8 0 X
# BDU r1 r2
1 1 X
1 0 X
2 1 X
2 0 X
3 1 X
3 0 X
4 1 X
4 0 X
5 1 X
5 0 X
6 1 X
6 0 X
7 1 X
7 0 X
8 1 X
8 0 X
# SET 30 r1
1 1 X
1 0 X
2 1 X
2 0 X
3 1 X
3 0 X
4 1 X
4 0 X
5 1 X
5 0 X
6 1 X
6 0 X
7 1 X
7 0 X
8 1 X
8 0 (30)
*/

/* Test case CMP:
Tick Pulse Test_out
# SET 2 r2
memory ProgramMemory(0)=240;
memory ProgramMemory(1)=34;
# SET 5 r3
memory ProgramMemory(2)=240;
memory ProgramMemory(3)=83;
# CMP r3 r3
memory ProgramMemory(4)=81;
memory ProgramMemory(5)=51;
# BIE 10
memory ProgramMemory(6)=208;
memory ProgramMemory(7)=10;
# SET 50 r1
memory ProgramMemory(8)=243;
memory ProgramMemory(9)=33;
# SET 30 r1
memory ProgramMemory(10)=241;
memory ProgramMemory(11)=225;
# CMP r3 r2
memory ProgramMemory(12)=81;
memory ProgramMemory(13)=35;
# BIE 18
memory ProgramMemory(14)=208;
memory ProgramMemory(15)=18;
# SET 50 r1
memory ProgramMemory(16)=243;
memory ProgramMemory(17)=33;
# SET 30 r1
memory ProgramMemory(18)=241;
memory ProgramMemory(19)=225;
# SET 2 r2
1 1 X
1 0 X
2 1 X
2 0 X
3 1 X
3 0 X
4 1 X
4 0 X
5 1 X
5 0 X
6 1 X
6 0 X
7 1 X
7 0 X
8 1 X
8 0 X
# SET 5 r3
1 1 X
1 0 X
2 1 X
2 0 X
3 1 X
3 0 X
4 1 X
4 0 X
5 1 X
5 0 X
6 1 X
6 0 X
7 1 X
7 0 X
8 1 X
8 0 X
# CMP r3 r3
1 1 X
1 0 X
2 1 X
2 0 X
3 1 X
3 0 X
4 1 X
4 0 X
5 1 X
5 0 X
6 1 X
6 0 X
7 1 X
7 0 X
8 1 X
8 0 X
# BIE 10
1 1 X
1 0 X
2 1 X
2 0 X
3 1 X
3 0 X
4 1 X
4 0 X
5 1 X
5 0 X
6 1 X
6 0 X
7 1 X
7 0 X
8 1 X
8 0 X
# SET 30 r1
1 1 X
1 0 X
2 1 X
2 0 X
3 1 X
3 0 X
4 1 X
4 0 X
5 1 X
5 0 X
6 1 X
6 0 X
7 1 X
7 0 X
8 1 X
8 0 (30)
# CMP r3 r2
1 1 X
1 0 X
2 1 X
2 0 X
3 1 X
3 0 X
4 1 X
4 0 X
5 1 X
5 0 X
6 1 X
6 0 X
7 1 X
7 0 X
8 1 X
8 0 X
# BIE 18
1 1 X
1 0 X
2 1 X
2 0 X
3 1 X
3 0 X
4 1 X
4 0 X
5 1 X
5 0 X
6 1 X
6 0 X
7 1 X
7 0 X
8 1 X
8 0 X
# SET 30 r1
1 1 X
1 0 X
2 1 X
2 0 X
3 1 X
3 0 X
4 1 X
4 0 X
5 1 X
5 0 X
6 1 X
6 0 X
7 1 X
7 0 X
8 1 X
8 0 (50)
*/

/* Test case BIU:
Tick Pulse Test_out
# BIU 4
memory ProgramMemory(0)=160;
memory ProgramMemory(1)=4;
# SET 50 r1
memory ProgramMemory(2)=243;
memory ProgramMemory(3)=33;
# SET 30 r1
memory ProgramMemory(4)=241;
memory ProgramMemory(5)=225;
# BIU 4
1 1 X
1 0 X
2 1 X
2 0 X
3 1 X
3 0 X
4 1 X
4 0 X
5 1 X
5 0 X
6 1 X
6 0 X
7 1 X
7 0 X
8 1 X
8 0 X
# SET 30 r1
1 1 X
1 0 X
2 1 X
2 0 X
3 1 X
3 0 X
4 1 X
4 0 X
5 1 X
5 0 X
6 1 X
6 0 X
7 1 X
7 0 X
8 1 X
8 0 (30)
*/

/* Test case SBC:
Tick Pulse Test_out
# SET 50 r2
memory ProgramMemory(0)=243;
memory ProgramMemory(1)=34;
# SET 100 r3
memory ProgramMemory(2)=246;
memory ProgramMemory(3)=67;
# SET 4 r4
memory ProgramMemory(4)=240;
memory ProgramMemory(5)=68;
# SET 2 r5
memory ProgramMemory(6)=240;
memory ProgramMemory(7)=37;
# SUB r2 r3
memory ProgramMemory(8)=40;
memory ProgramMemory(9)=50;
# MOV r1 r2
memory ProgramMemory(10)=33;
memory ProgramMemory(11)=33;
# SBC r4 r5
memory ProgramMemory(12)=56;
memory ProgramMemory(13)=84;
# MOV r1 r4
memory ProgramMemory(14)=33;
memory ProgramMemory(15)=65;
# SBC r5 r4
memory ProgramMemory(16)=56;
memory ProgramMemory(17)=69;
# MOV r1 r5
memory ProgramMemory(18)=33;
memory ProgramMemory(19)=81;
# SET 50 r2
1 1 X
1 0 X
2 1 X
2 0 X
3 1 X
3 0 X
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*/

/* Test case NOT:
Tick Pulse Test_out
# SET 45 r1
memory ProgramMemory(0)=242;
memory ProgramMemory(1)=209;
# NOT r1 r1
memory ProgramMemory(2)=52;
memory ProgramMemory(3)=17;
# SET 45 r1
1 1 X
1 0 X
2 1 X
2 0 X
3 1 X
3 0 X
4 1 X
4 0 X
5 1 X
5 0 X
6 1 X
6 0 X
7 1 X
7 0 X
8 1 X
8 0 X
# NOT r1 r1
1 1 X
1 0 X
2 1 X
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*/

/* Test case BDG:
Tick Pulse Test_out
# SET 0 r4
memory ProgramMemory(0)=240;
memory ProgramMemory(1)=4;
# SET 18 r5
memory ProgramMemory(2)=241;
memory ProgramMemory(3)=37;
# SET 0 r6
memory ProgramMemory(4)=240;
memory ProgramMemory(5)=6;
# SET 26 r7
memory ProgramMemory(6)=241;
memory ProgramMemory(7)=167;
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*/

/* Test case TST:
Tick Pulse Test_out
# SET 2 r2
memory ProgramMemory(0)=240;
memory ProgramMemory(1)=34;
# SET -60 r3
memory ProgramMemory(2)=252;
memory ProgramMemory(3)=67;
# TST r2
memory ProgramMemory(4)=97;
memory ProgramMemory(5)=2;
# BIG 10
memory ProgramMemory(6)=176;
memory ProgramMemory(7)=10;
# SET 50 r1
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*/

/* Test case BIG:
Tick Pulse Test_out
# SET 2 r2
memory ProgramMemory(0)=240;
memory ProgramMemory(1)=34;
# SET 0 r3
memory ProgramMemory(2)=240;
memory ProgramMemory(3)=3;
# SUB r2 r3
memory ProgramMemory(4)=40;
memory ProgramMemory(5)=50;
# BIG 10
memory ProgramMemory(6)=176;
memory ProgramMemory(7)=10;
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*/

/* Test case INC:
Tick Pulse Test_out
# SET 3 r6
memory ProgramMemory(0)=240;
memory ProgramMemory(1)=54;
# INC r6
memory ProgramMemory(2)=72;
memory ProgramMemory(3)=6;
# MOV r1 r6
memory ProgramMemory(4)=33;
memory ProgramMemory(5)=97;
# SET -8 r3
memory ProgramMemory(6)=255;
memory ProgramMemory(7)=131;
# INC r3
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*/

/* Test case BDE:
Tick Pulse Test_out
# SET 0 r4
memory ProgramMemory(0)=240;
memory ProgramMemory(1)=4;
# SET 18 r5
memory ProgramMemory(2)=241;
memory ProgramMemory(3)=37;
# SET 0 r6
memory ProgramMemory(4)=240;
memory ProgramMemory(5)=6;
# SET 26 r7
memory ProgramMemory(6)=241;
memory ProgramMemory(7)=167;
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*/

/* Test case BIE:
Tick Pulse Test_out
# SET 2 r2
memory ProgramMemory(0)=240;
memory ProgramMemory(1)=34;
# SET 5 r3
memory ProgramMemory(2)=240;
memory ProgramMemory(3)=83;
# SUB r3 r3
memory ProgramMemory(4)=40;
memory ProgramMemory(5)=51;
# BIE 10
memory ProgramMemory(6)=208;
memory ProgramMemory(7)=10;
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*/

/* Test case DEC:
Tick Pulse Test_out
# SET 3 r6
memory ProgramMemory(0)=240;
memory ProgramMemory(1)=54;
# DEC r6
memory ProgramMemory(2)=88;
memory ProgramMemory(3)=6;
# MOV r1 r6
memory ProgramMemory(4)=33;
memory ProgramMemory(5)=97;
# SET -8 r3
memory ProgramMemory(6)=255;
memory ProgramMemory(7)=131;
# DEC r3
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*/

/* Test case BDN:
Tick Pulse Test_out
# SET 0 r4
memory ProgramMemory(0)=240;
memory ProgramMemory(1)=4;
# SET 18 r5
memory ProgramMemory(2)=241;
memory ProgramMemory(3)=37;
# SET 0 r6
memory ProgramMemory(4)=240;
memory ProgramMemory(5)=6;
# SET 26 r7
memory ProgramMemory(6)=241;
memory ProgramMemory(7)=167;
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*/

/* Test case BIN:
Tick Pulse Test_out
# SET 2 r2
memory ProgramMemory(0)=240;
memory ProgramMemory(1)=34;
# SET 5 r3
memory ProgramMemory(2)=240;
memory ProgramMemory(3)=83;
# SUB r3 r2
memory ProgramMemory(4)=40;
memory ProgramMemory(5)=35;
# BIN 10
memory ProgramMemory(6)=224;
memory ProgramMemory(7)=10;
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*/

/* Test case INV:
Tick Pulse Test_out
# SET -34 r8
memory ProgramMemory(0)=253;
memory ProgramMemory(1)=232;
# INV r1 r8
memory ProgramMemory(2)=104;
memory ProgramMemory(3)=129;
# SET 7 r1
memory ProgramMemory(4)=240;
memory ProgramMemory(5)=113;
# INV r1 r1
memory ProgramMemory(6)=104;
memory ProgramMemory(7)=17;
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*/
