// Digital circuit Clock.dig as structural Verilog
module Clock (
  input  S_CTL_HLT,
  input  TestPulse,
  output [7:0] Clock
);

  wire _1k_2_out, _1k_out, _10k_2_out, _10k_3_out, _10k_4_out, _10k_out, _555_1_control, _555_1_output,
       and_2_1_1__4_y, not_1_1_1__5_y, not_1_1_1__6_y, or_3_1_1__1_y, or_3_1_1__2_y, or_3_1_1__3_y,
       resistor_1_out, resistor_2_out, resistor_3_out, resistor_4_out, resistor_5_out, resistor_6_out,
       resistor_7_out, resistor_8_out, resistor_9_out, resistor_10_out;

  _555 _555_1 (
    .GND(1'b0), .VCC(1'b1), .Trigger(_10k_3_out), .Reset(1'b1), .Threshold(_10k_3_out), .Dischrg(_10k_4_out),
    .Output(_555_1_output), .Control(_555_1_control));
  Capacitor capacitor_1 (.In(1'b0), .Out(resistor_6_out));
  Capacitor capacitor_2 (.In(1'b0), .Out(resistor_7_out));
  Capacitor _0_01uF (.In(_1k_2_out), .Out(1'b0));
  D_Flip_Flop d_flip_flop_1 (
    .nEN(1'b0), ._1_Q(Clock[0]), .VCC(1'b1), .GND(1'b0), ._1_D(and_2_1_1__4_y), ._2_D(_10k_2_out),
    ._3_Q(Clock[2]), .CLK(TestPulse), ._2_Q(Clock[1]), ._3_D(resistor_10_out), ._4_D(resistor_9_out),
    ._4_Q(Clock[3]), ._5_Q(Clock[4]), ._5_D(resistor_8_out), ._6_D(_10k_out), ._7_Q(Clock[6]),
    ._6_Q(Clock[5]), ._7_D(resistor_1_out), ._8_D(resistor_2_out), ._8_Q(Clock[7]));
  OR_3_1 or_3_1_1 (
    ._1_B(Clock[1]), ._1_Y(or_3_1_1__1_y), .VCC(1'b1), .GND(1'b0), ._1_C(Clock[0]), ._3_A(Clock[4]),
    ._3_Y(or_3_1_1__3_y), ._2_C(or_3_1_1__3_y), ._3_C(Clock[6]), ._2_Y(or_3_1_1__2_y), ._3_B(Clock[5]),
    ._1_A(Clock[2]), ._2_B(Clock[3]), ._2_A(or_3_1_1__1_y));
  NOT_1_1 not_1_1_1 (
    ._1_A(1'b0), ._2_A(1'b0), ._3_A(1'b0), ._4_A(1'b0), .VCC(1'b1), .GND(1'b0), ._5_A(S_CTL_HLT),
    ._5_Y(not_1_1_1__5_y), ._6_A(or_3_1_1__2_y), ._6_Y(not_1_1_1__6_y));  // open: _1_Y, _2_Y, _3_Y, _4_Y
  AND_2_1 and_2_1_1 (
    ._1_A(1'b0), .VCC(1'b1), .GND(1'b0), ._1_B(1'b0), ._2_A(1'b0), ._2_B(1'b0), ._3_B(1'b0), ._3_A(1'b0),
    ._4_B(not_1_1_1__6_y), ._4_Y(and_2_1_1__4_y), ._4_A(not_1_1_1__5_y));  // open: _1_Y, _2_Y, _3_Y
  Resistor _10k (.In(resistor_6_out), .Out(_10k_out));
  Resistor resistor_1 (.In(resistor_7_out), .Out(resistor_1_out));
  Resistor resistor_2 (.In(_1k_2_out), .Out(resistor_2_out));
  Resistor _1k (.In(Clock[3]), .Out(_1k_out));
  Resistor resistor_3 (.In(Clock[2]), .Out(resistor_3_out));
  Resistor resistor_4 (.In(Clock[1]), .Out(resistor_4_out));
  Resistor resistor_5 (.In(Clock[0]), .Out(resistor_5_out));
  Resistor resistor_6 (.In(Clock[4]), .Out(resistor_6_out));
  Resistor resistor_7 (.In(Clock[5]), .Out(resistor_7_out));
  Resistor _1k_2 (.In(Clock[6]), .Out(_1k_2_out));
  Resistor resistor_8 (.In(_1k_out), .Out(resistor_8_out));
  Resistor resistor_9 (.In(resistor_3_out), .Out(resistor_9_out));
  Resistor resistor_10 (.In(resistor_4_out), .Out(resistor_10_out));
  Resistor _10k_2 (.In(resistor_5_out), .Out(_10k_2_out));
  Resistor _10k_3 (.In(_10k_4_out), .Out(_10k_3_out));
  Capacitor _1uF (.In(1'b0), .Out(_10k_4_out));
  Resistor _10k_4 (.In(1'b1), .Out(_10k_4_out));
  Capacitor _1uF_2 (.In(1'b0), .Out(_555_1_control));
  Capacitor capacitor_3 (.In(1'b0), .Out(_1k_out));
  Capacitor capacitor_4 (.In(1'b0), .Out(resistor_3_out));
  Capacitor capacitor_5 (.In(1'b0), .Out(resistor_4_out));
  Capacitor _0_01uF_2 (.In(1'b0), .Out(resistor_5_out));

  // Notes on the sheet:
  //   S_CTL_HLT: pin 36
  //   TestPulse: pin 38
  //   Clock: pin 37
  //   Width
  //   20 holes
  //   5 cm
  //   Height
  //   58 holes
  //   14.5 cm
endmodule

/* Test case:
S-CTL-HLT TestPulse Clock
0	  0	        0
0	  1	        1
0	  0	        1
0         1	        2
0         0	        2
0         1	        4
0         0	        4
0         1	        8
0         0	        8
0         1	        16
0         0	        16
0         1	        32
0         0	        32
0         1	        64
0         0	        64
0         1	        128
0         0	        128
0         1	        1

0	  0	        1
0         1	        2
0         0	        2
0         1	        4
1         0	        4
1         1	        8
1         0	        8
1         1	        16
1         0	        16
1         1	        32
1         0	        32
1         1	        64
1         0	        64
1         1	        128
1         0	        128
1         1	        0
*/
