// Digital circuit Decoder.dig as structural Verilog
module Decoder (
  input  [3:0] Nibble_1,
  output IsOpcodeNibble,
  output [7:0] Counter
);

  wire not_1_1_1__4_y, not_1_1_1__5_y, not_1_1_1__6_y;

  NOT_1_1 not_1_1_1 (
    ._1_A(1'b0), ._2_A(1'b0), ._3_A(1'b0), ._4_A(Nibble_1[0]), ._4_Y(not_1_1_1__4_y), .VCC(1'b1), .GND(1'b0),
    ._5_A(Nibble_1[1]), ._5_Y(not_1_1_1__5_y), ._6_A(Nibble_1[2]), ._6_Y(not_1_1_1__6_y));  // open: _1_Y, _2_Y, _3_Y
  AND_4_1 and_4_1_1 (
    ._1_B(not_1_1_1__4_y), ._1_Y(Counter[0]), .VCC(1'b1), .GND(1'b0), ._1_C(not_1_1_1__5_y), .NC_2(1'b0),
    ._2_A(1'b1), ._2_D(not_1_1_1__6_y), ._2_Y(Counter[1]), ._2_C(not_1_1_1__5_y), ._1_A(1'b1), .NC_1(1'b0),
    ._1_D(not_1_1_1__6_y), ._2_B(Nibble_1[0]));
  AND_4_1 and_4_1_2 (
    ._1_B(not_1_1_1__4_y), ._1_Y(Counter[2]), .VCC(1'b1), .GND(1'b0), ._1_C(Nibble_1[1]), .NC_2(1'b0),
    ._2_A(1'b1), ._2_D(not_1_1_1__6_y), ._2_Y(Counter[3]), ._2_C(Nibble_1[1]), ._1_A(1'b1), .NC_1(1'b0),
    ._1_D(not_1_1_1__6_y), ._2_B(Nibble_1[0]));
  AND_4_1 and_4_1_3 (
    ._1_B(not_1_1_1__4_y), ._1_Y(Counter[4]), .VCC(1'b1), .GND(1'b0), ._1_C(not_1_1_1__5_y), .NC_2(1'b0),
    ._2_A(1'b1), ._2_D(Nibble_1[2]), ._2_Y(Counter[5]), ._2_C(not_1_1_1__5_y), ._1_A(1'b1), .NC_1(1'b0),
    ._1_D(Nibble_1[2]), ._2_B(Nibble_1[0]));
  AND_4_1 and_4_1_4 (
    ._1_B(not_1_1_1__4_y), ._1_Y(Counter[6]), .VCC(1'b1), .GND(1'b0), ._1_C(Nibble_1[1]), .NC_2(1'b0),
    ._2_A(1'b1), ._2_D(Nibble_1[2]), ._2_Y(Counter[7]), ._2_C(Nibble_1[1]), ._1_A(1'b1), .NC_1(1'b0),
    ._1_D(Nibble_1[2]), ._2_B(Nibble_1[0]));
  LED _3 (.in(Nibble_1[2]));
  LED _2 (.in(Nibble_1[1]));
  LED _1 (.in(Nibble_1[0]));
  LED _3_2 (.in(not_1_1_1__6_y));
  LED _2_2 (.in(not_1_1_1__5_y));
  LED _1_2 (.in(not_1_1_1__4_y));

  assign IsOpcodeNibble = Nibble_1[3];

  // Notes on the sheet:
  //   Nibble_1: pin 28
  //   IsOpcodeNibble: pin 15
  //   Counter: pin 14
endmodule
