// Digital circuit MDR.dig as structural Verilog
module MDR (
  input  [7:0] Data_alu,
  input  nS_MDR_WriteALU,
  input  nS_MDR_WriteMEM,
  input  [7:0] Data_mem,
  input  D_WRT_MDR,
  output [7:0] Data_out
);

  wire buffer_8_1_1__1_y, buffer_8_1_1__2_y, buffer_8_1_1__3_y, buffer_8_1_1__4_y, buffer_8_1_1__5_y,
       buffer_8_1_1__6_y, buffer_8_1_1__7_y, buffer_8_1_1__8_y;

  Buffer_8_1 buffer_8_1_1 (
    .OE1(nS_MDR_WriteALU), ._1_Y(buffer_8_1_1__1_y), .VCC(1'b1), .GND(1'b0), ._1_A(Data_alu[0]),
    ._2_A(Data_alu[1]), ._2_Y(buffer_8_1_1__2_y), ._4_A(Data_alu[3]), ._5_A(Data_alu[4]),
    ._3_Y(buffer_8_1_1__3_y), ._3_A(Data_alu[2]), .OE2(1'b0), ._4_Y(buffer_8_1_1__4_y), ._6_A(Data_alu[5]),
    ._7_A(Data_alu[6]), ._8_A(Data_alu[7]), ._5_Y(buffer_8_1_1__5_y), ._6_Y(buffer_8_1_1__6_y),
    ._7_Y(buffer_8_1_1__7_y), ._8_Y(buffer_8_1_1__8_y));
  Buffer_8_1 buffer_8_1_2 (
    .OE1(nS_MDR_WriteMEM), ._1_Y(buffer_8_1_1__1_y), .VCC(1'b1), .GND(1'b0), ._1_A(Data_mem[0]),
    ._2_A(Data_mem[1]), ._2_Y(buffer_8_1_1__2_y), ._4_A(Data_mem[3]), ._5_A(Data_mem[4]),
    ._3_Y(buffer_8_1_1__3_y), ._3_A(Data_mem[2]), .OE2(1'b0), ._4_Y(buffer_8_1_1__4_y), ._6_A(Data_mem[5]),
    ._7_A(Data_mem[6]), ._8_A(Data_mem[7]), ._5_Y(buffer_8_1_1__5_y), ._6_Y(buffer_8_1_1__6_y),
    ._7_Y(buffer_8_1_1__7_y), ._8_Y(buffer_8_1_1__8_y));
  D_Flip_Flop d_flip_flop_1 (
    .nEN(1'b0), ._1_Q(Data_out[0]), .VCC(1'b1), .GND(1'b0), ._1_D(buffer_8_1_1__1_y),
    ._2_D(buffer_8_1_1__2_y), ._3_Q(Data_out[2]), .CLK(D_WRT_MDR), ._2_Q(Data_out[1]),
    ._3_D(buffer_8_1_1__3_y), ._4_D(buffer_8_1_1__4_y), ._4_Q(Data_out[3]), ._5_Q(Data_out[4]),
    ._5_D(buffer_8_1_1__5_y), ._6_D(buffer_8_1_1__6_y), ._7_Q(Data_out[6]), ._6_Q(Data_out[5]),
    ._7_D(buffer_8_1_1__7_y), ._8_D(buffer_8_1_1__8_y), ._8_Q(Data_out[7]));
  PullDown pulldown_1 (.out(buffer_8_1_1__1_y));
  PullDown pulldown_2 (.out(buffer_8_1_1__2_y));
  PullDown pulldown_3 (.out(buffer_8_1_1__3_y));
  PullDown pulldown_4 (.out(buffer_8_1_1__4_y));
  PullDown pulldown_5 (.out(buffer_8_1_1__5_y));
  PullDown pulldown_6 (.out(buffer_8_1_1__6_y));
  PullDown pulldown_7 (.out(buffer_8_1_1__7_y));
  PullDown pulldown_8 (.out(buffer_8_1_1__8_y));

  // Notes on the sheet:
  //   Data_alu: pin 2
  //   nS_MDR_WriteALU: pin 1
  //   nS_MDR_WriteMEM: pin 3
  //   Data_mem: pin 4
  //   D_WRT_MDR: pin 5
  //   Data_out: pin 6
  //   Width
  //   20 holes
  //   5 cm
  //   Height
  //   36 holes
  //   9 cm
endmodule

/* Test case Write None:
	Clk_write ~{Write_alu} ~{Write_mem} Data_alu Data_mem Data_out
loop(a, 512)
	0	  1	       1	    Z        Z	      0
	1	  1	       1	    Z        Z	      0
end loop
*/

/* Test case Write ALU:
	Clk_write ~{Write_alu} ~{Write_mem} Data_alu Data_mem Data_out
loop(a, 512)
	let b = random(1<<16);
	0	  0	       1	    (b)      Z	      X
	1	  0	       1	    (b)      Z	      (b)
end loop
*/

/* Test case Write Mem:
	Clk_write ~{Write_alu} ~{Write_mem} Data_alu Data_mem Data_out
loop(a, 512)
	let b = random(1<<16);
	0	  1	       0	    0        (b)	X
	1	  1	       0	    0        (b)	(b)
end loop
*/
