// Digital circuit OperandIntegrator.dig as structural Verilog
module OperandIntegrator (
  input  [3:0] Nibble_2,
  input  [7:0] LSB,
  input  D_SEL_First,
  input  D_SEL_Second,
  input  S_INS_ValRead,
  input  nS_INS_ValRead,
  output [3:0] Select,
  output [11:0] Value
);

  wire and_2_1_2__1_y, and_2_1_2__2_y, and_2_1_2__3_y, and_2_1_2__4_y, and_2_1_3__1_y, and_2_1_3__2_y,
       and_2_1_3__3_y, and_2_1_3__4_y;

  Buffer_8_1 buffer_8_1_1 (
    .OE1(nS_INS_ValRead), ._1_Y(Value[0]), .VCC(1'b1), .GND(1'b0), ._1_A(LSB[0]), ._2_A(LSB[1]),
    ._2_Y(Value[1]), ._4_A(LSB[3]), ._5_A(LSB[4]), ._3_Y(Value[2]), ._3_A(LSB[2]), .OE2(1'b0),
    ._4_Y(Value[3]), ._6_A(LSB[5]), ._7_A(LSB[6]), ._8_A(LSB[7]), ._5_Y(Value[4]), ._6_Y(Value[5]),
    ._7_Y(Value[6]), ._8_Y(Value[7]));
  AND_2_1 and_2_1_1 (
    ._1_A(Nibble_2[0]), ._1_Y(Value[8]), .VCC(1'b1), .GND(1'b0), ._1_B(S_INS_ValRead), ._2_A(Nibble_2[1]),
    ._2_Y(Value[9]), ._2_B(S_INS_ValRead), ._3_B(Nibble_2[2]), ._3_Y(Value[10]), ._3_A(S_INS_ValRead),
    ._4_B(Nibble_2[3]), ._4_Y(Value[11]), ._4_A(S_INS_ValRead));
  AND_2_1 and_2_1_2 (
    ._1_A(LSB[0]), ._1_Y(and_2_1_2__1_y), .VCC(1'b1), .GND(1'b0), ._1_B(D_SEL_Second), ._2_A(LSB[1]),
    ._2_Y(and_2_1_2__2_y), ._2_B(D_SEL_Second), ._3_B(LSB[2]), ._3_Y(and_2_1_2__3_y), ._3_A(D_SEL_Second),
    ._4_B(LSB[3]), ._4_Y(and_2_1_2__4_y), ._4_A(D_SEL_Second));
  AND_2_1 and_2_1_3 (
    ._1_A(LSB[4]), ._1_Y(and_2_1_3__1_y), .VCC(1'b1), .GND(1'b0), ._1_B(D_SEL_First), ._2_A(LSB[5]),
    ._2_Y(and_2_1_3__2_y), ._2_B(D_SEL_First), ._3_B(LSB[6]), ._3_Y(and_2_1_3__3_y), ._3_A(D_SEL_First),
    ._4_B(LSB[7]), ._4_Y(and_2_1_3__4_y), ._4_A(D_SEL_First));
  OR_2_1 or_2_1_1 (
    ._1_A(and_2_1_3__1_y), ._1_Y(Select[0]), .VCC(1'b1), .GND(1'b0), ._1_B(and_2_1_2__1_y),
    ._2_A(and_2_1_3__2_y), ._2_Y(Select[1]), ._2_B(and_2_1_2__2_y), ._3_B(and_2_1_3__3_y), ._3_Y(Select[2]),
    ._3_A(and_2_1_2__3_y), ._4_B(and_2_1_3__4_y), ._4_Y(Select[3]), ._4_A(and_2_1_2__4_y));

  // Notes on the sheet:
  //   Nibble_2: pin 2
  //   LSB: pin 1
  //   D_SEL_First: pin 6
  //   D_SEL_Second: pin 5
  //   S_INS_ValRead: pin 4
  //   Select: pin 13
  //   Value: pin 14
  //   nS_INS_ValRead: pin 3
  //   Width
  //   22 holes
  //   5.5 cm
  //   Height
  //   52 holes
  //   13 cm
endmodule
