// Digital circuit RAM.dig as structural Verilog
module RAM (
  input  [11:0] Address,
  input  [7:0] Data,
  input  nD_WRT_SRAM,
  output [7:0] Out
);

  wire not_1_out;

  SRAM sram_1 (
    .NC(1'b0), .A_0(Address[0]), .A_1(Address[1]), .A_2(Address[2]), .A_3(Address[3]), .A_4(Address[4]),
    .A_5(Address[5]), .A_6(Address[6]), .A_7(Address[7]), .A_8(Address[8]), .A_9(Address[9]),
    .A_10(Address[10]), .A_11(Address[11]), .GND(1'b0), .VCC(1'b1), .nWE(nD_WRT_SRAM), .A_12(1'b0),
    .CS_2(1'b1), .nCS_1(1'b0), .D_0(Out[0]), .D_1(Out[1]), .D_2(Out[2]), .D_3(Out[3]), .D_4(Out[4]),
    .D_5(Out[5]), .D_6(Out[6]), .D_7(Out[7]), .nOE(1'b0));
  Buffer_4_1 buffer_4_1_1 (
    .n1OE(nD_WRT_SRAM), ._11_Y(Out[7]), .VCC(1'b1), .GND(1'b0), ._11_A(Data[7]), ._12_A(Data[6]),
    ._12_Y(Out[6]), ._14_A(Data[4]), ._21_A(Data[3]), ._13_Y(Out[5]), ._13_A(Data[5]), ._2OE(not_1_out),
    ._14_Y(Out[4]), ._22_A(Data[2]), ._23_A(Data[1]), ._24_A(Data[0]), ._21_Y(Out[3]), ._22_Y(Out[2]),
    ._23_Y(Out[1]), ._24_Y(Out[0]));
  not not_1 (not_1_out, nD_WRT_SRAM);

  // Notes on the sheet:
  //   Address: pin 1
  //   Data: pin 2
  //   nD_WRT_SRAM: pin 14
  //   Out: pin 13
  //   Width
  //   20 holes
  //   5 cm
  //   Height
  //   32 holes
  //   8 cm
endmodule

/* Test case:
	Read ~{Read} Address Data Out
loop(a, 256)
	let data = random(1<<8);
	let address = random(1<<16);

	1    0       (address)  (data)  X
	0    1       (address)  (data)  X

	1    0       (address)  0       X
	1    0       (address)  0       (data)
end loop
*/
