// Digital circuit RPC.dig as structural Verilog
module RPC (
  input  D_WRT_RPC,
  input  D_RPC_Registers,
  input  nD_RPC_Registers,
  input  nD_RPC_MemAdder,
  input  [11:0] Add_in,
  input  [11:0] Reg_in,
  output [11:0] Address
);

  wire buffer_4_1_1__11_y, buffer_4_1_1__12_y, buffer_4_1_1__13_y, buffer_4_1_1__14_y, buffer_8_1_1__1_y,
       buffer_8_1_1__2_y, buffer_8_1_1__3_y, buffer_8_1_1__4_y, buffer_8_1_1__5_y, buffer_8_1_1__6_y,
       buffer_8_1_1__7_y, buffer_8_1_1__8_y;

  LED _1 (.in(Add_in[2]));
  LED _2 (.in(Add_in[1]));
  LED _3 (.in(Add_in[0]));
  LED _0 (.in(Add_in[3]));
  Buffer_8_1 buffer_8_1_1 (
    .OE1(nD_RPC_MemAdder), ._1_Y(buffer_8_1_1__1_y), .VCC(1'b1), .GND(1'b0), ._1_A(Add_in[11]),
    ._2_A(Add_in[10]), ._2_Y(buffer_8_1_1__2_y), ._4_A(Add_in[8]), ._5_A(Add_in[7]),
    ._3_Y(buffer_8_1_1__3_y), ._3_A(Add_in[9]), .OE2(1'b0), ._4_Y(buffer_8_1_1__4_y), ._6_A(Add_in[6]),
    ._7_A(Add_in[5]), ._8_A(Add_in[4]), ._5_Y(buffer_8_1_1__5_y), ._6_Y(buffer_8_1_1__6_y),
    ._7_Y(buffer_8_1_1__7_y), ._8_Y(buffer_8_1_1__8_y));
  D_Flip_Flop d_flip_flop_1 (
    .nEN(1'b0), ._1_Q(Address[4]), .VCC(1'b1), .GND(1'b0), ._1_D(buffer_8_1_1__8_y),
    ._2_D(buffer_8_1_1__7_y), ._3_Q(Address[6]), .CLK(D_WRT_RPC), ._2_Q(Address[5]),
    ._3_D(buffer_8_1_1__6_y), ._4_D(buffer_8_1_1__5_y), ._4_Q(Address[7]), ._5_Q(Address[8]),
    ._5_D(buffer_8_1_1__4_y), ._6_D(buffer_8_1_1__3_y), ._7_Q(Address[10]), ._6_Q(Address[9]),
    ._7_D(buffer_8_1_1__2_y), ._8_D(buffer_8_1_1__1_y), ._8_Q(Address[11]));
  LED _7 (.in(buffer_8_1_1__5_y));
  LED _4 (.in(buffer_8_1_1__8_y));
  LED _5 (.in(buffer_8_1_1__7_y));
  LED _6 (.in(buffer_8_1_1__6_y));
  LED _11 (.in(buffer_8_1_1__1_y));
  LED _10 (.in(buffer_8_1_1__2_y));
  LED _9 (.in(buffer_8_1_1__3_y));
  LED _8 (.in(buffer_8_1_1__4_y));
  LED _0_2 (.in(buffer_4_1_1__14_y));
  LED _1_2 (.in(buffer_4_1_1__13_y));
  LED _2_2 (.in(buffer_4_1_1__12_y));
  D_Flip_Flop d_flip_flop_2 (
    .nEN(1'b0), ._1_Q(Address[0]), .VCC(1'b1), .GND(1'b0), ._1_D(buffer_4_1_1__14_y),
    ._2_D(buffer_4_1_1__13_y), ._3_Q(Address[2]), .CLK(D_WRT_RPC), ._2_Q(Address[1]),
    ._3_D(buffer_4_1_1__12_y), ._4_D(buffer_4_1_1__11_y), ._4_Q(Address[3]), ._5_D(1'b0), ._6_D(1'b0),
    ._7_D(1'b0), ._8_D(1'b0));  // open: _5_Q, _7_Q, _6_Q, _8_Q
  Buffer_4_1 buffer_4_1_1 (
    .n1OE(nD_RPC_MemAdder), ._11_Y(buffer_4_1_1__11_y), .VCC(1'b1), .GND(1'b0), ._11_A(Add_in[3]),
    ._12_A(Add_in[2]), ._12_Y(buffer_4_1_1__12_y), ._14_A(Add_in[0]), ._21_A(Reg_in[0]),
    ._13_Y(buffer_4_1_1__13_y), ._13_A(Add_in[1]), ._2OE(D_RPC_Registers), ._14_Y(buffer_4_1_1__14_y),
    ._22_A(Reg_in[1]), ._23_A(Reg_in[2]), ._24_A(Reg_in[3]), ._21_Y(buffer_4_1_1__14_y),
    ._22_Y(buffer_4_1_1__13_y), ._23_Y(buffer_4_1_1__12_y), ._24_Y(buffer_4_1_1__11_y));
  LED _3_2 (.in(buffer_4_1_1__11_y));
  Buffer_8_1 buffer_8_1_2 (
    .OE1(1'b0), ._1_Y(buffer_8_1_1__8_y), .VCC(1'b1), .GND(1'b0), ._1_A(Reg_in[4]), ._2_A(Reg_in[5]),
    ._2_Y(buffer_8_1_1__7_y), ._4_A(Reg_in[7]), ._5_A(Reg_in[8]), ._3_Y(buffer_8_1_1__6_y), ._3_A(Reg_in[6]),
    .OE2(nD_RPC_Registers), ._4_Y(buffer_8_1_1__5_y), ._6_A(Reg_in[9]), ._7_A(Reg_in[10]), ._8_A(Reg_in[11]),
    ._5_Y(buffer_8_1_1__4_y), ._6_Y(buffer_8_1_1__3_y), ._7_Y(buffer_8_1_1__2_y), ._8_Y(buffer_8_1_1__1_y));
  LED _0_3 (.in(Reg_in[0]));
  LED _1_3 (.in(Reg_in[1]));
  LED _2_3 (.in(Reg_in[2]));
  LED _3_3 (.in(Reg_in[3]));

  // Notes on the sheet:
  //   D_WRT_RPC: pin 4
  //   D_RPC_Registers: pin 5
  //   nD_RPC_Registers: pin 2
  //   nD_RPC_MemAdder: pin 3
  //   Add_in: pin 1
  //   Reg_in: pin 13
  //   Address: pin 14
  //   Width
  //   44 holes
  //   11 cm
  //   Height
  //   52 holes
  //   13 cm
endmodule

/* Test case:
Add_in Reg_in Clk_write ~{Reg_write} ~{Add_write} Reg_write Address
52     704    0         1            0            0         0
52     704    1         1            0            0         52

52     704    0         0            1            1         52
52     704    1         0            1            1         704
*/
