// Digital circuit Register File.dig as structural Verilog
module Register_File (
  input  [15:0] Select,
  input  D_WRT_RegOutput,
  input  [7:0] Data_alu,
  input  nS_REG_WriteALU,
  input  [11:0] Data_val,
  input  nS_REG_WriteVal,
  input  nS_REG_WriteMDR,
  input  [7:0] Data_mdr,
  output [7:0] Data_out,
  output [7:0] Test_out
);

  wire buffer_8_1_1__1_y, buffer_8_1_1__2_y, buffer_8_1_1__3_y, buffer_8_1_1__4_y, buffer_8_1_1__5_y,
       buffer_8_1_1__6_y, buffer_8_1_1__7_y, buffer_8_1_1__8_y, d_flip_flop_1__1_q, d_flip_flop_1__2_q,
       d_flip_flop_1__3_q, d_flip_flop_1__4_q, d_flip_flop_1__5_q, d_flip_flop_1__6_q, d_flip_flop_1__7_q,
       d_flip_flop_1__8_q, d_flip_flop_2__1_q, d_flip_flop_2__2_q, d_flip_flop_2__3_q, d_flip_flop_2__4_q,
       d_flip_flop_2__5_q, d_flip_flop_2__6_q, d_flip_flop_2__7_q, d_flip_flop_2__8_q, d_flip_flop_3__1_q,
       d_flip_flop_3__2_q, d_flip_flop_3__3_q, d_flip_flop_3__4_q, d_flip_flop_3__5_q, d_flip_flop_3__6_q,
       d_flip_flop_3__7_q, d_flip_flop_3__8_q, d_flip_flop_4__1_q, d_flip_flop_4__2_q, d_flip_flop_4__3_q,
       d_flip_flop_4__4_q, d_flip_flop_4__5_q, d_flip_flop_4__6_q, d_flip_flop_4__7_q, d_flip_flop_4__8_q,
       d_flip_flop_5__1_q, d_flip_flop_5__2_q, d_flip_flop_5__3_q, d_flip_flop_5__4_q, d_flip_flop_5__5_q,
       d_flip_flop_5__6_q, d_flip_flop_5__7_q, d_flip_flop_5__8_q, d_flip_flop_6__1_q, d_flip_flop_6__2_q,
       d_flip_flop_6__3_q, d_flip_flop_6__4_q, d_flip_flop_6__5_q, d_flip_flop_6__6_q, d_flip_flop_6__7_q,
       d_flip_flop_6__8_q, d_flip_flop_7__1_q, d_flip_flop_7__2_q, d_flip_flop_7__3_q, d_flip_flop_7__4_q,
       d_flip_flop_7__5_q, d_flip_flop_7__6_q, d_flip_flop_7__7_q, d_flip_flop_7__8_q, d_flip_flop_8__1_q,
       d_flip_flop_8__2_q, d_flip_flop_8__3_q, d_flip_flop_8__4_q, d_flip_flop_8__5_q, d_flip_flop_8__6_q,
       d_flip_flop_8__7_q, d_flip_flop_8__8_q, d_flip_flop_9__1_q, d_flip_flop_9__2_q, d_flip_flop_9__3_q,
       d_flip_flop_9__4_q, d_flip_flop_9__5_q, d_flip_flop_9__6_q, d_flip_flop_9__7_q, d_flip_flop_9__8_q,
       d_flip_flop_10__1_q, d_flip_flop_10__2_q, d_flip_flop_10__3_q, d_flip_flop_10__4_q,
       d_flip_flop_10__5_q, d_flip_flop_10__6_q, d_flip_flop_10__7_q, d_flip_flop_10__8_q,
       d_flip_flop_11__1_q, d_flip_flop_11__2_q, d_flip_flop_11__3_q, d_flip_flop_11__4_q,
       d_flip_flop_11__5_q, d_flip_flop_11__6_q, d_flip_flop_11__7_q, d_flip_flop_11__8_q,
       d_flip_flop_12__1_q, d_flip_flop_12__2_q, d_flip_flop_12__3_q, d_flip_flop_12__4_q,
       d_flip_flop_12__5_q, d_flip_flop_12__6_q, d_flip_flop_12__7_q, d_flip_flop_12__8_q,
       d_flip_flop_14__1_q, d_flip_flop_14__2_q, d_flip_flop_14__3_q, d_flip_flop_14__4_q,
       d_flip_flop_14__5_q, d_flip_flop_14__6_q, d_flip_flop_14__7_q, d_flip_flop_14__8_q;

  Buffer_8_1 buffer_8_1_1 (
    .OE1(nS_REG_WriteALU), ._1_Y(buffer_8_1_1__1_y), .VCC(1'b1), .GND(1'b0), ._1_A(Data_alu[0]),
    ._2_A(Data_alu[1]), ._2_Y(buffer_8_1_1__2_y), ._4_A(Data_alu[3]), ._5_A(Data_alu[4]),
    ._3_Y(buffer_8_1_1__3_y), ._3_A(Data_alu[2]), .OE2(1'b0), ._4_Y(buffer_8_1_1__4_y), ._6_A(Data_alu[5]),
    ._7_A(Data_alu[6]), ._8_A(Data_alu[7]), ._5_Y(buffer_8_1_1__5_y), ._6_Y(buffer_8_1_1__6_y),
    ._7_Y(buffer_8_1_1__7_y), ._8_Y(buffer_8_1_1__8_y));
  Buffer_8_1 buffer_8_1_2 (
    .OE1(nS_REG_WriteVal), ._1_Y(buffer_8_1_1__1_y), .VCC(1'b1), .GND(1'b0), ._1_A(Data_val[4]),
    ._2_A(Data_val[5]), ._2_Y(buffer_8_1_1__2_y), ._4_A(Data_val[7]), ._5_A(Data_val[8]),
    ._3_Y(buffer_8_1_1__3_y), ._3_A(Data_val[6]), .OE2(1'b0), ._4_Y(buffer_8_1_1__4_y), ._6_A(Data_val[9]),
    ._7_A(Data_val[10]), ._8_A(Data_val[11]), ._5_Y(buffer_8_1_1__5_y), ._6_Y(buffer_8_1_1__6_y),
    ._7_Y(buffer_8_1_1__7_y), ._8_Y(buffer_8_1_1__8_y));
  Buffer_8_1 buffer_8_1_3 (
    .OE1(nS_REG_WriteMDR), ._1_Y(buffer_8_1_1__1_y), .VCC(1'b1), .GND(1'b0), ._1_A(Data_mdr[0]),
    ._2_A(Data_mdr[1]), ._2_Y(buffer_8_1_1__2_y), ._4_A(Data_mdr[3]), ._5_A(Data_mdr[4]),
    ._3_Y(buffer_8_1_1__3_y), ._3_A(Data_mdr[2]), .OE2(1'b0), ._4_Y(buffer_8_1_1__4_y), ._6_A(Data_mdr[5]),
    ._7_A(Data_mdr[6]), ._8_A(Data_mdr[7]), ._5_Y(buffer_8_1_1__5_y), ._6_Y(buffer_8_1_1__6_y),
    ._7_Y(buffer_8_1_1__7_y), ._8_Y(buffer_8_1_1__8_y));
  D_Flip_Flop d_flip_flop_1 (
    .nEN(Select[7]), ._1_Q(d_flip_flop_1__1_q), .VCC(1'b1), .GND(1'b0), ._1_D(buffer_8_1_1__1_y),
    ._2_D(buffer_8_1_1__2_y), ._3_Q(d_flip_flop_1__3_q), .CLK(D_WRT_RegOutput), ._2_Q(d_flip_flop_1__2_q),
    ._3_D(buffer_8_1_1__3_y), ._4_D(buffer_8_1_1__4_y), ._4_Q(d_flip_flop_1__4_q), ._5_Q(d_flip_flop_1__5_q),
    ._5_D(buffer_8_1_1__5_y), ._6_D(buffer_8_1_1__6_y), ._7_Q(d_flip_flop_1__7_q), ._6_Q(d_flip_flop_1__6_q),
    ._7_D(buffer_8_1_1__7_y), ._8_D(buffer_8_1_1__8_y), ._8_Q(d_flip_flop_1__8_q));
  Buffer_8_1 buffer_8_1_4 (
    .OE1(Select[7]), ._1_Y(Data_out[7]), .VCC(1'b1), .GND(1'b0), ._1_A(d_flip_flop_1__8_q),
    ._2_A(d_flip_flop_1__7_q), ._2_Y(Data_out[6]), ._4_A(d_flip_flop_1__5_q), ._5_A(d_flip_flop_1__4_q),
    ._3_Y(Data_out[5]), ._3_A(d_flip_flop_1__6_q), .OE2(1'b0), ._4_Y(Data_out[4]), ._6_A(d_flip_flop_1__3_q),
    ._7_A(d_flip_flop_1__2_q), ._8_A(d_flip_flop_1__1_q), ._5_Y(Data_out[3]), ._6_Y(Data_out[2]),
    ._7_Y(Data_out[1]), ._8_Y(Data_out[0]));
  Buffer_8_1 buffer_8_1_5 (
    .OE1(Select[8]), ._1_Y(Data_out[7]), .VCC(1'b1), .GND(1'b0), ._1_A(d_flip_flop_2__8_q),
    ._2_A(d_flip_flop_2__7_q), ._2_Y(Data_out[6]), ._4_A(d_flip_flop_2__5_q), ._5_A(d_flip_flop_2__4_q),
    ._3_Y(Data_out[5]), ._3_A(d_flip_flop_2__6_q), .OE2(1'b0), ._4_Y(Data_out[4]), ._6_A(d_flip_flop_2__3_q),
    ._7_A(d_flip_flop_2__2_q), ._8_A(d_flip_flop_2__1_q), ._5_Y(Data_out[3]), ._6_Y(Data_out[2]),
    ._7_Y(Data_out[1]), ._8_Y(Data_out[0]));
  D_Flip_Flop d_flip_flop_2 (
    .nEN(Select[8]), ._1_Q(d_flip_flop_2__1_q), .VCC(1'b1), .GND(1'b0), ._1_D(buffer_8_1_1__1_y),
    ._2_D(buffer_8_1_1__2_y), ._3_Q(d_flip_flop_2__3_q), .CLK(D_WRT_RegOutput), ._2_Q(d_flip_flop_2__2_q),
    ._3_D(buffer_8_1_1__3_y), ._4_D(buffer_8_1_1__4_y), ._4_Q(d_flip_flop_2__4_q), ._5_Q(d_flip_flop_2__5_q),
    ._5_D(buffer_8_1_1__5_y), ._6_D(buffer_8_1_1__6_y), ._7_Q(d_flip_flop_2__7_q), ._6_Q(d_flip_flop_2__6_q),
    ._7_D(buffer_8_1_1__7_y), ._8_D(buffer_8_1_1__8_y), ._8_Q(d_flip_flop_2__8_q));
  D_Flip_Flop d_flip_flop_3 (
    .nEN(Select[6]), ._1_Q(d_flip_flop_3__1_q), .VCC(1'b1), .GND(1'b0), ._1_D(buffer_8_1_1__1_y),
    ._2_D(buffer_8_1_1__2_y), ._3_Q(d_flip_flop_3__3_q), .CLK(D_WRT_RegOutput), ._2_Q(d_flip_flop_3__2_q),
    ._3_D(buffer_8_1_1__3_y), ._4_D(buffer_8_1_1__4_y), ._4_Q(d_flip_flop_3__4_q), ._5_Q(d_flip_flop_3__5_q),
    ._5_D(buffer_8_1_1__5_y), ._6_D(buffer_8_1_1__6_y), ._7_Q(d_flip_flop_3__7_q), ._6_Q(d_flip_flop_3__6_q),
    ._7_D(buffer_8_1_1__7_y), ._8_D(buffer_8_1_1__8_y), ._8_Q(d_flip_flop_3__8_q));
  Buffer_8_1 buffer_8_1_6 (
    .OE1(Select[6]), ._1_Y(Data_out[7]), .VCC(1'b1), .GND(1'b0), ._1_A(d_flip_flop_3__8_q),
    ._2_A(d_flip_flop_3__7_q), ._2_Y(Data_out[6]), ._4_A(d_flip_flop_3__5_q), ._5_A(d_flip_flop_3__4_q),
    ._3_Y(Data_out[5]), ._3_A(d_flip_flop_3__6_q), .OE2(1'b0), ._4_Y(Data_out[4]), ._6_A(d_flip_flop_3__3_q),
    ._7_A(d_flip_flop_3__2_q), ._8_A(d_flip_flop_3__1_q), ._5_Y(Data_out[3]), ._6_Y(Data_out[2]),
    ._7_Y(Data_out[1]), ._8_Y(Data_out[0]));
  Buffer_8_1 buffer_8_1_7 (
    .OE1(Select[9]), ._1_Y(Data_out[7]), .VCC(1'b1), .GND(1'b0), ._1_A(d_flip_flop_4__8_q),
    ._2_A(d_flip_flop_4__7_q), ._2_Y(Data_out[6]), ._4_A(d_flip_flop_4__5_q), ._5_A(d_flip_flop_4__4_q),
    ._3_Y(Data_out[5]), ._3_A(d_flip_flop_4__6_q), .OE2(1'b0), ._4_Y(Data_out[4]), ._6_A(d_flip_flop_4__3_q),
    ._7_A(d_flip_flop_4__2_q), ._8_A(d_flip_flop_4__1_q), ._5_Y(Data_out[3]), ._6_Y(Data_out[2]),
    ._7_Y(Data_out[1]), ._8_Y(Data_out[0]));
  D_Flip_Flop d_flip_flop_4 (
    .nEN(Select[9]), ._1_Q(d_flip_flop_4__1_q), .VCC(1'b1), .GND(1'b0), ._1_D(buffer_8_1_1__1_y),
    ._2_D(buffer_8_1_1__2_y), ._3_Q(d_flip_flop_4__3_q), .CLK(D_WRT_RegOutput), ._2_Q(d_flip_flop_4__2_q),
    ._3_D(buffer_8_1_1__3_y), ._4_D(buffer_8_1_1__4_y), ._4_Q(d_flip_flop_4__4_q), ._5_Q(d_flip_flop_4__5_q),
    ._5_D(buffer_8_1_1__5_y), ._6_D(buffer_8_1_1__6_y), ._7_Q(d_flip_flop_4__7_q), ._6_Q(d_flip_flop_4__6_q),
    ._7_D(buffer_8_1_1__7_y), ._8_D(buffer_8_1_1__8_y), ._8_Q(d_flip_flop_4__8_q));
  D_Flip_Flop d_flip_flop_5 (
    .nEN(Select[5]), ._1_Q(d_flip_flop_5__1_q), .VCC(1'b1), .GND(1'b0), ._1_D(buffer_8_1_1__1_y),
    ._2_D(buffer_8_1_1__2_y), ._3_Q(d_flip_flop_5__3_q), .CLK(D_WRT_RegOutput), ._2_Q(d_flip_flop_5__2_q),
    ._3_D(buffer_8_1_1__3_y), ._4_D(buffer_8_1_1__4_y), ._4_Q(d_flip_flop_5__4_q), ._5_Q(d_flip_flop_5__5_q),
    ._5_D(buffer_8_1_1__5_y), ._6_D(buffer_8_1_1__6_y), ._7_Q(d_flip_flop_5__7_q), ._6_Q(d_flip_flop_5__6_q),
    ._7_D(buffer_8_1_1__7_y), ._8_D(buffer_8_1_1__8_y), ._8_Q(d_flip_flop_5__8_q));
  Buffer_8_1 buffer_8_1_8 (
    .OE1(Select[5]), ._1_Y(Data_out[7]), .VCC(1'b1), .GND(1'b0), ._1_A(d_flip_flop_5__8_q),
    ._2_A(d_flip_flop_5__7_q), ._2_Y(Data_out[6]), ._4_A(d_flip_flop_5__5_q), ._5_A(d_flip_flop_5__4_q),
    ._3_Y(Data_out[5]), ._3_A(d_flip_flop_5__6_q), .OE2(1'b0), ._4_Y(Data_out[4]), ._6_A(d_flip_flop_5__3_q),
    ._7_A(d_flip_flop_5__2_q), ._8_A(d_flip_flop_5__1_q), ._5_Y(Data_out[3]), ._6_Y(Data_out[2]),
    ._7_Y(Data_out[1]), ._8_Y(Data_out[0]));
  Buffer_8_1 buffer_8_1_9 (
    .OE1(Select[10]), ._1_Y(Data_out[7]), .VCC(1'b1), .GND(1'b0), ._1_A(d_flip_flop_6__8_q),
    ._2_A(d_flip_flop_6__7_q), ._2_Y(Data_out[6]), ._4_A(d_flip_flop_6__5_q), ._5_A(d_flip_flop_6__4_q),
    ._3_Y(Data_out[5]), ._3_A(d_flip_flop_6__6_q), .OE2(1'b0), ._4_Y(Data_out[4]), ._6_A(d_flip_flop_6__3_q),
    ._7_A(d_flip_flop_6__2_q), ._8_A(d_flip_flop_6__1_q), ._5_Y(Data_out[3]), ._6_Y(Data_out[2]),
    ._7_Y(Data_out[1]), ._8_Y(Data_out[0]));
  D_Flip_Flop d_flip_flop_6 (
    .nEN(Select[10]), ._1_Q(d_flip_flop_6__1_q), .VCC(1'b1), .GND(1'b0), ._1_D(buffer_8_1_1__1_y),
    ._2_D(buffer_8_1_1__2_y), ._3_Q(d_flip_flop_6__3_q), .CLK(D_WRT_RegOutput), ._2_Q(d_flip_flop_6__2_q),
    ._3_D(buffer_8_1_1__3_y), ._4_D(buffer_8_1_1__4_y), ._4_Q(d_flip_flop_6__4_q), ._5_Q(d_flip_flop_6__5_q),
    ._5_D(buffer_8_1_1__5_y), ._6_D(buffer_8_1_1__6_y), ._7_Q(d_flip_flop_6__7_q), ._6_Q(d_flip_flop_6__6_q),
    ._7_D(buffer_8_1_1__7_y), ._8_D(buffer_8_1_1__8_y), ._8_Q(d_flip_flop_6__8_q));
  D_Flip_Flop d_flip_flop_7 (
    .nEN(Select[4]), ._1_Q(d_flip_flop_7__1_q), .VCC(1'b1), .GND(1'b0), ._1_D(buffer_8_1_1__1_y),
    ._2_D(buffer_8_1_1__2_y), ._3_Q(d_flip_flop_7__3_q), .CLK(D_WRT_RegOutput), ._2_Q(d_flip_flop_7__2_q),
    ._3_D(buffer_8_1_1__3_y), ._4_D(buffer_8_1_1__4_y), ._4_Q(d_flip_flop_7__4_q), ._5_Q(d_flip_flop_7__5_q),
    ._5_D(buffer_8_1_1__5_y), ._6_D(buffer_8_1_1__6_y), ._7_Q(d_flip_flop_7__7_q), ._6_Q(d_flip_flop_7__6_q),
    ._7_D(buffer_8_1_1__7_y), ._8_D(buffer_8_1_1__8_y), ._8_Q(d_flip_flop_7__8_q));
  Buffer_8_1 buffer_8_1_10 (
    .OE1(Select[4]), ._1_Y(Data_out[7]), .VCC(1'b1), .GND(1'b0), ._1_A(d_flip_flop_7__8_q),
    ._2_A(d_flip_flop_7__7_q), ._2_Y(Data_out[6]), ._4_A(d_flip_flop_7__5_q), ._5_A(d_flip_flop_7__4_q),
    ._3_Y(Data_out[5]), ._3_A(d_flip_flop_7__6_q), .OE2(1'b0), ._4_Y(Data_out[4]), ._6_A(d_flip_flop_7__3_q),
    ._7_A(d_flip_flop_7__2_q), ._8_A(d_flip_flop_7__1_q), ._5_Y(Data_out[3]), ._6_Y(Data_out[2]),
    ._7_Y(Data_out[1]), ._8_Y(Data_out[0]));
  Buffer_8_1 buffer_8_1_11 (
    .OE1(Select[11]), ._1_Y(Data_out[7]), .VCC(1'b1), .GND(1'b0), ._1_A(d_flip_flop_8__8_q),
    ._2_A(d_flip_flop_8__7_q), ._2_Y(Data_out[6]), ._4_A(d_flip_flop_8__5_q), ._5_A(d_flip_flop_8__4_q),
    ._3_Y(Data_out[5]), ._3_A(d_flip_flop_8__6_q), .OE2(1'b0), ._4_Y(Data_out[4]), ._6_A(d_flip_flop_8__3_q),
    ._7_A(d_flip_flop_8__2_q), ._8_A(d_flip_flop_8__1_q), ._5_Y(Data_out[3]), ._6_Y(Data_out[2]),
    ._7_Y(Data_out[1]), ._8_Y(Data_out[0]));
  D_Flip_Flop d_flip_flop_8 (
    .nEN(Select[11]), ._1_Q(d_flip_flop_8__1_q), .VCC(1'b1), .GND(1'b0), ._1_D(buffer_8_1_1__1_y),
    ._2_D(buffer_8_1_1__2_y), ._3_Q(d_flip_flop_8__3_q), .CLK(D_WRT_RegOutput), ._2_Q(d_flip_flop_8__2_q),
    ._3_D(buffer_8_1_1__3_y), ._4_D(buffer_8_1_1__4_y), ._4_Q(d_flip_flop_8__4_q), ._5_Q(d_flip_flop_8__5_q),
    ._5_D(buffer_8_1_1__5_y), ._6_D(buffer_8_1_1__6_y), ._7_Q(d_flip_flop_8__7_q), ._6_Q(d_flip_flop_8__6_q),
    ._7_D(buffer_8_1_1__7_y), ._8_D(buffer_8_1_1__8_y), ._8_Q(d_flip_flop_8__8_q));
  D_Flip_Flop d_flip_flop_9 (
    .nEN(Select[3]), ._1_Q(d_flip_flop_9__1_q), .VCC(1'b1), .GND(1'b0), ._1_D(buffer_8_1_1__1_y),
    ._2_D(buffer_8_1_1__2_y), ._3_Q(d_flip_flop_9__3_q), .CLK(D_WRT_RegOutput), ._2_Q(d_flip_flop_9__2_q),
    ._3_D(buffer_8_1_1__3_y), ._4_D(buffer_8_1_1__4_y), ._4_Q(d_flip_flop_9__4_q), ._5_Q(d_flip_flop_9__5_q),
    ._5_D(buffer_8_1_1__5_y), ._6_D(buffer_8_1_1__6_y), ._7_Q(d_flip_flop_9__7_q), ._6_Q(d_flip_flop_9__6_q),
    ._7_D(buffer_8_1_1__7_y), ._8_D(buffer_8_1_1__8_y), ._8_Q(d_flip_flop_9__8_q));
  Buffer_8_1 buffer_8_1_12 (
    .OE1(Select[3]), ._1_Y(Data_out[7]), .VCC(1'b1), .GND(1'b0), ._1_A(d_flip_flop_9__8_q),
    ._2_A(d_flip_flop_9__7_q), ._2_Y(Data_out[6]), ._4_A(d_flip_flop_9__5_q), ._5_A(d_flip_flop_9__4_q),
    ._3_Y(Data_out[5]), ._3_A(d_flip_flop_9__6_q), .OE2(1'b0), ._4_Y(Data_out[4]), ._6_A(d_flip_flop_9__3_q),
    ._7_A(d_flip_flop_9__2_q), ._8_A(d_flip_flop_9__1_q), ._5_Y(Data_out[3]), ._6_Y(Data_out[2]),
    ._7_Y(Data_out[1]), ._8_Y(Data_out[0]));
  Buffer_8_1 buffer_8_1_13 (
    .OE1(Select[12]), ._1_Y(Data_out[7]), .VCC(1'b1), .GND(1'b0), ._1_A(d_flip_flop_10__8_q),
    ._2_A(d_flip_flop_10__7_q), ._2_Y(Data_out[6]), ._4_A(d_flip_flop_10__5_q), ._5_A(d_flip_flop_10__4_q),
    ._3_Y(Data_out[5]), ._3_A(d_flip_flop_10__6_q), .OE2(1'b0), ._4_Y(Data_out[4]),
    ._6_A(d_flip_flop_10__3_q), ._7_A(d_flip_flop_10__2_q), ._8_A(d_flip_flop_10__1_q), ._5_Y(Data_out[3]),
    ._6_Y(Data_out[2]), ._7_Y(Data_out[1]), ._8_Y(Data_out[0]));
  D_Flip_Flop d_flip_flop_10 (
    .nEN(Select[12]), ._1_Q(d_flip_flop_10__1_q), .VCC(1'b1), .GND(1'b0), ._1_D(buffer_8_1_1__1_y),
    ._2_D(buffer_8_1_1__2_y), ._3_Q(d_flip_flop_10__3_q), .CLK(D_WRT_RegOutput), ._2_Q(d_flip_flop_10__2_q),
    ._3_D(buffer_8_1_1__3_y), ._4_D(buffer_8_1_1__4_y), ._4_Q(d_flip_flop_10__4_q),
    ._5_Q(d_flip_flop_10__5_q), ._5_D(buffer_8_1_1__5_y), ._6_D(buffer_8_1_1__6_y),
    ._7_Q(d_flip_flop_10__7_q), ._6_Q(d_flip_flop_10__6_q), ._7_D(buffer_8_1_1__7_y),
    ._8_D(buffer_8_1_1__8_y), ._8_Q(d_flip_flop_10__8_q));
  D_Flip_Flop d_flip_flop_11 (
    .nEN(Select[2]), ._1_Q(d_flip_flop_11__1_q), .VCC(1'b1), .GND(1'b0), ._1_D(buffer_8_1_1__1_y),
    ._2_D(buffer_8_1_1__2_y), ._3_Q(d_flip_flop_11__3_q), .CLK(D_WRT_RegOutput), ._2_Q(d_flip_flop_11__2_q),
    ._3_D(buffer_8_1_1__3_y), ._4_D(buffer_8_1_1__4_y), ._4_Q(d_flip_flop_11__4_q),
    ._5_Q(d_flip_flop_11__5_q), ._5_D(buffer_8_1_1__5_y), ._6_D(buffer_8_1_1__6_y),
    ._7_Q(d_flip_flop_11__7_q), ._6_Q(d_flip_flop_11__6_q), ._7_D(buffer_8_1_1__7_y),
    ._8_D(buffer_8_1_1__8_y), ._8_Q(d_flip_flop_11__8_q));
  Buffer_8_1 buffer_8_1_14 (
    .OE1(Select[2]), ._1_Y(Data_out[7]), .VCC(1'b1), .GND(1'b0), ._1_A(d_flip_flop_11__8_q),
    ._2_A(d_flip_flop_11__7_q), ._2_Y(Data_out[6]), ._4_A(d_flip_flop_11__5_q), ._5_A(d_flip_flop_11__4_q),
    ._3_Y(Data_out[5]), ._3_A(d_flip_flop_11__6_q), .OE2(1'b0), ._4_Y(Data_out[4]),
    ._6_A(d_flip_flop_11__3_q), ._7_A(d_flip_flop_11__2_q), ._8_A(d_flip_flop_11__1_q), ._5_Y(Data_out[3]),
    ._6_Y(Data_out[2]), ._7_Y(Data_out[1]), ._8_Y(Data_out[0]));
  Buffer_8_1 buffer_8_1_15 (
    .OE1(Select[13]), ._1_Y(Data_out[7]), .VCC(1'b1), .GND(1'b0), ._1_A(d_flip_flop_12__8_q),
    ._2_A(d_flip_flop_12__7_q), ._2_Y(Data_out[6]), ._4_A(d_flip_flop_12__5_q), ._5_A(d_flip_flop_12__4_q),
    ._3_Y(Data_out[5]), ._3_A(d_flip_flop_12__6_q), .OE2(1'b0), ._4_Y(Data_out[4]),
    ._6_A(d_flip_flop_12__3_q), ._7_A(d_flip_flop_12__2_q), ._8_A(d_flip_flop_12__1_q), ._5_Y(Data_out[3]),
    ._6_Y(Data_out[2]), ._7_Y(Data_out[1]), ._8_Y(Data_out[0]));
  D_Flip_Flop d_flip_flop_12 (
    .nEN(Select[13]), ._1_Q(d_flip_flop_12__1_q), .VCC(1'b1), .GND(1'b0), ._1_D(buffer_8_1_1__1_y),
    ._2_D(buffer_8_1_1__2_y), ._3_Q(d_flip_flop_12__3_q), .CLK(D_WRT_RegOutput), ._2_Q(d_flip_flop_12__2_q),
    ._3_D(buffer_8_1_1__3_y), ._4_D(buffer_8_1_1__4_y), ._4_Q(d_flip_flop_12__4_q),
    ._5_Q(d_flip_flop_12__5_q), ._5_D(buffer_8_1_1__5_y), ._6_D(buffer_8_1_1__6_y),
    ._7_Q(d_flip_flop_12__7_q), ._6_Q(d_flip_flop_12__6_q), ._7_D(buffer_8_1_1__7_y),
    ._8_D(buffer_8_1_1__8_y), ._8_Q(d_flip_flop_12__8_q));
  D_Flip_Flop d_flip_flop_13 (
    .nEN(Select[1]), ._1_Q(Test_out[0]), .VCC(1'b1), .GND(1'b0), ._1_D(buffer_8_1_1__1_y),
    ._2_D(buffer_8_1_1__2_y), ._3_Q(Test_out[2]), .CLK(D_WRT_RegOutput), ._2_Q(Test_out[1]),
    ._3_D(buffer_8_1_1__3_y), ._4_D(buffer_8_1_1__4_y), ._4_Q(Test_out[3]), ._5_Q(Test_out[4]),
    ._5_D(buffer_8_1_1__5_y), ._6_D(buffer_8_1_1__6_y), ._7_Q(Test_out[6]), ._6_Q(Test_out[5]),
    ._7_D(buffer_8_1_1__7_y), ._8_D(buffer_8_1_1__8_y), ._8_Q(Test_out[7]));
  Buffer_8_1 buffer_8_1_16 (
    .OE1(Select[1]), ._1_Y(Data_out[7]), .VCC(1'b1), .GND(1'b0), ._1_A(Test_out[7]), ._2_A(Test_out[6]),
    ._2_Y(Data_out[6]), ._4_A(Test_out[4]), ._5_A(Test_out[3]), ._3_Y(Data_out[5]), ._3_A(Test_out[5]),
    .OE2(1'b0), ._4_Y(Data_out[4]), ._6_A(Test_out[2]), ._7_A(Test_out[1]), ._8_A(Test_out[0]),
    ._5_Y(Data_out[3]), ._6_Y(Data_out[2]), ._7_Y(Data_out[1]), ._8_Y(Data_out[0]));
  Buffer_8_1 buffer_8_1_17 (
    .OE1(Select[14]), ._1_Y(Data_out[7]), .VCC(1'b1), .GND(1'b0), ._1_A(d_flip_flop_14__8_q),
    ._2_A(d_flip_flop_14__7_q), ._2_Y(Data_out[6]), ._4_A(d_flip_flop_14__5_q), ._5_A(d_flip_flop_14__4_q),
    ._3_Y(Data_out[5]), ._3_A(d_flip_flop_14__6_q), .OE2(1'b0), ._4_Y(Data_out[4]),
    ._6_A(d_flip_flop_14__3_q), ._7_A(d_flip_flop_14__2_q), ._8_A(d_flip_flop_14__1_q), ._5_Y(Data_out[3]),
    ._6_Y(Data_out[2]), ._7_Y(Data_out[1]), ._8_Y(Data_out[0]));
  D_Flip_Flop d_flip_flop_14 (
    .nEN(Select[14]), ._1_Q(d_flip_flop_14__1_q), .VCC(1'b1), .GND(1'b0), ._1_D(buffer_8_1_1__1_y),
    ._2_D(buffer_8_1_1__2_y), ._3_Q(d_flip_flop_14__3_q), .CLK(D_WRT_RegOutput), ._2_Q(d_flip_flop_14__2_q),
    ._3_D(buffer_8_1_1__3_y), ._4_D(buffer_8_1_1__4_y), ._4_Q(d_flip_flop_14__4_q),
    ._5_Q(d_flip_flop_14__5_q), ._5_D(buffer_8_1_1__5_y), ._6_D(buffer_8_1_1__6_y),
    ._7_Q(d_flip_flop_14__7_q), ._6_Q(d_flip_flop_14__6_q), ._7_D(buffer_8_1_1__7_y),
    ._8_D(buffer_8_1_1__8_y), ._8_Q(d_flip_flop_14__8_q));
  PullDown pulldown_1 (.out(Data_out[7]));
  PullDown pulldown_2 (.out(Data_out[6]));
  PullDown pulldown_3 (.out(Data_out[5]));
  PullDown pulldown_4 (.out(Data_out[4]));
  PullDown pulldown_5 (.out(Data_out[2]));
  PullDown pulldown_6 (.out(Data_out[3]));
  PullDown pulldown_7 (.out(Data_out[1]));
  PullDown pulldown_8 (.out(Data_out[0]));

  // Notes on the sheet:
  //   Select: pin 1
  //   D_WRT_RegOutput: pin 6
  //   Data_alu: pin 3
  //   nS_REG_WriteALU: pin 2
  //   Data_val: pin 5
  //   nS_REG_WriteVal: pin 4
  //   Data_out: pin 32
  //   Test_out: pin 17
  //   nS_REG_WriteMDR: pin 7
  //   Data_mdr: pin 8
  //   Width
  //   144 holes
  //   36 cm
  //   Height
  //   78 holes
  //   19.5
  //   cm
  //   8
  //   7
  //   9
  //   6
  //   10
  //   5
  //   11
  //   4
  //   12
  //   3
  //   13
  //   2
  //   14
  //   1
endmodule

/* Test case:
Select Data_alu Data_mdr Data_val ~{Write_alu} ~{Write_mdr} ~{Write_val} Clk_write Data_out
(-9)   53       0        0        0            1            1            0         X
(-9)   53       0        0        0            1            1            1         X

(-257) 0        203      0        1            0            1            0         X
(-257) 0        203      0        1            0            1            1         X

(-3)   53       0        65       1            1            0            0         X
(-3)   53       0        65       1            1            0            1         X

(-257) 0        0        0        0            0            0            0         203
(-9)   0        0        0        0            0            0            0         53
(-3)   0        0        0        0            0            0            0         4
*/
