// Digital circuit RegisterBuffer.dig as structural Verilog
module RegisterBuffer (
  input  [7:0] Data_in,
  input  D_WRT_BufferSecond,
  input  D_WRT_BufferFirst,
  output [7:0] R2_out,
  output [7:0] R1_out
);

  D_Flip_Flop d_flip_flop_1 (
    .nEN(1'b0), ._1_Q(R1_out[0]), .VCC(1'b1), .GND(1'b0), ._1_D(Data_in[0]), ._2_D(Data_in[1]),
    ._3_Q(R1_out[2]), .CLK(D_WRT_BufferFirst), ._2_Q(R1_out[1]), ._3_D(Data_in[2]), ._4_D(Data_in[3]),
    ._4_Q(R1_out[3]), ._5_Q(R1_out[4]), ._5_D(Data_in[4]), ._6_D(Data_in[5]), ._7_Q(R1_out[6]),
    ._6_Q(R1_out[5]), ._7_D(Data_in[6]), ._8_D(Data_in[7]), ._8_Q(R1_out[7]));
  D_Flip_Flop d_flip_flop_2 (
    .nEN(1'b0), ._1_Q(R2_out[0]), .VCC(1'b1), .GND(1'b0), ._1_D(Data_in[0]), ._2_D(Data_in[1]),
    ._3_Q(R2_out[2]), .CLK(D_WRT_BufferSecond), ._2_Q(R2_out[1]), ._3_D(Data_in[2]), ._4_D(Data_in[3]),
    ._4_Q(R2_out[3]), ._5_Q(R2_out[4]), ._5_D(Data_in[4]), ._6_D(Data_in[5]), ._7_Q(R2_out[6]),
    ._6_Q(R2_out[5]), ._7_D(Data_in[6]), ._8_D(Data_in[7]), ._8_Q(R2_out[7]));

  // Notes on the sheet:
  //   Data_in: pin 1
  //   D_WRT_BufferSecond: pin 3
  //   D_WRT_BufferFirst: pin 2
  //   R2_out: pin 8
  //   R1_out: pin 9
  //   Width
  //   16 holes
  //   4 cm
  //   Height
  //   32 holes
  //   8 cm
endmodule
