// Digital circuit D Flip Flop.dig as structural Verilog
module D_Flip_Flop (
  input  nEN,
  input  VCC,
  input  GND,
  input  _1_D,
  input  _2_D,
  input  CLK,
  input  _3_D,
  input  _4_D,
  input  _5_D,
  input  _6_D,
  input  _7_D,
  input  _8_D,
  output _1_Q,
  output _3_Q,
  output _2_Q,
  output _4_Q,
  output _5_Q,
  output _7_Q,
  output _6_Q,
  output _8_Q
);

  wire and_1_out, not_1_out;

  PowerSupply powersupply_1 (.VDD(VCC), .GND(GND));
  not not_1 (not_1_out, nEN);
  and and_1 (and_1_out, not_1_out, CLK);
  D_FF #(.Bits(8)) d_ff_1 (
    .D({_8_D, _7_D, _6_D, _5_D, _4_D, _3_D, _2_D, _1_D}), .C(and_1_out),
    .Q({_8_Q, _7_Q, _6_Q, _5_Q, _4_Q, _3_Q, _2_Q, _1_Q}));  // open: nQ

  // Notes on the sheet:
  //   nEN: pin 1
  //   _1_Q: pin 2
  //   VCC: pin 20
  //   GND: pin 10
  //   _1_D: pin 3
  //   _2_D: pin 4
  //   _3_Q: pin 6
  //   CLK: pin 11
  //   _2_Q: pin 5
  //   _3_D: pin 7
  //   _4_D: pin 8
  //   _4_Q: pin 9
  //   _5_Q: pin 12
  //   _5_D: pin 13
  //   _6_D: pin 14
  //   _7_Q: pin 16
  //   _6_Q: pin 15
  //   _7_D: pin 17
  //   _8_D: pin 18
  //   _8_Q: pin 19
endmodule
