// Digital circuit SRAM.dig as structural Verilog
module SRAM (
  input  NC,
  input  A_0,
  input  A_1,
  input  A_2,
  input  A_3,
  input  A_4,
  input  A_5,
  input  A_6,
  input  A_7,
  input  A_8,
  input  A_9,
  input  A_10,
  input  A_11,
  input  GND,
  input  VCC,
  input  nWE,
  input  A_12,
  input  CS_2,
  input  nCS_1,
  input  nOE,
  output D_0,
  output D_1,
  output D_2,
  output D_3,
  output D_4,
  output D_5,
  output D_6,
  output D_7
);

  wire and_1_out, not_1_out, not_2_out;
  wire [7:0] RAM_d;

  PullDown pulldown_1 (.out(NC));
  RAMSinglePortSel #(.AddrBits(13), .Bits(8)) RAM (
    .A({A_12, A_11, A_10, A_9, A_8, A_7, A_6, A_5, A_4, A_3, A_2, A_1, A_0}), .CS(and_1_out), .WE(not_2_out),
    .OE(nWE), .D(RAM_d));
  BusSplitter #(.Bits(8)) bussplitter_1 (
    .D(RAM_d), .OE(nWE), .D0(D_0), .D1(D_1), .D2(D_2), .D3(D_3), .D4(D_4), .D5(D_5), .D6(D_6), .D7(D_7));
  and and_1 (and_1_out, not_1_out, CS_2);
  not not_1 (not_1_out, nCS_1);
  not not_2 (not_2_out, nWE);

  // Notes on the sheet:
  //   NC: pin 1
  //   A_0: pin 10
  //   A_1: pin 9
  //   A_2: pin 8
  //   A_3: pin 7
  //   A_4: pin 6
  //   A_5: pin 5
  //   A_6: pin 4
  //   A_7: pin 3
  //   A_8: pin 25
  //   A_9: pin 24
  //   A_10: pin 21
  //   A_11: pin 23
  //   GND: pin 14
  //   VCC: pin 28
  //   nWE: pin 27
  //   A_12: pin 2
  //   CS_2: pin 26
  //   nCS_1: pin 20
  //   D_0: pin 11
  //   D_1: pin 12
  //   D_2: pin 13
  //   D_3: pin 15
  //   D_4: pin 16
  //   D_5: pin 17
  //   D_6: pin 18
  //   D_7: pin 19
  //   nOE: pin 22
endmodule
